// Logisim project TP01S.circ as structural Verilog: 4 circuits, main circuit b2_nand
module b2_original (
  input  A1,
  input  B1,
  input  A0,
  input  B0,
  input  G,
  input  P,
  input  E,
  output ZG,
  output ZP,
  output ZE
);

  wire and_1_out, and_2_out, and_3_out, and_4_out, and_5_out, and_6_out, and_7_out, and_8_out, and_9_out,
       and_10_out, not_1_out, not_2_out, not_3_out, not_4_out, not_5_out, not_6_out, or_1_out, or_2_out;

  not not_1 (not_1_out, A1);
  not not_2 (not_2_out, B1);
  not not_3 (not_3_out, A0);
  not not_4 (not_4_out, B0);
  and and_1 (and_1_out, not_1_out, B1);
  and and_2 (and_2_out, A1, not_2_out);
  and and_3 (and_3_out, not_3_out, B0);
  and and_4 (and_4_out, A0, not_4_out);
  or or_1 (or_1_out, and_1_out, and_2_out);
  or or_2 (or_2_out, and_3_out, and_4_out);
  not not_5 (not_5_out, or_1_out);
  not not_6 (not_6_out, or_2_out);
  and and_5 (and_5_out, B1, not_1_out);
  and and_6 (and_6_out, not_2_out, A1);
  and and_7 (and_7_out, B0, not_5_out, not_3_out);
  and and_8 (and_8_out, not_4_out, not_5_out, A0);
  and and_9 (and_9_out, not_5_out, not_6_out, G);
  and and_10 (and_10_out, not_5_out, not_6_out, P);
  and and_11 (ZE, not_5_out, not_6_out, E);
  or or_3 (ZG, and_6_out, and_8_out, and_9_out);
  or or_4 (ZP, and_5_out, and_7_out, and_10_out);
endmodule

module b2_subc (
  input  A0,
  input  B0,
  output E0,
  output E0b
);

  wire and_1_out, and_2_out, nand_1_out, nand_2_out, nand_3_out, nand_4_out, nand_5_out, not_1_out,
       not_2_out, or_1_out;

  not not_1 (not_1_out, A0);
  not not_2 (not_2_out, B0);
  nand nand_1 (nand_1_out, A0, 1'b1);
  nand nand_2 (nand_2_out, B0, 1'b1);
  and and_1 (and_1_out, not_1_out, B0);
  and and_2 (and_2_out, A0, not_2_out);
  nand nand_3 (nand_3_out, nand_1_out, B0);
  nand nand_4 (nand_4_out, A0, nand_2_out);
  or or_1 (or_1_out, and_1_out, and_2_out);
  nand nand_5 (nand_5_out, nand_3_out, nand_4_out);
  not not_3 (E0, or_1_out);
  nand nand_6 (E0b, nand_5_out, nand_5_out);
endmodule

module b2_nand (
  input  A1,
  input  B1,
  input  A0,
  input  B0,
  input  G,
  input  P,
  input  E,
  output ZG,
  output ZP,
  output ZE
);

  wire nand_1_out, nand_2_out, nand_3_out, nand_4_out, nand_5_out, nand_6_out, nand_7_out, nand_8_out,
       nand_9_out, nand_10_out, nand_11_out, nand_12_out, nand_13_out, nand_14_out, nand_15_out, nand_16_out,
       nand_17_out, nand_18_out, nand_19_out;

  nand nand_1 (nand_1_out, A1, 1'b1);
  nand nand_2 (nand_2_out, B1, 1'b1);
  nand nand_3 (nand_3_out, A0, 1'b1);
  nand nand_4 (nand_4_out, B0, 1'b1);
  nand nand_5 (nand_5_out, nand_1_out, B1);
  nand nand_6 (nand_6_out, A1, nand_2_out);
  nand nand_7 (nand_7_out, nand_3_out, B0);
  nand nand_8 (nand_8_out, A0, nand_4_out);
  nand nand_9 (nand_9_out, nand_5_out, nand_6_out);
  nand nand_10 (nand_10_out, nand_7_out, nand_8_out);
  nand nand_11 (nand_11_out, nand_9_out, nand_9_out);
  nand nand_12 (nand_12_out, nand_10_out, nand_10_out);
  nand nand_13 (nand_13_out, B1, nand_1_out);
  nand nand_14 (nand_14_out, nand_2_out, A1);
  nand nand_15 (nand_15_out, B0, nand_11_out, nand_3_out);
  nand nand_16 (nand_16_out, nand_4_out, nand_11_out, A0);
  nand nand_17 (nand_17_out, nand_11_out, nand_12_out, G);
  nand nand_18 (nand_18_out, nand_11_out, nand_12_out, P);
  nand nand_19 (nand_19_out, nand_11_out, nand_12_out, E);
  nand nand_20 (ZG, nand_14_out, nand_16_out, nand_17_out);
  nand nand_21 (ZP, nand_13_out, nand_15_out, nand_18_out);
  nand nand_22 (ZE, nand_19_out, nand_19_out);
endmodule

module b2_c2 (
);

  wire b2_i01_ze, b2_i01_zg, b2_i01_zp, b2_i02_ze, b2_i02_zg, b2_i02_zp, DipSwitch_1_sw1, DipSwitch_1_sw2,
       DipSwitch_1_sw3, DipSwitch_1_sw4, DipSwitch_1_sw7, DipSwitch_1_sw8, DipSwitch_1_sw9, DipSwitch_1_sw10;

  DipSwitch #(.number(10)) DipSwitch_1 (
    .sw1(DipSwitch_1_sw1), .sw2(DipSwitch_1_sw2), .sw3(DipSwitch_1_sw3), .sw4(DipSwitch_1_sw4),
    .sw7(DipSwitch_1_sw7), .sw8(DipSwitch_1_sw8), .sw9(DipSwitch_1_sw9), .sw10(DipSwitch_1_sw10));  // open: sw5, sw6
  b2_nand b2_i01 (
    .A1(DipSwitch_1_sw1), .B1(DipSwitch_1_sw2), .A0(DipSwitch_1_sw3), .B0(DipSwitch_1_sw4), .G(1'b0),
    .P(1'b0), .E(1'b1), .ZG(b2_i01_zg), .ZP(b2_i01_zp), .ZE(b2_i01_ze));
  b2_nand b2_i02 (
    .A1(DipSwitch_1_sw7), .B1(DipSwitch_1_sw8), .A0(DipSwitch_1_sw9), .B0(DipSwitch_1_sw10), .G(b2_i01_zg),
    .P(b2_i01_zp), .E(b2_i01_ze), .ZG(b2_i02_zg), .ZP(b2_i02_zp), .ZE(b2_i02_ze));
  LED ZG (.in(b2_i02_zg));
  LED ZP (.in(b2_i02_zp));
  LED ZE (.in(b2_i02_ze));
endmodule
