// Logisim project TP02S.circ as structural Verilog: 12 circuits, main circuit seven_seg_controller
module seven_seg_controller (
);

  wire DipSwitch_1_sw1, DipSwitch_1_sw2, DipSwitch_1_sw3, DipSwitch_1_sw4, fonction_a_1_a, fonction_b_1_b,
       fonction_c_1_c, fonction_d_1_d, fonction_e_1_e, fonction_f_1_f, fonction_g_1_g;

  DipSwitch #(.number(4)) DipSwitch_1 (
    .sw1(DipSwitch_1_sw1), .sw2(DipSwitch_1_sw2), .sw3(DipSwitch_1_sw3), .sw4(DipSwitch_1_sw4));
  fonction_a fonction_a_1 (
    .W(DipSwitch_1_sw1), .X(DipSwitch_1_sw2), .Y(DipSwitch_1_sw3), .Z(DipSwitch_1_sw4), .a(fonction_a_1_a));
  fonction_b fonction_b_1 (
    .W(DipSwitch_1_sw1), .X(DipSwitch_1_sw2), .Y(DipSwitch_1_sw3), .Z(DipSwitch_1_sw4), .b(fonction_b_1_b));
  fonction_c fonction_c_1 (
    .W(DipSwitch_1_sw1), .X(DipSwitch_1_sw2), .Y(DipSwitch_1_sw3), .Z(DipSwitch_1_sw4), .c(fonction_c_1_c));
  fonction_d fonction_d_1 (
    .W(DipSwitch_1_sw1), .X(DipSwitch_1_sw2), .Y(DipSwitch_1_sw3), .Z(DipSwitch_1_sw4), .d(fonction_d_1_d));
  fonction_e fonction_e_1 (
    .W(DipSwitch_1_sw1), .X(DipSwitch_1_sw2), .Y(DipSwitch_1_sw3), .Z(DipSwitch_1_sw4), .e(fonction_e_1_e));
  fonction_f fonction_f_1 (
    .W(DipSwitch_1_sw1), .X(DipSwitch_1_sw2), .Y(DipSwitch_1_sw3), .Z(DipSwitch_1_sw4), .f(fonction_f_1_f));
  fonction_g fonction_g_1 (
    .W(DipSwitch_1_sw1), .X(DipSwitch_1_sw2), .Y(DipSwitch_1_sw3), .Z(DipSwitch_1_sw4), .g(fonction_g_1_g));
  _7_Segment_Display L_7_Segment_Display_1 (
    .g(fonction_g_1_g), .f(fonction_f_1_f), .a(fonction_a_1_a), .b(fonction_b_1_b), .e(fonction_e_1_e),
    .d(fonction_d_1_d), .c(fonction_c_1_c));  // open: dp
endmodule

module fonction_a (
  input  W,
  input  X,
  input  Y,
  input  Z,
  output a
);

  wire and_1_out, and_2_out, and_3_out, and_4_out, not_1_out, not_2_out, not_3_out, not_4_out, or_1_out;

  not not_1 (not_1_out, W);
  not not_2 (not_2_out, X);
  not not_3 (not_3_out, Y);
  not not_4 (not_4_out, Z);
  and and_1 (and_1_out, not_1_out, not_2_out, not_3_out, Z);
  and and_2 (and_2_out, not_1_out, X, not_3_out, not_4_out);
  and and_3 (and_3_out, W, not_2_out, Y, Z);
  and and_4 (and_4_out, W, X, not_3_out, Z);
  or or_1 (or_1_out, and_1_out, and_2_out, and_3_out, and_4_out);
  not not_5 (a, or_1_out);
endmodule

module fonction_b (
  input  W,
  input  X,
  input  Y,
  input  Z,
  output b
);

  wire and_1_out, and_2_out, and_3_out, and_4_out, and_5_out, not_1_out, not_2_out, not_3_out, not_4_out;

  not not_1 (not_1_out, W);
  not not_2 (not_2_out, X);
  not not_3 (not_3_out, Y);
  not not_4 (not_4_out, Z);
  and and_1 (and_1_out, not_1_out, not_2_out);
  and and_2 (and_2_out, not_2_out, not_4_out);
  and and_3 (and_3_out, not_1_out, not_3_out, not_4_out);
  and and_4 (and_4_out, not_1_out, Y, Z);
  and and_5 (and_5_out, W, not_3_out, Z);
  or or_1 (b, and_1_out, and_2_out, and_3_out, and_4_out, and_5_out);
endmodule

module fonction_c (
  input  W,
  input  X,
  input  Y,
  input  Z,
  output c
);

  wire and_1_out, and_2_out, and_3_out, not_1_out, not_2_out, not_3_out, not_4_out, or_1_out;

  not not_1 (not_1_out, W);
  not not_2 (not_2_out, X);
  not not_3 (not_3_out, Y);
  not not_4 (not_4_out, Z);
  and and_1 (and_1_out, W, X, not_4_out);
  and and_2 (and_2_out, W, X, Y);
  and and_3 (and_3_out, not_1_out, not_2_out, Y, not_4_out);
  or or_1 (or_1_out, and_1_out, and_2_out, and_3_out);
  not not_5 (c, or_1_out);
endmodule

module fonction_d (
  input  W,
  input  X,
  input  Y,
  input  Z,
  output d
);

  wire and_1_out, and_2_out, and_3_out, and_4_out, and_5_out, not_1_out, not_2_out, not_3_out, not_4_out;

  not not_1 (not_1_out, W);
  not not_2 (not_2_out, X);
  not not_3 (not_3_out, Y);
  not not_4 (not_4_out, Z);
  and and_1 (and_1_out, W, not_3_out);
  and and_2 (and_2_out, X, Y, not_4_out);
  and and_3 (and_3_out, not_2_out, Y, Z);
  and and_4 (and_4_out, not_1_out, not_2_out, not_4_out);
  and and_5 (and_5_out, X, not_3_out, Z);
  or or_1 (d, and_1_out, and_2_out, and_3_out, and_4_out, and_5_out);
endmodule

module fonction_e (
  input  W,
  input  X,
  input  Y,
  input  Z,
  output e
);

  wire and_1_out, and_2_out, and_3_out, and_4_out, not_1_out, not_2_out, not_3_out, not_4_out;

  not not_1 (not_1_out, W);
  not not_2 (not_2_out, X);
  not not_3 (not_3_out, Y);
  not not_4 (not_4_out, Z);
  and and_1 (and_1_out, W, X);
  and and_2 (and_2_out, W, Y);
  and and_3 (and_3_out, not_2_out, not_4_out);
  and and_4 (and_4_out, Y, not_4_out);
  or or_1 (e, and_1_out, and_2_out, and_3_out, and_4_out);
endmodule

module fonction_f (
  input  W,
  input  X,
  input  Y,
  input  Z,
  output f
);

  wire and_1_out, and_2_out, and_3_out, and_4_out, not_1_out, not_2_out, not_3_out, not_4_out, or_1_out;

  not not_1 (not_1_out, W);
  not not_2 (not_2_out, X);
  not not_3 (not_3_out, Y);
  not not_4 (not_4_out, Z);
  and and_1 (and_1_out, W, X, not_3_out, Z);
  and and_2 (and_2_out, not_1_out, Y, Z);
  and and_3 (and_3_out, not_1_out, not_2_out, Y);
  and and_4 (and_4_out, not_1_out, not_2_out, Z);
  or or_1 (or_1_out, and_1_out, and_2_out, and_3_out, and_4_out);
  not not_5 (f, or_1_out);
endmodule

module fonction_g (
  input  W,
  input  X,
  input  Y,
  input  Z,
  output g
);

  wire and_1_out, and_2_out, and_3_out, not_1_out, not_2_out, not_3_out, not_4_out, or_1_out;

  not not_1 (not_1_out, W);
  not not_2 (not_2_out, X);
  not not_3 (not_3_out, Y);
  not not_4 (not_4_out, Z);
  and and_1 (and_1_out, not_1_out, not_2_out, not_3_out);
  and and_2 (and_2_out, W, X, not_3_out, not_4_out);
  and and_3 (and_3_out, not_1_out, X, Y, Z);
  or or_1 (or_1_out, and_1_out, and_2_out, and_3_out);
  not not_5 (g, or_1_out);
endmodule

module fonction_a_nor (
  input  W,
  input  X,
  input  Y,
  input  Z,
  output a
);

  wire nor_1_out, nor_2_out, nor_3_out, nor_4_out, nor_5_out, nor_6_out, nor_7_out, nor_8_out;

  nor nor_1 (nor_1_out, W, 1'b0);
  nor nor_2 (nor_2_out, X, 1'b0);
  nor nor_3 (nor_3_out, Y, 1'b0);
  nor nor_4 (nor_4_out, Z, 1'b0);
  nor nor_5 (nor_5_out, W, X, Y, nor_4_out);
  nor nor_6 (nor_6_out, W, nor_2_out, Y, Z);
  nor nor_7 (nor_7_out, nor_1_out, X, nor_3_out, nor_4_out);
  nor nor_8 (nor_8_out, nor_1_out, nor_2_out, Y, nor_4_out);
  nor nor_9 (a, nor_5_out, nor_6_out, nor_7_out, nor_8_out);
endmodule

module fonction_b_nand (
  input  W,
  input  X,
  input  Y,
  input  Z,
  output b
);

  wire nand_1_out, nand_2_out, nand_3_out, nand_4_out, nand_5_out, nand_6_out, nand_7_out, nand_8_out,
       nand_9_out;

  nand nand_1 (nand_1_out, W, W);
  nand nand_2 (nand_2_out, X, X);
  nand nand_3 (nand_3_out, Y, Y);
  nand nand_4 (nand_4_out, Z, Z);
  nand nand_5 (nand_5_out, nand_1_out, nand_2_out);
  nand nand_6 (nand_6_out, nand_2_out, nand_4_out);
  nand nand_7 (nand_7_out, nand_1_out, nand_3_out, nand_4_out);
  nand nand_8 (nand_8_out, nand_1_out, Y, Z);
  nand nand_9 (nand_9_out, W, nand_3_out, Z);
  nand nand_10 (b, nand_5_out, nand_6_out, nand_7_out, nand_8_out, nand_9_out);
endmodule

module fonction_c_or_xor (
  input  W,
  input  X,
  input  Y,
  input  Z,
  output c
);

  wire or_1_out, or_2_out, or_3_out, or_4_out, xor_1_out, xor_2_out, xor_3_out, xor_4_out, xor_5_out,
       xor_6_out, xor_7_out;

  xor xor_1 (xor_1_out, W, 1'b1);
  xor xor_2 (xor_2_out, X, 1'b1);
  xor xor_3 (xor_3_out, Y, 1'b1);
  xor xor_4 (xor_4_out, Z, 1'b1);
  or or_1 (or_1_out, xor_1_out, xor_2_out, Z);
  or or_2 (or_2_out, xor_1_out, xor_2_out, xor_3_out);
  or or_3 (or_3_out, W, X, xor_3_out, Z);
  xor xor_5 (xor_5_out, or_1_out, 1'b1);
  xor xor_6 (xor_6_out, or_2_out, 1'b1);
  xor xor_7 (xor_7_out, or_3_out, 1'b1);
  or or_4 (or_4_out, xor_5_out, xor_6_out, xor_7_out);
  xor xor_8 (c, 1'b1, or_4_out);
endmodule

module fonction_e_forme_conjunctive (
  input  W,
  input  X,
  input  Y,
  input  Z,
  output e
);

  wire not_1_out, not_2_out, not_3_out, not_4_out, or_1_out, or_2_out, or_3_out, or_4_out;

  not not_1 (not_1_out, W);
  not not_2 (not_2_out, X);
  not not_3 (not_3_out, Y);
  not not_4 (not_4_out, Z);
  or or_1 (or_1_out, not_1_out, not_2_out);
  or or_2 (or_2_out, not_1_out, not_3_out);
  or or_3 (or_3_out, W, Z);
  or or_4 (or_4_out, not_2_out, Z);
  nand nand_1 (e, or_1_out, or_2_out, or_3_out, or_4_out);
endmodule
