// Logisim project TP03S.circ as structural Verilog: 13 circuits, main circuit exercise_2
module exercise_2 (
  input  [3:0] A,
  input  [3:0] B,
  output Overflow,
  output [3:0] P
);

  wire Full_adder_1_rn, Full_adder_2_rn, Half_adder_1_r0;

  Prob_1 Half_adder_1 (.P0(P[0]), .r0(Half_adder_1_r0), .B0(B[0]), .A0(A[0]));
  Prob_2_3_4 Full_adder_3 (.Pn(P[3]), .rn(Overflow), .Bn(B[3]), .rn_1(Full_adder_2_rn), .An(A[3]));
  Prob_2_3_4 Full_adder_2 (.Pn(P[2]), .rn(Full_adder_2_rn), .Bn(B[2]), .rn_1(Full_adder_1_rn), .An(A[2]));
  Prob_2_3_4 Full_adder_1 (.Pn(P[1]), .rn(Full_adder_1_rn), .Bn(B[1]), .rn_1(Half_adder_1_r0), .An(A[1]));
endmodule

module Prob_1 (
  input  A0,
  input  B0,
  output P0,
  output r0
);

  and and_1 (r0, A0, B0);
  xor xor_1 (P0, A0, B0);
endmodule

module Prob_2_3_4 (
  input  An,
  input  Bn,
  input  rn_1,
  output Pn,
  output rn
);

  wire and_1_out, and_2_out, and_3_out, xor_1_out;

  xor xor_1 (xor_1_out, An, Bn);
  and and_1 (and_1_out, An, Bn);
  and and_2 (and_2_out, An, rn_1);
  and and_3 (and_3_out, Bn, rn_1);
  xor xor_2 (Pn, xor_1_out, rn_1);
  or or_1 (rn, and_1_out, and_2_out, and_3_out);
endmodule

module exercise_4 (
  input  [3:0] A,
  input  [3:0] B,
  output Underflow,
  output [3:0] M
);

  wire Full_sub_2_en, Full_subtractor1_en, Half_subtractor_1_e0;

  Prob_5 Half_subtractor_1 (.M0(M[0]), .e0(Half_subtractor_1_e0), .B0(B[0]), .A0(A[0]));
  Prob_6_7_8 Full_sub_3 (.Mn(M[3]), .en(Underflow), .Bn(B[3]), .en_1(Full_sub_2_en), .An(A[3]));
  Prob_6_7_8 Full_sub_2 (.Mn(M[2]), .en(Full_sub_2_en), .Bn(B[2]), .en_1(Full_subtractor1_en), .An(A[2]));
  Prob_6_7_8 Full_subtractor1 (.Mn(M[1]), .en(Full_subtractor1_en), .Bn(B[1]), .en_1(Half_subtractor_1_e0), .An(A[1]));
endmodule

module Prob_5 (
  input  A0,
  input  B0,
  output M0,
  output e0
);

  wire not_1_out;

  not not_1 (not_1_out, A0);
  and and_1 (e0, not_1_out, B0);
  xor xor_1 (M0, A0, B0);
endmodule

module Prob_6_7_8 (
  input  An,
  input  Bn,
  input  en_1,
  output Mn,
  output en
);

  wire and_1_out, and_2_out, and_3_out, not_1_out, xor_1_out;

  not not_1 (not_1_out, An);
  xor xor_1 (xor_1_out, An, Bn);
  and and_1 (and_1_out, not_1_out, Bn);
  and and_2 (and_2_out, not_1_out, en_1);
  and and_3 (and_3_out, Bn, en_1);
  xor xor_2 (Mn, xor_1_out, en_1);
  or or_1 (en, and_1_out, and_2_out, and_3_out);
endmodule

module exercise_5 (
);

  wire and_1_out, and_2_out, and_3_out, and_4_out, and_5_out, and_6_out, But_out, or_1_out, or_2_out,
       or_3_out, POR_out, sr_latch_1_q, sr_latch_2_q, sr_latch_3_q;

  Button But (.out(But_out));
  Button POR (.out(POR_out));
  and and_1 (and_1_out, sr_latch_1_q, sr_latch_2_q, sr_latch_3_q, ~But_out);  // AND_Gate
  and and_2 (and_2_out, ~sr_latch_1_q, ~sr_latch_2_q, ~sr_latch_3_q, But_out);  // AND_Gate
  and and_3 (and_3_out, ~sr_latch_1_q, sr_latch_2_q, sr_latch_3_q, But_out);  // AND_Gate
  and and_4 (and_4_out, sr_latch_1_q, ~sr_latch_2_q, ~sr_latch_3_q, ~But_out);  // AND_Gate
  and and_5 (and_5_out, ~sr_latch_1_q, ~sr_latch_2_q, sr_latch_3_q, ~But_out);  // AND_Gate
  and and_6 (and_6_out, sr_latch_1_q, sr_latch_2_q, ~sr_latch_3_q, But_out);  // AND_Gate
  or or_1 (or_1_out, and_1_out, POR_out);
  or or_2 (or_2_out, and_3_out, POR_out);
  or or_3 (or_3_out, and_5_out, POR_out);
  sr_latch sr_latch_1 (.Reset(or_1_out), .Set(and_2_out), .Q(sr_latch_1_q));
  sr_latch sr_latch_2 (.Reset(or_2_out), .Set(and_4_out), .Q(sr_latch_2_q));
  sr_latch sr_latch_3 (.Reset(or_3_out), .Set(and_6_out), .Q(sr_latch_3_q));
  LED Lamp1 (.in(sr_latch_1_q));
  LED Lamp2 (.in(sr_latch_2_q));
  LED Lamp3 (.in(sr_latch_3_q));

  // Notes on the sheet:
  //   Aynchronous solution: SR.latches
endmodule

module sr_latch (
  input  Reset,
  input  Set,
  output Q
);

  wire nor_2_out;

  nor nor_1 (Q, Reset, nor_2_out);
  nor nor_2 (nor_2_out, Q, Set);
endmodule

module exercise_5_b (
);

  wire and_1_out, and_2_out, and_3_out, and_4_out, and_5_out, and_6_out, But_out, CLK_1kHz_out, d_ff_1_q,
       or_1_out, or_2_out, or_3_out, POR_out, sr_latch_1_q, sr_latch_2_q, sr_latch_3_q;

  Button But (.out(But_out));
  Clock CLK_1kHz (.out(CLK_1kHz_out));
  Button POR (.out(POR_out));
  D_Flip_Flop d_ff_1 (.D(But_out), .clk(CLK_1kHz_out), .Q(d_ff_1_q), .reset(POR_out));  // open: Qn, preset
  and and_1 (and_1_out, sr_latch_1_q, sr_latch_2_q, sr_latch_3_q, ~d_ff_1_q);  // AND_Gate
  and and_2 (and_2_out, ~sr_latch_1_q, ~sr_latch_2_q, ~sr_latch_3_q, d_ff_1_q);  // AND_Gate
  and and_3 (and_3_out, ~sr_latch_1_q, sr_latch_2_q, sr_latch_3_q, d_ff_1_q);  // AND_Gate
  and and_4 (and_4_out, sr_latch_1_q, ~sr_latch_2_q, ~sr_latch_3_q, ~d_ff_1_q);  // AND_Gate
  and and_5 (and_5_out, ~sr_latch_1_q, ~sr_latch_2_q, sr_latch_3_q, ~d_ff_1_q);  // AND_Gate
  and and_6 (and_6_out, sr_latch_1_q, sr_latch_2_q, ~sr_latch_3_q, d_ff_1_q);  // AND_Gate
  or or_1 (or_1_out, and_1_out, POR_out);
  or or_2 (or_2_out, and_3_out, POR_out);
  or or_3 (or_3_out, and_5_out, POR_out);
  sr_latch sr_latch_1 (.Reset(or_1_out), .Set(and_2_out), .Q(sr_latch_1_q));
  sr_latch sr_latch_2 (.Reset(or_2_out), .Set(and_4_out), .Q(sr_latch_2_q));
  sr_latch sr_latch_3 (.Reset(or_3_out), .Set(and_6_out), .Q(sr_latch_3_q));
  LED LED_1 (.in(sr_latch_1_q));
  LED LED_2 (.in(sr_latch_2_q));
  LED LED_3 (.in(sr_latch_3_q));

  // Notes on the sheet:
  //   Aynchronous solution: SR.latches
endmodule

module exercise_5_c (
);

  wire and_1_out, and_2_out, and_3_out, and_4_out, and_5_out, and_6_out, But_out, CLK_1kHz_out, d_ff_1_q,
       or_1_out, or_2_out, or_3_out, POR_out, s_r_ff_1_q, s_r_ff_2_q, s_r_ff_3_q;

  Button But (.out(But_out));
  Clock CLK_1kHz (.out(CLK_1kHz_out));
  Button POR (.out(POR_out));
  D_Flip_Flop d_ff_1 (.D(But_out), .clk(CLK_1kHz_out), .Q(d_ff_1_q), .reset(POR_out));  // open: Qn, preset
  and and_1 (and_1_out, ~s_r_ff_1_q, ~s_r_ff_2_q, ~s_r_ff_3_q, d_ff_1_q);  // AND_Gate
  and and_2 (and_2_out, s_r_ff_1_q, s_r_ff_2_q, s_r_ff_3_q, ~d_ff_1_q);  // AND_Gate
  and and_3 (and_3_out, s_r_ff_1_q, ~s_r_ff_2_q, ~s_r_ff_3_q, ~d_ff_1_q);  // AND_Gate
  and and_4 (and_4_out, ~s_r_ff_1_q, s_r_ff_2_q, s_r_ff_2_q, d_ff_1_q);  // AND_Gate
  and and_5 (and_5_out, s_r_ff_1_q, s_r_ff_2_q, ~s_r_ff_3_q, d_ff_1_q);  // AND_Gate
  and and_6 (and_6_out, ~s_r_ff_1_q, ~s_r_ff_2_q, s_r_ff_3_q, ~d_ff_1_q);  // AND_Gate
  or or_1 (or_1_out, and_2_out, POR_out);
  or or_2 (or_2_out, and_4_out, POR_out);
  or or_3 (or_3_out, and_6_out, POR_out);
  S_R_Flip_Flop s_r_ff_1 (.clk(1'b0), .Q(s_r_ff_1_q), .reset(or_1_out), .preset(and_1_out));  // open: S, R, Qn
  S_R_Flip_Flop s_r_ff_2 (.clk(1'b0), .Q(s_r_ff_2_q), .reset(or_2_out), .preset(and_3_out));  // open: S, R, Qn
  S_R_Flip_Flop s_r_ff_3 (.clk(1'b0), .Q(s_r_ff_3_q), .reset(or_3_out), .preset(and_5_out));  // open: S, R, Qn
  LED LED_1 (.in(s_r_ff_1_q));
  LED LED_2 (.in(s_r_ff_2_q));
  LED LED_3 (.in(s_r_ff_3_q));

  // Notes on the sheet:
  //   Asynchronous solution: asynchronous control of SR-FFs
endmodule

module exercise_5_d (
);

  wire and_1_out, and_2_out, and_3_out, and_4_out, and_5_out, and_6_out, But_out, CLK_1kHz_out, d_ff_1_q,
       or_1_out, or_2_out, or_3_out, POR_out, s_r_ff_1_q, s_r_ff_2_q, s_r_ff_3_q;

  Button But (.out(But_out));
  Clock CLK_1kHz (.out(CLK_1kHz_out));
  Button POR (.out(POR_out));
  D_Flip_Flop d_ff_1 (.D(But_out), .clk(CLK_1kHz_out), .Q(d_ff_1_q), .reset(POR_out));  // open: Qn, preset
  and and_1 (and_1_out, ~s_r_ff_1_q, ~s_r_ff_2_q, ~s_r_ff_3_q, d_ff_1_q);  // AND_Gate
  and and_2 (and_2_out, s_r_ff_1_q, s_r_ff_2_q, s_r_ff_3_q, ~d_ff_1_q);  // AND_Gate
  and and_3 (and_3_out, s_r_ff_1_q, ~s_r_ff_2_q, ~s_r_ff_3_q, ~d_ff_1_q);  // AND_Gate
  and and_4 (and_4_out, ~s_r_ff_1_q, s_r_ff_2_q, s_r_ff_2_q, d_ff_1_q);  // AND_Gate
  and and_5 (and_5_out, s_r_ff_1_q, s_r_ff_2_q, ~s_r_ff_3_q, d_ff_1_q);  // AND_Gate
  and and_6 (and_6_out, ~s_r_ff_1_q, ~s_r_ff_2_q, s_r_ff_3_q, ~d_ff_1_q);  // AND_Gate
  or or_1 (or_1_out, and_2_out, POR_out);
  or or_2 (or_2_out, and_4_out, POR_out);
  or or_3 (or_3_out, and_6_out, POR_out);
  S_R_Flip_Flop s_r_ff_1 (.S(and_1_out), .R(or_1_out), .clk(CLK_1kHz_out), .Q(s_r_ff_1_q));  // open: reset, Qn, preset
  S_R_Flip_Flop s_r_ff_2 (.S(and_3_out), .R(or_2_out), .clk(CLK_1kHz_out), .Q(s_r_ff_2_q));  // open: reset, Qn, preset
  S_R_Flip_Flop s_r_ff_3 (.S(and_5_out), .R(or_3_out), .clk(CLK_1kHz_out), .Q(s_r_ff_3_q));  // open: reset, Qn, preset
  LED LED_1 (.in(s_r_ff_1_q));
  LED LED_2 (.in(s_r_ff_2_q));
  LED LED_3 (.in(s_r_ff_3_q));

  // Notes on the sheet:
  //   Pseudo-asynchronous solution: high-frequency clocled SR-FFs
endmodule

module exercise_5_e (
);

  wire But_out, CLK_1kHz_out, CLK_250Hz_out, d_ff_1_q, d_ff_2_q, d_ff_3_q, d_ff_4_q, POR_out, TL5e_l1_next,
       TL5e_l2_next, TL5e_l3_next;

  Button But (.out(But_out));
  Clock CLK_1kHz (.out(CLK_1kHz_out));
  Clock #(.highDuration(4), .lowDuration(4)) CLK_250Hz (.out(CLK_250Hz_out));
  Button POR (.out(POR_out));
  D_Flip_Flop d_ff_1 (.D(But_out), .clk(CLK_1kHz_out), .Q(d_ff_1_q), .reset(POR_out));  // open: Qn, preset
  Transition_Logic_5_e TL5e (
    .B(d_ff_1_q), .L1_current(d_ff_2_q), .L2_current(d_ff_3_q), .L3_current(d_ff_4_q),
    .L1_next(TL5e_l1_next), .L2_next(TL5e_l2_next), .L3_next(TL5e_l3_next));
  D_Flip_Flop d_ff_2 (.D(TL5e_l1_next), .clk(CLK_250Hz_out), .Q(d_ff_2_q), .reset(POR_out));  // open: Qn, preset
  D_Flip_Flop d_ff_3 (.D(TL5e_l2_next), .clk(CLK_250Hz_out), .Q(d_ff_3_q), .reset(POR_out));  // open: Qn, preset
  D_Flip_Flop d_ff_4 (.D(TL5e_l3_next), .clk(CLK_250Hz_out), .Q(d_ff_4_q), .reset(POR_out));  // open: Qn, preset
  LED LED_1 (.in(d_ff_2_q));
  LED LED_2 (.in(d_ff_3_q));
  LED LED_3 (.in(d_ff_4_q));

  // Notes on the sheet:
  //   Synchronous solution: Medvedev FSM
endmodule

module Transition_Logic_5_e (
  input  B,
  input  L1_current,
  input  L2_current,
  input  L3_current,
  output L1_next,
  output L2_next,
  output L3_next
);

  wire and_1_out, and_2_out, and_3_out, and_4_out, and_5_out, and_6_out, and_7_out, and_8_out, and_9_out,
       not_1_out, not_2_out;

  not not_1 (not_1_out, B);
  not not_2 (not_2_out, L3_current);
  and and_1 (and_1_out, L1_current, not_2_out);
  and and_2 (and_2_out, B, not_2_out);
  and and_3 (and_3_out, B, L1_current);
  and and_4 (and_4_out, not_1_out, L2_current);
  and and_5 (and_5_out, not_1_out, L1_current);
  and and_6 (and_6_out, L1_current, L2_current);
  and and_7 (and_7_out, L2_current, L3_current);
  and and_8 (and_8_out, B, L3_current);
  and and_9 (and_9_out, B, L2_current);
  or or_1 (L1_next, and_1_out, and_2_out, and_3_out);
  or or_2 (L2_next, and_4_out, and_5_out, and_6_out);
  or or_3 (L3_next, and_7_out, and_8_out, and_9_out);
endmodule
