// Logisim project application16x2display.circ as structural Verilog
module LCD16x2_tb_exe (
  input  lcdLoadLI,
  input  resetHI,
  output lcdctst,
  output lcdrwO,
  output lcdrsO,
  output lcdeO,
  output [7:0] lcddataO8
);

  wire clock_1_out, DipSwitch_1_sw1, pgen_ppn01_no1, pgen_ppn01_p1o1, pgen_ppn01_p2o1;
  wire [7:0] CNTR01_q;
  wire [31:0] data1a32_q, data1b_q, data1c_q, data1d_q, data2a_q, data2b_q, data2c_q, data2d_q, register_1_q,
       register_2_q, register_3_q, register_4_q, register_5_q, register_6_q, register_7_q, register_8_q;

  DipSwitch #(.number(2)) DipSwitch_1 (.sw1(DipSwitch_1_sw1));  // open: sw2
  Counter CNTR01 (
    .clr(resetHI), .load(DipSwitch_1_sw1), .up(1'b1), .clk(lcdLoadLI), .D(8'h30), .Q(CNTR01_q));  // open: count, carry
  Register #(.width(32)) register_1 (
    .D(32'h4550464c), .clk(pgen_ppn01_p1o1), .Q(register_1_q), .clr(resetHI));  // open: en
  Register #(.width(32)) register_2 (
    .D(32'h20454531), .clk(pgen_ppn01_p1o1), .Q(register_2_q), .clr(resetHI));  // open: en
  Register #(.width(32)) register_3 (
    .D(32'h31302d45), .clk(pgen_ppn01_p1o1), .Q(register_3_q), .clr(resetHI));  // open: en
  Register #(.width(32)) register_4 (
    .D(32'h45323037), .clk(pgen_ppn01_p1o1), .Q(register_4_q), .clr(resetHI));  // open: en
  Register #(.width(32)) register_5 (
    .D(32'h50757368), .clk(pgen_ppn01_p1o1), .Q(register_5_q), .clr(resetHI));  // open: en
  Register #(.width(32)) register_6 (
    .D(32'h20503120), .clk(pgen_ppn01_p1o1), .Q(register_6_q), .clr(resetHI));  // open: en
  Register #(.width(32)) register_7 (
    .D(32'h20202020), .clk(pgen_ppn01_p1o1), .Q(register_7_q), .clr(resetHI));  // open: en
  Register #(.width(32)) register_8 (
    .D({24'h20207e, CNTR01_q}), .clk(pgen_ppn01_p1o1), .Q(register_8_q), .clr(resetHI));  // open: en
  Pulsegen_ppn pgen_ppn01 (.setreset(lcdLoadLI), .p1O1(pgen_ppn01_p1o1), .p2O1(pgen_ppn01_p2o1), .nO1(pgen_ppn01_no1));
  Register #(.width(32)) data1a32 (.D(register_1_q), .clk(pgen_ppn01_p2o1), .Q(data1a32_q), .clr(resetHI));  // open: en
  Register #(.width(32)) data1b (.D(register_2_q), .clk(pgen_ppn01_p2o1), .Q(data1b_q), .clr(resetHI));  // open: en
  Register #(.width(32)) data1c (.D(register_3_q), .clk(pgen_ppn01_p2o1), .Q(data1c_q), .clr(resetHI));  // open: en
  Register #(.width(32)) data1d (.D(register_4_q), .clk(pgen_ppn01_p2o1), .Q(data1d_q), .clr(resetHI));  // open: en
  Register #(.width(32)) data2a (.D(register_5_q), .clk(pgen_ppn01_p2o1), .Q(data2a_q), .clr(resetHI));  // open: en
  Register #(.width(32)) data2b (.D(register_6_q), .clk(pgen_ppn01_p2o1), .Q(data2b_q), .clr(resetHI));  // open: en
  Register #(.width(32)) data2c (.D(register_7_q), .clk(pgen_ppn01_p2o1), .Q(data2c_q), .clr(resetHI));  // open: en
  Register #(.width(32)) data2d (.D(register_8_q), .clk(pgen_ppn01_p2o1), .Q(data2d_q), .clr(resetHI));  // open: en
  Clock #(.lowDuration(5)) clock_1 (.out(clock_1_out));
  LCD16x2_driver LCD16x2_driver_1 (
    .resetLI(pgen_ppn01_no1), .data1aI32(data1a32_q), .data1bI32(data1b_q), .data1cI32(data1c_q),
    .data1dI32(data1d_q), .data2aI32(data2a_q), .data2bI32(data2b_q), .data2cI32(data2c_q),
    .data2dI32(data2d_q), .rwO(lcdrwO), .rsO(lcdrsO), .eO(lcdeO), .dataO(lcddataO8));
  buf buffer_1 (lcdctst, clock_1_out);

  // Notes on the sheet:
  //   E = 45, P = 50, F = 46, L = 4c
  //   BLOCK01: LCD Application Example
  //   BLOCK02: LCD 16x2 Driver
  //   BLOCK03: LCD 16x2 Simulator 
  //   removed for execution
endmodule

module LCD16x2_tb_sim (
  input  lcdLoadLI,
  input  resetHI
);

  wire DipSwitch_1_sw1, pgen_ppn01_no1, pgen_ppn01_p1o1, pgen_ppn01_p2o1;
  wire [7:0] CNTR01_q, lcd_char4_encoder_1_ldata_c0_o40_2, lcd_char4_encoder_1_ldata_c1_o40,
       lcd_char4_encoder_1_ldata_c1_o40_2, lcd_char4_encoder_1_ldata_c1_o40_3,
       lcd_char4_encoder_1_ldata_c1_o40_4, lcd_char4_encoder_1_ldata_c1_o40_5,
       lcd_char4_encoder_1_ldata_c2_o40, lcd_char4_encoder_1_ldata_c2_o40_2,
       lcd_char4_encoder_1_ldata_c2_o40_3, lcd_char4_encoder_1_ldata_c2_o40_4,
       lcd_char4_encoder_1_ldata_c2_o40_5, lcd_char4_encoder_1_ldata_c3_o40,
       lcd_char4_encoder_1_ldata_c3_o40_2, lcd_char4_encoder_1_ldata_c3_o40_3,
       lcd_char4_encoder_1_ldata_c3_o40_4, lcd_char4_encoder_1_ldata_c3_o40_5,
       lcd_char4_encoder_2_ldata_c0_o40_2, lcd_char4_encoder_2_ldata_c0_o40_3,
       lcd_char4_encoder_2_ldata_c0_o40_4, lcd_char4_encoder_2_ldata_c1_o40_2,
       lcd_char4_encoder_2_ldata_c1_o40_3, lcd_char4_encoder_2_ldata_c1_o40_4,
       lcd_char4_encoder_2_ldata_c2_o40_2, lcd_char4_encoder_2_ldata_c2_o40_3,
       lcd_char4_encoder_2_ldata_c2_o40_4, lcd_char4_encoder_2_ldata_c3_o40_2,
       lcd_char4_encoder_2_ldata_c3_o40_3, lcd_char4_encoder_2_ldata_c3_o40_4,
       lcd_char4_encoder_3_ldata_c0_o40_2, lcd_char4_encoder_3_ldata_c1_o40,
       lcd_char4_encoder_3_ldata_c1_o40_2, lcd_char4_encoder_3_ldata_c1_o40_3,
       lcd_char4_encoder_3_ldata_c1_o40_4, lcd_char4_encoder_3_ldata_c1_o40_5,
       lcd_char4_encoder_3_ldata_c2_o40, lcd_char4_encoder_3_ldata_c2_o40_2,
       lcd_char4_encoder_3_ldata_c2_o40_3, lcd_char4_encoder_3_ldata_c2_o40_4,
       lcd_char4_encoder_3_ldata_c2_o40_5, lcd_char4_encoder_3_ldata_c3_o40,
       lcd_char4_encoder_3_ldata_c3_o40_2, lcd_char4_encoder_3_ldata_c3_o40_3,
       lcd_char4_encoder_3_ldata_c3_o40_4, lcd_char4_encoder_3_ldata_c3_o40_5,
       lcd_char4_encoder_4_ldata_c0_o40_2, lcd_char4_encoder_4_ldata_c0_o40_3,
       lcd_char4_encoder_4_ldata_c0_o40_4, lcd_char4_encoder_4_ldata_c1_o40_2,
       lcd_char4_encoder_4_ldata_c1_o40_3, lcd_char4_encoder_4_ldata_c1_o40_4,
       lcd_char4_encoder_4_ldata_c2_o40_2, lcd_char4_encoder_4_ldata_c2_o40_3,
       lcd_char4_encoder_4_ldata_c2_o40_4, lcd_char4_encoder_4_ldata_c3_o40_2,
       lcd_char4_encoder_4_ldata_c3_o40_3, lcd_char4_encoder_4_ldata_c3_o40_4,
       lcd_char4_encoder_5_ldata_c0_o40_2, lcd_char4_encoder_5_ldata_c1_o40,
       lcd_char4_encoder_5_ldata_c1_o40_2, lcd_char4_encoder_5_ldata_c1_o40_3,
       lcd_char4_encoder_5_ldata_c1_o40_4, lcd_char4_encoder_5_ldata_c1_o40_5,
       lcd_char4_encoder_5_ldata_c2_o40, lcd_char4_encoder_5_ldata_c2_o40_2,
       lcd_char4_encoder_5_ldata_c2_o40_3, lcd_char4_encoder_5_ldata_c2_o40_4,
       lcd_char4_encoder_5_ldata_c2_o40_5, lcd_char4_encoder_5_ldata_c3_o40,
       lcd_char4_encoder_5_ldata_c3_o40_2, lcd_char4_encoder_5_ldata_c3_o40_3,
       lcd_char4_encoder_5_ldata_c3_o40_4, lcd_char4_encoder_5_ldata_c3_o40_5,
       lcd_char4_encoder_6_ldata_c0_o40_2, lcd_char4_encoder_6_ldata_c0_o40_3,
       lcd_char4_encoder_6_ldata_c0_o40_4, lcd_char4_encoder_6_ldata_c1_o40_2,
       lcd_char4_encoder_6_ldata_c1_o40_3, lcd_char4_encoder_6_ldata_c1_o40_4,
       lcd_char4_encoder_6_ldata_c2_o40_2, lcd_char4_encoder_6_ldata_c2_o40_3,
       lcd_char4_encoder_6_ldata_c2_o40_4, lcd_char4_encoder_6_ldata_c3_o40_2,
       lcd_char4_encoder_6_ldata_c3_o40_3, lcd_char4_encoder_6_ldata_c3_o40_4,
       lcd_char4_encoder_7_ldata_c0_o40_2, lcd_char4_encoder_7_ldata_c1_o40,
       lcd_char4_encoder_7_ldata_c1_o40_2, lcd_char4_encoder_7_ldata_c1_o40_3,
       lcd_char4_encoder_7_ldata_c1_o40_4, lcd_char4_encoder_7_ldata_c1_o40_5,
       lcd_char4_encoder_7_ldata_c2_o40, lcd_char4_encoder_7_ldata_c2_o40_2,
       lcd_char4_encoder_7_ldata_c2_o40_3, lcd_char4_encoder_7_ldata_c2_o40_4,
       lcd_char4_encoder_7_ldata_c2_o40_5, lcd_char4_encoder_7_ldata_c3_o40,
       lcd_char4_encoder_7_ldata_c3_o40_2, lcd_char4_encoder_7_ldata_c3_o40_3,
       lcd_char4_encoder_7_ldata_c3_o40_4, lcd_char4_encoder_7_ldata_c3_o40_5,
       lcd_char4_encoder_8_ldata_c0_o40_2, lcd_char4_encoder_8_ldata_c0_o40_3,
       lcd_char4_encoder_8_ldata_c0_o40_4, lcd_char4_encoder_8_ldata_c1_o40_2,
       lcd_char4_encoder_8_ldata_c1_o40_3, lcd_char4_encoder_8_ldata_c1_o40_4,
       lcd_char4_encoder_8_ldata_c2_o40_2, lcd_char4_encoder_8_ldata_c2_o40_3,
       lcd_char4_encoder_8_ldata_c2_o40_4, lcd_char4_encoder_8_ldata_c3_o40_2,
       lcd_char4_encoder_8_ldata_c3_o40_3, lcd_char4_encoder_8_ldata_c3_o40_4;
  wire [15:0] lcd_char4_encoder_2_ldata_c0_o40, lcd_char4_encoder_2_ldata_c1_o40,
       lcd_char4_encoder_2_ldata_c2_o40, lcd_char4_encoder_2_ldata_c3_o40, lcd_char4_encoder_4_ldata_c0_o40,
       lcd_char4_encoder_4_ldata_c1_o40, lcd_char4_encoder_4_ldata_c2_o40, lcd_char4_encoder_4_ldata_c3_o40,
       lcd_char4_encoder_6_ldata_c0_o40, lcd_char4_encoder_6_ldata_c1_o40, lcd_char4_encoder_6_ldata_c2_o40,
       lcd_char4_encoder_6_ldata_c3_o40, lcd_char4_encoder_8_ldata_c0_o40, lcd_char4_encoder_8_ldata_c1_o40,
       lcd_char4_encoder_8_ldata_c2_o40, lcd_char4_encoder_8_ldata_c3_o40;
  wire [31:0] data1a32_q, data1b_q, data1c_q, data1d_q, data2a_q, data2b_q, data2c_q, data2d_q,
       lcd_char4_encoder_1_ldata_c0_o40, lcd_char4_encoder_3_ldata_c0_o40, lcd_char4_encoder_5_ldata_c0_o40,
       lcd_char4_encoder_7_ldata_c0_o40, register_1_q, register_2_q, register_3_q, register_4_q,
       register_5_q, register_6_q, register_7_q, register_8_q;

  DipSwitch #(.number(2)) DipSwitch_1 (.sw1(DipSwitch_1_sw1));  // open: sw2
  Counter CNTR01 (
    .clr(resetHI), .load(DipSwitch_1_sw1), .up(1'b1), .clk(lcdLoadLI), .D(8'h30), .Q(CNTR01_q));  // open: count, carry
  Register #(.width(32)) register_1 (
    .D(32'h4550464c), .clk(pgen_ppn01_p1o1), .Q(register_1_q), .clr(resetHI));  // open: en
  Register #(.width(32)) register_2 (
    .D(32'h20454531), .clk(pgen_ppn01_p1o1), .Q(register_2_q), .clr(resetHI));  // open: en
  Register #(.width(32)) register_3 (
    .D(32'h31302d45), .clk(pgen_ppn01_p1o1), .Q(register_3_q), .clr(resetHI));  // open: en
  Register #(.width(32)) register_4 (
    .D(32'h45323037), .clk(pgen_ppn01_p1o1), .Q(register_4_q), .clr(resetHI));  // open: en
  Register #(.width(32)) register_5 (
    .D(32'h50757368), .clk(pgen_ppn01_p1o1), .Q(register_5_q), .clr(resetHI));  // open: en
  Register #(.width(32)) register_6 (
    .D(32'h20503120), .clk(pgen_ppn01_p1o1), .Q(register_6_q), .clr(resetHI));  // open: en
  Register #(.width(32)) register_7 (
    .D(32'h20202020), .clk(pgen_ppn01_p1o1), .Q(register_7_q), .clr(resetHI));  // open: en
  Register #(.width(32)) register_8 (
    .D({24'h20207e, CNTR01_q}), .clk(pgen_ppn01_p1o1), .Q(register_8_q), .clr(resetHI));  // open: en
  Pulsegen_ppn pgen_ppn01 (.setreset(lcdLoadLI), .p1O1(pgen_ppn01_p1o1), .p2O1(pgen_ppn01_p2o1), .nO1(pgen_ppn01_no1));
  Register #(.width(32)) data1a32 (.D(register_1_q), .clk(pgen_ppn01_p2o1), .Q(data1a32_q), .clr(resetHI));  // open: en
  Register #(.width(32)) data1b (.D(register_2_q), .clk(pgen_ppn01_p2o1), .Q(data1b_q), .clr(resetHI));  // open: en
  Register #(.width(32)) data1c (.D(register_3_q), .clk(pgen_ppn01_p2o1), .Q(data1c_q), .clr(resetHI));  // open: en
  Register #(.width(32)) data1d (.D(register_4_q), .clk(pgen_ppn01_p2o1), .Q(data1d_q), .clr(resetHI));  // open: en
  Register #(.width(32)) data2a (.D(register_5_q), .clk(pgen_ppn01_p2o1), .Q(data2a_q), .clr(resetHI));  // open: en
  Register #(.width(32)) data2b (.D(register_6_q), .clk(pgen_ppn01_p2o1), .Q(data2b_q), .clr(resetHI));  // open: en
  Register #(.width(32)) data2c (.D(register_7_q), .clk(pgen_ppn01_p2o1), .Q(data2c_q), .clr(resetHI));  // open: en
  Register #(.width(32)) data2d (.D(register_8_q), .clk(pgen_ppn01_p2o1), .Q(data2d_q), .clr(resetHI));  // open: en
  DotMatrix #(.matrixrows(8)) L1C0 (
    .col0(lcd_char4_encoder_1_ldata_c3_o40_5), .col1(lcd_char4_encoder_1_ldata_c3_o40_4),
    .col2(lcd_char4_encoder_1_ldata_c3_o40_3), .col3(lcd_char4_encoder_1_ldata_c3_o40_2),
    .col4(lcd_char4_encoder_1_ldata_c3_o40));
  DotMatrix #(.matrixrows(8)) dotmatrix_1 (
    .col0(lcd_char4_encoder_2_ldata_c3_o40_4), .col1(lcd_char4_encoder_2_ldata_c3_o40_3),
    .col2(lcd_char4_encoder_2_ldata_c3_o40_2), .col3(lcd_char4_encoder_2_ldata_c3_o40[15:8]),
    .col4(lcd_char4_encoder_2_ldata_c3_o40[7:0]));
  DotMatrix #(.matrixrows(8)) dotmatrix_2 (
    .col0(lcd_char4_encoder_1_ldata_c2_o40_5), .col1(lcd_char4_encoder_1_ldata_c2_o40_4),
    .col2(lcd_char4_encoder_1_ldata_c2_o40_3), .col3(lcd_char4_encoder_1_ldata_c2_o40_2),
    .col4(lcd_char4_encoder_1_ldata_c2_o40));
  DotMatrix #(.matrixrows(8)) dotmatrix_3 (
    .col0(lcd_char4_encoder_2_ldata_c2_o40_4), .col1(lcd_char4_encoder_2_ldata_c2_o40_3),
    .col2(lcd_char4_encoder_2_ldata_c2_o40_2), .col3(lcd_char4_encoder_2_ldata_c2_o40[15:8]),
    .col4(lcd_char4_encoder_2_ldata_c2_o40[7:0]));
  DotMatrix #(.matrixrows(8)) dotmatrix_4 (
    .col0(lcd_char4_encoder_1_ldata_c1_o40_5), .col1(lcd_char4_encoder_1_ldata_c1_o40_4),
    .col2(lcd_char4_encoder_1_ldata_c1_o40_3), .col3(lcd_char4_encoder_1_ldata_c1_o40_2),
    .col4(lcd_char4_encoder_1_ldata_c1_o40));
  DotMatrix #(.matrixrows(8)) dotmatrix_5 (
    .col0(lcd_char4_encoder_2_ldata_c1_o40_4), .col1(lcd_char4_encoder_2_ldata_c1_o40_3),
    .col2(lcd_char4_encoder_2_ldata_c1_o40_2), .col3(lcd_char4_encoder_2_ldata_c1_o40[15:8]),
    .col4(lcd_char4_encoder_2_ldata_c1_o40[7:0]));
  LCD_char4_encoder lcd_char4_encoder_1 (
    .Ldata_I32(data1a32_q), .load_IL(pgen_ppn01_no1), .reset_IH(resetHI),
    .Ldata_C0_O40({lcd_char4_encoder_1_ldata_c0_o40_2, lcd_char4_encoder_1_ldata_c0_o40}),
    .Ldata_C1_O40({lcd_char4_encoder_1_ldata_c1_o40_5, lcd_char4_encoder_1_ldata_c1_o40_4, lcd_char4_encoder_1_ldata_c1_o40_3, lcd_char4_encoder_1_ldata_c1_o40_2, lcd_char4_encoder_1_ldata_c1_o40}),
    .Ldata_C2_O40({lcd_char4_encoder_1_ldata_c2_o40_5, lcd_char4_encoder_1_ldata_c2_o40_4, lcd_char4_encoder_1_ldata_c2_o40_3, lcd_char4_encoder_1_ldata_c2_o40_2, lcd_char4_encoder_1_ldata_c2_o40}),
    .Ldata_C3_O40({lcd_char4_encoder_1_ldata_c3_o40_5, lcd_char4_encoder_1_ldata_c3_o40_4, lcd_char4_encoder_1_ldata_c3_o40_3, lcd_char4_encoder_1_ldata_c3_o40_2, lcd_char4_encoder_1_ldata_c3_o40}));
  DotMatrix #(.matrixrows(8)) dotmatrix_6 (
    .col0(lcd_char4_encoder_1_ldata_c0_o40_2), .col1(lcd_char4_encoder_1_ldata_c0_o40[31:24]),
    .col2(lcd_char4_encoder_1_ldata_c0_o40[23:16]), .col3(lcd_char4_encoder_1_ldata_c0_o40[15:8]),
    .col4(lcd_char4_encoder_1_ldata_c0_o40[7:0]));
  DotMatrix #(.matrixrows(8)) dotmatrix_7 (
    .col0(lcd_char4_encoder_2_ldata_c0_o40_4), .col1(lcd_char4_encoder_2_ldata_c0_o40_3),
    .col2(lcd_char4_encoder_2_ldata_c0_o40_2), .col3(lcd_char4_encoder_2_ldata_c0_o40[15:8]),
    .col4(lcd_char4_encoder_2_ldata_c0_o40[7:0]));
  LCD_char4_encoder lcd_char4_encoder_2 (
    .Ldata_I32(data2a_q), .load_IL(pgen_ppn01_no1), .reset_IH(resetHI),
    .Ldata_C0_O40({lcd_char4_encoder_2_ldata_c0_o40_4, lcd_char4_encoder_2_ldata_c0_o40_3, lcd_char4_encoder_2_ldata_c0_o40_2, lcd_char4_encoder_2_ldata_c0_o40}),
    .Ldata_C1_O40({lcd_char4_encoder_2_ldata_c1_o40_4, lcd_char4_encoder_2_ldata_c1_o40_3, lcd_char4_encoder_2_ldata_c1_o40_2, lcd_char4_encoder_2_ldata_c1_o40}),
    .Ldata_C2_O40({lcd_char4_encoder_2_ldata_c2_o40_4, lcd_char4_encoder_2_ldata_c2_o40_3, lcd_char4_encoder_2_ldata_c2_o40_2, lcd_char4_encoder_2_ldata_c2_o40}),
    .Ldata_C3_O40({lcd_char4_encoder_2_ldata_c3_o40_4, lcd_char4_encoder_2_ldata_c3_o40_3, lcd_char4_encoder_2_ldata_c3_o40_2, lcd_char4_encoder_2_ldata_c3_o40}));
  DotMatrix #(.matrixrows(8)) dotmatrix_8 (
    .col0(lcd_char4_encoder_3_ldata_c3_o40_5), .col1(lcd_char4_encoder_3_ldata_c3_o40_4),
    .col2(lcd_char4_encoder_3_ldata_c3_o40_3), .col3(lcd_char4_encoder_3_ldata_c3_o40_2),
    .col4(lcd_char4_encoder_3_ldata_c3_o40));
  DotMatrix #(.matrixrows(8)) dotmatrix_9 (
    .col0(lcd_char4_encoder_4_ldata_c3_o40_4), .col1(lcd_char4_encoder_4_ldata_c3_o40_3),
    .col2(lcd_char4_encoder_4_ldata_c3_o40_2), .col3(lcd_char4_encoder_4_ldata_c3_o40[15:8]),
    .col4(lcd_char4_encoder_4_ldata_c3_o40[7:0]));
  DotMatrix #(.matrixrows(8)) dotmatrix_10 (
    .col0(lcd_char4_encoder_3_ldata_c2_o40_5), .col1(lcd_char4_encoder_3_ldata_c2_o40_4),
    .col2(lcd_char4_encoder_3_ldata_c2_o40_3), .col3(lcd_char4_encoder_3_ldata_c2_o40_2),
    .col4(lcd_char4_encoder_3_ldata_c2_o40));
  DotMatrix #(.matrixrows(8)) dotmatrix_11 (
    .col0(lcd_char4_encoder_4_ldata_c2_o40_4), .col1(lcd_char4_encoder_4_ldata_c2_o40_3),
    .col2(lcd_char4_encoder_4_ldata_c2_o40_2), .col3(lcd_char4_encoder_4_ldata_c2_o40[15:8]),
    .col4(lcd_char4_encoder_4_ldata_c2_o40[7:0]));
  DotMatrix #(.matrixrows(8)) dotmatrix_12 (
    .col0(lcd_char4_encoder_3_ldata_c1_o40_5), .col1(lcd_char4_encoder_3_ldata_c1_o40_4),
    .col2(lcd_char4_encoder_3_ldata_c1_o40_3), .col3(lcd_char4_encoder_3_ldata_c1_o40_2),
    .col4(lcd_char4_encoder_3_ldata_c1_o40));
  DotMatrix #(.matrixrows(8)) dotmatrix_13 (
    .col0(lcd_char4_encoder_4_ldata_c1_o40_4), .col1(lcd_char4_encoder_4_ldata_c1_o40_3),
    .col2(lcd_char4_encoder_4_ldata_c1_o40_2), .col3(lcd_char4_encoder_4_ldata_c1_o40[15:8]),
    .col4(lcd_char4_encoder_4_ldata_c1_o40[7:0]));
  LCD_char4_encoder lcd_char4_encoder_3 (
    .Ldata_I32(data1b_q), .load_IL(pgen_ppn01_no1), .reset_IH(resetHI),
    .Ldata_C0_O40({lcd_char4_encoder_3_ldata_c0_o40_2, lcd_char4_encoder_3_ldata_c0_o40}),
    .Ldata_C1_O40({lcd_char4_encoder_3_ldata_c1_o40_5, lcd_char4_encoder_3_ldata_c1_o40_4, lcd_char4_encoder_3_ldata_c1_o40_3, lcd_char4_encoder_3_ldata_c1_o40_2, lcd_char4_encoder_3_ldata_c1_o40}),
    .Ldata_C2_O40({lcd_char4_encoder_3_ldata_c2_o40_5, lcd_char4_encoder_3_ldata_c2_o40_4, lcd_char4_encoder_3_ldata_c2_o40_3, lcd_char4_encoder_3_ldata_c2_o40_2, lcd_char4_encoder_3_ldata_c2_o40}),
    .Ldata_C3_O40({lcd_char4_encoder_3_ldata_c3_o40_5, lcd_char4_encoder_3_ldata_c3_o40_4, lcd_char4_encoder_3_ldata_c3_o40_3, lcd_char4_encoder_3_ldata_c3_o40_2, lcd_char4_encoder_3_ldata_c3_o40}));
  DotMatrix #(.matrixrows(8)) dotmatrix_14 (
    .col0(lcd_char4_encoder_3_ldata_c0_o40_2), .col1(lcd_char4_encoder_3_ldata_c0_o40[31:24]),
    .col2(lcd_char4_encoder_3_ldata_c0_o40[23:16]), .col3(lcd_char4_encoder_3_ldata_c0_o40[15:8]),
    .col4(lcd_char4_encoder_3_ldata_c0_o40[7:0]));
  DotMatrix #(.matrixrows(8)) dotmatrix_15 (
    .col0(lcd_char4_encoder_4_ldata_c0_o40_4), .col1(lcd_char4_encoder_4_ldata_c0_o40_3),
    .col2(lcd_char4_encoder_4_ldata_c0_o40_2), .col3(lcd_char4_encoder_4_ldata_c0_o40[15:8]),
    .col4(lcd_char4_encoder_4_ldata_c0_o40[7:0]));
  LCD_char4_encoder lcd_char4_encoder_4 (
    .Ldata_I32(data2b_q), .load_IL(pgen_ppn01_no1), .reset_IH(resetHI),
    .Ldata_C0_O40({lcd_char4_encoder_4_ldata_c0_o40_4, lcd_char4_encoder_4_ldata_c0_o40_3, lcd_char4_encoder_4_ldata_c0_o40_2, lcd_char4_encoder_4_ldata_c0_o40}),
    .Ldata_C1_O40({lcd_char4_encoder_4_ldata_c1_o40_4, lcd_char4_encoder_4_ldata_c1_o40_3, lcd_char4_encoder_4_ldata_c1_o40_2, lcd_char4_encoder_4_ldata_c1_o40}),
    .Ldata_C2_O40({lcd_char4_encoder_4_ldata_c2_o40_4, lcd_char4_encoder_4_ldata_c2_o40_3, lcd_char4_encoder_4_ldata_c2_o40_2, lcd_char4_encoder_4_ldata_c2_o40}),
    .Ldata_C3_O40({lcd_char4_encoder_4_ldata_c3_o40_4, lcd_char4_encoder_4_ldata_c3_o40_3, lcd_char4_encoder_4_ldata_c3_o40_2, lcd_char4_encoder_4_ldata_c3_o40}));
  DotMatrix #(.matrixrows(8)) dotmatrix_16 (
    .col0(lcd_char4_encoder_5_ldata_c3_o40_5), .col1(lcd_char4_encoder_5_ldata_c3_o40_4),
    .col2(lcd_char4_encoder_5_ldata_c3_o40_3), .col3(lcd_char4_encoder_5_ldata_c3_o40_2),
    .col4(lcd_char4_encoder_5_ldata_c3_o40));
  DotMatrix #(.matrixrows(8)) dotmatrix_17 (
    .col0(lcd_char4_encoder_6_ldata_c3_o40_4), .col1(lcd_char4_encoder_6_ldata_c3_o40_3),
    .col2(lcd_char4_encoder_6_ldata_c3_o40_2), .col3(lcd_char4_encoder_6_ldata_c3_o40[15:8]),
    .col4(lcd_char4_encoder_6_ldata_c3_o40[7:0]));
  DotMatrix #(.matrixrows(8)) dotmatrix_18 (
    .col0(lcd_char4_encoder_5_ldata_c2_o40_5), .col1(lcd_char4_encoder_5_ldata_c2_o40_4),
    .col2(lcd_char4_encoder_5_ldata_c2_o40_3), .col3(lcd_char4_encoder_5_ldata_c2_o40_2),
    .col4(lcd_char4_encoder_5_ldata_c2_o40));
  DotMatrix #(.matrixrows(8)) dotmatrix_19 (
    .col0(lcd_char4_encoder_6_ldata_c2_o40_4), .col1(lcd_char4_encoder_6_ldata_c2_o40_3),
    .col2(lcd_char4_encoder_6_ldata_c2_o40_2), .col3(lcd_char4_encoder_6_ldata_c2_o40[15:8]),
    .col4(lcd_char4_encoder_6_ldata_c2_o40[7:0]));
  DotMatrix #(.matrixrows(8)) dotmatrix_20 (
    .col0(lcd_char4_encoder_5_ldata_c1_o40_5), .col1(lcd_char4_encoder_5_ldata_c1_o40_4),
    .col2(lcd_char4_encoder_5_ldata_c1_o40_3), .col3(lcd_char4_encoder_5_ldata_c1_o40_2),
    .col4(lcd_char4_encoder_5_ldata_c1_o40));
  DotMatrix #(.matrixrows(8)) dotmatrix_21 (
    .col0(lcd_char4_encoder_6_ldata_c1_o40_4), .col1(lcd_char4_encoder_6_ldata_c1_o40_3),
    .col2(lcd_char4_encoder_6_ldata_c1_o40_2), .col3(lcd_char4_encoder_6_ldata_c1_o40[15:8]),
    .col4(lcd_char4_encoder_6_ldata_c1_o40[7:0]));
  LCD_char4_encoder lcd_char4_encoder_5 (
    .Ldata_I32(data1c_q), .load_IL(pgen_ppn01_no1), .reset_IH(resetHI),
    .Ldata_C0_O40({lcd_char4_encoder_5_ldata_c0_o40_2, lcd_char4_encoder_5_ldata_c0_o40}),
    .Ldata_C1_O40({lcd_char4_encoder_5_ldata_c1_o40_5, lcd_char4_encoder_5_ldata_c1_o40_4, lcd_char4_encoder_5_ldata_c1_o40_3, lcd_char4_encoder_5_ldata_c1_o40_2, lcd_char4_encoder_5_ldata_c1_o40}),
    .Ldata_C2_O40({lcd_char4_encoder_5_ldata_c2_o40_5, lcd_char4_encoder_5_ldata_c2_o40_4, lcd_char4_encoder_5_ldata_c2_o40_3, lcd_char4_encoder_5_ldata_c2_o40_2, lcd_char4_encoder_5_ldata_c2_o40}),
    .Ldata_C3_O40({lcd_char4_encoder_5_ldata_c3_o40_5, lcd_char4_encoder_5_ldata_c3_o40_4, lcd_char4_encoder_5_ldata_c3_o40_3, lcd_char4_encoder_5_ldata_c3_o40_2, lcd_char4_encoder_5_ldata_c3_o40}));
  DotMatrix #(.matrixrows(8)) dotmatrix_22 (
    .col0(lcd_char4_encoder_5_ldata_c0_o40_2), .col1(lcd_char4_encoder_5_ldata_c0_o40[31:24]),
    .col2(lcd_char4_encoder_5_ldata_c0_o40[23:16]), .col3(lcd_char4_encoder_5_ldata_c0_o40[15:8]),
    .col4(lcd_char4_encoder_5_ldata_c0_o40[7:0]));
  DotMatrix #(.matrixrows(8)) dotmatrix_23 (
    .col0(lcd_char4_encoder_6_ldata_c0_o40_4), .col1(lcd_char4_encoder_6_ldata_c0_o40_3),
    .col2(lcd_char4_encoder_6_ldata_c0_o40_2), .col3(lcd_char4_encoder_6_ldata_c0_o40[15:8]),
    .col4(lcd_char4_encoder_6_ldata_c0_o40[7:0]));
  LCD_char4_encoder lcd_char4_encoder_6 (
    .Ldata_I32(data2c_q), .load_IL(pgen_ppn01_no1), .reset_IH(resetHI),
    .Ldata_C0_O40({lcd_char4_encoder_6_ldata_c0_o40_4, lcd_char4_encoder_6_ldata_c0_o40_3, lcd_char4_encoder_6_ldata_c0_o40_2, lcd_char4_encoder_6_ldata_c0_o40}),
    .Ldata_C1_O40({lcd_char4_encoder_6_ldata_c1_o40_4, lcd_char4_encoder_6_ldata_c1_o40_3, lcd_char4_encoder_6_ldata_c1_o40_2, lcd_char4_encoder_6_ldata_c1_o40}),
    .Ldata_C2_O40({lcd_char4_encoder_6_ldata_c2_o40_4, lcd_char4_encoder_6_ldata_c2_o40_3, lcd_char4_encoder_6_ldata_c2_o40_2, lcd_char4_encoder_6_ldata_c2_o40}),
    .Ldata_C3_O40({lcd_char4_encoder_6_ldata_c3_o40_4, lcd_char4_encoder_6_ldata_c3_o40_3, lcd_char4_encoder_6_ldata_c3_o40_2, lcd_char4_encoder_6_ldata_c3_o40}));
  DotMatrix #(.matrixrows(8)) dotmatrix_24 (
    .col0(lcd_char4_encoder_7_ldata_c3_o40_5), .col1(lcd_char4_encoder_7_ldata_c3_o40_4),
    .col2(lcd_char4_encoder_7_ldata_c3_o40_3), .col3(lcd_char4_encoder_7_ldata_c3_o40_2),
    .col4(lcd_char4_encoder_7_ldata_c3_o40));
  DotMatrix #(.matrixrows(8)) dotmatrix_25 (
    .col0(lcd_char4_encoder_8_ldata_c3_o40_4), .col1(lcd_char4_encoder_8_ldata_c3_o40_3),
    .col2(lcd_char4_encoder_8_ldata_c3_o40_2), .col3(lcd_char4_encoder_8_ldata_c3_o40[15:8]),
    .col4(lcd_char4_encoder_8_ldata_c3_o40[7:0]));
  DotMatrix #(.matrixrows(8)) dotmatrix_26 (
    .col0(lcd_char4_encoder_7_ldata_c2_o40_5), .col1(lcd_char4_encoder_7_ldata_c2_o40_4),
    .col2(lcd_char4_encoder_7_ldata_c2_o40_3), .col3(lcd_char4_encoder_7_ldata_c2_o40_2),
    .col4(lcd_char4_encoder_7_ldata_c2_o40));
  DotMatrix #(.matrixrows(8)) dotmatrix_27 (
    .col0(lcd_char4_encoder_8_ldata_c2_o40_4), .col1(lcd_char4_encoder_8_ldata_c2_o40_3),
    .col2(lcd_char4_encoder_8_ldata_c2_o40_2), .col3(lcd_char4_encoder_8_ldata_c2_o40[15:8]),
    .col4(lcd_char4_encoder_8_ldata_c2_o40[7:0]));
  DotMatrix #(.matrixrows(8)) dotmatrix_28 (
    .col0(lcd_char4_encoder_7_ldata_c1_o40_5), .col1(lcd_char4_encoder_7_ldata_c1_o40_4),
    .col2(lcd_char4_encoder_7_ldata_c1_o40_3), .col3(lcd_char4_encoder_7_ldata_c1_o40_2),
    .col4(lcd_char4_encoder_7_ldata_c1_o40));
  DotMatrix #(.matrixrows(8)) dotmatrix_29 (
    .col0(lcd_char4_encoder_8_ldata_c1_o40_4), .col1(lcd_char4_encoder_8_ldata_c1_o40_3),
    .col2(lcd_char4_encoder_8_ldata_c1_o40_2), .col3(lcd_char4_encoder_8_ldata_c1_o40[15:8]),
    .col4(lcd_char4_encoder_8_ldata_c1_o40[7:0]));
  LCD_char4_encoder lcd_char4_encoder_7 (
    .Ldata_I32(data1d_q), .load_IL(pgen_ppn01_no1), .reset_IH(resetHI),
    .Ldata_C0_O40({lcd_char4_encoder_7_ldata_c0_o40_2, lcd_char4_encoder_7_ldata_c0_o40}),
    .Ldata_C1_O40({lcd_char4_encoder_7_ldata_c1_o40_5, lcd_char4_encoder_7_ldata_c1_o40_4, lcd_char4_encoder_7_ldata_c1_o40_3, lcd_char4_encoder_7_ldata_c1_o40_2, lcd_char4_encoder_7_ldata_c1_o40}),
    .Ldata_C2_O40({lcd_char4_encoder_7_ldata_c2_o40_5, lcd_char4_encoder_7_ldata_c2_o40_4, lcd_char4_encoder_7_ldata_c2_o40_3, lcd_char4_encoder_7_ldata_c2_o40_2, lcd_char4_encoder_7_ldata_c2_o40}),
    .Ldata_C3_O40({lcd_char4_encoder_7_ldata_c3_o40_5, lcd_char4_encoder_7_ldata_c3_o40_4, lcd_char4_encoder_7_ldata_c3_o40_3, lcd_char4_encoder_7_ldata_c3_o40_2, lcd_char4_encoder_7_ldata_c3_o40}));
  DotMatrix #(.matrixrows(8)) dotmatrix_30 (
    .col0(lcd_char4_encoder_7_ldata_c0_o40_2), .col1(lcd_char4_encoder_7_ldata_c0_o40[31:24]),
    .col2(lcd_char4_encoder_7_ldata_c0_o40[23:16]), .col3(lcd_char4_encoder_7_ldata_c0_o40[15:8]),
    .col4(lcd_char4_encoder_7_ldata_c0_o40[7:0]));
  DotMatrix #(.matrixrows(8)) dotmatrix_31 (
    .col0(lcd_char4_encoder_8_ldata_c0_o40_4), .col1(lcd_char4_encoder_8_ldata_c0_o40_3),
    .col2(lcd_char4_encoder_8_ldata_c0_o40_2), .col3(lcd_char4_encoder_8_ldata_c0_o40[15:8]),
    .col4(lcd_char4_encoder_8_ldata_c0_o40[7:0]));
  LCD_char4_encoder lcd_char4_encoder_8 (
    .Ldata_I32(data2d_q), .load_IL(pgen_ppn01_no1), .reset_IH(resetHI),
    .Ldata_C0_O40({lcd_char4_encoder_8_ldata_c0_o40_4, lcd_char4_encoder_8_ldata_c0_o40_3, lcd_char4_encoder_8_ldata_c0_o40_2, lcd_char4_encoder_8_ldata_c0_o40}),
    .Ldata_C1_O40({lcd_char4_encoder_8_ldata_c1_o40_4, lcd_char4_encoder_8_ldata_c1_o40_3, lcd_char4_encoder_8_ldata_c1_o40_2, lcd_char4_encoder_8_ldata_c1_o40}),
    .Ldata_C2_O40({lcd_char4_encoder_8_ldata_c2_o40_4, lcd_char4_encoder_8_ldata_c2_o40_3, lcd_char4_encoder_8_ldata_c2_o40_2, lcd_char4_encoder_8_ldata_c2_o40}),
    .Ldata_C3_O40({lcd_char4_encoder_8_ldata_c3_o40_4, lcd_char4_encoder_8_ldata_c3_o40_3, lcd_char4_encoder_8_ldata_c3_o40_2, lcd_char4_encoder_8_ldata_c3_o40}));

  // Notes on the sheet:
  //   BLOCK01: LCD Application Example
  //   removed for simulation
  //   BLOCK02: LCD 16x2 Driver
  //   BLOCK03: LCD 16x2 Simulator 
endmodule

module LCD16x2_driver (
  input  resetLI,
  input  [31:0] data1aI32,
  input  [31:0] data1bI32,
  input  [31:0] data1cI32,
  input  [31:0] data1dI32,
  input  [31:0] data2aI32,
  input  [31:0] data2bI32,
  input  [31:0] data2cI32,
  input  [31:0] data2dI32,
  output rwO,
  output rsO,
  output eO,
  output [7:0] dataO
);

  wire clkI_out;

  Clock clkI (.out(clkI_out));
  lcd_example lcd_example_1 (
    .clk(clkI_out), .rst(resetLI), .data1a(data1aI32), .data1b(data1bI32), .data1c(data1cI32),
    .data1d(data1dI32), .data2a(data2aI32), .data2b(data2bI32), .data2c(data2cI32), .data2d(data2dI32),
    .rw(rwO), .rs(rsO), .e(eO), .lcd_data(dataO));
  lcd_controller lcd_controller_1 (
    .clk(1'b0), .reset_n(1'b0), .lcd_enable(1'b0), .lcd_bus({10{1'b0}}));  // open: busy, rw, rs, e, lcd_data

  // Notes on the sheet:
  //   Tested functional at 1MHz. DE10-Lite. AxS 2023.03.30
endmodule

module Pulsegen_ppn (
  input  setreset,
  output p1O1,
  output p2O1,
  output nO1
);

  wire clk_out, d_ff_1_q, d_ff_3_q, d_ff_5_q;

  Clock clk (.out(clk_out));
  D_Flip_Flop d_ff_1 (.D(1'b0), .clk(clk_out), .Q(d_ff_1_q), .preset(setreset));  // open: Qn, reset
  D_Flip_Flop d_ff_2 (.D(d_ff_1_q), .clk(clk_out), .Q(p1O1), .reset(setreset));  // open: Qn, preset
  D_Flip_Flop d_ff_3 (.D(p1O1), .clk(clk_out), .Q(d_ff_3_q), .reset(setreset));  // open: Qn, preset
  D_Flip_Flop d_ff_4 (.D(d_ff_3_q), .clk(clk_out), .Q(p2O1), .reset(setreset));  // open: Qn, preset
  D_Flip_Flop d_ff_5 (.D(p2O1), .clk(clk_out), .Q(d_ff_5_q), .reset(setreset));  // open: Qn, preset
  D_Flip_Flop d_ff_6 (.D(d_ff_5_q), .clk(clk_out), .Qn(nO1), .reset(setreset));  // open: Q, preset
endmodule

module LCD_char4_encoder (
  input  [31:0] Ldata_I32,
  input  load_IL,
  input  reset_IH,
  output [39:0] Ldata_C0_O40,
  output [39:0] Ldata_C1_O40,
  output [39:0] Ldata_C2_O40,
  output [39:0] Ldata_C3_O40
);

  LCD_char_encoder lcd_char_encoder_1 (
    .asciiL0a_I8(Ldata_I32[7:0]), .loadLI(load_IL), .resetHI(reset_IH), .LED0C0O8(Ldata_C0_O40));
  LCD_char_encoder lcd_char_encoder_2 (
    .asciiL0a_I8(Ldata_I32[15:8]), .loadLI(load_IL), .resetHI(reset_IH), .LED0C0O8(Ldata_C1_O40));
  LCD_char_encoder lcd_char_encoder_3 (
    .asciiL0a_I8(Ldata_I32[23:16]), .loadLI(load_IL), .resetHI(reset_IH), .LED0C0O8(Ldata_C2_O40));
  LCD_char_encoder lcd_char_encoder_4 (
    .asciiL0a_I8(Ldata_I32[31:24]), .loadLI(load_IL), .resetHI(reset_IH), .LED0C0O8(Ldata_C3_O40));
endmodule

module LCD_char_encoder (
  input  [7:0] asciiL0a_I8,
  input  loadLI,
  input  resetHI,
  output [39:0] LED0C0O8
);

  wire [7:0] D0_ledmc0o8, D0_ledmc1o8, D0_ledmc2o8, D0_ledmc3o8, D0_ledmc4o8;

  HD44780UA00FlippedFont D0 (
    .ascii_I8(asciiL0a_I8), .ledmC0O8(D0_ledmc0o8), .ledmC1O8(D0_ledmc1o8), .ledmC2O8(D0_ledmc2o8),
    .ledmC3O8(D0_ledmc3o8), .ledmC4O8(D0_ledmc4o8));
  Register #(.trigger("falling")) D0DFF0 (.D(D0_ledmc0o8), .clk(loadLI), .Q(LED0C0O8[7:0]), .clr(resetHI));  // open: en
  Register #(.trigger("falling")) D0DFF1 (
    .D(D0_ledmc1o8), .clk(loadLI), .Q(LED0C0O8[15:8]), .clr(resetHI));  // open: en
  Register #(.trigger("falling")) D0DFF2 (
    .D(D0_ledmc2o8), .clk(loadLI), .Q(LED0C0O8[23:16]), .clr(resetHI));  // open: en
  Register #(.trigger("falling")) D0DFF3 (
    .D(D0_ledmc3o8), .clk(loadLI), .Q(LED0C0O8[31:24]), .clr(resetHI));  // open: en
  Register #(.trigger("falling")) D0DFF4 (
    .D(D0_ledmc4o8), .clk(loadLI), .Q(LED0C0O8[39:32]), .clr(resetHI));  // open: en

  // Notes on the sheet:
  //   IN 8-bit
  //   OUT 5x8bit
endmodule

module HD44780UA00FlippedFont (
  input  [7:0] ascii_I8,
  output [7:0] ledmC0O8,
  output [7:0] ledmC1O8,
  output [7:0] ledmC2O8,
  output [7:0] ledmC3O8,
  output [7:0] ledmC4O8
);

  wire and_1_out, and_2_out, and_3_out, and_4_out, and_5_out, and_6_out, and_7_out, and_8_out, and_9_out,
       and_10_out, and_11_out, and_12_out, and_13_out, and_14_out, and_15_out, and_16_out, and_17_out,
       and_18_out, and_19_out, and_20_out, and_21_out, and_22_out, and_23_out, and_24_out, and_25_out,
       and_26_out, and_27_out, and_28_out, and_29_out, and_30_out, and_31_out, and_32_out, and_33_out,
       and_34_out, and_35_out, and_36_out, and_37_out, and_38_out, and_39_out, and_40_out, and_41_out,
       and_42_out, and_43_out, and_44_out, and_45_out, and_46_out, and_47_out, and_48_out, and_49_out,
       and_50_out, and_51_out, and_52_out, and_53_out, and_54_out, and_55_out, and_56_out, and_57_out,
       and_58_out, and_59_out, and_60_out, and_61_out, and_62_out, and_63_out, and_64_out, and_65_out,
       and_66_out, and_67_out, and_68_out, and_69_out, and_70_out, and_71_out, and_72_out, and_73_out,
       and_74_out, and_75_out, and_76_out, and_77_out, and_78_out, and_79_out, and_80_out, and_81_out,
       and_82_out, and_83_out, and_84_out, and_85_out, and_86_out, and_87_out, and_88_out, and_89_out,
       and_90_out, and_91_out, and_92_out, and_93_out, and_94_out, and_95_out, and_96_out, and_97_out,
       and_98_out, and_99_out, and_100_out, and_101_out, and_102_out, and_103_out, and_104_out, and_105_out,
       and_106_out, and_107_out, and_108_out, and_109_out, and_110_out, and_111_out, and_112_out,
       and_113_out, and_114_out, and_115_out, and_116_out, and_117_out, and_118_out, and_119_out,
       and_120_out, and_121_out, and_122_out, and_123_out, and_124_out, and_125_out, and_126_out,
       and_127_out, and_128_out, and_129_out, and_130_out, and_131_out, and_132_out, and_133_out,
       and_134_out, and_135_out, and_136_out, and_137_out, and_138_out, and_139_out, and_140_out,
       and_141_out, and_142_out, and_143_out, and_144_out, and_145_out, and_146_out, and_147_out,
       and_148_out, and_149_out, and_150_out, and_151_out, and_152_out, and_153_out, and_154_out,
       and_155_out, and_156_out, and_157_out, and_158_out, and_159_out, and_160_out, and_161_out,
       and_162_out, and_163_out, and_164_out, and_165_out, and_166_out, and_167_out, and_168_out,
       and_169_out, and_170_out, and_171_out, and_172_out, and_173_out, and_174_out, and_175_out,
       and_176_out, and_177_out, and_178_out, and_179_out, and_180_out, and_181_out, and_182_out,
       and_183_out, and_184_out, and_185_out, and_186_out, and_187_out, and_188_out, and_189_out,
       and_190_out, and_191_out, and_192_out, and_193_out, and_194_out, and_195_out, and_196_out,
       and_197_out, and_198_out, and_199_out, and_200_out, and_201_out, and_202_out, and_203_out,
       and_204_out, and_205_out, and_206_out, and_207_out, and_208_out, and_209_out, and_210_out,
       and_211_out, and_212_out, and_213_out, and_214_out, and_215_out, and_216_out, and_217_out,
       and_218_out, and_219_out, and_220_out, and_221_out, and_222_out, and_223_out, and_224_out,
       and_225_out, and_226_out, and_227_out, and_228_out, and_229_out, and_230_out, and_231_out,
       and_232_out, and_233_out, and_234_out, and_235_out, and_236_out, and_237_out, and_238_out,
       and_239_out, and_240_out, and_241_out, and_242_out, and_243_out, and_244_out, and_245_out,
       and_246_out, and_247_out, and_248_out, and_249_out, and_250_out, and_251_out, and_252_out,
       and_253_out, and_254_out, and_255_out, and_256_out, and_257_out, and_258_out, and_259_out,
       and_260_out, and_261_out, and_262_out, and_263_out, and_264_out, and_265_out, and_266_out,
       and_267_out, and_268_out, and_269_out, and_270_out, and_271_out, and_272_out, and_273_out,
       and_274_out, and_275_out, and_276_out, and_277_out, and_278_out, and_279_out, and_280_out,
       and_281_out, and_282_out, and_283_out, and_284_out, and_285_out, and_286_out, and_287_out,
       and_288_out, and_289_out, and_290_out, and_291_out, and_292_out, and_293_out, and_294_out,
       and_295_out, and_296_out, and_297_out, and_298_out, and_299_out, and_300_out, and_301_out,
       and_302_out, and_303_out, and_304_out, and_305_out, and_306_out, and_307_out, and_308_out,
       and_309_out, and_310_out, and_311_out, and_312_out, and_313_out, and_314_out, and_315_out,
       and_316_out, and_317_out, and_318_out, and_319_out, and_320_out, and_321_out, and_322_out,
       and_323_out, and_324_out, and_325_out, and_326_out, and_327_out, and_328_out, and_329_out,
       and_330_out, and_331_out, and_332_out, and_333_out, and_334_out, and_335_out, and_336_out,
       and_337_out, and_338_out, and_339_out, and_340_out, and_341_out, and_342_out, and_343_out,
       and_344_out, and_345_out, and_346_out, and_347_out, and_348_out, and_349_out, and_350_out,
       and_351_out, and_352_out, and_353_out, and_354_out, and_355_out, and_356_out, and_357_out,
       and_358_out, and_359_out, and_360_out, and_361_out, and_362_out, and_363_out, and_364_out,
       and_365_out, and_366_out, and_367_out, and_368_out, and_369_out, and_370_out, and_371_out,
       and_372_out, and_373_out, and_374_out, and_375_out, and_376_out, and_377_out, and_378_out,
       and_379_out, and_380_out, and_381_out, and_382_out, and_383_out, and_384_out, and_385_out,
       and_386_out, and_387_out, and_388_out, and_389_out, and_390_out, and_391_out, and_392_out,
       and_393_out, and_394_out, and_395_out, and_396_out, and_397_out, and_398_out, and_399_out,
       and_400_out, and_401_out, and_402_out, and_403_out, and_404_out, and_405_out, and_406_out,
       and_407_out, and_408_out, and_409_out, and_410_out, and_411_out, and_412_out, and_413_out,
       and_414_out, and_415_out, and_416_out, and_417_out, and_418_out, and_419_out, and_420_out,
       and_421_out, and_422_out, and_423_out, and_424_out, and_425_out, and_426_out, and_427_out,
       and_428_out, and_429_out, and_430_out, and_431_out, and_432_out, and_433_out, and_434_out,
       and_435_out, and_436_out, and_437_out, and_438_out, and_439_out, and_440_out, and_441_out,
       and_442_out, and_443_out, and_444_out, and_445_out, and_446_out, and_447_out, and_448_out,
       and_449_out, and_450_out, and_451_out, and_452_out, and_453_out, and_454_out, and_455_out,
       and_456_out, and_457_out, and_458_out, and_459_out, and_460_out, and_461_out, and_462_out,
       and_463_out, and_464_out, and_465_out, and_466_out, and_467_out, and_468_out, and_469_out,
       and_470_out, and_471_out, and_472_out, and_473_out, and_474_out, and_475_out, and_476_out,
       and_477_out, and_478_out, and_479_out, and_480_out, and_481_out, and_482_out, and_483_out,
       and_484_out, and_485_out, and_486_out, and_487_out, and_488_out, and_489_out, and_490_out,
       and_491_out, and_492_out, and_493_out, and_494_out, and_495_out, and_496_out, and_497_out,
       and_498_out, and_499_out, and_500_out, and_501_out, and_502_out, and_503_out, and_504_out,
       and_505_out, and_506_out, and_507_out, and_508_out, and_509_out, and_510_out, and_511_out,
       and_512_out, and_513_out, and_514_out, and_515_out, and_516_out, and_517_out, and_518_out,
       and_519_out, and_520_out, and_521_out, and_522_out, and_523_out, and_524_out, and_525_out,
       and_526_out, and_527_out, and_528_out, and_529_out, and_530_out, and_531_out, and_532_out,
       and_533_out, and_534_out, and_535_out, and_536_out, and_537_out, and_538_out, and_539_out,
       and_540_out, and_541_out, and_542_out, and_543_out, and_544_out, and_545_out, and_546_out,
       and_547_out, and_548_out, and_549_out, and_550_out, and_551_out, and_552_out, and_553_out,
       and_554_out, and_555_out, and_556_out, and_557_out, and_558_out, and_559_out, and_560_out,
       and_561_out, not_1_out, not_2_out, not_3_out, not_4_out, not_5_out, not_6_out, not_7_out;

  not not_1 (not_1_out, ascii_I8[6]);
  not not_2 (not_2_out, ascii_I8[5]);
  not not_3 (not_3_out, ascii_I8[4]);
  not not_4 (not_4_out, ascii_I8[3]);
  not not_5 (not_5_out, ascii_I8[2]);
  not not_6 (not_6_out, ascii_I8[1]);
  not not_7 (not_7_out, ascii_I8[0]);
  and and_1 (and_1_out, not_2_out, not_3_out, ascii_I8[2], not_6_out, ascii_I8[0]);
  and and_2 (and_2_out, not_2_out, not_3_out, ascii_I8[2], ascii_I8[1], not_7_out);
  and and_3 (and_3_out, not_2_out, ascii_I8[3], not_5_out, not_7_out);
  and and_4 (and_4_out, not_2_out, not_3_out, ascii_I8[3], not_5_out, ascii_I8[1]);
  and and_5 (and_5_out, not_1_out, ascii_I8[4], not_4_out, ascii_I8[1], ascii_I8[0]);
  and and_6 (and_6_out, not_2_out, ascii_I8[4], not_4_out, ascii_I8[1], ascii_I8[0]);
  and and_7 (and_7_out, not_2_out, ascii_I8[4], not_4_out, ascii_I8[2]);
  and and_8 (and_8_out, not_1_out, ascii_I8[4], not_4_out, ascii_I8[2], ascii_I8[0]);
  and and_9 (and_9_out, not_2_out, ascii_I8[4], ascii_I8[3], not_5_out, not_6_out);
  and and_10 (and_10_out, not_2_out, ascii_I8[4], ascii_I8[3], not_6_out, not_7_out);
  and and_11 (and_11_out, ascii_I8[6], ascii_I8[5], not_3_out, not_4_out, ascii_I8[2], not_6_out, not_7_out);
  and and_12 (and_12_out, not_2_out, not_3_out, not_4_out, not_5_out);
  and and_13 (and_13_out, not_2_out, not_5_out, not_6_out, not_7_out);
  and and_14 (and_14_out, not_1_out, not_3_out, not_4_out, ascii_I8[2], not_6_out);
  and and_15 (and_15_out, not_2_out, not_4_out, ascii_I8[2], ascii_I8[1], ascii_I8[0]);
  and and_16 (and_16_out, not_2_out, not_3_out, ascii_I8[3], ascii_I8[2], ascii_I8[0]);
  and and_17 (and_17_out, not_2_out, not_3_out, ascii_I8[3], ascii_I8[2], ascii_I8[1]);
  and and_18 (and_18_out, not_1_out, ascii_I8[3], ascii_I8[2], ascii_I8[1], ascii_I8[0]);
  and and_19 (and_19_out, not_1_out, ascii_I8[4], not_4_out, not_5_out, not_7_out);
  and and_20 (and_20_out, not_2_out, ascii_I8[4], not_5_out, not_6_out);
  and and_21 (and_21_out, not_2_out, ascii_I8[4], not_5_out, not_7_out);
  and and_22 (and_22_out, not_2_out, ascii_I8[4], not_4_out, not_6_out, ascii_I8[0]);
  and and_23 (and_23_out, not_2_out, ascii_I8[4], not_4_out, ascii_I8[1], not_7_out);
  and and_24 (and_24_out, not_1_out, ascii_I8[4], ascii_I8[2], ascii_I8[1], ascii_I8[0]);
  and and_25 (and_25_out, not_1_out, ascii_I8[4], ascii_I8[3], not_5_out, not_6_out);
  and and_26 (and_26_out, ascii_I8[6], ascii_I8[5], not_3_out, not_4_out, ascii_I8[2], not_7_out);
  and and_27 (and_27_out, ascii_I8[6], ascii_I8[5], not_3_out, not_4_out, ascii_I8[2], ascii_I8[1]);
  and and_28 (and_28_out, not_2_out, not_3_out, not_5_out, not_6_out, not_7_out);
  and and_29 (and_29_out, not_2_out, not_4_out, not_5_out, not_6_out);
  and and_30 (and_30_out, not_2_out, not_4_out, not_5_out, not_7_out);
  and and_31 (and_31_out, not_1_out, not_3_out, not_4_out, not_5_out, ascii_I8[1], ascii_I8[0]);
  and and_32 (and_32_out, not_1_out, not_3_out, ascii_I8[3], not_5_out, ascii_I8[1], not_7_out);
  and and_33 (and_33_out, not_2_out, not_3_out, ascii_I8[3], ascii_I8[2], ascii_I8[0]);
  and and_34 (and_34_out, not_2_out, not_3_out, ascii_I8[3], ascii_I8[2], ascii_I8[1]);
  and and_35 (and_35_out, not_1_out, ascii_I8[4], not_4_out, not_5_out, not_7_out);
  and and_36 (and_36_out, ascii_I8[4], not_4_out, ascii_I8[2], ascii_I8[1], ascii_I8[0]);
  and and_37 (and_37_out, not_2_out, ascii_I8[4], ascii_I8[3], ascii_I8[2], not_7_out);
  and and_38 (and_38_out, not_1_out, ascii_I8[4], ascii_I8[3], ascii_I8[2], ascii_I8[0]);
  and and_39 (and_39_out, ascii_I8[5], ascii_I8[4], ascii_I8[3], not_5_out, not_6_out);
  and and_40 (and_40_out, ascii_I8[6], not_3_out, not_4_out, ascii_I8[2], not_6_out, not_7_out);
  and and_41 (and_41_out, ascii_I8[6], ascii_I8[4], not_4_out, not_6_out, ascii_I8[0]);
  and and_42 (and_42_out, ascii_I8[6], ascii_I8[4], not_5_out, not_6_out, ascii_I8[0]);
  and and_43 (and_43_out, ascii_I8[6], ascii_I8[4], not_4_out, ascii_I8[2], ascii_I8[1]);
  and and_44 (and_44_out, ascii_I8[6], ascii_I8[5], not_4_out, ascii_I8[2], ascii_I8[1], ascii_I8[0]);
  and and_45 (and_45_out, ascii_I8[6], ascii_I8[5], ascii_I8[4], ascii_I8[3], not_5_out, not_7_out);
  and and_46 (and_46_out, not_2_out, not_3_out, not_5_out, not_6_out, not_7_out);
  and and_47 (and_47_out, not_2_out, not_3_out, ascii_I8[2], ascii_I8[1], ascii_I8[0]);
  and and_48 (and_48_out, not_1_out, not_3_out, ascii_I8[3], not_5_out, ascii_I8[1], ascii_I8[0]);
  and and_49 (and_49_out, not_3_out, ascii_I8[3], ascii_I8[2], not_6_out, ascii_I8[0]);
  and and_50 (and_50_out, not_1_out, ascii_I8[4], not_4_out, not_5_out, not_6_out, not_7_out);
  and and_51 (and_51_out, ascii_I8[4], not_4_out, ascii_I8[2], not_6_out, ascii_I8[0]);
  and and_52 (and_52_out, not_2_out, ascii_I8[4], not_4_out, ascii_I8[2], ascii_I8[1]);
  and and_53 (and_53_out, not_1_out, ascii_I8[4], ascii_I8[3], ascii_I8[2], ascii_I8[1], not_7_out);
  and and_54 (and_54_out, ascii_I8[5], ascii_I8[4], ascii_I8[3], not_5_out, not_6_out, ascii_I8[0]);
  and and_55 (and_55_out, ascii_I8[6], not_4_out, not_5_out, not_6_out, ascii_I8[0]);
  and and_56 (and_56_out, ascii_I8[6], not_3_out, not_4_out, ascii_I8[2], not_6_out, not_7_out);
  and and_57 (and_57_out, ascii_I8[6], not_3_out, ascii_I8[3], not_5_out, not_6_out, not_7_out);
  and and_58 (and_58_out, ascii_I8[6], not_3_out, ascii_I8[3], ascii_I8[2], ascii_I8[0]);
  and and_59 (and_59_out, ascii_I8[6], not_3_out, ascii_I8[3], ascii_I8[2], ascii_I8[1]);
  and and_60 (and_60_out, ascii_I8[6], ascii_I8[4], not_4_out, ascii_I8[2], ascii_I8[0]);
  and and_61 (and_61_out, ascii_I8[6], ascii_I8[5], not_4_out, not_5_out, ascii_I8[1], not_7_out);
  and and_62 (and_62_out, ascii_I8[6], ascii_I8[5], not_3_out, ascii_I8[2], ascii_I8[0]);
  and and_63 (and_63_out, ascii_I8[6], ascii_I8[5], ascii_I8[2], ascii_I8[1], ascii_I8[0]);
  and and_64 (and_64_out, ascii_I8[6], ascii_I8[5], ascii_I8[4], not_4_out, not_5_out, not_7_out);
  and and_65 (and_65_out, ascii_I8[6], ascii_I8[5], ascii_I8[4], ascii_I8[2], ascii_I8[1]);
  and and_66 (and_66_out, not_2_out, not_3_out, not_4_out, not_6_out, not_7_out);
  and and_67 (and_67_out, not_1_out, not_4_out, not_5_out, ascii_I8[1], ascii_I8[0]);
  and and_68 (and_68_out, not_1_out, not_4_out, ascii_I8[2], not_7_out);
  and and_69 (and_69_out, not_3_out, not_4_out, ascii_I8[2], not_6_out, not_7_out);
  and and_70 (and_70_out, not_2_out, not_3_out, ascii_I8[2], ascii_I8[1], ascii_I8[0]);
  and and_71 (and_71_out, not_1_out, not_3_out, ascii_I8[3], not_5_out, ascii_I8[1], not_7_out);
  and and_72 (and_72_out, not_1_out, ascii_I8[4], not_5_out, not_6_out, not_7_out);
  and and_73 (and_73_out, not_2_out, ascii_I8[4], not_4_out, ascii_I8[0]);
  and and_74 (and_74_out, not_1_out, ascii_I8[4], ascii_I8[2], not_6_out, ascii_I8[0]);
  and and_75 (and_75_out, not_1_out, ascii_I8[4], ascii_I8[3], not_6_out, ascii_I8[0]);
  and and_76 (and_76_out, not_2_out, ascii_I8[4], ascii_I8[3], ascii_I8[2], not_6_out, not_7_out);
  and and_77 (and_77_out, ascii_I8[6], not_4_out, not_5_out, not_6_out, ascii_I8[0]);
  and and_78 (and_78_out, ascii_I8[6], not_3_out, not_4_out, not_5_out, ascii_I8[1], not_7_out);
  and and_79 (and_79_out, ascii_I8[6], not_3_out, ascii_I8[3], not_5_out, not_6_out, not_7_out);
  and and_80 (and_80_out, ascii_I8[6], not_3_out, ascii_I8[3], ascii_I8[2], ascii_I8[0]);
  and and_81 (and_81_out, ascii_I8[6], not_3_out, ascii_I8[3], ascii_I8[2], ascii_I8[1]);
  and and_82 (and_82_out, ascii_I8[6], ascii_I8[4], not_4_out, ascii_I8[2], ascii_I8[1]);
  and and_83 (and_83_out, ascii_I8[6], ascii_I8[5], not_4_out, ascii_I8[2], ascii_I8[0]);
  and and_84 (and_84_out, ascii_I8[6], ascii_I8[5], ascii_I8[4], not_5_out, not_6_out, ascii_I8[0]);
  and and_85 (and_85_out, not_2_out, not_3_out, not_4_out, not_5_out);
  and and_86 (and_86_out, not_1_out, not_4_out, ascii_I8[2], not_6_out, ascii_I8[0]);
  and and_87 (and_87_out, not_2_out, ascii_I8[3], not_5_out, not_6_out, not_7_out);
  and and_88 (and_88_out, not_1_out, ascii_I8[4], not_5_out, not_6_out, not_7_out);
  and and_89 (and_89_out, ascii_I8[4], not_4_out, not_5_out, ascii_I8[1], ascii_I8[0]);
  and and_90 (and_90_out, not_1_out, ascii_I8[4], not_4_out, ascii_I8[2], ascii_I8[1], not_7_out);
  and and_91 (and_91_out, ascii_I8[6], not_3_out, not_4_out, not_5_out, ascii_I8[0]);
  and and_92 (and_92_out, ascii_I8[6], not_3_out, not_4_out, not_5_out, ascii_I8[1]);
  and and_93 (and_93_out, ascii_I8[6], not_4_out, ascii_I8[1], ascii_I8[0]);
  and and_94 (and_94_out, ascii_I8[6], not_3_out, ascii_I8[3], not_5_out, not_6_out, not_7_out);
  and and_95 (and_95_out, ascii_I8[6], not_3_out, ascii_I8[3], ascii_I8[2], ascii_I8[0]);
  and and_96 (and_96_out, ascii_I8[6], not_3_out, ascii_I8[3], ascii_I8[2], ascii_I8[1]);
  and and_97 (and_97_out, ascii_I8[6], ascii_I8[4], not_4_out, ascii_I8[2], ascii_I8[0]);
  and and_98 (and_98_out, ascii_I8[6], ascii_I8[5], not_4_out, ascii_I8[2], not_6_out, not_7_out);
  and and_99 (and_99_out, ascii_I8[6], ascii_I8[5], ascii_I8[4], not_5_out, not_6_out, ascii_I8[0]);
  and and_100 (and_100_out, not_1_out, not_3_out, not_4_out, ascii_I8[2], not_6_out, ascii_I8[0]);
  and and_101 (and_101_out, not_2_out, not_3_out, not_4_out, ascii_I8[2], ascii_I8[0]);
  and and_102 (and_102_out, not_2_out, not_3_out, ascii_I8[2], not_6_out, ascii_I8[0]);
  and and_103 (and_103_out, not_1_out, not_3_out, not_4_out, ascii_I8[2], ascii_I8[1], not_7_out);
  and and_104 (and_104_out, not_2_out, not_3_out, ascii_I8[3], not_5_out, ascii_I8[1], ascii_I8[0]);
  and and_105 (and_105_out, not_2_out, not_3_out, ascii_I8[3], ascii_I8[2], not_7_out);
  and and_106 (and_106_out, not_1_out, ascii_I8[4], not_4_out, not_5_out, ascii_I8[1], not_7_out);
  and and_107 (and_107_out, not_2_out, ascii_I8[4], not_5_out, ascii_I8[1], not_7_out);
  and and_108 (and_108_out, not_2_out, ascii_I8[4], ascii_I8[3], ascii_I8[2], ascii_I8[1], ascii_I8[0]);
  and and_109 (and_109_out, ascii_I8[6], not_4_out, not_5_out, not_6_out, ascii_I8[0]);
  and and_110 (and_110_out, ascii_I8[6], ascii_I8[3], not_5_out, not_6_out, not_7_out);
  and and_111 (and_111_out, ascii_I8[6], not_3_out, ascii_I8[3], ascii_I8[2], not_6_out, ascii_I8[0]);
  and and_112 (and_112_out, ascii_I8[6], not_3_out, ascii_I8[3], ascii_I8[2], ascii_I8[1], not_7_out);
  and and_113 (and_113_out, ascii_I8[6], ascii_I8[4], ascii_I8[3], not_5_out, not_7_out);
  and and_114 (and_114_out, ascii_I8[6], ascii_I8[5], not_3_out, not_4_out, ascii_I8[2], not_6_out, not_7_out);
  and and_115 (and_115_out, ascii_I8[6], ascii_I8[5], ascii_I8[4], not_4_out, not_6_out, ascii_I8[0]);
  and and_116 (and_116_out, not_2_out, not_4_out, not_5_out);
  and and_117 (and_117_out, not_2_out, not_3_out, not_4_out, ascii_I8[0]);
  and and_118 (and_118_out, not_2_out, not_3_out, not_5_out, not_6_out, ascii_I8[0]);
  and and_119 (and_119_out, not_1_out, not_4_out, not_5_out, ascii_I8[1]);
  and and_120 (and_120_out, not_2_out, not_5_out, ascii_I8[1], not_7_out);
  and and_121 (and_121_out, not_2_out, not_3_out, ascii_I8[2], ascii_I8[1], ascii_I8[0]);
  and and_122 (and_122_out, not_1_out, ascii_I8[3], not_5_out, not_6_out, not_7_out);
  and and_123 (and_123_out, not_1_out, ascii_I8[4], not_6_out, not_7_out);
  and and_124 (and_124_out, not_2_out, ascii_I8[4], not_4_out, not_6_out, not_7_out);
  and and_125 (and_125_out, not_1_out, ascii_I8[4], not_4_out, ascii_I8[2]);
  and and_126 (and_126_out, not_1_out, ascii_I8[4], ascii_I8[2], ascii_I8[1], ascii_I8[0]);
  and and_127 (and_127_out, not_1_out, ascii_I8[4], ascii_I8[3], not_5_out, not_6_out);
  and and_128 (and_128_out, not_2_out, ascii_I8[4], ascii_I8[3], ascii_I8[2], not_6_out, ascii_I8[0]);
  and and_129 (and_129_out, ascii_I8[6], not_3_out, not_4_out, ascii_I8[2], ascii_I8[1], not_7_out);
  and and_130 (and_130_out, ascii_I8[6], not_3_out, ascii_I8[3], not_5_out, ascii_I8[1], not_7_out);
  and and_131 (and_131_out, ascii_I8[6], ascii_I8[5], ascii_I8[4], ascii_I8[3], not_5_out, ascii_I8[1], ascii_I8[0]);
  and and_132 (and_132_out, not_1_out, not_3_out, not_4_out, ascii_I8[1], not_7_out);
  and and_133 (and_133_out, not_1_out, not_4_out, not_5_out, ascii_I8[1], ascii_I8[0]);
  and and_134 (and_134_out, not_1_out, not_4_out, ascii_I8[2], not_6_out, not_7_out);
  and and_135 (and_135_out, not_2_out, not_3_out, not_4_out, ascii_I8[2], not_6_out, not_7_out);
  and and_136 (and_136_out, not_2_out, not_3_out, ascii_I8[3], not_5_out, ascii_I8[1]);
  and and_137 (and_137_out, not_2_out, ascii_I8[3], ascii_I8[2], not_6_out, ascii_I8[0]);
  and and_138 (and_138_out, not_2_out, ascii_I8[4], ascii_I8[3], ascii_I8[2], not_7_out);
  and and_139 (and_139_out, ascii_I8[6], ascii_I8[5], not_3_out, not_4_out, ascii_I8[2], ascii_I8[1], ascii_I8[0]);
  and and_140 (and_140_out, not_1_out, not_3_out, not_4_out, not_5_out, ascii_I8[1]);
  and and_141 (and_141_out, not_1_out, not_4_out, ascii_I8[2], not_6_out, ascii_I8[0]);
  and and_142 (and_142_out, not_1_out, not_3_out, ascii_I8[3], not_5_out, not_6_out, ascii_I8[0]);
  and and_143 (and_143_out, not_1_out, not_3_out, ascii_I8[3], ascii_I8[2], ascii_I8[1], ascii_I8[0]);
  and and_144 (and_144_out, not_1_out, ascii_I8[4], not_4_out, not_6_out, not_7_out);
  and and_145 (and_145_out, not_1_out, ascii_I8[4], ascii_I8[2], not_6_out, ascii_I8[0]);
  and and_146 (and_146_out, not_2_out, ascii_I8[4], ascii_I8[3], not_5_out, not_7_out);
  and and_147 (and_147_out, not_2_out, ascii_I8[4], ascii_I8[3], ascii_I8[2], not_6_out);
  and and_148 (and_148_out, ascii_I8[5], ascii_I8[4], ascii_I8[3], ascii_I8[2], ascii_I8[1], not_7_out);
  and and_149 (and_149_out, ascii_I8[6], ascii_I8[3], not_5_out, ascii_I8[1], not_7_out);
  and and_150 (and_150_out, ascii_I8[6], ascii_I8[5], not_3_out, not_4_out, not_5_out);
  and and_151 (and_151_out, ascii_I8[6], ascii_I8[5], not_3_out, not_5_out, not_7_out);
  and and_152 (and_152_out, ascii_I8[6], ascii_I8[5], not_4_out, not_5_out, not_7_out);
  and and_153 (and_153_out, ascii_I8[6], ascii_I8[5], not_4_out, not_5_out, ascii_I8[1]);
  and and_154 (and_154_out, ascii_I8[6], ascii_I8[5], not_3_out, ascii_I8[2], not_6_out, ascii_I8[0]);
  and and_155 (and_155_out, ascii_I8[6], ascii_I8[5], not_3_out, ascii_I8[3], ascii_I8[1]);
  and and_156 (and_156_out, not_2_out, not_3_out, not_4_out, ascii_I8[1], not_7_out);
  and and_157 (and_157_out, not_2_out, not_4_out, not_5_out, ascii_I8[1], not_7_out);
  and and_158 (and_158_out, not_1_out, not_3_out, not_5_out, ascii_I8[1], ascii_I8[0]);
  and and_159 (and_159_out, not_1_out, not_4_out, ascii_I8[2], not_6_out, not_7_out);
  and and_160 (and_160_out, not_2_out, not_3_out, not_4_out, ascii_I8[2], ascii_I8[0]);
  and and_161 (and_161_out, not_2_out, not_3_out, ascii_I8[3], not_5_out, not_7_out);
  and and_162 (and_162_out, not_1_out, not_3_out, ascii_I8[3], not_6_out, ascii_I8[0]);
  and and_163 (and_163_out, not_1_out, ascii_I8[3], not_5_out, not_6_out, ascii_I8[0]);
  and and_164 (and_164_out, not_3_out, ascii_I8[3], not_5_out, ascii_I8[1], not_7_out);
  and and_165 (and_165_out, not_2_out, ascii_I8[4], not_4_out, not_5_out, not_7_out);
  and and_166 (and_166_out, not_1_out, ascii_I8[4], not_4_out, ascii_I8[1]);
  and and_167 (and_167_out, not_2_out, ascii_I8[4], not_4_out, not_5_out, ascii_I8[1]);
  and and_168 (and_168_out, not_2_out, ascii_I8[4], ascii_I8[3], not_6_out, ascii_I8[0]);
  and and_169 (and_169_out, ascii_I8[5], not_3_out, not_4_out, ascii_I8[2], not_6_out, not_7_out);
  and and_170 (and_170_out, ascii_I8[5], ascii_I8[4], ascii_I8[3], not_5_out, not_6_out, not_7_out);
  and and_171 (and_171_out, ascii_I8[5], ascii_I8[4], ascii_I8[3], ascii_I8[2], ascii_I8[1], ascii_I8[0]);
  and and_172 (and_172_out, ascii_I8[6], ascii_I8[4], ascii_I8[3], ascii_I8[2], not_6_out, ascii_I8[0]);
  and and_173 (and_173_out, ascii_I8[6], ascii_I8[5], ascii_I8[4], not_4_out, not_5_out, not_6_out, ascii_I8[0]);
  and and_174 (and_174_out, ascii_I8[6], ascii_I8[5], ascii_I8[4], ascii_I8[3], ascii_I8[1], not_7_out);
  and and_175 (and_175_out, not_2_out, not_3_out, not_4_out, not_5_out, not_6_out, ascii_I8[0]);
  and and_176 (and_176_out, not_1_out, not_3_out, not_4_out, not_5_out, ascii_I8[1], ascii_I8[0]);
  and and_177 (and_177_out, not_1_out, not_3_out, ascii_I8[3], not_5_out, not_6_out, ascii_I8[0]);
  and and_178 (and_178_out, not_2_out, not_3_out, ascii_I8[3], ascii_I8[1], not_7_out);
  and and_179 (and_179_out, not_1_out, ascii_I8[4], not_4_out, ascii_I8[2], not_6_out, not_7_out);
  and and_180 (and_180_out, not_2_out, ascii_I8[4], ascii_I8[3], not_6_out, not_7_out);
  and and_181 (and_181_out, not_2_out, ascii_I8[4], ascii_I8[3], ascii_I8[2], not_6_out);
  and and_182 (and_182_out, not_1_out, ascii_I8[4], ascii_I8[3], ascii_I8[2], not_6_out, ascii_I8[0]);
  and and_183 (and_183_out, ascii_I8[5], ascii_I8[4], ascii_I8[3], ascii_I8[2], ascii_I8[1], not_7_out);
  and and_184 (and_184_out, ascii_I8[6], not_3_out, ascii_I8[3], not_5_out, ascii_I8[1], not_7_out);
  and and_185 (and_185_out, ascii_I8[6], ascii_I8[5], not_4_out, not_5_out, not_6_out, ascii_I8[0]);
  and and_186 (and_186_out, ascii_I8[6], ascii_I8[5], not_3_out, not_4_out, ascii_I8[2], ascii_I8[0]);
  and and_187 (and_187_out, ascii_I8[6], ascii_I8[5], ascii_I8[4], not_4_out, not_5_out, not_6_out);
  and and_188 (and_188_out, ascii_I8[6], ascii_I8[5], ascii_I8[4], not_4_out, not_5_out, ascii_I8[0]);
  and and_189 (and_189_out, ascii_I8[6], ascii_I8[5], ascii_I8[4], not_5_out, not_6_out, ascii_I8[0]);
  and and_190 (and_190_out, not_1_out, not_3_out, not_4_out, not_5_out, ascii_I8[1], ascii_I8[0]);
  and and_191 (and_191_out, not_1_out, not_3_out, not_4_out, ascii_I8[2], not_6_out);
  and and_192 (and_192_out, not_1_out, not_3_out, not_4_out, ascii_I8[2], not_7_out);
  and and_193 (and_193_out, not_1_out, not_4_out, ascii_I8[2], not_6_out, not_7_out);
  and and_194 (and_194_out, not_2_out, not_3_out, not_4_out, ascii_I8[2], not_6_out, not_7_out);
  and and_195 (and_195_out, not_2_out, not_3_out, ascii_I8[3], not_5_out, ascii_I8[1]);
  and and_196 (and_196_out, not_2_out, ascii_I8[4], not_4_out, not_5_out, not_6_out, ascii_I8[0]);
  and and_197 (and_197_out, not_2_out, ascii_I8[4], not_4_out, ascii_I8[1], not_7_out);
  and and_198 (and_198_out, not_1_out, ascii_I8[4], ascii_I8[3], not_5_out, not_6_out, ascii_I8[0]);
  and and_199 (and_199_out, not_2_out, ascii_I8[4], ascii_I8[3], ascii_I8[2], not_6_out, ascii_I8[0]);
  and and_200 (and_200_out, ascii_I8[6], not_3_out, ascii_I8[3], not_5_out, ascii_I8[1], not_7_out);
  and and_201 (and_201_out, ascii_I8[6], ascii_I8[4], not_4_out, ascii_I8[2], ascii_I8[1], not_7_out);
  and and_202 (and_202_out, ascii_I8[6], ascii_I8[5], ascii_I8[4], not_4_out, ascii_I8[2], not_6_out, ascii_I8[0]);
  and and_203 (and_203_out, ascii_I8[6], ascii_I8[5], ascii_I8[4], ascii_I8[3], not_5_out, not_6_out, not_7_out);
  and and_204 (and_204_out, not_2_out, not_3_out, not_4_out, not_5_out, not_7_out);
  and and_205 (and_205_out, not_4_out, not_5_out, ascii_I8[1], ascii_I8[0]);
  and and_206 (and_206_out, not_3_out, not_4_out, ascii_I8[2], not_6_out, ascii_I8[0]);
  and and_207 (and_207_out, not_1_out, ascii_I8[3], not_5_out, not_6_out, not_7_out);
  and and_208 (and_208_out, not_2_out, not_3_out, ascii_I8[3], not_5_out, not_6_out, ascii_I8[0]);
  and and_209 (and_209_out, not_1_out, ascii_I8[4], not_4_out, not_6_out);
  and and_210 (and_210_out, not_1_out, ascii_I8[4], not_4_out, not_7_out);
  and and_211 (and_211_out, not_1_out, ascii_I8[4], not_6_out, not_7_out);
  and and_212 (and_212_out, not_2_out, ascii_I8[4], ascii_I8[2], ascii_I8[0]);
  and and_213 (and_213_out, ascii_I8[6], not_3_out, not_4_out, not_5_out, ascii_I8[1]);
  and and_214 (and_214_out, ascii_I8[6], not_4_out, ascii_I8[1], ascii_I8[0]);
  and and_215 (and_215_out, ascii_I8[6], not_3_out, not_4_out, ascii_I8[2], ascii_I8[0]);
  and and_216 (and_216_out, ascii_I8[6], not_3_out, ascii_I8[2], ascii_I8[1], ascii_I8[0]);
  and and_217 (and_217_out, ascii_I8[6], not_3_out, ascii_I8[3], ascii_I8[2], not_6_out, not_7_out);
  and and_218 (and_218_out, ascii_I8[6], ascii_I8[4], ascii_I8[3], not_5_out, ascii_I8[1], not_7_out);
  and and_219 (and_219_out, ascii_I8[6], ascii_I8[5], not_3_out, not_4_out, ascii_I8[0]);
  and and_220 (and_220_out, ascii_I8[6], ascii_I8[5], not_4_out, ascii_I8[2], not_6_out, not_7_out);
  and and_221 (and_221_out, ascii_I8[6], ascii_I8[5], ascii_I8[3], not_5_out, ascii_I8[0]);
  and and_222 (and_222_out, not_2_out, not_3_out, not_4_out);
  and and_223 (and_223_out, not_2_out, not_4_out, not_5_out);
  and and_224 (and_224_out, not_2_out, not_4_out, not_6_out, not_7_out);
  and and_225 (and_225_out, not_1_out, not_4_out, not_5_out, not_6_out, ascii_I8[0]);
  and and_226 (and_226_out, not_2_out, not_5_out, ascii_I8[1], not_7_out);
  and and_227 (and_227_out, not_1_out, not_3_out, not_4_out, ascii_I8[2], not_7_out);
  and and_228 (and_228_out, not_1_out, not_4_out, ascii_I8[2], ascii_I8[1]);
  and and_229 (and_229_out, not_3_out, not_4_out, ascii_I8[2], ascii_I8[1], not_7_out);
  and and_230 (and_230_out, not_2_out, not_3_out, ascii_I8[2], ascii_I8[1], ascii_I8[0]);
  and and_231 (and_231_out, not_1_out, ascii_I8[4], not_4_out, not_5_out);
  and and_232 (and_232_out, not_1_out, ascii_I8[4], not_5_out, not_6_out);
  and and_233 (and_233_out, not_1_out, ascii_I8[4], not_4_out, ascii_I8[0]);
  and and_234 (and_234_out, not_2_out, ascii_I8[4], not_5_out, ascii_I8[1]);
  and and_235 (and_235_out, not_1_out, ascii_I8[4], ascii_I8[2], ascii_I8[1], ascii_I8[0]);
  and and_236 (and_236_out, not_2_out, ascii_I8[4], ascii_I8[3], ascii_I8[1], not_7_out);
  and and_237 (and_237_out, not_2_out, ascii_I8[4], ascii_I8[3], ascii_I8[2], not_6_out, ascii_I8[0]);
  and and_238 (and_238_out, ascii_I8[6], not_3_out, ascii_I8[3], not_5_out, not_6_out, ascii_I8[0]);
  and and_239 (and_239_out, ascii_I8[6], ascii_I8[5], ascii_I8[3], ascii_I8[2], not_6_out, not_7_out);
  and and_240 (and_240_out, not_1_out, not_4_out, not_5_out, not_6_out, ascii_I8[0]);
  and and_241 (and_241_out, not_1_out, not_4_out, ascii_I8[2], not_6_out, not_7_out);
  and and_242 (and_242_out, not_1_out, not_3_out, ascii_I8[3], not_5_out);
  and and_243 (and_243_out, not_2_out, not_3_out, ascii_I8[3], not_5_out, not_6_out, ascii_I8[0]);
  and and_244 (and_244_out, not_1_out, ascii_I8[3], not_5_out, ascii_I8[1]);
  and and_245 (and_245_out, not_2_out, ascii_I8[4], not_4_out, ascii_I8[2], not_6_out, not_7_out);
  and and_246 (and_246_out, ascii_I8[5], not_3_out, not_4_out, ascii_I8[2], ascii_I8[1], ascii_I8[0]);
  and and_247 (and_247_out, ascii_I8[5], ascii_I8[4], ascii_I8[3], not_5_out, ascii_I8[1], ascii_I8[0]);
  and and_248 (and_248_out, ascii_I8[5], ascii_I8[4], ascii_I8[3], ascii_I8[2], not_7_out);
  and and_249 (and_249_out, ascii_I8[6], ascii_I8[5], not_3_out, not_4_out, not_5_out, not_6_out, not_7_out);
  and and_250 (and_250_out, ascii_I8[6], ascii_I8[5], ascii_I8[3], ascii_I8[2], not_6_out, not_7_out);
  and and_251 (and_251_out, ascii_I8[6], ascii_I8[5], ascii_I8[4], ascii_I8[3], ascii_I8[2]);
  and and_252 (and_252_out, not_1_out, not_3_out, not_4_out, ascii_I8[2], not_7_out);
  and and_253 (and_253_out, not_2_out, not_3_out, ascii_I8[3], not_5_out, ascii_I8[0]);
  and and_254 (and_254_out, not_2_out, not_3_out, ascii_I8[3], not_6_out, ascii_I8[0]);
  and and_255 (and_255_out, not_1_out, ascii_I8[3], not_5_out, ascii_I8[1]);
  and and_256 (and_256_out, not_2_out, ascii_I8[4], ascii_I8[2], not_6_out, not_7_out);
  and and_257 (and_257_out, not_1_out, ascii_I8[4], ascii_I8[2], not_6_out, ascii_I8[0]);
  and and_258 (and_258_out, ascii_I8[5], not_4_out, not_5_out, ascii_I8[0]);
  and and_259 (and_259_out, ascii_I8[5], ascii_I8[3], not_5_out, ascii_I8[1], not_7_out);
  and and_260 (and_260_out, ascii_I8[5], ascii_I8[4], not_5_out, ascii_I8[1], ascii_I8[0]);
  and and_261 (and_261_out, ascii_I8[6], not_3_out, ascii_I8[3], not_5_out, not_6_out, ascii_I8[0]);
  and and_262 (and_262_out, ascii_I8[6], ascii_I8[5], not_4_out, not_5_out, ascii_I8[1]);
  and and_263 (and_263_out, ascii_I8[6], ascii_I8[5], not_3_out, not_4_out, ascii_I8[2], not_6_out);
  and and_264 (and_264_out, ascii_I8[6], ascii_I8[5], ascii_I8[2], not_6_out, not_7_out);
  and and_265 (and_265_out, ascii_I8[6], ascii_I8[5], not_3_out, ascii_I8[3], not_7_out);
  and and_266 (and_266_out, ascii_I8[6], ascii_I8[5], not_3_out, ascii_I8[3], ascii_I8[2], ascii_I8[1]);
  and and_267 (and_267_out, ascii_I8[6], ascii_I8[5], ascii_I8[4], not_4_out, not_5_out);
  and and_268 (and_268_out, ascii_I8[6], ascii_I8[5], ascii_I8[4], ascii_I8[3], ascii_I8[2], not_6_out);
  and and_269 (and_269_out, not_2_out, not_4_out, not_5_out, not_7_out);
  and and_270 (and_270_out, not_2_out, not_5_out, not_6_out, not_7_out);
  and and_271 (and_271_out, not_1_out, not_3_out, not_4_out, not_6_out, ascii_I8[0]);
  and and_272 (and_272_out, not_1_out, not_3_out, not_4_out, ascii_I8[2], not_6_out);
  and and_273 (and_273_out, not_2_out, not_3_out, not_4_out, ascii_I8[2], ascii_I8[0]);
  and and_274 (and_274_out, not_2_out, not_3_out, ascii_I8[2], ascii_I8[1], not_7_out);
  and and_275 (and_275_out, not_2_out, not_4_out, ascii_I8[2], ascii_I8[1], ascii_I8[0]);
  and and_276 (and_276_out, not_1_out, not_3_out, ascii_I8[3], not_5_out, ascii_I8[1]);
  and and_277 (and_277_out, not_1_out, not_3_out, ascii_I8[3], ascii_I8[2], ascii_I8[0]);
  and and_278 (and_278_out, not_1_out, ascii_I8[4], not_5_out, not_6_out);
  and and_279 (and_279_out, not_2_out, ascii_I8[4], not_5_out, not_7_out);
  and and_280 (and_280_out, not_2_out, ascii_I8[4], not_6_out, not_7_out);
  and and_281 (and_281_out, not_2_out, ascii_I8[4], not_4_out, not_5_out, ascii_I8[1]);
  and and_282 (and_282_out, not_1_out, ascii_I8[4], not_4_out, ascii_I8[2], ascii_I8[1], not_7_out);
  and and_283 (and_283_out, ascii_I8[6], not_3_out, not_4_out, ascii_I8[2], ascii_I8[1], not_7_out);
  and and_284 (and_284_out, ascii_I8[6], not_3_out, ascii_I8[3], not_6_out, ascii_I8[0]);
  and and_285 (and_285_out, ascii_I8[6], ascii_I8[5], not_3_out, ascii_I8[3], not_5_out, ascii_I8[0]);
  and and_286 (and_286_out, ascii_I8[6], ascii_I8[5], not_3_out, ascii_I8[3], ascii_I8[2], not_6_out);
  and and_287 (and_287_out, ascii_I8[6], ascii_I8[5], ascii_I8[4], ascii_I8[2], ascii_I8[1], ascii_I8[0]);
  and and_288 (and_288_out, ascii_I8[6], ascii_I8[5], ascii_I8[4], ascii_I8[3], ascii_I8[2], not_7_out);
  and and_289 (and_289_out, not_2_out, not_3_out, not_4_out, not_5_out, not_6_out);
  and and_290 (and_290_out, not_1_out, not_3_out, not_5_out, ascii_I8[1], ascii_I8[0]);
  and and_291 (and_291_out, not_1_out, not_3_out, not_4_out, ascii_I8[2], not_7_out);
  and and_292 (and_292_out, not_1_out, not_3_out, ascii_I8[2], not_6_out, not_7_out);
  and and_293 (and_293_out, not_1_out, not_4_out, ascii_I8[2], not_6_out, not_7_out);
  and and_294 (and_294_out, not_2_out, not_3_out, ascii_I8[3], not_5_out, ascii_I8[0]);
  and and_295 (and_295_out, not_1_out, ascii_I8[3], not_5_out, ascii_I8[1]);
  and and_296 (and_296_out, ascii_I8[4], not_4_out, not_5_out, not_6_out, ascii_I8[0]);
  and and_297 (and_297_out, not_1_out, ascii_I8[4], not_5_out, ascii_I8[1], not_7_out);
  and and_298 (and_298_out, not_2_out, ascii_I8[4], not_4_out, not_5_out, ascii_I8[1], not_7_out);
  and and_299 (and_299_out, not_2_out, ascii_I8[4], ascii_I8[2], not_6_out, not_7_out);
  and and_300 (and_300_out, ascii_I8[4], not_4_out, ascii_I8[2], ascii_I8[1], ascii_I8[0]);
  and and_301 (and_301_out, not_1_out, ascii_I8[4], ascii_I8[3], ascii_I8[1], ascii_I8[0]);
  and and_302 (and_302_out, not_1_out, ascii_I8[4], ascii_I8[3], ascii_I8[2], ascii_I8[0]);
  and and_303 (and_303_out, ascii_I8[6], not_5_out, not_6_out, ascii_I8[0]);
  and and_304 (and_304_out, ascii_I8[6], ascii_I8[5], not_3_out, not_4_out, ascii_I8[2], ascii_I8[0]);
  and and_305 (and_305_out, ascii_I8[6], ascii_I8[5], ascii_I8[3], not_6_out, ascii_I8[0]);
  and and_306 (and_306_out, ascii_I8[6], ascii_I8[5], ascii_I8[3], ascii_I8[2], not_6_out);
  and and_307 (and_307_out, ascii_I8[6], ascii_I8[5], ascii_I8[4], not_5_out, not_6_out);
  and and_308 (and_308_out, ascii_I8[6], ascii_I8[5], ascii_I8[4], not_5_out, ascii_I8[0]);
  and and_309 (and_309_out, ascii_I8[6], ascii_I8[5], ascii_I8[4], ascii_I8[3], not_5_out);
  and and_310 (and_310_out, not_2_out, not_3_out, not_4_out, not_5_out, not_6_out, not_7_out);
  and and_311 (and_311_out, not_1_out, not_3_out, ascii_I8[2], not_6_out, not_7_out);
  and and_312 (and_312_out, not_1_out, not_3_out, ascii_I8[3], not_5_out);
  and and_313 (and_313_out, not_2_out, ascii_I8[3], not_5_out, not_6_out, ascii_I8[0]);
  and and_314 (and_314_out, not_3_out, ascii_I8[3], not_5_out, not_6_out, ascii_I8[0]);
  and and_315 (and_315_out, not_1_out, ascii_I8[3], ascii_I8[1], not_7_out);
  and and_316 (and_316_out, not_1_out, ascii_I8[4], not_4_out, not_5_out, not_6_out, ascii_I8[0]);
  and and_317 (and_317_out, not_2_out, ascii_I8[4], ascii_I8[2], not_6_out, not_7_out);
  and and_318 (and_318_out, ascii_I8[4], not_4_out, ascii_I8[2], ascii_I8[1], ascii_I8[0]);
  and and_319 (and_319_out, ascii_I8[5], ascii_I8[3], not_5_out, ascii_I8[1], ascii_I8[0]);
  and and_320 (and_320_out, ascii_I8[5], ascii_I8[3], ascii_I8[2], not_6_out, not_7_out);
  and and_321 (and_321_out, ascii_I8[6], ascii_I8[5], ascii_I8[4], ascii_I8[3], ascii_I8[2]);
  and and_322 (and_322_out, not_2_out, not_3_out, not_4_out, not_5_out, not_7_out);
  and and_323 (and_323_out, not_1_out, not_4_out, not_5_out, not_6_out, ascii_I8[0]);
  and and_324 (and_324_out, not_3_out, not_4_out, ascii_I8[2], not_6_out, not_7_out);
  and and_325 (and_325_out, not_1_out, not_3_out, ascii_I8[2], ascii_I8[1], not_7_out);
  and and_326 (and_326_out, not_1_out, not_4_out, ascii_I8[2], ascii_I8[1], not_7_out);
  and and_327 (and_327_out, not_1_out, ascii_I8[4], not_4_out, not_5_out);
  and and_328 (and_328_out, not_1_out, ascii_I8[4], not_5_out, not_6_out);
  and and_329 (and_329_out, not_1_out, ascii_I8[4], not_4_out, ascii_I8[0]);
  and and_330 (and_330_out, not_2_out, ascii_I8[4], not_5_out, ascii_I8[0]);
  and and_331 (and_331_out, ascii_I8[4], not_4_out, ascii_I8[2], ascii_I8[1], not_7_out);
  and and_332 (and_332_out, not_1_out, ascii_I8[4], ascii_I8[2], ascii_I8[1], ascii_I8[0]);
  and and_333 (and_333_out, not_2_out, ascii_I8[4], ascii_I8[3], ascii_I8[0]);
  and and_334 (and_334_out, ascii_I8[6], not_3_out, not_5_out, ascii_I8[1], not_7_out);
  and and_335 (and_335_out, ascii_I8[6], not_4_out, not_5_out, ascii_I8[1], ascii_I8[0]);
  and and_336 (and_336_out, ascii_I8[6], not_4_out, ascii_I8[2], not_6_out);
  and and_337 (and_337_out, ascii_I8[6], ascii_I8[2], not_6_out, not_7_out);
  and and_338 (and_338_out, ascii_I8[6], not_3_out, ascii_I8[2], ascii_I8[1], ascii_I8[0]);
  and and_339 (and_339_out, ascii_I8[6], ascii_I8[3], not_5_out, not_6_out, ascii_I8[0]);
  and and_340 (and_340_out, ascii_I8[6], ascii_I8[3], not_5_out, ascii_I8[1], not_7_out);
  and and_341 (and_341_out, ascii_I8[6], ascii_I8[5], not_3_out, not_5_out, not_6_out, ascii_I8[0]);
  and and_342 (and_342_out, not_2_out, not_3_out, not_4_out);
  and and_343 (and_343_out, not_2_out, not_4_out, not_5_out);
  and and_344 (and_344_out, not_2_out, not_3_out, not_5_out, not_6_out, ascii_I8[0]);
  and and_345 (and_345_out, not_1_out, not_3_out, not_4_out, ascii_I8[1]);
  and and_346 (and_346_out, not_1_out, not_4_out, ascii_I8[1], ascii_I8[0]);
  and and_347 (and_347_out, not_1_out, not_4_out, ascii_I8[2], ascii_I8[0]);
  and and_348 (and_348_out, not_2_out, not_3_out, ascii_I8[2], ascii_I8[1], ascii_I8[0]);
  and and_349 (and_349_out, not_1_out, ascii_I8[3], not_5_out, not_6_out, ascii_I8[0]);
  and and_350 (and_350_out, not_1_out, ascii_I8[4], not_4_out, not_5_out, not_7_out);
  and and_351 (and_351_out, not_1_out, ascii_I8[4], not_5_out, not_6_out, not_7_out);
  and and_352 (and_352_out, not_2_out, ascii_I8[4], not_5_out, ascii_I8[1]);
  and and_353 (and_353_out, not_1_out, ascii_I8[4], ascii_I8[3], ascii_I8[2], ascii_I8[1]);
  and and_354 (and_354_out, ascii_I8[6], not_3_out, not_4_out, not_5_out, not_6_out, not_7_out);
  and and_355 (and_355_out, ascii_I8[6], ascii_I8[4], not_4_out, ascii_I8[2], not_6_out, not_7_out);
  and and_356 (and_356_out, ascii_I8[6], ascii_I8[4], ascii_I8[3], ascii_I8[2], not_6_out, ascii_I8[0]);
  and and_357 (and_357_out, ascii_I8[6], ascii_I8[5], not_3_out, ascii_I8[3], ascii_I8[2], not_6_out, not_7_out);
  and and_358 (and_358_out, not_1_out, not_3_out, not_4_out, not_5_out, ascii_I8[1]);
  and and_359 (and_359_out, not_1_out, not_3_out, not_4_out, ascii_I8[2], not_6_out);
  and and_360 (and_360_out, not_2_out, not_3_out, ascii_I8[3], ascii_I8[2], not_6_out, ascii_I8[0]);
  and and_361 (and_361_out, not_1_out, ascii_I8[4], not_4_out, not_5_out, not_6_out, ascii_I8[0]);
  and and_362 (and_362_out, not_1_out, ascii_I8[4], not_4_out, ascii_I8[2], ascii_I8[1], not_7_out);
  and and_363 (and_363_out, not_1_out, ascii_I8[4], ascii_I8[3], not_5_out, ascii_I8[1]);
  and and_364 (and_364_out, not_2_out, ascii_I8[4], ascii_I8[3], ascii_I8[2], not_7_out);
  and and_365 (and_365_out, ascii_I8[6], ascii_I8[5], not_3_out, not_4_out, ascii_I8[2], ascii_I8[1]);
  and and_366 (and_366_out, ascii_I8[6], ascii_I8[5], ascii_I8[4], not_4_out, ascii_I8[2], not_6_out, not_7_out);
  and and_367 (and_367_out, not_1_out, not_3_out, not_4_out, not_5_out, ascii_I8[1]);
  and and_368 (and_368_out, not_1_out, not_3_out, not_4_out, ascii_I8[1], ascii_I8[0]);
  and and_369 (and_369_out, not_1_out, not_3_out, ascii_I8[3], not_5_out, not_6_out, not_7_out);
  and and_370 (and_370_out, not_2_out, not_3_out, ascii_I8[3], ascii_I8[2], ascii_I8[1], not_7_out);
  and and_371 (and_371_out, not_1_out, ascii_I8[4], ascii_I8[2], not_6_out);
  and and_372 (and_372_out, not_2_out, ascii_I8[4], ascii_I8[3], not_6_out, not_7_out);
  and and_373 (and_373_out, not_1_out, ascii_I8[4], ascii_I8[3], not_5_out, ascii_I8[1]);
  and and_374 (and_374_out, ascii_I8[5], ascii_I8[4], ascii_I8[3], not_5_out, ascii_I8[1], not_7_out);
  and and_375 (and_375_out, ascii_I8[6], ascii_I8[5], not_3_out, not_6_out, ascii_I8[0]);
  and and_376 (and_376_out, ascii_I8[6], ascii_I8[5], not_4_out, not_5_out, ascii_I8[0]);
  and and_377 (and_377_out, ascii_I8[6], ascii_I8[5], not_3_out, not_4_out, ascii_I8[2], not_7_out);
  and and_378 (and_378_out, ascii_I8[6], ascii_I8[5], not_4_out, ascii_I8[2], not_6_out, not_7_out);
  and and_379 (and_379_out, ascii_I8[6], ascii_I8[5], ascii_I8[3], ascii_I8[2], ascii_I8[1], ascii_I8[0]);
  and and_380 (and_380_out, ascii_I8[6], ascii_I8[5], ascii_I8[4], not_4_out, not_5_out, not_6_out);
  and and_381 (and_381_out, not_2_out, not_3_out, not_5_out, not_6_out, not_7_out);
  and and_382 (and_382_out, not_2_out, not_4_out, not_5_out, not_7_out);
  and and_383 (and_383_out, not_1_out, not_3_out, not_5_out, ascii_I8[1], ascii_I8[0]);
  and and_384 (and_384_out, not_1_out, not_3_out, not_4_out, ascii_I8[2], not_7_out);
  and and_385 (and_385_out, not_2_out, not_3_out, not_4_out, ascii_I8[2], not_6_out, ascii_I8[0]);
  and and_386 (and_386_out, not_1_out, not_4_out, ascii_I8[2], ascii_I8[1], not_7_out);
  and and_387 (and_387_out, not_3_out, not_4_out, ascii_I8[2], ascii_I8[1], not_7_out);
  and and_388 (and_388_out, not_1_out, not_3_out, ascii_I8[3], not_5_out, not_7_out);
  and and_389 (and_389_out, not_2_out, not_3_out, ascii_I8[3], not_5_out, ascii_I8[1], ascii_I8[0]);
  and and_390 (and_390_out, not_1_out, not_3_out, ascii_I8[3], ascii_I8[2], not_6_out, ascii_I8[0]);
  and and_391 (and_391_out, not_2_out, ascii_I8[4], not_4_out, not_5_out, ascii_I8[1]);
  and and_392 (and_392_out, not_1_out, ascii_I8[4], ascii_I8[3], not_5_out, not_6_out);
  and and_393 (and_393_out, not_2_out, ascii_I8[4], ascii_I8[3], not_5_out, not_6_out, ascii_I8[0]);
  and and_394 (and_394_out, ascii_I8[5], ascii_I8[3], not_5_out, not_6_out, not_7_out);
  and and_395 (and_395_out, ascii_I8[6], not_4_out, not_5_out, ascii_I8[1], not_7_out);
  and and_396 (and_396_out, ascii_I8[6], ascii_I8[5], ascii_I8[3], ascii_I8[2], ascii_I8[1], not_7_out);
  and and_397 (and_397_out, ascii_I8[6], ascii_I8[5], ascii_I8[4], not_4_out, ascii_I8[2], not_6_out, not_7_out);
  and and_398 (and_398_out, ascii_I8[6], ascii_I8[5], ascii_I8[4], ascii_I8[3], ascii_I8[1], ascii_I8[0]);
  and and_399 (and_399_out, not_2_out, not_3_out, not_4_out, not_5_out, not_6_out, ascii_I8[0]);
  and and_400 (and_400_out, not_1_out, not_3_out, not_4_out, not_5_out, ascii_I8[1], ascii_I8[0]);
  and and_401 (and_401_out, not_1_out, not_3_out, not_4_out, ascii_I8[2], not_6_out, ascii_I8[0]);
  and and_402 (and_402_out, not_1_out, not_3_out, ascii_I8[3], not_6_out, not_7_out);
  and and_403 (and_403_out, not_1_out, not_3_out, ascii_I8[3], ascii_I8[2], ascii_I8[1], ascii_I8[0]);
  and and_404 (and_404_out, not_1_out, ascii_I8[4], ascii_I8[2], not_6_out, not_7_out);
  and and_405 (and_405_out, not_2_out, ascii_I8[4], ascii_I8[3], not_5_out, not_7_out);
  and and_406 (and_406_out, not_2_out, ascii_I8[4], ascii_I8[3], not_6_out, not_7_out);
  and and_407 (and_407_out, not_1_out, ascii_I8[4], ascii_I8[3], not_5_out, ascii_I8[1]);
  and and_408 (and_408_out, not_1_out, ascii_I8[4], ascii_I8[3], ascii_I8[2], not_6_out);
  and and_409 (and_409_out, ascii_I8[5], ascii_I8[4], not_4_out, not_6_out, not_7_out);
  and and_410 (and_410_out, ascii_I8[6], ascii_I8[5], not_4_out, not_5_out, not_6_out, ascii_I8[0]);
  and and_411 (and_411_out, ascii_I8[6], ascii_I8[5], not_3_out, not_4_out, ascii_I8[2], ascii_I8[0]);
  and and_412 (and_412_out, ascii_I8[6], ascii_I8[5], not_3_out, not_4_out, ascii_I8[2], ascii_I8[1]);
  and and_413 (and_413_out, ascii_I8[6], ascii_I8[5], not_3_out, ascii_I8[3], not_5_out, ascii_I8[1], ascii_I8[0]);
  and and_414 (and_414_out, ascii_I8[6], ascii_I8[5], ascii_I8[4], not_4_out, not_5_out, ascii_I8[0]);
  and and_415 (and_415_out, ascii_I8[6], ascii_I8[5], ascii_I8[4], not_5_out, not_6_out, ascii_I8[0]);
  and and_416 (and_416_out, ascii_I8[6], ascii_I8[5], ascii_I8[4], ascii_I8[3], ascii_I8[2], ascii_I8[1], ascii_I8[0]);
  and and_417 (and_417_out, not_1_out, not_3_out, not_4_out, not_5_out, ascii_I8[1], ascii_I8[0]);
  and and_418 (and_418_out, not_1_out, not_3_out, not_4_out, ascii_I8[2], not_6_out, not_7_out);
  and and_419 (and_419_out, not_1_out, not_3_out, ascii_I8[3], ascii_I8[2], ascii_I8[1], not_7_out);
  and and_420 (and_420_out, not_1_out, ascii_I8[4], not_5_out, ascii_I8[1], not_7_out);
  and and_421 (and_421_out, not_2_out, ascii_I8[4], not_4_out, ascii_I8[2], ascii_I8[1], not_7_out);
  and and_422 (and_422_out, ascii_I8[6], ascii_I8[5], not_4_out, ascii_I8[2], ascii_I8[1], not_7_out);
  and and_423 (and_423_out, ascii_I8[6], ascii_I8[5], ascii_I8[4], not_4_out, ascii_I8[2], not_7_out);
  and and_424 (and_424_out, ascii_I8[6], ascii_I8[5], ascii_I8[4], ascii_I8[3], not_5_out, not_7_out);
  and and_425 (and_425_out, not_2_out, not_3_out, not_4_out, not_5_out, not_7_out);
  and and_426 (and_426_out, not_4_out, not_5_out, ascii_I8[1], ascii_I8[0]);
  and and_427 (and_427_out, not_1_out, ascii_I8[2], ascii_I8[1], not_7_out);
  and and_428 (and_428_out, not_3_out, ascii_I8[3], not_5_out, not_6_out, ascii_I8[0]);
  and and_429 (and_429_out, not_3_out, ascii_I8[3], ascii_I8[2], not_6_out, not_7_out);
  and and_430 (and_430_out, not_1_out, ascii_I8[4], not_4_out, not_5_out);
  and and_431 (and_431_out, not_1_out, ascii_I8[4], not_5_out, not_6_out);
  and and_432 (and_432_out, not_1_out, ascii_I8[4], not_4_out, not_6_out, ascii_I8[0]);
  and and_433 (and_433_out, not_1_out, ascii_I8[4], not_5_out, ascii_I8[0]);
  and and_434 (and_434_out, not_2_out, ascii_I8[4], not_4_out, ascii_I8[0]);
  and and_435 (and_435_out, not_2_out, ascii_I8[4], ascii_I8[1], ascii_I8[0]);
  and and_436 (and_436_out, ascii_I8[5], ascii_I8[3], not_5_out, not_6_out, ascii_I8[0]);
  and and_437 (and_437_out, ascii_I8[6], not_3_out, not_5_out, ascii_I8[1], not_7_out);
  and and_438 (and_438_out, ascii_I8[6], not_3_out, ascii_I8[2], not_6_out, not_7_out);
  and and_439 (and_439_out, ascii_I8[6], not_4_out, ascii_I8[2], ascii_I8[0]);
  and and_440 (and_440_out, ascii_I8[6], not_3_out, ascii_I8[2], ascii_I8[1], ascii_I8[0]);
  and and_441 (and_441_out, ascii_I8[6], ascii_I8[3], not_5_out, ascii_I8[1], not_7_out);
  and and_442 (and_442_out, ascii_I8[6], ascii_I8[4], ascii_I8[2], not_6_out, ascii_I8[0]);
  and and_443 (and_443_out, ascii_I8[6], ascii_I8[5], not_3_out, not_4_out, ascii_I8[0]);
  and and_444 (and_444_out, ascii_I8[6], ascii_I8[5], not_3_out, not_4_out, ascii_I8[2]);
  and and_445 (and_445_out, not_2_out, not_4_out, ascii_I8[1], not_7_out);
  and and_446 (and_446_out, not_2_out, not_3_out, ascii_I8[2], not_6_out);
  and and_447 (and_447_out, not_2_out, not_3_out, ascii_I8[2], not_7_out);
  and and_448 (and_448_out, not_2_out, ascii_I8[2], not_6_out, not_7_out);
  and and_449 (and_449_out, not_1_out, not_4_out, ascii_I8[2], not_6_out, ascii_I8[0]);
  and and_450 (and_450_out, not_2_out, ascii_I8[4], not_6_out, not_7_out);
  and and_451 (and_451_out, not_1_out, ascii_I8[4], not_4_out, ascii_I8[1], ascii_I8[0]);
  and and_452 (and_452_out, not_2_out, ascii_I8[4], not_4_out, ascii_I8[2]);
  and and_453 (and_453_out, not_2_out, ascii_I8[4], ascii_I8[3], not_5_out);
  and and_454 (and_454_out, ascii_I8[6], not_3_out, not_4_out, not_5_out, ascii_I8[1], not_7_out);
  and and_455 (and_455_out, ascii_I8[6], not_3_out, ascii_I8[3], not_5_out, not_6_out, not_7_out);
  and and_456 (and_456_out, ascii_I8[6], not_3_out, ascii_I8[3], not_5_out, ascii_I8[1], ascii_I8[0]);
  and and_457 (and_457_out, not_2_out, not_5_out, not_6_out, not_7_out);
  and and_458 (and_458_out, not_2_out, not_4_out, ascii_I8[0]);
  and and_459 (and_459_out, not_2_out, not_4_out, ascii_I8[1]);
  and and_460 (and_460_out, not_2_out, not_5_out, ascii_I8[1], ascii_I8[0]);
  and and_461 (and_461_out, not_2_out, not_3_out, ascii_I8[2]);
  and and_462 (and_462_out, not_1_out, not_4_out, ascii_I8[2], not_6_out, ascii_I8[0]);
  and and_463 (and_463_out, not_1_out, not_3_out, not_4_out, ascii_I8[2], ascii_I8[1], not_7_out);
  and and_464 (and_464_out, not_1_out, ascii_I8[4], not_4_out, not_5_out, not_7_out);
  and and_465 (and_465_out, not_2_out, ascii_I8[4], not_5_out, not_6_out);
  and and_466 (and_466_out, not_1_out, ascii_I8[4], ascii_I8[2], ascii_I8[1], ascii_I8[0]);
  and and_467 (and_467_out, not_1_out, ascii_I8[4], ascii_I8[3], not_5_out, not_6_out);
  and and_468 (and_468_out, ascii_I8[6], not_3_out, not_4_out, not_5_out, ascii_I8[1], not_7_out);
  and and_469 (and_469_out, ascii_I8[6], not_3_out, ascii_I8[3], not_5_out, not_6_out, not_7_out);
  and and_470 (and_470_out, ascii_I8[6], not_3_out, ascii_I8[3], not_5_out, ascii_I8[1], ascii_I8[0]);
  and and_471 (and_471_out, not_2_out, not_4_out, ascii_I8[0]);
  and and_472 (and_472_out, not_1_out, not_3_out, not_4_out, not_5_out, ascii_I8[1], ascii_I8[0]);
  and and_473 (and_473_out, not_1_out, not_3_out, not_4_out, ascii_I8[2], not_7_out);
  and and_474 (and_474_out, not_2_out, not_3_out, ascii_I8[2]);
  and and_475 (and_475_out, not_1_out, not_4_out, ascii_I8[2], ascii_I8[1], not_7_out);
  and and_476 (and_476_out, not_1_out, not_3_out, ascii_I8[3], not_5_out, ascii_I8[1], not_7_out);
  and and_477 (and_477_out, not_2_out, ascii_I8[3], ascii_I8[2], not_7_out);
  and and_478 (and_478_out, not_2_out, ascii_I8[4], not_5_out, ascii_I8[0]);
  and and_479 (and_479_out, not_1_out, ascii_I8[4], ascii_I8[2], not_6_out, ascii_I8[0]);
  and and_480 (and_480_out, ascii_I8[4], ascii_I8[3], not_5_out, not_6_out, ascii_I8[0]);
  and and_481 (and_481_out, ascii_I8[5], ascii_I8[4], not_5_out, not_6_out, not_7_out);
  and and_482 (and_482_out, ascii_I8[6], not_4_out, not_5_out, ascii_I8[1], not_7_out);
  and and_483 (and_483_out, ascii_I8[6], not_4_out, ascii_I8[2], ascii_I8[1], ascii_I8[0]);
  and and_484 (and_484_out, ascii_I8[6], not_3_out, ascii_I8[3], not_5_out, not_6_out, not_7_out);
  and and_485 (and_485_out, ascii_I8[6], not_3_out, ascii_I8[3], not_5_out, ascii_I8[1], ascii_I8[0]);
  and and_486 (and_486_out, ascii_I8[6], not_3_out, ascii_I8[3], ascii_I8[2], not_6_out, ascii_I8[0]);
  and and_487 (and_487_out, ascii_I8[6], not_3_out, ascii_I8[3], ascii_I8[2], ascii_I8[1], not_7_out);
  and and_488 (and_488_out, ascii_I8[6], ascii_I8[4], not_4_out, not_5_out, not_7_out);
  and and_489 (and_489_out, ascii_I8[6], ascii_I8[4], not_4_out, ascii_I8[2], ascii_I8[1]);
  and and_490 (and_490_out, ascii_I8[6], ascii_I8[5], ascii_I8[4], not_5_out, not_7_out);
  and and_491 (and_491_out, ascii_I8[6], ascii_I8[5], ascii_I8[4], not_4_out, ascii_I8[2]);
  and and_492 (and_492_out, not_2_out, not_4_out, not_6_out, ascii_I8[0]);
  and and_493 (and_493_out, not_2_out, not_3_out, not_4_out, ascii_I8[1]);
  and and_494 (and_494_out, not_2_out, not_3_out, ascii_I8[2]);
  and and_495 (and_495_out, not_2_out, ascii_I8[3], not_5_out, ascii_I8[1], ascii_I8[0]);
  and and_496 (and_496_out, not_3_out, ascii_I8[3], not_5_out, ascii_I8[1], ascii_I8[0]);
  and and_497 (and_497_out, not_3_out, ascii_I8[3], ascii_I8[2], not_6_out, ascii_I8[0]);
  and and_498 (and_498_out, ascii_I8[4], not_4_out, not_5_out, not_6_out, not_7_out);
  and and_499 (and_499_out, not_1_out, ascii_I8[4], not_4_out, ascii_I8[2], not_7_out);
  and and_500 (and_500_out, not_1_out, ascii_I8[4], ascii_I8[2], not_6_out, not_7_out);
  and and_501 (and_501_out, ascii_I8[6], not_3_out, ascii_I8[1], ascii_I8[0]);
  and and_502 (and_502_out, ascii_I8[6], not_3_out, not_4_out, ascii_I8[2]);
  and and_503 (and_503_out, ascii_I8[6], not_3_out, ascii_I8[2], ascii_I8[0]);
  and and_504 (and_504_out, ascii_I8[6], not_4_out, ascii_I8[2], ascii_I8[0]);
  and and_505 (and_505_out, ascii_I8[6], not_4_out, ascii_I8[2], ascii_I8[1]);
  and and_506 (and_506_out, ascii_I8[6], not_3_out, ascii_I8[3], not_5_out, not_6_out, not_7_out);
  and and_507 (and_507_out, ascii_I8[6], ascii_I8[4], not_4_out, not_5_out, not_7_out);
  and and_508 (and_508_out, ascii_I8[6], ascii_I8[5], not_4_out, ascii_I8[1]);
  and and_509 (and_509_out, ascii_I8[6], ascii_I8[5], ascii_I8[2], ascii_I8[1]);
  and and_510 (and_510_out, ascii_I8[6], ascii_I8[5], ascii_I8[4], not_5_out, not_6_out, ascii_I8[0]);
  and and_511 (and_511_out, not_2_out, not_3_out, not_4_out);
  and and_512 (and_512_out, not_2_out, not_4_out, not_6_out, ascii_I8[0]);
  and and_513 (and_513_out, not_3_out, not_4_out, not_5_out, ascii_I8[1], ascii_I8[0]);
  and and_514 (and_514_out, not_2_out, not_4_out, ascii_I8[2], ascii_I8[0]);
  and and_515 (and_515_out, not_1_out, not_4_out, ascii_I8[2], ascii_I8[1], not_7_out);
  and and_516 (and_516_out, not_1_out, not_3_out, ascii_I8[3], not_5_out, ascii_I8[1], not_7_out);
  and and_517 (and_517_out, not_2_out, ascii_I8[3], not_5_out, ascii_I8[1], ascii_I8[0]);
  and and_518 (and_518_out, not_2_out, ascii_I8[3], ascii_I8[2], not_6_out, not_7_out);
  and and_519 (and_519_out, not_1_out, ascii_I8[4], not_4_out, not_6_out, not_7_out);
  and and_520 (and_520_out, not_1_out, ascii_I8[4], not_5_out, not_6_out, not_7_out);
  and and_521 (and_521_out, ascii_I8[4], not_4_out, not_5_out, not_6_out, not_7_out);
  and and_522 (and_522_out, not_1_out, ascii_I8[4], ascii_I8[3], ascii_I8[2], not_6_out, ascii_I8[0]);
  and and_523 (and_523_out, ascii_I8[6], not_4_out, not_5_out, ascii_I8[1], not_7_out);
  and and_524 (and_524_out, ascii_I8[6], not_3_out, not_5_out, ascii_I8[1], ascii_I8[0]);
  and and_525 (and_525_out, ascii_I8[6], not_3_out, not_4_out, ascii_I8[2], not_6_out);
  and and_526 (and_526_out, ascii_I8[6], not_4_out, ascii_I8[2], not_6_out, ascii_I8[0]);
  and and_527 (and_527_out, ascii_I8[6], not_3_out, ascii_I8[3], not_5_out, not_6_out, not_7_out);
  and and_528 (and_528_out, ascii_I8[6], not_3_out, ascii_I8[3], ascii_I8[2], ascii_I8[0]);
  and and_529 (and_529_out, ascii_I8[6], not_3_out, ascii_I8[3], ascii_I8[2], ascii_I8[1]);
  and and_530 (and_530_out, ascii_I8[6], ascii_I8[4], not_4_out, ascii_I8[2], ascii_I8[1]);
  and and_531 (and_531_out, not_2_out, not_3_out, not_4_out);
  and and_532 (and_532_out, not_2_out, not_3_out, not_7_out);
  and and_533 (and_533_out, not_2_out, not_4_out, not_5_out, not_6_out);
  and and_534 (and_534_out, not_2_out, not_5_out, not_7_out);
  and and_535 (and_535_out, not_3_out, not_4_out, ascii_I8[2], not_6_out);
  and and_536 (and_536_out, not_4_out, ascii_I8[2], not_6_out, ascii_I8[0]);
  and and_537 (and_537_out, not_1_out, not_4_out, ascii_I8[2], ascii_I8[1], not_7_out);
  and and_538 (and_538_out, not_2_out, ascii_I8[3], not_5_out, ascii_I8[1]);
  and and_539 (and_539_out, not_3_out, ascii_I8[3], ascii_I8[2], ascii_I8[1], ascii_I8[0]);
  and and_540 (and_540_out, not_1_out, ascii_I8[4], not_5_out, not_6_out, not_7_out);
  and and_541 (and_541_out, ascii_I8[4], not_4_out, not_5_out, not_6_out, not_7_out);
  and and_542 (and_542_out, not_1_out, ascii_I8[4], not_4_out, not_5_out, ascii_I8[1], ascii_I8[0]);
  and and_543 (and_543_out, ascii_I8[6], not_3_out, not_4_out, not_6_out, ascii_I8[0]);
  and and_544 (and_544_out, ascii_I8[6], not_3_out, not_5_out, ascii_I8[1]);
  and and_545 (and_545_out, ascii_I8[6], not_4_out, not_5_out, ascii_I8[1], not_7_out);
  and and_546 (and_546_out, ascii_I8[6], not_3_out, ascii_I8[3], not_5_out, not_7_out);
  and and_547 (and_547_out, ascii_I8[6], not_3_out, ascii_I8[3], ascii_I8[1]);
  and and_548 (and_548_out, ascii_I8[6], not_3_out, ascii_I8[3], ascii_I8[2], ascii_I8[0]);
  and and_549 (and_549_out, ascii_I8[6], ascii_I8[4], not_4_out, ascii_I8[2], ascii_I8[0]);
  and and_550 (and_550_out, not_2_out, not_3_out, not_4_out, not_6_out, ascii_I8[0]);
  and and_551 (and_551_out, not_2_out, not_3_out, ascii_I8[2], not_7_out);
  and and_552 (and_552_out, not_2_out, ascii_I8[4], not_5_out, ascii_I8[1]);
  and and_553 (and_553_out, ascii_I8[4], not_4_out, not_5_out, ascii_I8[1], not_7_out);
  and and_554 (and_554_out, not_2_out, ascii_I8[4], ascii_I8[3], ascii_I8[1], ascii_I8[0]);
  and and_555 (and_555_out, ascii_I8[6], not_4_out, not_5_out, ascii_I8[1], not_7_out);
  and and_556 (and_556_out, ascii_I8[6], ascii_I8[3], not_5_out, not_6_out, not_7_out);
  and and_557 (and_557_out, ascii_I8[6], not_3_out, ascii_I8[3], not_5_out, ascii_I8[1], ascii_I8[0]);
  and and_558 (and_558_out, ascii_I8[6], not_3_out, ascii_I8[3], ascii_I8[2], not_6_out, ascii_I8[0]);
  and and_559 (and_559_out, ascii_I8[6], not_3_out, ascii_I8[3], ascii_I8[2], ascii_I8[1], not_7_out);
  and and_560 (and_560_out, ascii_I8[6], ascii_I8[4], not_5_out, not_7_out);
  and and_561 (and_561_out, ascii_I8[6], ascii_I8[4], not_4_out, not_5_out, ascii_I8[1]);
  or or_1 (ledmC0O8[7], and_1_out, and_2_out, and_3_out, and_4_out, and_5_out, and_6_out, and_7_out, and_8_out, and_9_out, and_10_out, and_11_out);
  or or_2 (ledmC1O8[6], and_132_out, and_133_out, and_134_out, and_135_out, and_136_out, and_137_out, and_138_out, and_139_out);
  or or_3 (ledmC2O8[6], and_240_out, and_241_out, and_242_out, and_243_out, and_244_out, and_245_out, and_246_out, and_247_out, and_248_out, and_249_out, and_250_out, and_251_out);
  or or_4 (ledmC2O8[2], and_310_out, and_311_out, and_312_out, and_313_out, and_314_out, and_315_out, and_316_out, and_317_out, and_318_out, and_319_out, and_320_out, and_321_out);
  or or_5 (ledmC3O8[6], and_358_out, and_359_out, and_360_out, and_361_out, and_362_out, and_363_out, and_364_out, and_365_out, and_366_out);
  or or_6 (ledmC3O8[2], and_417_out, and_418_out, and_419_out, and_420_out, and_421_out, and_422_out, and_423_out, and_424_out);
  or or_7 (ledmC4O8[7], and_445_out, and_446_out, and_447_out, and_448_out, and_449_out, and_450_out, and_451_out, and_452_out, and_453_out, and_454_out, and_455_out, and_456_out);
  or or_8 (ledmC4O8[1], and_550_out, and_551_out, and_552_out, and_553_out, and_554_out, and_555_out, and_556_out, and_557_out, and_558_out, and_559_out, and_560_out, and_561_out);
  or or_9 (ledmC0O8[6], and_12_out, and_13_out, and_14_out, and_15_out, and_16_out, and_17_out, and_18_out, and_19_out, and_20_out, and_21_out, and_22_out, and_23_out, and_24_out, and_25_out, and_26_out, and_27_out);
  or or_10 (ledmC0O8[5], and_28_out, and_29_out, and_30_out, and_31_out, and_32_out, and_33_out, and_34_out, and_35_out, and_36_out, and_37_out, and_38_out, and_39_out, and_40_out, and_41_out, and_42_out, and_43_out, and_44_out, and_45_out);
  or or_11 (ledmC0O8[4], and_46_out, and_47_out, and_48_out, and_49_out, and_50_out, and_51_out, and_52_out, and_53_out, and_54_out, and_55_out, and_56_out, and_57_out, and_58_out, and_59_out, and_60_out, and_61_out, and_62_out, and_63_out, and_64_out, and_65_out);
  or or_12 (ledmC0O8[3], and_66_out, and_67_out, and_68_out, and_69_out, and_70_out, and_71_out, and_72_out, and_73_out, and_74_out, and_75_out, and_76_out, and_77_out, and_78_out, and_79_out, and_80_out, and_81_out, and_82_out, and_83_out, and_84_out);
  or or_13 (ledmC0O8[2], and_85_out, and_86_out, and_87_out, and_88_out, and_89_out, and_90_out, and_91_out, and_92_out, and_93_out, and_94_out, and_95_out, and_96_out, and_97_out, and_98_out, and_99_out);
  or or_14 (ledmC0O8[1], and_100_out, and_101_out, and_102_out, and_103_out, and_104_out, and_105_out, and_106_out, and_107_out, and_108_out, and_109_out, and_110_out, and_111_out, and_112_out, and_113_out, and_114_out, and_115_out);
  or or_15 (ledmC1O8[7], and_116_out, and_117_out, and_118_out, and_119_out, and_120_out, and_121_out, and_122_out, and_123_out, and_124_out, and_125_out, and_126_out, and_127_out, and_128_out, and_129_out, and_130_out, and_131_out);
  or or_16 (ledmC1O8[5], and_140_out, and_141_out, and_142_out, and_143_out, and_144_out, and_145_out, and_146_out, and_147_out, and_148_out, and_149_out, and_150_out, and_151_out, and_152_out, and_153_out, and_154_out, and_155_out);
  or or_17 (ledmC1O8[4], and_156_out, and_157_out, and_158_out, and_159_out, and_160_out, and_161_out, and_162_out, and_163_out, and_164_out, and_165_out, and_166_out, and_167_out, and_168_out, and_169_out, and_170_out, and_171_out, and_172_out, and_173_out, and_174_out);
  or or_18 (ledmC1O8[3], and_175_out, and_176_out, and_177_out, and_178_out, and_179_out, and_180_out, and_181_out, and_182_out, and_183_out, and_184_out, and_185_out, and_186_out, and_187_out, and_188_out, and_189_out);
  or or_19 (ledmC1O8[2], and_190_out, and_191_out, and_192_out, and_193_out, and_194_out, and_195_out, and_196_out, and_197_out, and_198_out, and_199_out, and_200_out, and_201_out, and_202_out, and_203_out);
  or or_20 (ledmC1O8[1], and_204_out, and_205_out, and_206_out, and_207_out, and_208_out, and_209_out, and_210_out, and_211_out, and_212_out, and_213_out, and_214_out, and_215_out, and_216_out, and_217_out, and_218_out, and_219_out, and_220_out, and_221_out);
  or or_21 (ledmC2O8[7], and_222_out, and_223_out, and_224_out, and_225_out, and_226_out, and_227_out, and_228_out, and_229_out, and_230_out, and_231_out, and_232_out, and_233_out, and_234_out, and_235_out, and_236_out, and_237_out, and_238_out, and_239_out);
  or or_22 (ledmC2O8[5], and_252_out, and_253_out, and_254_out, and_255_out, and_256_out, and_257_out, and_258_out, and_259_out, and_260_out, and_261_out, and_262_out, and_263_out, and_264_out, and_265_out, and_266_out, and_267_out, and_268_out);
  or or_23 (ledmC2O8[4], and_269_out, and_270_out, and_271_out, and_272_out, and_273_out, and_274_out, and_275_out, and_276_out, and_277_out, and_278_out, and_279_out, and_280_out, and_281_out, and_282_out, and_283_out, and_284_out, and_285_out, and_286_out, and_287_out, and_288_out);
  or or_24 (ledmC2O8[3], and_289_out, and_290_out, and_291_out, and_292_out, and_293_out, and_294_out, and_295_out, and_296_out, and_297_out, and_298_out, and_299_out, and_300_out, and_301_out, and_302_out, and_303_out, and_304_out, and_305_out, and_306_out, and_307_out, and_308_out, and_309_out);
  or or_25 (ledmC2O8[1], and_322_out, and_323_out, and_324_out, and_325_out, and_326_out, and_327_out, and_328_out, and_329_out, and_330_out, and_331_out, and_332_out, and_333_out, and_334_out, and_335_out, and_336_out, and_337_out, and_338_out, and_339_out, and_340_out, and_341_out);
  or or_26 (ledmC3O8[7], and_342_out, and_343_out, and_344_out, and_345_out, and_346_out, and_347_out, and_348_out, and_349_out, and_350_out, and_351_out, and_352_out, and_353_out, and_354_out, and_355_out, and_356_out, and_357_out);
  or or_27 (ledmC3O8[5], and_367_out, and_368_out, and_369_out, and_370_out, and_371_out, and_372_out, and_373_out, and_374_out, and_375_out, and_376_out, and_377_out, and_378_out, and_379_out, and_380_out);
  or or_28 (ledmC3O8[4], and_381_out, and_382_out, and_383_out, and_384_out, and_385_out, and_386_out, and_387_out, and_388_out, and_389_out, and_390_out, and_391_out, and_392_out, and_393_out, and_394_out, and_395_out, and_396_out, and_397_out, and_398_out);
  or or_29 (ledmC3O8[3], and_399_out, and_400_out, and_401_out, and_402_out, and_403_out, and_404_out, and_405_out, and_406_out, and_407_out, and_408_out, and_409_out, and_410_out, and_411_out, and_412_out, and_413_out, and_414_out, and_415_out, and_416_out);
  or or_30 (ledmC3O8[1], and_425_out, and_426_out, and_427_out, and_428_out, and_429_out, and_430_out, and_431_out, and_432_out, and_433_out, and_434_out, and_435_out, and_436_out, and_437_out, and_438_out, and_439_out, and_440_out, and_441_out, and_442_out, and_443_out, and_444_out);
  or or_31 (ledmC4O8[6], and_457_out, and_458_out, and_459_out, and_460_out, and_461_out, and_462_out, and_463_out, and_464_out, and_465_out, and_466_out, and_467_out, and_468_out, and_469_out, and_470_out);
  or or_32 (ledmC4O8[5], and_471_out, and_472_out, and_473_out, and_474_out, and_475_out, and_476_out, and_477_out, and_478_out, and_479_out, and_480_out, and_481_out, and_482_out, and_483_out, and_484_out, and_485_out, and_486_out, and_487_out, and_488_out, and_489_out, and_490_out, and_491_out);
  or or_33 (ledmC4O8[4], and_492_out, and_493_out, and_494_out, and_495_out, and_496_out, and_497_out, and_498_out, and_499_out, and_500_out, and_501_out, and_502_out, and_503_out, and_504_out, and_505_out, and_506_out, and_507_out, and_508_out, and_509_out, and_510_out);
  or or_34 (ledmC4O8[3], and_511_out, and_512_out, and_513_out, and_514_out, and_515_out, and_516_out, and_517_out, and_518_out, and_519_out, and_520_out, and_521_out, and_522_out, and_523_out, and_524_out, and_525_out, and_526_out, and_527_out, and_528_out, and_529_out, and_530_out);
  or or_35 (ledmC4O8[2], and_531_out, and_532_out, and_533_out, and_534_out, and_535_out, and_536_out, and_537_out, and_538_out, and_539_out, and_540_out, and_541_out, and_542_out, and_543_out, and_544_out, and_545_out, and_546_out, and_547_out, and_548_out, and_549_out);

  assign ledmC0O8[0] = 1'b0;
  assign ledmC1O8[0] = 1'b0;
  assign ledmC2O8[0] = 1'b0;
  assign ledmC3O8[0] = 1'b0;
  assign ledmC4O8[0] = 1'b0;
endmodule
// VHDL entity lcd_controller, as the project stores it:
--------------------------------------------------------------------------------
--
--   FileName:         lcd_controller.vhd
--   Dependencies:     none
--   Design Software:  Quartus II 32-bit Version 11.1 Build 173 SJ Full Version
--
--   HDL CODE IS PROVIDED "AS IS."  DIGI-KEY EXPRESSLY DISCLAIMS ANY
--   WARRANTY OF ANY KIND, WHETHER EXPRESS OR IMPLIED, INCLUDING BUT NOT
--   LIMITED TO, THE IMPLIED WARRANTIES OF MERCHANTABILITY, FITNESS FOR A
--   PARTICULAR PURPOSE, OR NON-INFRINGEMENT. IN NO EVENT SHALL DIGI-KEY
--   BE LIABLE FOR ANY INCIDENTAL, SPECIAL, INDIRECT OR CONSEQUENTIAL
--   DAMAGES, LOST PROFITS OR LOST DATA, HARM TO YOUR EQUIPMENT, COST OF
--   PROCUREMENT OF SUBSTITUTE GOODS, TECHNOLOGY OR SERVICES, ANY CLAIMS
--   BY THIRD PARTIES (INCLUDING BUT NOT LIMITED TO ANY DEFENSE THEREOF),
--   ANY CLAIMS FOR INDEMNITY OR CONTRIBUTION, OR OTHER SIMILAR COSTS.
--
--   Version History
--   Version 1.0 6/2/2006 Scott Larson
--     Initial Public Release
--   Version 2.0 6/13/2012 Scott Larson
--
--   CLOCK FREQUENCY: to change system clock frequency, change Line 65
--
--   LCD INITIALIZATION SETTINGS: to change, comment/uncomment lines:
--
--   Function Set  
--      2-line mode, display on             Line 93    lcd_data <= "00111100";
--      1-line mode, display on             Line 94    lcd_data <= "00110100";
--      1-line mode, display off            Line 95    lcd_data <= "00110000";
--      2-line mode, display off            Line 96    lcd_data <= "00111000";
--   Display ON/OFF
--      display on, cursor off, blink off   Line 104   lcd_data <= "00001100";
--      display on, cursor off, blink on    Line 105   lcd_data <= "00001101";
--      display on, cursor on, blink off    Line 106   lcd_data <= "00001110";
--      display on, cursor on, blink on     Line 107   lcd_data <= "00001111";
--      display off, cursor off, blink off  Line 108   lcd_data <= "00001000";
--      display off, cursor off, blink on   Line 109   lcd_data <= "00001001";
--      display off, cursor on, blink off   Line 110   lcd_data <= "00001010";
--      display off, cursor on, blink on    Line 111   lcd_data <= "00001011";
--   Entry Mode Set
--      increment mode, entire shift off    Line 127   lcd_data <= "00000110";
--      increment mode, entire shift on     Line 128   lcd_data <= "00000111";
--      decrement mode, entire shift off    Line 129   lcd_data <= "00000100";
--      decrement mode, entire shift on     Line 130   lcd_data <= "00000101";
--    
--------------------------------------------------------------------------------
--	2023.04.04	Alexandre Schmid	command to switch to ROM A02 font "00111000"
--								(but we have ROM A00 chipsets) table 4 of
--								HD44780U datasheets
--------------------------------------------------------------------------------

LIBRARY ieee;
USE ieee.std_logic_1164.ALL;

ENTITY lcd_controller IS
  PORT(
    clk        : IN    STD_LOGIC;  --system clock
    reset_n    : IN    STD_LOGIC;  --active low reinitializes lcd
    lcd_enable : IN    STD_LOGIC;  --latches data into lcd controller
    lcd_bus    : IN    STD_LOGIC_VECTOR(9 DOWNTO 0);  --data and control signals
    busy       : OUT   STD_LOGIC;  --lcd controller busy/idle feedback
    rw, rs, e  : OUT   STD_LOGIC;  --read/write, setup/data, and enable for lcd
    lcd_data   : OUT   STD_LOGIC_VECTOR(7 DOWNTO 0)); --data signals for lcd
END lcd_controller;

ARCHITECTURE controller OF lcd_controller IS
  TYPE CONTROL IS(power_up, initialize, ready, send);
  SIGNAL    state      : CONTROL;
  CONSTANT  freq       : INTEGER := 1; --system clock frequency in MHz
BEGIN
  PROCESS(clk, reset_n)
    VARIABLE clk_count : INTEGER := 0; --event counter for timing
  BEGIN
  IF(clk'EVENT and clk = '1') THEN
    
      CASE state IS
        
        --wait 50 ms to ensure Vdd has risen and required LCD wait is met
        WHEN power_up =>
          busy <= '1';
          IF(clk_count < (50000 * freq)) THEN    --wait 50 ms
            clk_count := clk_count + 1;
            state <= power_up;
          ELSE                                   --power-up complete
            clk_count := 0;
            rs <= '0';
            rw <= '0';
            lcd_data <= "00111000";
            state <= initialize;
          END IF;
          
        --cycle through initialization sequence  
        WHEN initialize =>
          busy <= '1';
          clk_count := clk_count + 1;
          IF(clk_count < (10 * freq)) THEN       --function set
            lcd_data <= "00111100";      --2-line mode, display on
            --lcd_data <= "00110100";    --1-line mode, display on, 5x10 font
            --lcd_data <= "00110000";    --1-line mdoe, display off
            --lcd_data <= "00111000";    --2-line mode, display off
            e <= '1';
            state <= initialize;
          ELSIF(clk_count < (60 * freq)) THEN    --wait 50 us
            lcd_data <= "00000000";
            e <= '0';
            state <= initialize;
          ELSIF(clk_count < (70 * freq)) THEN    --display on/off control
            --lcd_data <= "00001100";      --display on, cursor off, blink off
            lcd_data <= "00001101";    --display on, cursor off, blink on
            --lcd_data <= "00001110";    --display on, cursor on, blink off
            --lcd_data <= "00001111";    --display on, cursor on, blink on
            --lcd_data <= "00001000";    --display off, cursor off, blink off
            --lcd_data <= "00001001";    --display off, cursor off, blink on
            --lcd_data <= "00001010";    --display off, cursor on, blink off
            --lcd_data <= "00001011";    --display off, cursor on, blink on            
            e <= '1';
            state <= initialize;
          ELSIF(clk_count < (120 * freq)) THEN   --wait 50 us
            lcd_data <= "00000000";
            e <= '0';
            state <= initialize;
          ELSIF(clk_count < (130 * freq)) THEN   --display clear
            lcd_data <= "00000001";
            e <= '1';
            state <= initialize;
          ELSIF(clk_count < (2130 * freq)) THEN  --wait 2 ms
            lcd_data <= "00000000";
            e <= '0';
            state <= initialize;
          ELSIF(clk_count < (2140 * freq)) THEN  --entry mode set
            lcd_data <= "00000110";      --increment mode, entire shift off
            --lcd_data <= "00000111";    --increment mode, entire shift on
            --lcd_data <= "00000100";    --decrement mode, entire shift off
            --lcd_data <= "00000101";    --decrement mode, entire shift on
            e <= '1';
            state <= initialize;
          ELSIF(clk_count < (2200 * freq)) THEN  --wait 60 us
            lcd_data <= "00000000";
            e <= '0';
            state <= initialize;
          ELSE                                   --initialization complete
            clk_count := 0;
            busy <= '0';
            state <= ready;
          END IF;    
       
        --wait for the enable signal and then latch in the instruction
        WHEN ready =>
          IF(lcd_enable = '1') THEN
            busy <= '1';
            rs <= lcd_bus(9);
            rw <= lcd_bus(8);
            lcd_data <= lcd_bus(7 DOWNTO 0);
            clk_count := 0;            
            state <= send;
          ELSE
            busy <= '0';
            rs <= '0';
            rw <= '0';
            lcd_data <= "00000000";
            clk_count := 0;
            state <= ready;
          END IF;
        
        --send instruction to lcd        
        WHEN send =>
        busy <= '1';
        IF(clk_count < (50 * freq)) THEN  --do not exit for 50us
           busy <= '1';
           IF(clk_count < freq) THEN      --negative enable
             e <= '0';
           ELSIF(clk_count < (14 * freq)) THEN  --positive enable half-cycle
             e <= '1';
           ELSIF(clk_count < (27 * freq)) THEN  --negative enable half-cycle
             e <= '0';
           END IF;
           clk_count := clk_count + 1;
           state <= send;
        ELSE
          clk_count := 0;
          state <= ready;
        END IF;

      END CASE;    
    
      --reset
      IF(reset_n = '0') THEN
        state <= power_up;
        busy <= '1';
      END IF;
    
    END IF;
  END PROCESS;
END controller;

// VHDL entity lcd_example, as the project stores it:
--------------------------------------------------------------------------------
--
--   FileName:         lcd_example.vhd
--   Dependencies:     none
--   Design Software:  Quartus II 32-bit Version 11.1 Build 173 SJ Full Version
--
--   HDL CODE IS PROVIDED "AS IS."  DIGI-KEY EXPRESSLY DISCLAIMS ANY
--   WARRANTY OF ANY KIND, WHETHER EXPRESS OR IMPLIED, INCLUDING BUT NOT
--   LIMITED TO, THE IMPLIED WARRANTIES OF MERCHANTABILITY, FITNESS FOR A
--   PARTICULAR PURPOSE, OR NON-INFRINGEMENT. IN NO EVENT SHALL DIGI-KEY
--   BE LIABLE FOR ANY INCIDENTAL, SPECIAL, INDIRECT OR CONSEQUENTIAL
--   DAMAGES, LOST PROFITS OR LOST DATA, HARM TO YOUR EQUIPMENT, COST OF
--   PROCUREMENT OF SUBSTITUTE GOODS, TECHNOLOGY OR SERVICES, ANY CLAIMS
--   BY THIRD PARTIES (INCLUDING BUT NOT LIMITED TO ANY DEFENSE THEREOF),
--   ANY CLAIMS FOR INDEMNITY OR CONTRIBUTION, OR OTHER SIMILAR COSTS.
--
--   Version History
--   Version 1.0 6/13/2012 Scott Larson
--     Initial Public Release
--
--   Prints "123456789" on a HD44780 compatible 8-bit interface character LCD 
--   module using the lcd_controller.vhd component.
--
--------------------------------------------------------------------------------
--	2023.03.30	Alexandre Schmid	adaptation to EE110-EE207 logisim-evolution
--------------------------------------------------------------------------------

LIBRARY ieee;
USE ieee.std_logic_1164.all;

ENTITY lcd_example IS
  PORT(
      clk       : IN  STD_LOGIC;  --system clock
      rst		 : IN  STD_LOGIC;
      data1a	 : IN  STD_LOGIC_VECTOR(31 DOWNTO 0); --bus limitation imposed by
      data1b	 : IN  STD_LOGIC_VECTOR(31 DOWNTO 0); --logisim-evolution
      data1c	 : IN  STD_LOGIC_VECTOR(31 DOWNTO 0);
      data1d	 : IN  STD_LOGIC_VECTOR(31 DOWNTO 0);
      data2a	 : IN  STD_LOGIC_VECTOR(31 DOWNTO 0);
      data2b	 : IN  STD_LOGIC_VECTOR(31 DOWNTO 0);
      data2c	 : IN  STD_LOGIC_VECTOR(31 DOWNTO 0);
      data2d	 : IN  STD_LOGIC_VECTOR(31 DOWNTO 0);
      rw, rs, e : OUT STD_LOGIC;  --read/write, setup/data, and enable for lcd
      lcd_data  : OUT STD_LOGIC_VECTOR(7 DOWNTO 0)); --data signals for lcd
END lcd_example;

ARCHITECTURE behavior OF lcd_example IS
  SIGNAL   lcd_enable : STD_LOGIC;
  SIGNAL   lcd_bus    : STD_LOGIC_VECTOR(9 DOWNTO 0);
  SIGNAL   lcd_busy   : STD_LOGIC;
  SIGNAL	 reset_n	: STD_LOGIC;
  COMPONENT lcd_controller IS
    PORT(
       clk        : IN  STD_LOGIC; --system clock
       reset_n    : IN  STD_LOGIC; --active low reinitializes lcd
       lcd_enable : IN  STD_LOGIC; --latches data into lcd controller
       lcd_bus    : IN  STD_LOGIC_VECTOR(9 DOWNTO 0); --data and control signals
       busy       : OUT STD_LOGIC; --lcd controller busy/idle feedback
       rw, rs, e  : OUT STD_LOGIC; --read/write, setup/data, and enable for lcd
       lcd_data   : OUT STD_LOGIC_VECTOR(7 DOWNTO 0)); --data signals for lcd
  END COMPONENT;
BEGIN

  --instantiate the lcd controller
  dut: lcd_controller
    PORT MAP(clk => clk, reset_n => reset_n, lcd_enable => lcd_enable, lcd_bus => lcd_bus, 
             busy => lcd_busy, rw => rw, rs => rs, e => e, lcd_data => lcd_data);
  
  PROCESS(clk, rst)
    VARIABLE char  :  INTEGER RANGE 0 TO 34 := 0;
  BEGIN
   IF (rst = '0') THEN
    reset_n <= '0';
    char := 0;
   ELSE
    reset_n <= '1';
    
    IF(clk'EVENT AND clk = '1') THEN
      IF(lcd_busy = '0' AND lcd_enable = '0') THEN
        lcd_enable <= '1';
        IF(char < 35) THEN  -- WARNING to match the line number in the "case char" clause
          char := char + 1;
        END IF;
        CASE char IS								
          WHEN 1 => lcd_bus <= "0010000000"; --change to first line, AC add=0x00
          WHEN 2 => lcd_bus <= "10" & data1a(31 downto 24);
          WHEN 3 => lcd_bus <= "10" & data1a(23 downto 16);
          WHEN 4 => lcd_bus <= "10" & data1a(15 downto 8);
          WHEN 5 => lcd_bus <= "10" & data1a(7 downto 0);
          WHEN 6 => lcd_bus <= "10" & data1b(31 downto 24);
          WHEN 7 => lcd_bus <= "10" & data1b(23 downto 16);
          WHEN 8 => lcd_bus <= "10" & data1b(15 downto 8);
          WHEN 9 => lcd_bus <= "10" & data1b(7 downto 0);
          WHEN 10 => lcd_bus <= "10" & data1c(31 downto 24);
          WHEN 11 => lcd_bus <= "10" & data1c(23 downto 16);
          WHEN 12 => lcd_bus <= "10" & data1c(15 downto 8);
          WHEN 13 => lcd_bus <= "10" & data1c(7 downto 0);
          WHEN 14 => lcd_bus <= "10" & data1d(31 downto 24);
          WHEN 15 => lcd_bus <= "10" & data1d(23 downto 16);
          WHEN 16 => lcd_bus <= "10" & data1d(15 downto 8);
          WHEN 17 => lcd_bus <= "10" & data1d(7 downto 0);
          
          WHEN 18 => lcd_bus <= "0011000000";	--change to second line, AC add=0x40
        	WHEN 19 => lcd_bus <= "10" & data2a(31 downto 24);
          WHEN 20 => lcd_bus <= "10" & data2a(23 downto 16);
          WHEN 21 => lcd_bus <= "10" & data2a(15 downto 8);
          WHEN 22 => lcd_bus <= "10" & data2a(7 downto 0);
 		WHEN 23 => lcd_bus <= "10" & data2b(31 downto 24);
          WHEN 24 => lcd_bus <= "10" & data2b(23 downto 16);
          WHEN 25 => lcd_bus <= "10" & data2b(15 downto 8);
          WHEN 26 => lcd_bus <= "10" & data2b(7 downto 0);
          WHEN 27 => lcd_bus <= "10" & data2c(31 downto 24);
          WHEN 28 => lcd_bus <= "10" & data2c(23 downto 16);
          WHEN 29 => lcd_bus <= "10" & data2c(15 downto 8);
          WHEN 30 => lcd_bus <= "10" & data2c(7 downto 0);
          WHEN 31 => lcd_bus <= "10" & data2d(31 downto 24);
          WHEN 32 => lcd_bus <= "10" & data2d(23 downto 16);
          WHEN 33 => lcd_bus <= "10" & data2d(15 downto 8);
          WHEN 34 => lcd_bus <= "10" & data2d(7 downto 0);
          
          WHEN OTHERS => lcd_enable <= '0';
        END CASE;
      ELSE
        lcd_enable <= '0';
      END IF;
    END IF;
   END IF; 
  END PROCESS;
  
END behavior;
