// Logisim project accelerometer_experiments.circ as structural Verilog
module accel_final_driver_tb (
  input  rst,
  input  miso,
  input  accel_input,
  input  enable_accel,
  output mosi,
  output sclk,
  output cs
);

  wire absolute_val_and_sign_1_negative, absolute_val_and_sign_2_negative, absolute_val_and_sign_3_negative,
       accel_final_driver_v2_1_down, accel_final_driver_v2_1_left, accel_final_driver_v2_1_right,
       accel_final_driver_v2_1_up, accel_final_driver_v2_1_x_large, accel_final_driver_v2_1_x_medium,
       accel_final_driver_v2_1_x_small, accel_final_driver_v2_1_y_large, accel_final_driver_v2_1_y_medium,
       accel_final_driver_v2_1_y_small, multiplexer_1_out;
  wire [1:0] SELECTOR;
  wire [3:0] hex_to_decimal_16_bits_1_hundreds, hex_to_decimal_16_bits_1_ones, hex_to_decimal_16_bits_1_tens;
  wire [7:0] multiplexer_3_out, multiplexer_4_out, sevenseg_direction_angle_logic_1_letter_output,
       sevenseg_direction_angle_logic_2_letter_output, sevenseg_direction_angle_logic_3_letter_output,
       sevenseg_direction_angle_logic_4_letter_output;
  wire [15:0] absolute_val_and_sign_1_value, absolute_val_and_sign_2_value, absolute_val_and_sign_3_value,
       accel_final_driver_v2_1_x_filtered, accel_final_driver_v2_1_y_filtered,
       accel_final_driver_v2_1_z_filtered, multiplexer_2_out;

  DipSwitch #(.number(2)) DipSwitch_1 (.sw1(SELECTOR[0]), .sw2(SELECTOR[1]));
  accel_final_driver accel_final_driver_v2_1 (
    .rst(rst), .miso(miso), .accel_input(accel_input), .enable_accel(enable_accel), .x_offset(16'h3e),
    .y_offset(16'h39), .z_offset(16'h3a), .mosi(mosi), .sclk(sclk), .cs(cs),
    .x_filtered(accel_final_driver_v2_1_x_filtered), .y_filtered(accel_final_driver_v2_1_y_filtered),
    .z_filtered(accel_final_driver_v2_1_z_filtered), .left(accel_final_driver_v2_1_left),
    .down(accel_final_driver_v2_1_down), .right(accel_final_driver_v2_1_right),
    .up(accel_final_driver_v2_1_up), .x_small(accel_final_driver_v2_1_x_small),
    .y_small(accel_final_driver_v2_1_y_small), .x_medium(accel_final_driver_v2_1_x_medium),
    .y_medium(accel_final_driver_v2_1_y_medium), .x_large(accel_final_driver_v2_1_x_large),
    .y_large(accel_final_driver_v2_1_y_large));
  absolute_val_and_sign absolute_val_and_sign_1 (
    .unfiltered(accel_final_driver_v2_1_x_filtered), .value(absolute_val_and_sign_1_value),
    .negative(absolute_val_and_sign_1_negative));
  absolute_val_and_sign absolute_val_and_sign_2 (
    .unfiltered(accel_final_driver_v2_1_y_filtered), .value(absolute_val_and_sign_2_value),
    .negative(absolute_val_and_sign_2_negative));
  absolute_val_and_sign absolute_val_and_sign_3 (
    .unfiltered(accel_final_driver_v2_1_z_filtered), .value(absolute_val_and_sign_3_value),
    .negative(absolute_val_and_sign_3_negative));
  Multiplexer #(.select(2)) multiplexer_1 (
    .in0(absolute_val_and_sign_1_negative), .in1(absolute_val_and_sign_2_negative),
    .in2(absolute_val_and_sign_3_negative), .in3(1'b0), .out(multiplexer_1_out), .sel(SELECTOR));
  sign_hex_output HEX3 (.negative(multiplexer_1_out));
  Multiplexer #(.select(2), .width(16)) multiplexer_2 (
    .in0(absolute_val_and_sign_1_value), .in1(absolute_val_and_sign_2_value),
    .in2(absolute_val_and_sign_3_value), .in3({16{1'b0}}), .out(multiplexer_2_out), .sel(SELECTOR));
  sevenseg_direction_angle_logic sevenseg_direction_angle_logic_1 (
    .L(accel_final_driver_v2_1_left), .R(accel_final_driver_v2_1_right),
    .letter_output(sevenseg_direction_angle_logic_1_letter_output));  // open: U, D, S, M
  sevenseg_direction_angle_logic sevenseg_direction_angle_logic_2 (
    .U(accel_final_driver_v2_1_up), .D(accel_final_driver_v2_1_down),
    .letter_output(sevenseg_direction_angle_logic_2_letter_output));  // open: L, R, S, M
  sevenseg_direction_angle_logic sevenseg_direction_angle_logic_3 (
    .L(accel_final_driver_v2_1_x_large), .S(accel_final_driver_v2_1_x_small),
    .M(accel_final_driver_v2_1_x_medium), .letter_output(sevenseg_direction_angle_logic_3_letter_output));  // open: R, U, D
  sevenseg_direction_angle_logic sevenseg_direction_angle_logic_4 (
    .L(accel_final_driver_v2_1_y_large), .S(accel_final_driver_v2_1_y_small),
    .M(accel_final_driver_v2_1_y_medium), .letter_output(sevenseg_direction_angle_logic_4_letter_output));  // open: R, U, D
  hex_to_decimal_16_bits hex_to_decimal_16_bits_1 (
    .val(multiplexer_2_out), .hundreds(hex_to_decimal_16_bits_1_hundreds),
    .tens(hex_to_decimal_16_bits_1_tens), .ones(hex_to_decimal_16_bits_1_ones));
  sevenseg_numbers_output HEX2 (.input_bus(hex_to_decimal_16_bits_1_hundreds), .decimal(1'b1));
  sevenseg_numbers_output HEX1 (.input_bus(hex_to_decimal_16_bits_1_tens));  // open: decimal
  sevenseg_numbers_output HEX0 (.input_bus(hex_to_decimal_16_bits_1_ones));  // open: decimal
  Multiplexer #(.select(2), .width(8)) multiplexer_3 (
    .in0(sevenseg_direction_angle_logic_1_letter_output),
    .in1(sevenseg_direction_angle_logic_2_letter_output), .in2({8{1'b0}}), .in3({8{1'b0}}),
    .out(multiplexer_3_out), .sel(SELECTOR));
  sevenseg_mapped HEX4 (.sevenseg_input(multiplexer_3_out));
  Multiplexer #(.select(2), .width(8)) multiplexer_4 (
    .in0(sevenseg_direction_angle_logic_3_letter_output),
    .in1(sevenseg_direction_angle_logic_4_letter_output), .in2({8{1'b0}}), .in3({8{1'b0}}),
    .out(multiplexer_4_out), .sel(SELECTOR));
  sevenseg_mapped HEX5 (.sevenseg_input(multiplexer_4_out));

  // Notes on the sheet:
  //   OFFSETS BASED
  //   OUTPUTS THE VALUES READ BY THE 3-AXES OF THE ACCELEROMETER (HEX0 - HEX3)
  //   OUTPUTS THE DIRECTION THAT THE BOARD IS TILTED (HEX4)
  //   CHANGE THESE
  //   ON YOUR DE10LITE
  //   LEFT(L), RIGHT(r), UP(U), DOWN(d)
  //   SMALL (S), MEDIUM (M), LARGE(L)
  //   X - AXIS : SELECTOR = 00
  //   Y - AXIS : SELECTOR = 01
  //   Z - AXIS : SELECTOR = 10
  //   ACCELEROMETER MAIN DRIVER TESTBENCH
  //   THE VALUE OF THE OFFSETS CHANGES FROM DE10 TO DE10. 
  //   PLEASE REFER TO CALIBRATION_TB TO DETERMINE THE OFFSETS FOR EACH AXIS
  //   OUTPUTS THE AMOUNT OF TILT OF THE BOARD (HEX5)
  //   GSENSOR/PIN0 -> MOSI
  //   GSENSOR/PIN1 -> MISO
  //   GSENSOR/PIN2 -> SCLK
  //   GSENSOR/PIN3 -> CS
  //   GSENSOR/PIN4 -> ACCEL_INPUT
  //   Tested functional at 1MHz. DE10-Lite. 2024.05.24
  //   PIN MAPPING FOR TERASICDE10LITE_GSENSOR.xml
endmodule

module accel_final_driver_tb_sim (
  input  X_NEGATIVE,
  input  Y_NEGATIVE,
  input  Z_NEGATIVE
);

  wire absolute_val_and_sign_1_negative, absolute_val_and_sign_2_negative, absolute_val_and_sign_3_negative,
       accel_final_driver_sim_1_down, accel_final_driver_sim_1_left, accel_final_driver_sim_1_right,
       accel_final_driver_sim_1_up, accel_final_driver_sim_1_x_large, accel_final_driver_sim_1_x_medium,
       accel_final_driver_sim_1_x_small, accel_final_driver_sim_1_y_large, accel_final_driver_sim_1_y_medium,
       accel_final_driver_sim_1_y_small, HEX3;
  wire [1:0] SELECTOR;
  wire [3:0] HEX0, HEX1, HEX2;
  wire [7:0] HEX4, HEX5, sevenseg_direction_angle_logic_1_letter_output,
       sevenseg_direction_angle_logic_2_letter_output, sevenseg_direction_angle_logic_3_letter_output,
       sevenseg_direction_angle_logic_4_letter_output, X_SLIDER_out, Y_SLIDER_out, Z_SLIDER_out;
  wire [15:0] absolute_val_and_sign_1_value, absolute_val_and_sign_2_value, absolute_val_and_sign_3_value,
       accel_final_driver_sim_1_x_filtered, accel_final_driver_sim_1_y_filtered,
       accel_final_driver_sim_1_z_filtered, multiplexer_2_out;

  DipSwitch #(.number(2)) DipSwitch_1 (.sw1(SELECTOR[0]), .sw2(SELECTOR[1]));
  _7_Segment_Display u_7_segment_display_1 (
    .g(HEX5[6]), .f(HEX5[5]), .a(HEX5[0]), .b(HEX5[1]), .e(HEX5[4]), .d(HEX5[3]), .c(HEX5[2]));  // open: dp
  _7_Segment_Display u_7_segment_display_2 (
    .g(HEX4[6]), .f(HEX4[5]), .a(HEX4[0]), .b(HEX4[1]), .e(HEX4[4]), .d(HEX4[3]), .c(HEX4[2]));  // open: dp
  Slider X_SLIDER (.out(X_SLIDER_out));
  Slider Y_SLIDER (.out(Y_SLIDER_out));
  Slider Z_SLIDER (.out(Z_SLIDER_out));
  _7_Segment_Display u_7_segment_display_3 (.g(HEX3));  // open: f, a, b, e, d, c, dp
  Hex_Digit_Display hex_digit_display_1 (.value(HEX2));  // open: dp
  Hex_Digit_Display hex_digit_display_2 (.value(HEX1));  // open: dp
  Hex_Digit_Display hex_digit_display_3 (.value(HEX0));  // open: dp
  accel_final_driver_sim accel_final_driver_sim_1 (
    .x_value(X_SLIDER_out), .x_negative(X_NEGATIVE), .y_value(Y_SLIDER_out), .y_neg(Y_NEGATIVE),
    .z_value(Z_SLIDER_out), .z_neg(Z_NEGATIVE), .x_filtered(accel_final_driver_sim_1_x_filtered),
    .y_filtered(accel_final_driver_sim_1_y_filtered), .z_filtered(accel_final_driver_sim_1_z_filtered),
    .left(accel_final_driver_sim_1_left), .down(accel_final_driver_sim_1_down),
    .right(accel_final_driver_sim_1_right), .up(accel_final_driver_sim_1_up),
    .x_small(accel_final_driver_sim_1_x_small), .y_small(accel_final_driver_sim_1_y_small),
    .x_medium(accel_final_driver_sim_1_x_medium), .y_medium(accel_final_driver_sim_1_y_medium),
    .x_large(accel_final_driver_sim_1_x_large), .y_large(accel_final_driver_sim_1_y_large));  // open: x_offset, y_offset, z_offset
  absolute_val_and_sign absolute_val_and_sign_1 (
    .unfiltered(accel_final_driver_sim_1_x_filtered), .value(absolute_val_and_sign_1_value),
    .negative(absolute_val_and_sign_1_negative));
  absolute_val_and_sign absolute_val_and_sign_2 (
    .unfiltered(accel_final_driver_sim_1_y_filtered), .value(absolute_val_and_sign_2_value),
    .negative(absolute_val_and_sign_2_negative));
  absolute_val_and_sign absolute_val_and_sign_3 (
    .unfiltered(accel_final_driver_sim_1_z_filtered), .value(absolute_val_and_sign_3_value),
    .negative(absolute_val_and_sign_3_negative));
  Multiplexer #(.select(2)) multiplexer_1 (
    .in0(absolute_val_and_sign_1_negative), .in1(absolute_val_and_sign_2_negative),
    .in2(absolute_val_and_sign_3_negative), .in3(1'b0), .out(HEX3), .sel(SELECTOR));
  Multiplexer #(.select(2), .width(16)) multiplexer_2 (
    .in0(absolute_val_and_sign_1_value), .in1(absolute_val_and_sign_2_value),
    .in2(absolute_val_and_sign_3_value), .in3({16{1'b0}}), .out(multiplexer_2_out), .sel(SELECTOR));
  sevenseg_direction_angle_logic sevenseg_direction_angle_logic_1 (
    .L(accel_final_driver_sim_1_left), .R(accel_final_driver_sim_1_right),
    .letter_output(sevenseg_direction_angle_logic_1_letter_output));  // open: U, D, S, M
  sevenseg_direction_angle_logic sevenseg_direction_angle_logic_2 (
    .U(accel_final_driver_sim_1_up), .D(accel_final_driver_sim_1_down),
    .letter_output(sevenseg_direction_angle_logic_2_letter_output));  // open: L, R, S, M
  sevenseg_direction_angle_logic sevenseg_direction_angle_logic_3 (
    .L(accel_final_driver_sim_1_x_large), .S(accel_final_driver_sim_1_x_small),
    .M(accel_final_driver_sim_1_x_medium), .letter_output(sevenseg_direction_angle_logic_3_letter_output));  // open: R, U, D
  sevenseg_direction_angle_logic sevenseg_direction_angle_logic_4 (
    .L(accel_final_driver_sim_1_y_large), .S(accel_final_driver_sim_1_y_small),
    .M(accel_final_driver_sim_1_y_medium), .letter_output(sevenseg_direction_angle_logic_4_letter_output));  // open: R, U, D
  hex_to_decimal_sim hex_to_decimal_sim_1 (.VALUE(multiplexer_2_out), .hundreds(HEX2), .tens(HEX1), .ones(HEX0));
  Multiplexer #(.select(2), .width(8)) multiplexer_3 (
    .in0(sevenseg_direction_angle_logic_1_letter_output),
    .in1(sevenseg_direction_angle_logic_2_letter_output), .in2({8{1'b0}}), .in3({8{1'b0}}), .out(HEX4),
    .sel(SELECTOR));
  Multiplexer #(.select(2), .width(8)) multiplexer_4 (
    .in0(sevenseg_direction_angle_logic_3_letter_output),
    .in1(sevenseg_direction_angle_logic_4_letter_output), .in2({8{1'b0}}), .in3({8{1'b0}}), .out(HEX5),
    .sel(SELECTOR));

  // Notes on the sheet:
  //   OUTPUTS THE VALUES READ BY THE 3-AXES OF THE ACCELEROMETER (HEX0 - HEX3)
  //   OUTPUTS THE DIRECTION THAT THE BOARD IS TILTED (HEX4)
  //   LEFT(L), RIGHT(r), UP(U), DOWN(d)
  //   SMALL (S), MEDIUM (M), LARGE(L)
  //   X - AXIS : SELECTOR = 00
  //   Y - AXIS : SELECTOR = 01
  //   Z - AXIS : SELECTOR = 10
  //   ACCELEROMETER MAIN DRIVER SIMULATION
  //   OUTPUTS THE AMOUNT OF TILT OF THE BOARD (HEX5)
endmodule

module accel_final_driver (
  input  rst,
  input  miso,
  input  accel_input,
  input  enable_accel,
  input  [15:0] x_offset,
  input  [15:0] y_offset,
  input  [15:0] z_offset,
  output mosi,
  output sclk,
  output cs,
  output [15:0] x_filtered,
  output [15:0] y_filtered,
  output [15:0] z_filtered,
  output left,
  output down,
  output right,
  output up,
  output x_small,
  output y_small,
  output x_medium,
  output y_medium,
  output x_large,
  output y_large
);

  wire absolute_val_and_sign_1_negative, absolute_val_and_sign_2_negative, clock_1_out, comparator_1_gt,
       comparator_2_eq, comparator_2_lt, comparator_3_gt, comparator_4_eq, comparator_4_lt, comparator_6_gt,
       comparator_7_gt, comparator_8_gt, comparator_9_eq, comparator_9_lt, comparator_10_gt,
       comparator_11_eq, comparator_11_lt, d_ff_1_q, d_ff_2_q, d_ff_3_q, not_1_out, not_2_out, or_1_out,
       or_2_out, or_3_out, or_4_out, reset_logic_1_enable_out, reset_logic_1_reset_out,
       reset_logic_2_enable_out, reset_logic_2_reset_out, reset_logic_3_enable_out, reset_logic_3_reset_out;
  wire [15:0] absolute_val_and_sign_1_value, absolute_val_and_sign_2_value, multiplexer_1_out,
       multiplexer_2_out, multiplexer_3_out, signed_div_by_128_1_result, signed_div_by_128_2_result,
       signed_div_by_128_3_result, subtractor_1_out, subtractor_2_out, subtractor_3_out, x, y, z;

  Subtractor #(.width(16)) subtractor_1 (.a(x), .b(x_offset), .out(subtractor_1_out));  // open: bin, bout
  D_Flip_Flop d_ff_1 (
    .Q(d_ff_1_q), .preset(reset_logic_1_reset_out), .reset(reset_logic_1_enable_out));  // open: D, clk, Qn
  reset_logic reset_logic_1 (
    .reset(rst), .enable(enable_accel), .reset_out(reset_logic_1_reset_out),
    .enable_out(reset_logic_1_enable_out));
  Subtractor #(.width(16)) subtractor_2 (.a(y), .b(y_offset), .out(subtractor_2_out));  // open: bin, bout
  D_Flip_Flop d_ff_2 (
    .Q(d_ff_2_q), .preset(reset_logic_2_reset_out), .reset(reset_logic_2_enable_out));  // open: D, clk, Qn
  reset_logic reset_logic_2 (
    .reset(rst), .enable(enable_accel), .reset_out(reset_logic_2_reset_out),
    .enable_out(reset_logic_2_enable_out));
  Subtractor #(.width(16)) subtractor_3 (.a(z), .b(z_offset), .out(subtractor_3_out));  // open: bin, bout
  D_Flip_Flop d_ff_3 (
    .Q(d_ff_3_q), .preset(reset_logic_3_reset_out), .reset(reset_logic_3_enable_out));  // open: D, clk, Qn
  reset_logic reset_logic_3 (
    .reset(rst), .enable(enable_accel), .reset_out(reset_logic_3_reset_out),
    .enable_out(reset_logic_3_enable_out));
  absolute_val_and_sign absolute_val_and_sign_1 (
    .unfiltered(x_filtered), .value(absolute_val_and_sign_1_value),
    .negative(absolute_val_and_sign_1_negative));
  accel_driver_logisim accel_driver_logisim_1 (
    .rst(rst), .miso(miso), .accel_input(accel_input), .enable_accel(enable_accel), .mosi(mosi), .sclk(sclk),
    .cs(cs), .Accelerometer({z, y, x}));
  Multiplexer #(.width(16)) multiplexer_1 (
    .in0(subtractor_1_out), .in1({16{1'b0}}), .out(multiplexer_1_out), .sel(d_ff_1_q));
  Multiplexer #(.width(16)) multiplexer_2 (
    .in0(subtractor_2_out), .in1({16{1'b0}}), .out(multiplexer_2_out), .sel(d_ff_2_q));
  Multiplexer #(.width(16)) multiplexer_3 (
    .in0(subtractor_3_out), .in1({16{1'b0}}), .out(multiplexer_3_out), .sel(d_ff_3_q));
  Comparator #(.mode("unsigned"), .width(16)) comparator_1 (
    .a(absolute_val_and_sign_1_value), .b(16'ha), .gt(comparator_1_gt));  // open: eq, lt
  Comparator #(.mode("unsigned"), .width(16)) comparator_2 (
    .a(absolute_val_and_sign_1_value), .b(16'h28), .eq(comparator_2_eq), .lt(comparator_2_lt));  // open: gt
  Comparator #(.mode("unsigned"), .width(16)) comparator_3 (
    .a(absolute_val_and_sign_1_value), .b(16'h28), .gt(comparator_3_gt));  // open: eq, lt
  Comparator #(.mode("unsigned"), .width(16)) comparator_4 (
    .a(absolute_val_and_sign_1_value), .b(16'h46), .eq(comparator_4_eq), .lt(comparator_4_lt));  // open: gt
  Comparator #(.mode("unsigned"), .width(16)) comparator_5 (
    .a(absolute_val_and_sign_1_value), .b(16'h46), .gt(x_large));  // open: eq, lt
  Comparator #(.width(16)) comparator_6 (
    .a(absolute_val_and_sign_1_value), .b(16'ha), .gt(comparator_6_gt));  // open: eq, lt
  not not_1 (not_1_out, absolute_val_and_sign_1_negative);
  or or_1 (or_1_out, comparator_2_eq, comparator_2_lt);
  or or_2 (or_2_out, comparator_4_eq, comparator_4_lt);
  and and_1 (left, comparator_6_gt, not_1_out);
  and and_2 (right, comparator_6_gt, absolute_val_and_sign_1_negative);
  signed_div_by_128 signed_div_by_128_1 (.unfiltered(multiplexer_1_out), .result(signed_div_by_128_1_result));
  Clock #(.highDuration(125000), .lowDuration(125000)) clock_1 (.out(clock_1_out));
  signed_div_by_128 signed_div_by_128_2 (.unfiltered(multiplexer_2_out), .result(signed_div_by_128_2_result));
  signed_div_by_128 signed_div_by_128_3 (.unfiltered(multiplexer_3_out), .result(signed_div_by_128_3_result));
  and and_3 (x_small, comparator_1_gt, or_1_out);
  and and_4 (x_medium, comparator_3_gt, or_2_out);
  signed_fast_filter signed_fast_filter_1 (
    .unfiltered(signed_div_by_128_1_result), .clock(clock_1_out), .reset(rst), .filtered(x_filtered));
  signed_fast_filter signed_fast_filter_2 (
    .unfiltered(signed_div_by_128_2_result), .clock(clock_1_out), .reset(rst), .filtered(y_filtered));
  signed_fast_filter signed_fast_filter_3 (
    .unfiltered(signed_div_by_128_3_result), .clock(clock_1_out), .reset(rst), .filtered(z_filtered));
  absolute_val_and_sign absolute_val_and_sign_2 (
    .unfiltered(y_filtered), .value(absolute_val_and_sign_2_value),
    .negative(absolute_val_and_sign_2_negative));
  Comparator #(.width(16)) comparator_7 (
    .a(absolute_val_and_sign_2_value), .b(16'ha), .gt(comparator_7_gt));  // open: eq, lt
  Comparator #(.mode("unsigned"), .width(16)) comparator_8 (
    .a(absolute_val_and_sign_2_value), .b(16'ha), .gt(comparator_8_gt));  // open: eq, lt
  Comparator #(.mode("unsigned"), .width(16)) comparator_9 (
    .a(absolute_val_and_sign_2_value), .b(16'h28), .eq(comparator_9_eq), .lt(comparator_9_lt));  // open: gt
  Comparator #(.mode("unsigned"), .width(16)) comparator_10 (
    .a(absolute_val_and_sign_2_value), .b(16'h28), .gt(comparator_10_gt));  // open: eq, lt
  Comparator #(.mode("unsigned"), .width(16)) comparator_11 (
    .a(absolute_val_and_sign_2_value), .b(16'h46), .eq(comparator_11_eq), .lt(comparator_11_lt));  // open: gt
  Comparator #(.mode("unsigned"), .width(16)) comparator_12 (
    .a(absolute_val_and_sign_2_value), .b(16'h46), .gt(y_large));  // open: eq, lt
  and and_5 (down, comparator_7_gt, not_2_out);
  not not_2 (not_2_out, absolute_val_and_sign_2_negative);
  and and_6 (up, comparator_7_gt, absolute_val_and_sign_2_negative);
  or or_3 (or_3_out, comparator_9_eq, comparator_9_lt);
  or or_4 (or_4_out, comparator_11_eq, comparator_11_lt);
  and and_7 (y_small, comparator_8_gt, or_3_out);
  and and_8 (y_medium, comparator_10_gt, or_4_out);

  // Other names for the same wires on the sheet: enable = enable_accel; reset = rst;
  //   x_filtered_tunnel[15:0] = x_filtered; y_filtered_tunnel[15:0] = y_filtered;
  //   z_filtered_tunnel[15:0] = z_filtered

  // Notes on the sheet:
  //   ACCELEROMETER MAIN DRIVER
  //   THE DIRECTION OF TILT AND THE STEEPNESS
  //   X - AXIS : ACCELEROMETER BITS 0 TO 15
  //   Y - AXIS : ACCELEROMETER BITS 16 TO 31
  //   Z - AXIS : ACCELEROMETER BITS 32 TO 47
  //   OUTPUTS THE VALUES READ BY THE 3-AXES OF THE ACCELEROMETER 
  //   GSENSOR/PIN0 -> MOSI
  //   GSENSOR/PIN1 -> MISO
  //   GSENSOR/PIN2 -> SCLK
  //   GSENSOR/PIN3 -> CS
  //   Tested functional at 1MHz. DE10-Lite. 2024.05.24
  //   GSENSOR/PIN4 -> ACCEL_INPUT
  //   PIN MAPPING FOR TERASICDE10LITE_GSENSOR.xml
endmodule

module accel_final_driver_sim (
  input  [7:0] x_value,
  input  x_negative,
  input  [7:0] y_value,
  input  y_neg,
  input  [7:0] z_value,
  input  z_neg,
  input  [15:0] x_offset,
  input  [15:0] y_offset,
  input  [15:0] z_offset,
  output [15:0] x_filtered,
  output [15:0] y_filtered,
  output [15:0] z_filtered,
  output left,
  output down,
  output right,
  output up,
  output x_small,
  output y_small,
  output x_medium,
  output y_medium,
  output x_large,
  output y_large
);

  wire absolute_val_and_sign_1_negative, absolute_val_and_sign_2_negative, clock_1_out, comparator_1_gt,
       comparator_2_eq, comparator_2_lt, comparator_3_gt, comparator_4_eq, comparator_4_lt, comparator_6_gt,
       comparator_7_gt, comparator_8_gt, comparator_9_eq, comparator_9_lt, comparator_10_gt,
       comparator_11_eq, comparator_11_lt, d_ff_1_q, d_ff_2_q, d_ff_3_q, enable, not_1_out, not_2_out,
       or_1_out, or_2_out, or_3_out, or_4_out, reset, reset_logic_1_enable_out, reset_logic_1_reset_out,
       reset_logic_2_enable_out, reset_logic_2_reset_out, reset_logic_3_enable_out, reset_logic_3_reset_out;
  wire [15:0] absolute_val_and_sign_1_value, absolute_val_and_sign_2_value, multiplexer_1_out,
       multiplexer_2_out, multiplexer_3_out, signed_div_by_128_sim_1_result, signed_div_by_128_sim_2_result,
       signed_div_by_128_sim_3_result, subtractor_1_out, subtractor_2_out, subtractor_3_out, x, y, z;

  assign x = {{8{1'b0}}, x_value};  // Bit_Extender bit_extender_1
  assign y = {{8{1'b0}}, y_value};  // Bit_Extender bit_extender_2
  assign z = {{8{1'b0}}, z_value};  // Bit_Extender bit_extender_3
  Subtractor #(.width(16)) subtractor_1 (.a(x), .b(x_offset), .out(subtractor_1_out));  // open: bin, bout
  D_Flip_Flop d_ff_1 (
    .Q(d_ff_1_q), .preset(reset_logic_1_reset_out), .reset(reset_logic_1_enable_out));  // open: D, clk, Qn
  reset_logic reset_logic_1 (
    .reset(reset), .enable(enable), .reset_out(reset_logic_1_reset_out), .enable_out(reset_logic_1_enable_out));
  Subtractor #(.width(16)) subtractor_2 (.a(y), .b(y_offset), .out(subtractor_2_out));  // open: bin, bout
  D_Flip_Flop d_ff_2 (
    .Q(d_ff_2_q), .preset(reset_logic_2_reset_out), .reset(reset_logic_2_enable_out));  // open: D, clk, Qn
  reset_logic reset_logic_2 (
    .reset(reset), .enable(enable), .reset_out(reset_logic_2_reset_out), .enable_out(reset_logic_2_enable_out));
  Subtractor #(.width(16)) subtractor_3 (.a(z), .b(z_offset), .out(subtractor_3_out));  // open: bin, bout
  D_Flip_Flop d_ff_3 (
    .Q(d_ff_3_q), .preset(reset_logic_3_reset_out), .reset(reset_logic_3_enable_out));  // open: D, clk, Qn
  reset_logic reset_logic_3 (
    .reset(reset), .enable(enable), .reset_out(reset_logic_3_reset_out), .enable_out(reset_logic_3_enable_out));
  absolute_val_and_sign absolute_val_and_sign_1 (
    .unfiltered(x_filtered), .value(absolute_val_and_sign_1_value),
    .negative(absolute_val_and_sign_1_negative));
  Multiplexer #(.width(16)) multiplexer_1 (
    .in0(subtractor_1_out), .in1({16{1'b0}}), .out(multiplexer_1_out), .sel(d_ff_1_q));
  Multiplexer #(.width(16)) multiplexer_2 (
    .in0(subtractor_2_out), .in1({16{1'b0}}), .out(multiplexer_2_out), .sel(d_ff_2_q));
  Multiplexer #(.width(16)) multiplexer_3 (
    .in0(subtractor_3_out), .in1({16{1'b0}}), .out(multiplexer_3_out), .sel(d_ff_3_q));
  Comparator #(.mode("unsigned"), .width(16)) comparator_1 (
    .a(absolute_val_and_sign_1_value), .b(16'ha), .gt(comparator_1_gt));  // open: eq, lt
  Comparator #(.mode("unsigned"), .width(16)) comparator_2 (
    .a(absolute_val_and_sign_1_value), .b(16'h28), .eq(comparator_2_eq), .lt(comparator_2_lt));  // open: gt
  Comparator #(.mode("unsigned"), .width(16)) comparator_3 (
    .a(absolute_val_and_sign_1_value), .b(16'h28), .gt(comparator_3_gt));  // open: eq, lt
  Comparator #(.mode("unsigned"), .width(16)) comparator_4 (
    .a(absolute_val_and_sign_1_value), .b(16'h46), .eq(comparator_4_eq), .lt(comparator_4_lt));  // open: gt
  Comparator #(.mode("unsigned"), .width(16)) comparator_5 (
    .a(absolute_val_and_sign_1_value), .b(16'h46), .gt(x_large));  // open: eq, lt
  Comparator #(.width(16)) comparator_6 (
    .a(absolute_val_and_sign_1_value), .b(16'ha), .gt(comparator_6_gt));  // open: eq, lt
  not not_1 (not_1_out, absolute_val_and_sign_1_negative);
  or or_1 (or_1_out, comparator_2_eq, comparator_2_lt);
  or or_2 (or_2_out, comparator_4_eq, comparator_4_lt);
  and and_1 (left, comparator_6_gt, not_1_out);
  and and_2 (right, comparator_6_gt, absolute_val_and_sign_1_negative);
  signed_div_by_128_sim signed_div_by_128_sim_1 (
    .value_to_div(multiplexer_1_out), .negative(x_negative), .result(signed_div_by_128_sim_1_result));
  Clock clock_1 (.out(clock_1_out));
  and and_3 (x_small, comparator_1_gt, or_1_out);
  and and_4 (x_medium, comparator_3_gt, or_2_out);
  signed_div_by_128_sim signed_div_by_128_sim_2 (
    .value_to_div(multiplexer_2_out), .negative(y_neg), .result(signed_div_by_128_sim_2_result));
  signed_div_by_128_sim signed_div_by_128_sim_3 (
    .value_to_div(multiplexer_3_out), .negative(z_neg), .result(signed_div_by_128_sim_3_result));
  signed_fast_filter_sim signed_fast_filter_sim_1 (
    .unfiltered(signed_div_by_128_sim_1_result), .clock(clock_1_out), .reset(reset), .filtered(x_filtered));
  signed_fast_filter_sim signed_fast_filter_sim_2 (
    .unfiltered(signed_div_by_128_sim_2_result), .clock(clock_1_out), .reset(reset), .filtered(y_filtered));
  signed_fast_filter_sim signed_fast_filter_sim_3 (
    .unfiltered(signed_div_by_128_sim_3_result), .clock(clock_1_out), .reset(reset), .filtered(z_filtered));
  absolute_val_and_sign absolute_val_and_sign_2 (
    .unfiltered(y_filtered), .value(absolute_val_and_sign_2_value),
    .negative(absolute_val_and_sign_2_negative));
  Comparator #(.width(16)) comparator_7 (
    .a(absolute_val_and_sign_2_value), .b(16'ha), .gt(comparator_7_gt));  // open: eq, lt
  Comparator #(.mode("unsigned"), .width(16)) comparator_8 (
    .a(absolute_val_and_sign_2_value), .b(16'ha), .gt(comparator_8_gt));  // open: eq, lt
  Comparator #(.mode("unsigned"), .width(16)) comparator_9 (
    .a(absolute_val_and_sign_2_value), .b(16'h28), .eq(comparator_9_eq), .lt(comparator_9_lt));  // open: gt
  Comparator #(.mode("unsigned"), .width(16)) comparator_10 (
    .a(absolute_val_and_sign_2_value), .b(16'h28), .gt(comparator_10_gt));  // open: eq, lt
  Comparator #(.mode("unsigned"), .width(16)) comparator_11 (
    .a(absolute_val_and_sign_2_value), .b(16'h46), .eq(comparator_11_eq), .lt(comparator_11_lt));  // open: gt
  Comparator #(.mode("unsigned"), .width(16)) comparator_12 (
    .a(absolute_val_and_sign_2_value), .b(16'h46), .gt(y_large));  // open: eq, lt
  and and_5 (down, comparator_7_gt, not_2_out);
  not not_2 (not_2_out, absolute_val_and_sign_2_negative);
  and and_6 (up, comparator_7_gt, absolute_val_and_sign_2_negative);
  or or_3 (or_3_out, comparator_9_eq, comparator_9_lt);
  or or_4 (or_4_out, comparator_11_eq, comparator_11_lt);
  and and_7 (y_small, comparator_8_gt, or_3_out);
  and and_8 (y_medium, comparator_10_gt, or_4_out);

  // Other names for the same wires on the sheet: x_filtered_tunnel[15:0] = x_filtered; x_neg = x_negative;
  //   y_filtered_tunnel[15:0] = y_filtered; z_filtered_tunnel[15:0] = z_filtered
endmodule

module calibration_tb (
  input  rst,
  input  miso,
  input  accel_input,
  output mosi,
  output sclk,
  output cs
);

  wire absolute_val_and_sign_1_negative, absolute_val_and_sign_2_negative, absolute_val_and_sign_3_negative,
       multiplexer_1_out;
  wire [1:0] SELECTOR;
  wire [3:0] DipSwitch_1_sw3, DipSwitch_1_sw7, hex_to_decimal_16_bits_1_hundreds,
       hex_to_decimal_16_bits_1_ones, hex_to_decimal_16_bits_1_tens;
  wire [15:0] absolute_val_and_sign_1_value, absolute_val_and_sign_2_value, absolute_val_and_sign_3_value,
       calibration_1_x_filtered, calibration_1_y_filtered, calibration_1_z_filtered, multiplexer_2_out;

  DipSwitch #(.number(10)) DipSwitch_1 (
    .sw1(SELECTOR[0]), .sw2(SELECTOR[1]), .sw3(DipSwitch_1_sw3[0]), .sw4(DipSwitch_1_sw3[1]),
    .sw5(DipSwitch_1_sw3[2]), .sw6(DipSwitch_1_sw3[3]), .sw7(DipSwitch_1_sw7[0]), .sw8(DipSwitch_1_sw7[1]),
    .sw9(DipSwitch_1_sw7[2]), .sw10(DipSwitch_1_sw7[3]));
  calibration calibration_1 (
    .rst(rst), .miso(miso), .accel_input(accel_input), .enable_accel(1'b1),
    .x_offset({{8{1'b0}}, DipSwitch_1_sw7, DipSwitch_1_sw3}),
    .y_offset({{8{1'b0}}, DipSwitch_1_sw7, DipSwitch_1_sw3}),
    .z_offset({{8{1'b0}}, DipSwitch_1_sw7, DipSwitch_1_sw3}), .mosi(mosi), .sclk(sclk), .cs(cs),
    .x_filtered(calibration_1_x_filtered), .y_filtered(calibration_1_y_filtered),
    .z_filtered(calibration_1_z_filtered));
  absolute_val_and_sign absolute_val_and_sign_1 (
    .unfiltered(calibration_1_x_filtered), .value(absolute_val_and_sign_1_value),
    .negative(absolute_val_and_sign_1_negative));
  absolute_val_and_sign absolute_val_and_sign_2 (
    .unfiltered(calibration_1_y_filtered), .value(absolute_val_and_sign_2_value),
    .negative(absolute_val_and_sign_2_negative));
  absolute_val_and_sign absolute_val_and_sign_3 (
    .unfiltered(calibration_1_z_filtered), .value(absolute_val_and_sign_3_value),
    .negative(absolute_val_and_sign_3_negative));
  Multiplexer #(.select(2)) multiplexer_1 (
    .in0(absolute_val_and_sign_1_negative), .in1(absolute_val_and_sign_2_negative),
    .in2(absolute_val_and_sign_3_negative), .in3(1'b0), .out(multiplexer_1_out), .sel(SELECTOR));
  sign_hex_output HEX3 (.negative(multiplexer_1_out));
  Multiplexer #(.select(2), .width(16)) multiplexer_2 (
    .in0(absolute_val_and_sign_1_value), .in1(absolute_val_and_sign_2_value),
    .in2(absolute_val_and_sign_3_value), .in3({16{1'b0}}), .out(multiplexer_2_out), .sel(SELECTOR));
  hex_to_decimal_16_bits hex_to_decimal_16_bits_1 (
    .val(multiplexer_2_out), .hundreds(hex_to_decimal_16_bits_1_hundreds),
    .tens(hex_to_decimal_16_bits_1_tens), .ones(hex_to_decimal_16_bits_1_ones));
  sevenseg_numbers_output HEX2 (.input_bus(hex_to_decimal_16_bits_1_hundreds), .decimal(1'b1));
  sevenseg_numbers_output HEX1 (.input_bus(hex_to_decimal_16_bits_1_tens));  // open: decimal
  sevenseg_numbers_output HEX0 (.input_bus(hex_to_decimal_16_bits_1_ones));  // open: decimal
  sevenseg_numbers_output HEX4 (.input_bus(DipSwitch_1_sw3));  // open: decimal
  sevenseg_numbers_output HEX5 (.input_bus(DipSwitch_1_sw7));  // open: decimal
endmodule

module calibration (
  input  rst,
  input  miso,
  input  accel_input,
  input  enable_accel,
  input  [15:0] x_offset,
  input  [15:0] y_offset,
  input  [15:0] z_offset,
  output mosi,
  output sclk,
  output cs,
  output [15:0] x_filtered,
  output [15:0] y_filtered,
  output [15:0] z_filtered
);

  wire clock_1_out, d_ff_1_q, d_ff_2_q, d_ff_3_q, reset_logic_1_enable_out, reset_logic_1_reset_out,
       reset_logic_2_enable_out, reset_logic_2_reset_out, reset_logic_3_enable_out, reset_logic_3_reset_out;
  wire [15:0] multiplexer_1_out, multiplexer_2_out, multiplexer_3_out, signed_div_by_128_1_result,
       signed_div_by_128_2_result, signed_div_by_128_3_result, subtractor_1_out, subtractor_2_out,
       subtractor_3_out, x, y, z;

  Subtractor #(.width(16)) subtractor_1 (.a(x), .b(x_offset), .out(subtractor_1_out));  // open: bin, bout
  D_Flip_Flop d_ff_1 (
    .Q(d_ff_1_q), .preset(reset_logic_1_reset_out), .reset(reset_logic_1_enable_out));  // open: D, clk, Qn
  reset_logic reset_logic_1 (
    .reset(rst), .enable(enable_accel), .reset_out(reset_logic_1_reset_out),
    .enable_out(reset_logic_1_enable_out));
  Subtractor #(.width(16)) subtractor_2 (.a(y), .b(y_offset), .out(subtractor_2_out));  // open: bin, bout
  D_Flip_Flop d_ff_2 (
    .Q(d_ff_2_q), .preset(reset_logic_2_reset_out), .reset(reset_logic_2_enable_out));  // open: D, clk, Qn
  reset_logic reset_logic_2 (
    .reset(rst), .enable(enable_accel), .reset_out(reset_logic_2_reset_out),
    .enable_out(reset_logic_2_enable_out));
  Subtractor #(.width(16)) subtractor_3 (.a(z), .b(z_offset), .out(subtractor_3_out));  // open: bin, bout
  D_Flip_Flop d_ff_3 (
    .Q(d_ff_3_q), .preset(reset_logic_3_reset_out), .reset(reset_logic_3_enable_out));  // open: D, clk, Qn
  reset_logic reset_logic_3 (
    .reset(rst), .enable(enable_accel), .reset_out(reset_logic_3_reset_out),
    .enable_out(reset_logic_3_enable_out));
  accel_driver_logisim accel_driver_logisim_1 (
    .rst(rst), .miso(miso), .accel_input(accel_input), .enable_accel(enable_accel), .mosi(mosi), .sclk(sclk),
    .cs(cs), .Accelerometer({z, y, x}));
  Multiplexer #(.width(16)) multiplexer_1 (
    .in0(subtractor_1_out), .in1({16{1'b0}}), .out(multiplexer_1_out), .sel(d_ff_1_q));
  Multiplexer #(.width(16)) multiplexer_2 (
    .in0(subtractor_2_out), .in1({16{1'b0}}), .out(multiplexer_2_out), .sel(d_ff_2_q));
  Multiplexer #(.width(16)) multiplexer_3 (
    .in0(subtractor_3_out), .in1({16{1'b0}}), .out(multiplexer_3_out), .sel(d_ff_3_q));
  signed_div_by_128 signed_div_by_128_1 (.unfiltered(multiplexer_1_out), .result(signed_div_by_128_1_result));
  Clock #(.highDuration(125000), .lowDuration(125000)) clock_1 (.out(clock_1_out));
  signed_div_by_128 signed_div_by_128_2 (.unfiltered(multiplexer_2_out), .result(signed_div_by_128_2_result));
  signed_div_by_128 signed_div_by_128_3 (.unfiltered(multiplexer_3_out), .result(signed_div_by_128_3_result));
  signed_fast_filter signed_fast_filter_1 (
    .unfiltered(signed_div_by_128_1_result), .clock(clock_1_out), .reset(rst), .filtered(x_filtered));
  signed_fast_filter signed_fast_filter_2 (
    .unfiltered(signed_div_by_128_2_result), .clock(clock_1_out), .reset(rst), .filtered(y_filtered));
  signed_fast_filter signed_fast_filter_3 (
    .unfiltered(signed_div_by_128_3_result), .clock(clock_1_out), .reset(rst), .filtered(z_filtered));

  // Other names for the same wires on the sheet: enable = enable_accel; reset = rst;
  //   x_filtered_tunnel[15:0] = x_filtered; y_filtered_tunnel[15:0] = y_filtered;
  //   z_filtered_tunnel[15:0] = z_filtered

  // Notes on the sheet:
  //   ACCELEROMETER MAIN DRIVER
  //   X - AXIS : ACCELEROMETER BITS 0 TO 15
  //   Y - AXIS : ACCELEROMETER BITS 16 TO 31
  //   Z - AXIS : ACCELEROMETER BITS 32 TO 47
  //   OUTPUTS THE VALUES READ BY THE 3-AXES OF THE ACCELEROMETER 
  //   GSENSOR/PIN0 -> MOSI
  //   GSENSOR/PIN1 -> MISO
  //   GSENSOR/PIN2 -> SCLK
  //   GSENSOR/PIN3 -> CS
  //   Tested functional at 1MHz. DE10-Lite. 2024.05.24
  //   GSENSOR/PIN4 -> ACCEL_INPUT
  //   PIN MAPPING FOR TERASICDE10LITE_GSENSOR.xml
endmodule

module error_calc_tb (
  input  rst,
  input  miso,
  input  accel_input,
  input  enable_accel,
  input  selector,
  output mosi,
  output sclk,
  output cs,
  output led,
  output y
);

  wire and_1_out, clock_1_out, not_1_out, or_1_out;
  wire [3:0] register_1_q, register_1_q_2, register_1_q_3, register_1_q_4;
  wire [7:0] counter_1_q;
  wire [15:0] absolute_val_and_sign_1_value, adder_1_out, multiplexer_1_out, multiplier_1_out, x, y_t;

  or or_1 (or_1_out, led, rst);
  Multiplexer #(.width(16)) multiplexer_1 (.in0(x), .in1(y_t), .out(multiplexer_1_out), .sel(selector));
  accel_final_driver accel_final_driver_1 (
    .rst(or_1_out), .miso(miso), .accel_input(accel_input), .enable_accel(enable_accel), .x_offset(16'h3e),
    .y_offset(16'h39), .z_offset(16'h3a), .mosi(mosi), .sclk(sclk), .cs(cs), .x_filtered(x), .y_filtered(y_t));  // open: z_filtered, left, down, right, up, x_small, y_small, x_medium, y_medium, x_large, y_large
  Multiplier #(.width(16)) multiplier_1 (
    .a(absolute_val_and_sign_1_value), .b(absolute_val_and_sign_1_value), .out(multiplier_1_out));  // open: cin, cout
  not not_1 (not_1_out, led);
  and and_1 (and_1_out, not_1_out, enable_accel);
  // Probe on multiplier_1_out
  Adder #(.width(16)) adder_1 (
    .a(multiplier_1_out), .b({register_1_q_4, register_1_q_3, register_1_q_2, register_1_q}),
    .out(adder_1_out));  // open: cin, cout
  Clock #(.highDuration(125000), .lowDuration(125000)) clock_1 (.out(clock_1_out));
  absolute_val_and_sign absolute_val_and_sign_1 (
    .unfiltered(multiplexer_1_out), .value(absolute_val_and_sign_1_value));  // open: negative
  Counter counter_1 (.clr(rst), .count(and_1_out), .clk(clock_1_out), .Q(counter_1_q));  // open: load, up, D, carry
  Register #(.width(16)) register_1 (
    .D(adder_1_out), .en(1'b1), .clk(clock_1_out),
    .Q({register_1_q_4, register_1_q_3, register_1_q_2, register_1_q}), .clr(rst));
  Comparator comparator_1 (.a(counter_1_q), .b(8'h65), .eq(led));  // open: gt, lt
  sevenseg_numbers_output sevenseg_numbers_output_1 (.input_bus(register_1_q));  // open: decimal
  sevenseg_numbers_output sevenseg_numbers_output_2 (.input_bus(register_1_q_2));  // open: decimal
  sevenseg_numbers_output sevenseg_numbers_output_3 (.input_bus(register_1_q_3));  // open: decimal
  sevenseg_numbers_output sevenseg_numbers_output_4 (.input_bus(register_1_q_4));  // open: decimal

  assign y = selector;
endmodule

module accel_raw_tb (
  input  rst,
  input  miso,
  input  accel_input,
  input  enable_accel,
  output mosi,
  output sclk,
  output cs
);

  wire [1:0] SELECTOR;
  wire [3:0] multiplexer_1_out, multiplexer_2_out, multiplexer_3_out, multiplexer_4_out;
  wire [47:0] accel_driver_logisim_1_accelerometer;

  DipSwitch #(.number(2)) AXIS_SELECTOR (.sw1(SELECTOR[0]), .sw2(SELECTOR[1]));
  accel_driver_logisim accel_driver_logisim_1 (
    .rst(rst), .miso(miso), .accel_input(accel_input), .enable_accel(enable_accel), .mosi(mosi), .sclk(sclk),
    .cs(cs), .Accelerometer(accel_driver_logisim_1_accelerometer));
  Multiplexer #(.select(2), .width(4)) multiplexer_1 (
    .in0(accel_driver_logisim_1_accelerometer[3:0]), .in1(accel_driver_logisim_1_accelerometer[19:16]),
    .in2(accel_driver_logisim_1_accelerometer[35:32]), .out(multiplexer_1_out), .sel(SELECTOR));  // open: in3
  sevenseg_numbers_output HEX0 (.input_bus(multiplexer_1_out));  // open: decimal
  Multiplexer #(.select(2), .width(4)) multiplexer_2 (
    .in0(accel_driver_logisim_1_accelerometer[7:4]), .in1(accel_driver_logisim_1_accelerometer[23:20]),
    .in2(accel_driver_logisim_1_accelerometer[39:36]), .out(multiplexer_2_out), .sel(SELECTOR));  // open: in3
  sevenseg_numbers_output HEX1 (.input_bus(multiplexer_2_out));  // open: decimal
  Multiplexer #(.select(2), .width(4)) multiplexer_3 (
    .in0(accel_driver_logisim_1_accelerometer[11:8]), .in1(accel_driver_logisim_1_accelerometer[27:24]),
    .in2(accel_driver_logisim_1_accelerometer[43:40]), .out(multiplexer_3_out), .sel(SELECTOR));  // open: in3
  sevenseg_numbers_output HEX2 (.input_bus(multiplexer_3_out));  // open: decimal
  Multiplexer #(.select(2), .width(4)) multiplexer_4 (
    .in0(accel_driver_logisim_1_accelerometer[15:12]), .in1(accel_driver_logisim_1_accelerometer[31:28]),
    .in2(accel_driver_logisim_1_accelerometer[47:44]), .out(multiplexer_4_out), .sel(SELECTOR));  // open: in3
  sevenseg_numbers_output HEX3 (.input_bus(multiplexer_4_out));  // open: decimal

  // Notes on the sheet:
  //   ACCEL_VALUES_RAW
  //   00: X-AXIS
  //   01: Y-AXIS
  //   10: Z-AXIS
  //   THE "AXES_SELECTOR" ALLOWS US TO SWITCH BETWEEN THE DIFFERENT AXES
  //   OUTPUTS ON 4 HEXES THE VALUES OF THE ACCELERATION ON THE DIFFERENT AXES OF THE ACCELEROMETER
endmodule

module signed_fast_filter (
  input  [15:0] unfiltered,
  input  clock,
  input  reset,
  output [15:0] filtered
);

  wire absolute_val_and_sign_1_negative, fast, not_1_out, not_2_out, not_3_out, not_4_out, not_5_out;
  wire [15:0] absolute_val_and_sign_1_value, absolute_val_and_sign_2_value, adder_1_out, adder_2_out,
       adder_3_out, adder_4_out, adder_5_out, adder_6_out, adder_7_out, adder_8_out, adder_9_out,
       divide_two_num_1_final_answer_sixteen_bits, multiplexer_1_out, multiplexer_2_out, multiplexer_3_out,
       multiplexer_4_out, multiplexer_5_out, multiplexer_6_out, multiplexer_7_out, multiplexer_8_out,
       multiplexer_9_out, out1, out2, out3, out4, out5, out6, out7, out8, out9, out10, subtractor_1_out,
       twos_complement_1_absolute_val;

  Register #(.width(16)) register_1 (.D(unfiltered), .en(1'b1), .clk(clock), .Q(out1), .clr(reset));
  Register #(.width(16)) register_2 (.D(multiplexer_1_out), .en(1'b1), .clk(not_1_out), .Q(out6), .clr(reset));
  Multiplexer #(.width(16)) multiplexer_1 (.in0(out5), .in1(unfiltered), .out(multiplexer_1_out), .sel(fast));
  not not_1 (not_1_out, clock);
  Adder #(.width(16)) adder_1 (.a(out1), .b(out2), .out(adder_1_out));  // open: cin, cout
  Adder #(.width(16)) adder_2 (.a(adder_9_out), .b(out7), .out(adder_2_out));  // open: cin, cout
  Register #(.width(16)) register_3 (.D(multiplexer_2_out), .en(1'b1), .clk(not_2_out), .Q(out2), .clr(reset));
  Multiplexer #(.width(16)) multiplexer_2 (.in0(out1), .in1(unfiltered), .out(multiplexer_2_out), .sel(fast));
  not not_2 (not_2_out, clock);
  Register #(.width(16)) register_4 (.D(multiplexer_3_out), .en(1'b1), .clk(clock), .Q(out7), .clr(reset));
  Multiplexer #(.width(16)) multiplexer_3 (.in0(out6), .in1(unfiltered), .out(multiplexer_3_out), .sel(fast));
  absolute_val_and_sign absolute_val_and_sign_1 (
    .unfiltered(adder_8_out), .value(absolute_val_and_sign_1_value),
    .negative(absolute_val_and_sign_1_negative));
  Adder #(.width(16)) adder_3 (.a(adder_1_out), .b(out3), .out(adder_3_out));  // open: cin, cout
  Adder #(.width(16)) adder_4 (.a(adder_2_out), .b(out8), .out(adder_4_out));  // open: cin, cout
  Adder #(.width(16)) adder_5 (.a(adder_3_out), .b(out4), .out(adder_5_out));  // open: cin, cout
  Adder #(.width(16)) adder_6 (.a(adder_4_out), .b(out9), .out(adder_6_out));  // open: cin, cout
  Multiplexer #(.width(16)) multiplexer_4 (.in0(out2), .in1(unfiltered), .out(multiplexer_4_out), .sel(fast));
  Multiplexer #(.width(16)) multiplexer_5 (.in0(out7), .in1(unfiltered), .out(multiplexer_5_out), .sel(fast));
  Register #(.width(16)) register_5 (.D(multiplexer_4_out), .en(1'b1), .clk(clock), .Q(out3), .clr(reset));
  Register #(.width(16)) register_6 (.D(multiplexer_5_out), .en(1'b1), .clk(not_3_out), .Q(out8), .clr(reset));
  not not_3 (not_3_out, clock);
  Adder #(.width(16)) adder_7 (.a(adder_5_out), .b(out5), .out(adder_7_out));  // open: cin, cout
  Adder #(.width(16)) adder_8 (.a(adder_6_out), .b(out10), .out(adder_8_out));  // open: cin, cout
  Subtractor #(.width(16)) subtractor_1 (.a(out1), .b(out2), .out(subtractor_1_out));  // open: bin, bout
  divide_two_num divide_two_num_1 (
    .val(absolute_val_and_sign_1_value), .val2(16'hccd),
    .final_answer_sixteen_bits(divide_two_num_1_final_answer_sixteen_bits));  // open: final_answer
  Adder #(.width(16)) adder_9 (.a(adder_7_out), .b(out6), .out(adder_9_out));  // open: cin, cout
  Register #(.width(16)) register_7 (.D(multiplexer_6_out), .en(1'b1), .clk(not_4_out), .Q(out4), .clr(reset));
  Multiplexer #(.width(16)) multiplexer_6 (.in0(out3), .in1(unfiltered), .out(multiplexer_6_out), .sel(fast));
  not not_4 (not_4_out, clock);
  Register #(.width(16)) register_8 (.D(multiplexer_7_out), .en(1'b1), .clk(clock), .Q(out9), .clr(reset));
  Multiplexer #(.width(16)) multiplexer_7 (.in0(out8), .in1(unfiltered), .out(multiplexer_7_out), .sel(fast));
  absolute_val_and_sign absolute_val_and_sign_2 (
    .unfiltered(subtractor_1_out), .value(absolute_val_and_sign_2_value));  // open: negative
  Comparator #(.mode("unsigned"), .width(16)) comparator_1 (
    .a(absolute_val_and_sign_2_value), .b(16'ha), .gt(fast));  // open: eq, lt
  twos_complement twos_complement_1 (
    .negative_number(divide_two_num_1_final_answer_sixteen_bits),
    .absolute_val(twos_complement_1_absolute_val));
  Register #(.width(16)) register_9 (.D(multiplexer_8_out), .en(1'b1), .clk(clock), .Q(out5), .clr(reset));
  Multiplexer #(.width(16)) multiplexer_8 (.in0(out4), .in1(unfiltered), .out(multiplexer_8_out), .sel(fast));
  Register #(.width(16)) register_10 (.D(multiplexer_9_out), .en(1'b1), .clk(not_5_out), .Q(out10), .clr(reset));
  Multiplexer #(.width(16)) multiplexer_9 (.in0(out9), .in1(unfiltered), .out(multiplexer_9_out), .sel(fast));
  not not_5 (not_5_out, clock);
  Multiplexer #(.width(16)) multiplexer_10 (
    .in0(divide_two_num_1_final_answer_sixteen_bits), .in1(twos_complement_1_absolute_val), .out(filtered),
    .sel(absolute_val_and_sign_1_negative));

  // Other names for the same wires on the sheet: value[15:0] = unfiltered
endmodule

module signed_fast_filter_sim (
  input  [15:0] unfiltered,
  input  clock,
  input  reset,
  output [15:0] filtered
);

  wire fast, not_1_out, not_2_out, not_3_out, not_4_out, not_5_out;
  wire [15:0] absolute_val_and_sign_2_value, adder_1_out, adder_2_out, adder_3_out, adder_4_out, adder_5_out,
       adder_6_out, adder_7_out, adder_8_out, adder_9_out, multiplexer_1_out, multiplexer_2_out,
       multiplexer_3_out, multiplexer_4_out, multiplexer_5_out, multiplexer_6_out, multiplexer_7_out,
       multiplexer_8_out, multiplexer_9_out, out1, out2, out3, out4, out5, out6, out7, out8, out9, out10,
       subtractor_1_out;

  Register #(.width(16)) register_1 (.D(unfiltered), .en(1'b1), .clk(clock), .Q(out1), .clr(reset));
  Register #(.width(16)) register_2 (.D(multiplexer_1_out), .en(1'b1), .clk(not_1_out), .Q(out6), .clr(reset));
  Multiplexer #(.width(16)) multiplexer_1 (.in0(out5), .in1(unfiltered), .out(multiplexer_1_out), .sel(fast));
  not not_1 (not_1_out, clock);
  Adder #(.width(16)) adder_1 (.a(out1), .b(out2), .out(adder_1_out));  // open: cin, cout
  Adder #(.width(16)) adder_2 (.a(adder_9_out), .b(out7), .out(adder_2_out));  // open: cin, cout
  Register #(.width(16)) register_3 (.D(multiplexer_2_out), .en(1'b1), .clk(not_2_out), .Q(out2), .clr(reset));
  Multiplexer #(.width(16)) multiplexer_2 (.in0(out1), .in1(unfiltered), .out(multiplexer_2_out), .sel(fast));
  not not_2 (not_2_out, clock);
  Register #(.width(16)) register_4 (.D(multiplexer_3_out), .en(1'b1), .clk(clock), .Q(out7), .clr(reset));
  Multiplexer #(.width(16)) multiplexer_3 (.in0(out6), .in1(unfiltered), .out(multiplexer_3_out), .sel(fast));
  Adder #(.width(16)) adder_3 (.a(adder_1_out), .b(out3), .out(adder_3_out));  // open: cin, cout
  Adder #(.width(16)) adder_4 (.a(adder_2_out), .b(out8), .out(adder_4_out));  // open: cin, cout
  Adder #(.width(16)) adder_5 (.a(adder_3_out), .b(out4), .out(adder_5_out));  // open: cin, cout
  Adder #(.width(16)) adder_6 (.a(adder_4_out), .b(out9), .out(adder_6_out));  // open: cin, cout
  Multiplexer #(.width(16)) multiplexer_4 (.in0(out2), .in1(unfiltered), .out(multiplexer_4_out), .sel(fast));
  Multiplexer #(.width(16)) multiplexer_5 (.in0(out7), .in1(unfiltered), .out(multiplexer_5_out), .sel(fast));
  Register #(.width(16)) register_5 (.D(multiplexer_4_out), .en(1'b1), .clk(clock), .Q(out3), .clr(reset));
  Register #(.width(16)) register_6 (.D(multiplexer_5_out), .en(1'b1), .clk(not_3_out), .Q(out8), .clr(reset));
  not not_3 (not_3_out, clock);
  Adder #(.width(16)) adder_7 (.a(adder_5_out), .b(out5), .out(adder_7_out));  // open: cin, cout
  Adder #(.width(16)) adder_8 (.a(adder_6_out), .b(out10), .out(adder_8_out));  // open: cin, cout
  Divider #(.mode("twosComplement"), .width(16)) divider_1 (
    .a(adder_8_out), .b(16'ha), .out(filtered));  // open: upper, rem
  Subtractor #(.width(16)) subtractor_1 (.a(out1), .b(out2), .out(subtractor_1_out));  // open: bin, bout
  Adder #(.width(16)) adder_9 (.a(adder_7_out), .b(out6), .out(adder_9_out));  // open: cin, cout
  Register #(.width(16)) register_7 (.D(multiplexer_6_out), .en(1'b1), .clk(not_4_out), .Q(out4), .clr(reset));
  Multiplexer #(.width(16)) multiplexer_6 (.in0(out3), .in1(unfiltered), .out(multiplexer_6_out), .sel(fast));
  not not_4 (not_4_out, clock);
  Register #(.width(16)) register_8 (.D(multiplexer_7_out), .en(1'b1), .clk(clock), .Q(out9), .clr(reset));
  Multiplexer #(.width(16)) multiplexer_7 (.in0(out8), .in1(unfiltered), .out(multiplexer_7_out), .sel(fast));
  absolute_val_and_sign absolute_val_and_sign_2 (
    .unfiltered(subtractor_1_out), .value(absolute_val_and_sign_2_value));  // open: negative
  Comparator #(.mode("unsigned"), .width(16)) comparator_1 (
    .a(absolute_val_and_sign_2_value), .b(16'ha), .gt(fast));  // open: eq, lt
  Register #(.width(16)) register_9 (.D(multiplexer_8_out), .en(1'b1), .clk(clock), .Q(out5), .clr(reset));
  Multiplexer #(.width(16)) multiplexer_8 (.in0(out4), .in1(unfiltered), .out(multiplexer_8_out), .sel(fast));
  Register #(.width(16)) register_10 (.D(multiplexer_9_out), .en(1'b1), .clk(not_5_out), .Q(out10), .clr(reset));
  Multiplexer #(.width(16)) multiplexer_9 (.in0(out9), .in1(unfiltered), .out(multiplexer_9_out), .sel(fast));
  not not_5 (not_5_out, clock);

  // Other names for the same wires on the sheet: value[15:0] = unfiltered
endmodule

module signed_div_by_128 (
  input  [15:0] unfiltered,
  output [15:0] result
);

  wire absolute_val_and_sign_1_negative;
  wire [15:0] absolute_val_and_sign_1_value, divide_two_num_1_final_answer_sixteen_bits,
       twos_complement_1_absolute_val;

  absolute_val_and_sign absolute_val_and_sign_1 (
    .unfiltered(unfiltered), .value(absolute_val_and_sign_1_value),
    .negative(absolute_val_and_sign_1_negative));
  divide_two_num divide_two_num_1 (
    .val(absolute_val_and_sign_1_value), .val2(16'h6400),
    .final_answer_sixteen_bits(divide_two_num_1_final_answer_sixteen_bits));  // open: final_answer
  twos_complement twos_complement_1 (
    .negative_number(divide_two_num_1_final_answer_sixteen_bits),
    .absolute_val(twos_complement_1_absolute_val));
  Multiplexer #(.width(16)) multiplexer_1 (
    .in0(divide_two_num_1_final_answer_sixteen_bits), .in1(twos_complement_1_absolute_val), .out(result),
    .sel(absolute_val_and_sign_1_negative));
endmodule

module signed_div_by_128_sim (
  input  [15:0] value_to_div,
  input  negative,
  output [15:0] result
);

  wire [15:0] division_sim_1_result, twos_complement_1_absolute_val;

  division_sim division_sim_1 (.number1(value_to_div), .divider_tweaked(16'h80), .result(division_sim_1_result));
  twos_complement twos_complement_1 (
    .negative_number(division_sim_1_result), .absolute_val(twos_complement_1_absolute_val));
  Multiplexer #(.width(16)) multiplexer_1 (
    .in0(division_sim_1_result), .in1(twos_complement_1_absolute_val), .out(result), .sel(negative));
endmodule

module scale_down_sim (
  input  [15:0] number_input,
  input  [31:0] second_num,
  output negative,
  output [3:0] hundreds,
  output [3:0] tens,
  output [3:0] ones,
  output [7:0] answer
);

  wire [15:0] multiplexer_1_out, twos_complement_1_absolute_val;
  wire [31:0] bit_extender_4_out, hex_to_decimal_sim_1_p1, hex_to_decimal_sim_1_p2, hex_to_decimal_sim_1_p3,
       hex_to_decimal_sim_1_p4;

  twos_complement twos_complement_1 (.negative_number(number_input), .absolute_val(twos_complement_1_absolute_val));
  // hex_to_decimal_sim hex_to_decimal_sim_1: pin names not known; wires that end beside it: hex_to_decimal_sim_1_p1, hex_to_decimal_sim_1_p2, hex_to_decimal_sim_1_p3, hex_to_decimal_sim_1_p4
  Multiplexer #(.width(16)) multiplexer_1 (
    .in0(number_input), .in1(twos_complement_1_absolute_val), .out(multiplexer_1_out), .sel(number_input[15]));
  Bit_Extender #(.in_width(32), .out_width(4), .\type ("zero")) bit_extender_1 (
    .in(hex_to_decimal_sim_1_p2), .out(hundreds));
  Bit_Extender #(.in_width(32), .out_width(4), .\type ("zero")) bit_extender_2 (
    .in(hex_to_decimal_sim_1_p3), .out(tens));
  Bit_Extender #(.in_width(32), .out_width(4), .\type ("zero")) bit_extender_3 (
    .in(hex_to_decimal_sim_1_p4), .out(ones));
  assign bit_extender_4_out = {{16{1'b0}}, multiplexer_1_out};  // Bit_Extender bit_extender_4
  Bit_Extender #(.in_width(32), .out_width(8)) bit_extender_5 (.in(hex_to_decimal_sim_1_p1), .out(answer));
  divide_two_num_sim divide_two_num_sim_1 (
    .value1(bit_extender_4_out), .value2(second_num), .output_value(hex_to_decimal_sim_1_p1));

  assign negative = number_input[15];
endmodule

module scale_down (
  input  [15:0] number_input,
  input  [15:0] second_num,
  output negative,
  output [3:0] hundreds,
  output [3:0] tens,
  output [3:0] ones,
  output [15:0] answer
);

  wire [7:0] divide_two_num_1_final_answer;
  wire [15:0] multiplexer_1_out, twos_complement_1_absolute_val;

  twos_complement twos_complement_1 (.negative_number(number_input), .absolute_val(twos_complement_1_absolute_val));
  Multiplexer #(.width(16)) multiplexer_1 (
    .in0(number_input), .in1(twos_complement_1_absolute_val), .out(multiplexer_1_out), .sel(number_input[15]));
  divide_two_num divide_two_num_1 (
    .val(multiplexer_1_out), .val2(second_num), .final_answer(divide_two_num_1_final_answer),
    .final_answer_sixteen_bits(answer));
  hex_to_decimal hex_to_decimal_1 (.val(divide_two_num_1_final_answer), .hundreds(hundreds), .tens(tens), .ones(ones));

  assign negative = number_input[15];
endmodule

module accel_driver_logisim (
  input  rst,
  input  miso,
  input  accel_input,
  input  enable_accel,
  output mosi,
  output sclk,
  output cs,
  output [47:0] Accelerometer
);

  wire clock_1_out;

  Clock clock_1 (.out(clock_1_out));
  spi_accelerometer spi_accelerometer_1 (
    .clk50MHz(clock_1_out), .rst(rst), .miso(miso), .accel_input(accel_input), .enable_accel(enable_accel),
    .mosi(mosi), .sclk(sclk), .cs(cs), .accel(Accelerometer));
  accel_driver accel_driver_1 (
    .rst(1'b0), .clk(1'b0), .accel_input(1'b0), .rxDataReady(1'b0), .rxData({8{1'b0}}), .enable_accel(1'b0));  // open: go, pol, pha, bytes, txData, accel_data, stateID, c
  spi_master spi_master_1 (
    .clk(1'b0), .rst(1'b0), .miso(1'b0), .accel_input(1'b0), .int2(1'b0), .go(1'b0), .pol(1'b0), .pha(1'b0),
    .bytes(4'b0000), .txData({8{1'b0}}));  // open: mosi, sclk_out, cs_out, rxData, rxDataReady
  clock_div clock_div_1 (
    .clk_in(1'b0), .rst(1'b0), .enable(1'b0), .bytes(4'b0000), .polarity(1'b0));  // open: clk_out, clk_active, byte_flag

  // Notes on the sheet:
  //   ACCELEROMETER MAIN DRIVER
  //   X - AXIS : ACCELEROMETER BITS 0 TO 15
  //   Y - AXIS : ACCELEROMETER BITS 16 TO 31
  //   Z - AXIS : ACCELEROMETER BITS 32 TO 47
  //   OUTPUTS THE VALUES READ BY THE 3-AXES OF THE ACCELEROMETER 
  //   GSENSOR/PIN0 -> MOSI
  //   GSENSOR/PIN1 -> MISO
  //   GSENSOR/PIN2 -> SCLK
  //   GSENSOR/PIN3 -> CS
  //   GSENSOR/PIN4 -> ACCEL_INPUT
  //   PIN MAPPING FOR TERASICDE10LITE_ACCEL.xml
  //   Tested functional at 50MHz. DE10-Lite. 2024.03.15
endmodule

module absolute_val_and_sign (
  input  [15:0] unfiltered,
  output [15:0] value,
  output negative
);

  wire [15:0] twos_complement_1_absolute_val;

  twos_complement twos_complement_1 (.negative_number(unfiltered), .absolute_val(twos_complement_1_absolute_val));
  Multiplexer #(.width(16)) multiplexer_1 (
    .in0(unfiltered), .in1(twos_complement_1_absolute_val), .out(value), .sel(unfiltered[15]));

  assign negative = unfiltered[15];
endmodule

module hex_to_decimal_sim (
  input  [15:0] VALUE,
  output [3:0] hundreds,
  output [3:0] tens,
  output [3:0] ones
);

  wire [31:0] bit_extender_1_out, multiplier_1_out, multiplier_2_out, multiplier_3_out, multiplier_4_out,
       shifter_1_out, shifter_2_out, subtractor_1_out, subtractor_2_out;

  assign bit_extender_1_out = {{16{VALUE[15]}}, VALUE};  // Bit_Extender bit_extender_1
  Multiplier #(.width(32)) multiplier_1 (
    .a(bit_extender_1_out), .b(32'h148), .out(multiplier_1_out));  // open: cin, cout
  Multiplier #(.width(32)) multiplier_2 (.a(shifter_1_out), .b(32'h64), .out(multiplier_2_out));  // open: cin, cout
  Multiplier #(.width(32)) multiplier_3 (.a(subtractor_1_out), .b(32'hccd), .out(multiplier_3_out));  // open: cin, cout
  Multiplier #(.width(32)) multiplier_4 (.a(shifter_2_out), .b(32'ha), .out(multiplier_4_out));  // open: cin, cout
  Shifter #(.shift("lr"), .width(32)) shifter_1 (.in(multiplier_1_out), .\dist (5'b01111), .out(shifter_1_out));
  Subtractor #(.width(32)) subtractor_1 (
    .a(bit_extender_1_out), .b(multiplier_2_out), .out(subtractor_1_out));  // open: bin, bout
  Shifter #(.shift("lr"), .width(32)) shifter_2 (.in(multiplier_3_out), .\dist (5'b01111), .out(shifter_2_out));
  Subtractor #(.width(32)) subtractor_2 (
    .a(subtractor_1_out), .b(multiplier_4_out), .out(subtractor_2_out));  // open: bin, bout
  Bit_Extender #(.in_width(32), .out_width(4), .\type ("zero")) bit_extender_2 (.in(shifter_1_out), .out(hundreds));
  // Probe on subtractor_1_out
  Bit_Extender #(.in_width(32), .out_width(4), .\type ("zero")) bit_extender_3 (.in(shifter_2_out), .out(tens));
  Bit_Extender #(.in_width(32), .out_width(4), .\type ("zero")) bit_extender_4 (.in(subtractor_2_out), .out(ones));
endmodule

module divide_two_num_sim (
  input  [31:0] value1,
  input  [31:0] value2,
  output [31:0] output_value
);

  wire [31:0] multiplier_1_out;

  Multiplier #(.width(32)) multiplier_1 (.a(value1), .b(value2), .out(multiplier_1_out));  // open: cin, cout
  Shifter #(.shift("lr"), .width(32)) shifter_1 (.in(multiplier_1_out), .\dist (5'b01111), .out(output_value));
endmodule

module division_sim (
  input  [15:0] number1,
  input  [15:0] divider_tweaked,
  output [15:0] result
);

  wire [15:0] multiplier_2_out;
  wire [31:0] bit_extender_1_out, bit_extender_2_out, multiplier_1_out;
  wire [31:16] shifter_1_out;

  assign bit_extender_1_out = {{16{1'b0}}, number1};  // Bit_Extender bit_extender_1
  Multiplier #(.width(32)) multiplier_1 (
    .a(bit_extender_1_out), .b(bit_extender_2_out), .out(multiplier_1_out));  // open: cin, cout
  Multiplier #(.width(16)) multiplier_2 (.a(16'h64), .b(divider_tweaked), .out(multiplier_2_out));  // open: cin, cout
  assign bit_extender_2_out = {{16{1'b0}}, multiplier_2_out};  // Bit_Extender bit_extender_2
  Shifter #(.shift("lr"), .width(32)) shifter_1 (
    .in(multiplier_1_out), .\dist (5'b01111), .out({shifter_1_out, result}));
endmodule

module twos_complement (
  input  [15:0] negative_number,
  output [15:0] absolute_val
);

  wire [15:0] not_1_out;

  assign not_1_out = ~negative_number;  // NOT_Gate not_1, 16 bits wide
  Adder #(.width(16)) adder_1 (.a(not_1_out), .b(16'h1), .out(absolute_val));  // open: cin, cout
endmodule

module sign_hex_output (
  input  negative
);

  wire sign_hex_logic_1_a, sign_hex_logic_1_b, sign_hex_logic_1_c, sign_hex_logic_1_d, sign_hex_logic_1_e,
       sign_hex_logic_1_f, sign_hex_logic_1_g;

  sign_hex_logic sign_hex_logic_1 (
    .negative(negative), .a(sign_hex_logic_1_a), .b(sign_hex_logic_1_b), .c(sign_hex_logic_1_c),
    .d(sign_hex_logic_1_d), .e(sign_hex_logic_1_e), .f(sign_hex_logic_1_f), .g(sign_hex_logic_1_g));
  _7_Segment_Display L_7_Segment_Display_1 (
    .g(sign_hex_logic_1_g), .f(sign_hex_logic_1_f), .a(sign_hex_logic_1_a), .b(sign_hex_logic_1_b),
    .e(sign_hex_logic_1_e), .d(sign_hex_logic_1_d), .c(sign_hex_logic_1_c), .dp(1'b0));
endmodule

module sign_hex_logic (
  input  negative,
  output a,
  output b,
  output c,
  output d,
  output e,
  output f,
  output g
);


  assign a = 1'b0;
  assign b = 1'b0;
  assign c = 1'b0;
  assign d = 1'b0;
  assign e = 1'b0;
  assign f = 1'b0;
  assign g = negative;
endmodule

module sevenseg_direction_angle_logic (
  input  L,
  input  R,
  input  U,
  input  D,
  input  S,
  input  M,
  output [7:0] letter_output
);

  wire and_1_out, and_2_out, and_3_out, and_4_out, and_5_out, and_6_out, and_7_out, and_8_out, and_9_out,
       and_10_out, and_11_out, and_12_out, and_13_out, and_14_out, and_15_out, and_16_out, and_17_out,
       and_18_out, and_19_out, and_20_out, and_21_out, and_22_out, and_23_out, and_24_out, and_25_out,
       not_1_out, not_2_out, not_3_out, not_4_out, not_5_out, not_6_out;

  not not_1 (not_1_out, L);
  not not_2 (not_2_out, R);
  not not_3 (not_3_out, U);
  not not_4 (not_4_out, D);
  not not_5 (not_5_out, S);
  not not_6 (not_6_out, M);
  and and_1 (and_1_out, not_1_out, not_2_out, not_3_out, not_4_out, S, not_6_out);
  and and_2 (and_2_out, not_1_out, not_2_out, not_3_out, D, not_5_out, not_6_out);
  and and_3 (and_3_out, not_1_out, R, not_3_out, not_4_out, not_5_out, not_6_out);
  and and_4 (and_4_out, not_1_out, not_2_out, not_3_out, not_4_out, not_5_out, M);
  and and_5 (and_5_out, not_1_out, not_2_out, not_3_out, not_4_out, S, not_6_out);
  and and_6 (and_6_out, not_1_out, not_2_out, U, not_4_out, not_5_out, not_6_out);
  and and_7 (and_7_out, L, not_2_out, not_3_out, not_4_out, not_5_out, not_6_out);
  and and_8 (and_8_out, not_1_out, not_2_out, not_3_out, not_4_out, not_5_out, M);
  and and_9 (and_9_out, not_1_out, not_2_out, not_3_out, D, not_5_out, not_6_out);
  and and_10 (and_10_out, not_1_out, not_2_out, U, not_4_out, not_5_out, not_6_out);
  and and_11 (and_11_out, not_1_out, R, not_3_out, not_4_out, not_5_out, not_6_out);
  and and_12 (and_12_out, L, not_2_out, not_3_out, not_4_out, not_5_out, not_6_out);
  and and_13 (and_13_out, not_1_out, not_2_out, not_3_out, not_4_out, S, not_6_out);
  and and_14 (and_14_out, not_1_out, not_2_out, not_3_out, D, not_5_out, not_6_out);
  and and_15 (and_15_out, not_1_out, not_2_out, U, not_4_out, not_5_out, not_6_out);
  and and_16 (and_16_out, L, not_2_out, not_3_out, not_4_out, not_5_out, not_6_out);
  and and_17 (and_17_out, not_1_out, not_2_out, not_3_out, not_4_out, not_5_out, M);
  and and_18 (and_18_out, not_1_out, not_2_out, not_3_out, not_4_out, S, not_6_out);
  and and_19 (and_19_out, not_1_out, not_2_out, not_3_out, D, not_5_out, not_6_out);
  and and_20 (and_20_out, not_1_out, not_2_out, U, not_4_out, not_5_out, not_6_out);
  and and_21 (and_21_out, not_1_out, not_2_out, not_3_out, not_4_out, not_5_out, M);
  and and_22 (and_22_out, not_1_out, not_2_out, not_3_out, D, not_5_out, not_6_out);
  and and_23 (and_23_out, not_1_out, not_2_out, U, not_4_out, not_5_out, not_6_out);
  and and_24 (and_24_out, not_1_out, not_2_out, not_3_out, not_4_out, not_5_out, M);
  and and_25 (and_25_out, not_1_out, not_2_out, not_3_out, not_4_out, S, not_6_out);
  or or_1 (letter_output[6], and_1_out, and_2_out, and_3_out);
  or or_2 (letter_output[5], and_4_out, and_5_out, and_6_out, and_7_out);
  or or_3 (letter_output[4], and_8_out, and_9_out, and_10_out, and_11_out, and_12_out);
  or or_4 (letter_output[3], and_13_out, and_14_out, and_15_out, and_16_out);
  or or_5 (letter_output[2], and_17_out, and_18_out, and_19_out, and_20_out);
  or or_6 (letter_output[1], and_21_out, and_22_out, and_23_out);
  or or_7 (letter_output[0], and_24_out, and_25_out);

  assign letter_output[7] = 1'b0;
endmodule

module sevenseg_direction_angle_output (
  input  L,
  input  R,
  input  U,
  input  D,
  input  S,
  input  M
);

  wire [7:0] sevenseg_direction_angle_logic_1_letter_output;

  sevenseg_direction_angle_logic sevenseg_direction_angle_logic_1 (
    .L(L), .R(R), .U(U), .D(D), .S(S), .M(M), .letter_output(sevenseg_direction_angle_logic_1_letter_output));
  _7_Segment_Display HEX (
    .g(sevenseg_direction_angle_logic_1_letter_output[6]),
    .f(sevenseg_direction_angle_logic_1_letter_output[5]),
    .a(sevenseg_direction_angle_logic_1_letter_output[0]),
    .b(sevenseg_direction_angle_logic_1_letter_output[1]),
    .e(sevenseg_direction_angle_logic_1_letter_output[4]),
    .d(sevenseg_direction_angle_logic_1_letter_output[3]),
    .c(sevenseg_direction_angle_logic_1_letter_output[2]),
    .dp(sevenseg_direction_angle_logic_1_letter_output[7]));
endmodule

module sevenseg_numbers_logic (
  input  [3:0] accel,
  output [7:0] sevensegment
);

  wire and_1_out, and_2_out, and_3_out, and_4_out, and_5_out, and_6_out, and_7_out, and_8_out, and_9_out,
       and_10_out, and_11_out, and_12_out, and_13_out, and_14_out, and_15_out, and_16_out, and_17_out,
       and_18_out, and_19_out, and_20_out, and_21_out, and_22_out, and_23_out, and_24_out, and_25_out,
       and_26_out, and_27_out, and_28_out, and_29_out, and_30_out, and_31_out, and_32_out, and_33_out,
       and_34_out, and_35_out, and_36_out, not_1_out, not_2_out, not_3_out, not_4_out;

  not not_1 (not_1_out, accel[3]);
  not not_2 (not_2_out, accel[2]);
  not not_3 (not_3_out, accel[1]);
  not not_4 (not_4_out, accel[0]);
  and and_1 (and_1_out, not_2_out, accel[1]);
  and and_2 (and_2_out, accel[1], not_4_out);
  and and_3 (and_3_out, not_1_out, accel[2], not_3_out);
  and and_4 (and_4_out, accel[3], not_2_out);
  and and_5 (and_5_out, accel[3], accel[0]);
  and and_6 (and_6_out, not_3_out, not_4_out);
  and and_7 (and_7_out, not_1_out, accel[2], not_3_out);
  and and_8 (and_8_out, accel[2], not_4_out);
  and and_9 (and_9_out, accel[3], not_2_out);
  and and_10 (and_10_out, accel[3], accel[1]);
  and and_11 (and_11_out, not_2_out, not_4_out);
  and and_12 (and_12_out, accel[1], not_4_out);
  and and_13 (and_13_out, accel[3], accel[1]);
  and and_14 (and_14_out, accel[3], accel[2]);
  and and_15 (and_15_out, not_1_out, not_2_out, not_4_out);
  and and_16 (and_16_out, not_1_out, accel[1], not_4_out);
  and and_17 (and_17_out, not_2_out, accel[1], accel[0]);
  and and_18 (and_18_out, accel[2], not_3_out, accel[0]);
  and and_19 (and_19_out, accel[3], not_3_out);
  and and_20 (and_20_out, accel[3], accel[2], not_4_out);
  and and_21 (and_21_out, not_1_out, not_3_out);
  and and_22 (and_22_out, not_1_out, accel[0]);
  and and_23 (and_23_out, not_3_out, accel[0]);
  and and_24 (and_24_out, not_1_out, accel[2]);
  and and_25 (and_25_out, accel[3], not_2_out);
  and and_26 (and_26_out, not_1_out, not_2_out);
  and and_27 (and_27_out, not_1_out, not_3_out, not_4_out);
  and and_28 (and_28_out, not_2_out, not_4_out);
  and and_29 (and_29_out, not_1_out, accel[1], accel[0]);
  and and_30 (and_30_out, accel[3], not_3_out, accel[0]);
  and and_31 (and_31_out, not_2_out, not_4_out);
  and and_32 (and_32_out, not_1_out, accel[1]);
  and and_33 (and_33_out, not_1_out, accel[2], accel[0]);
  and and_34 (and_34_out, accel[2], accel[1]);
  and and_35 (and_35_out, accel[3], not_2_out, not_3_out);
  and and_36 (and_36_out, accel[3], not_4_out);
  or or_1 (sevensegment[6], and_1_out, and_2_out, and_3_out, and_4_out, and_5_out);
  or or_2 (sevensegment[5], and_6_out, and_7_out, and_8_out, and_9_out, and_10_out);
  or or_3 (sevensegment[4], and_11_out, and_12_out, and_13_out, and_14_out);
  or or_4 (sevensegment[3], and_15_out, and_16_out, and_17_out, and_18_out, and_19_out, and_20_out);
  or or_5 (sevensegment[2], and_21_out, and_22_out, and_23_out, and_24_out, and_25_out);
  or or_6 (sevensegment[1], and_26_out, and_27_out, and_28_out, and_29_out, and_30_out);
  or or_7 (sevensegment[0], and_31_out, and_32_out, and_33_out, and_34_out, and_35_out, and_36_out);

  assign sevensegment[7] = 1'b0;
endmodule

module sevenseg_numbers_output (
  input  [3:0] input_bus,
  input  decimal
);

  wire [7:0] sevenseg_numbers_logic_1_sevensegment;

  sevenseg_numbers_logic sevenseg_numbers_logic_1 (
    .accel(input_bus), .sevensegment(sevenseg_numbers_logic_1_sevensegment));
  _7_Segment_Display L_7_Segment_Display_1 (
    .g(sevenseg_numbers_logic_1_sevensegment[6]), .f(sevenseg_numbers_logic_1_sevensegment[5]),
    .a(sevenseg_numbers_logic_1_sevensegment[0]), .b(sevenseg_numbers_logic_1_sevensegment[1]),
    .e(sevenseg_numbers_logic_1_sevensegment[4]), .d(sevenseg_numbers_logic_1_sevensegment[3]),
    .c(sevenseg_numbers_logic_1_sevensegment[2]), .dp(decimal));
endmodule

module sevenseg_mapped (
  input  [7:0] sevenseg_input
);

  _7_Segment_Display HEX (
    .g(sevenseg_input[6]), .f(sevenseg_input[5]), .a(sevenseg_input[0]), .b(sevenseg_input[1]),
    .e(sevenseg_input[4]), .d(sevenseg_input[3]), .c(sevenseg_input[2]), .dp(sevenseg_input[7]));
endmodule

module reset_logic (
  input  reset,
  input  enable,
  output reset_out,
  output enable_out
);

  wire not_1_out;

  not not_1 (not_1_out, reset);
  and and_1 (enable_out, not_1_out, enable);

  assign reset_out = reset;
endmodule

// VHDL entity accel_driver, as the project stores it:
--accel_driver
-- TODO:
-- 1) Incorporate data range generic for calibration LSB/g for z axis
library ieee;
use ieee.std_logic_1164.all;
use ieee.numeric_std.all;

entity accel_driver is
	port (
		rst			:		in std_logic;
		clk			:		in std_logic;
		accel_input			:		in std_logic;
		rxDataReady	:		in	std_logic;
		go				:		out std_logic;
		pol			:		out std_logic;
		pha			:		out std_logic;
		bytes 		:		out std_logic_vector (3 downto 0);
		txData 		:		out std_logic_vector (7 downto 0);
		rxData		: 		in std_logic_vector ( 7 downto 0);
		accel_data	:		out std_logic_vector (47 downto 0);
		
		stateID 		:      out std_logic_vector (2 downto 0);
		c				: out std_logic;
		enable_accel   : in std_logic
		
		
	);
end accel_driver;



architecture fsm_1p of accel_driver is
	
	constant max	: natural := 50000000 /  500000 ;
	signal count			:		integer range 0 to max;
	signal countSignal		: std_logic;
	type STATE_TYPE is (S_START, S_IDLE, S_CONFIG, S_WRITE, S_READ, S_READ_WAIT, S_CALIBRATE, S_OUTPUT); --S_CONFIG_TEST, S_WRITE_TEST);
	signal STATE, NEXT_STATE			:		STATE_TYPE;
	--signal accel_x, accel_y, accel_z	:		std_logic_vector(15 downto 0);
	signal accel_data_buff : std_logic_vector( 47 downto 0);
	signal byteCount	: integer range -1 to 16 := 0;
	constant byteCountRead : integer := 7;
	signal mode			: std_logic;
	signal reg	: integer range 0 to 8;
	signal regTest : integer range 0 to 16;
	signal regAddr		: std_logic_vector (5 downto 0);
	signal regData		: std_logic_vector (7 downto 0);
	signal rxDataReadyLast : std_logic := '0';
	
	constant sampleBits : natural := 4;
	constant samples  : natural := 2 ** sampleBits;
	--signal div_padding : std_logic_vector (sampleBits - 1 downto 0);
	signal sample_count : integer range 0 to samples + 1;
	signal calibrate : std_logic;
	--type NIBBLE is array (3 downto 0) of std_ulogic;
	type calibration_array is array (2 downto 0) of std_logic_vector (15 downto 0);  -- (0) X accumulate, (1) Y accumulate, (2) Z accumulate
	signal calibData : calibration_array;
	
begin




	process(clk, rst)
	begin
		if(rst = '1') then
			state <= S_START;
			accel_data <= (others => '0');
			accel_data_buff <= (others => '0');
			regData <= "00000000";
			regAddr <= "000000";
			bytes <= "0000";
			txData <= "00000000";
			mode <= '0';
			count <= 0;
			go <= '0';
			reg <= 0;
			regTest <= 0;
			byteCount <= 0;
			stateID <= "000";
			calibrate <= '0';
			calibData(0) <= (others => '0');
			calibData(1) <= (others => '0');
			calibData(2) <= (others => '0');
			sample_count <= 0;
			--div_padding <= (others => '0');
			
		elsif(clk'event and clk = '1') then
			
			
			
			case state is
			
				when S_START =>
					byteCount <= 0;
					mode <= '0';
					reg <= 0;
					rxDataReadyLast <= '0';
					state <= S_IDLE;
					accel_data <= (others => '0');
					go <= '0';
					
					stateID <= "001";
				
				when S_IDLE =>
					stateID <= "010";
					--if(mode = '1' and int1 = '1') then state <= S_READ;
					--end if;
		
					if(count = max - 1) then							-- delay between each transmission 
						--count <= 0;
						c <= '1';
						
						if(mode = '0') then
							state <= S_CONFIG;		-- mode 0 is config. after config mode goes to 1 for read
							count <= 0; 
						--elsif(int1 = '1')   then
						else
							state <= S_READ_WAIT;	-- mode 1, but only read if interrupt for data_ready is set
							count <= 0;
						--else count <= max - 1;							-- do not set count to 0 to prevent running the delay loop again
						end if;	
			
					else 
						count <= count + 1;
						c <= '0';
					end if;
					
--					if(intBypass = '1') then state <= S_IDLE;
--					end if;
			
				when S_READ_WAIT =>
					stateID <= "111";
					if (calibrate = '1') then state <= S_CALIBRATE;
					elsif(accel_input = '1' or enable_accel = '1') then state <= S_READ;
					end if;
					
				when S_CALIBRATE => 
					case reg is								-- reg should be 0 from config state earlier, represents each offset register
						when 0 =>							-- calculate the negative of x and y offset. subtract 256 (1g) from z and shift 2 (8 bit conversion)
							if(calibData(0)(15) = '0') then  -- x axis negative conversion
								calibData(0) <= std_logic_vector(signed(not calibData(0)) + 1);	-- twos comp conversion from positive to negative
							else
								calibData(0) <= std_logic_vector(not(signed(calibData(0)) - 1));  -- twos comp conversion from negative to positive
							end if;
							
							if(calibData(1)(15) = '0') then -- y axis negative conversion
								calibData(1) <= std_logic_vector(signed(not calibData(1)) + 1);	-- twos comp conversion from positive to negative
							else
								calibData(1) <= std_logic_vector(not(signed(calibData(1)) - 1));  -- twos comp conversion from negative to positive
							end if;
							
							calibData(2) <=std_logic_vector(shift_right(signed(calibData(2)) - 256, 2));	-- find error realtive to gravity in z axis and divide by 4 for 10 to 8 bit conversion			
							reg <= reg + 1;
						
						when 1 =>																					-- calculate Z's negative, store x axis
						
							if(calibData(2)(15) = '0') then 													-- Z axis negative conversion
								calibData(2) <= std_logic_vector(signed(not calibData(2)) + 1);	-- twos comp conversion from positive to negative
							else
								calibData(2) <= std_logic_vector(not(signed(calibData(2)) - 1));  -- twos comp conversion from negative to positive
							end if;
							
							regAddr <= "011110";																	-- Register 0x1E: "X offset" 8 bit 2's comp offset for X axis
							regData <= calibData(0)(7 downto 0);															-- X offset data
							reg <= reg + 1;	
							state  <= S_WRITE;
						when 2 =>
							regAddr <= "011111";																	-- Register 0x1F: "Y offset" 8 bit 2's comp offset for Y axis
							regData <= calibData(1)(7 downto 0);
							reg <= reg + 1;
							state  <= S_WRITE;
						when 3 =>
							regAddr <= "100000";																	-- Register 0x20: "Z offset" 8 bit 2's comp offset for Z axis
							regData <= calibData(2)(7 downto 0);
							reg <= 0;
							state  <= S_WRITE;
							calibrate <= '0';																		-- de-assert calibration flag to continue reading normally
						when others => null;
						
					end case;
				
				when S_CONFIG =>
						stateID <= "011";
					case reg is
						when 0 =>
							regAddr <= "110001"; -- Register 0x31: "Data_Format" sets data range (0b00) to +/- 2g and full resultion (0b1000)
							regData <= "00001000";   
							reg <= reg + 1;
							state <= S_WRITE;
						when 1 => 
							regAddr <= "101100";  -- Register 0x2C: "BW_RATE" sets rate (0b0100) to 1.56 Hz, ideal should be 100hz which is default at power reset, but too fast for 7seg's
							regData <= "00000100";
							reg <= reg + 1;
							state <= S_WRITE;
						when 2 =>
							regAddr <= "011110";					-- Register 0x1E: "X offset" 8 bit 2's comp offset for X axis
							regData <= "00000000";				-- Clear X offset register so calibration will not use data from previous resets
							reg <= reg + 1;
							state  <= S_WRITE;
							
						when 3 =>
							regAddr <= "011111";					-- Register 0x1F: "Y offset" 8 bit 2's comp offset for Y axis
							regData <= "00000000";				-- Clear Y offset register so calibration will not use data from previous resets
							reg <= reg + 1;
							state  <= S_WRITE;
						
						when 4 =>
							regAddr <= "100000";					-- Register 0x20: "Z offset" 8 bit 2's comp offset for Z axis
							regData <= "00000000";				-- Clear Z offset register so calibration will not use data from previous resets
							reg <= reg + 1;
							state  <= S_WRITE;
						
						when 5 => 
							regAddr <= "101101";	 -- Register 0x2D: "Power_CTL" sets measure bit (0b1000) to start sampling. 
							regData <= "00001000";
							reg <= reg + 1;
							state <= S_WRITE;
							--mode <= '1';			-- Switch to Read mode so IDLE turns to S_READ and not S_CONFIG
						when 6 => 
							regAddr <= "101110";	 -- Register 0x2E: "INT_ENABLE" enables Data_Ready interrupt (0b10000000) 
							regData <= "10000000";
							reg <= 0;
							state <= S_WRITE;
							mode <= '1';			-- Switch to Read mode so IDLE turns to S_READ and not S_CONFIG
						when others => null;
					end case;
				
				when S_WRITE =>
					stateID <= "100";
					bytes <= "0010";
					rxDataReadyLast <= rxDataReady;
					if(byteCount = 0) then
						txData <= "00" & regAddr;
						go <= '1';
						byteCount <= 1;
					--elsif(rising_edge(rxDataReady) and byteCount = 1) then
					elsif((rxDataReadyLast = '0' and rxDataReady = '1') and byteCount = 1) then  -- rising edge
						byteCount <= 2;
						go <= '0';
						txData <= regData;
					elsif((rxDataReadyLast = '0' and rxDataReady = '1') and byteCount = 2) then  -- rising edge, nothing is transmitted here
						byteCount <= 3;
							
						
					elsif((rxDataReadyLast = '1' and rxDataReady = '0') and byteCount = 3) then  --falling edge
						state <= S_IDLE;
						byteCount <= 0;
					end if;
				--00111101 00001000
				when S_READ =>
					stateID <= "101";
					
					mode <= '1';
					bytes <= std_logic_vector(to_unsigned(byteCountRead, bytes'length));
					rxDataReadyLast <= rxDataReady;
					if(byteCount = 0) then														-- Send Read Command
						txData <= "11110010";
						go <= '1';
						byteCount <= 1;
					elsif(byteCount = 1) then													--next system clock enters here
						txData <= "00000000";							
						go <= '0';
						if((rxDataReadyLast = '1' and rxDataReady = '0')) then		--wait until 8 bits are sent to update byte count 
							byteCount <= 2;
						end if;
						
					else																				--read bytes 2 3 4 5 6 and 7
						txData <= "00000000";
						go <= '0';
						
						if((rxDataReadyLast = '1' and rxDataReady = '0') and byteCount <= byteCountRead) then
	--						byteCount <= byteCount + 1;
	--						accel_data_buff((byteCount * 8)  - 1 downto (byteCount-1) * 8) <= rxData;
	--						if(byteCount = byteCountRead - 1) then
	--							byteCount <= 0;
	--							next_state <= S_OUTPUT;
	--						end if;
							if(byteCount = byteCountRead) then
								byteCount <= 0;
								state <= S_OUTPUT;
							else
								byteCount <= byteCount + 1;
								accel_data_buff(((byteCount-1) * 8)  - 1 downto (byteCount-2) * 8) <=  rxData;-- std_logic_vector(to_unsigned(byteCount, bytes'length)); -- rxData;
							end if;


						end if;
						
						
					end if;
				when S_OUTPUT =>
					stateID <= "110";
					
					if(sample_count <= samples) then				-- enter for first n samples for calibration
						if(sample_count = samples) then			-- compare sample count to threshold 
							calibrate <= '1';							-- set flag to calibrate with new values
							calibData(0) <= std_logic_vector(shift_right(signed(calibData(0)), 2 + sampleBits)); -- divide by number of samples for average, and convert to 64 LSB/1g (shifting a 10 bit value right arithmetically for an 8 bit value)
							calibData(1) <= std_logic_vector(shift_right(signed(calibData(1)), 2 + sampleBits));
							calibData(2) <= std_logic_vector(shift_right(signed(calibData(2)), sampleBits)); -- get average. Next clock cycle will compare to 1g (2^8), and then convert to 64 LSB/1g
						else 												-- summation of samples
							calibData(0) <= std_logic_vector(signed(calibData(0)) + signed(accel_data_buff(15 downto   0))); -- summation of X data	
							calibData(1) <= std_logic_vector(signed(calibData(1)) + signed(accel_data_buff(31 downto  16))); -- summation of Y data	
							calibData(2) <= std_logic_vector(signed(calibData(2)) + signed(accel_data_buff(47 downto  32))); -- summation of Z data								
						end if;
						sample_count <= sample_count + 1;	-- increment count, if n samples have been collected, one more prevents entering this if statement
					accel_data <= accel_data_buff;
					else
						accel_data <= accel_data_buff;			-- clock collected accelerometer data for ouput
					end if;
						state <= S_IDLE;								-- go back to idle to repeat the cycle
					
				when others => 
					stateID <= "111";
						NULL;
				
			
			
			end case;


			pol <= '1';
			pha <= '1';
		
		end if;
		
	end process;

end fsm_1p;

// VHDL entity clock_div, as the project stores it:
--clock div
library ieee;
use ieee.std_logic_1164.all;
use ieee.numeric_std.all;

entity clock_div is
	port (
			clk_in : in std_logic;
			clk_out : out std_logic;
			rst	: in std_logic;
			enable : in std_logic;
			bytes : in std_logic_vector(3 downto 0);
			polarity : in std_logic;
			clk_active :	out std_logic;
			byte_flag : out std_logic
			);
end clock_div;

architecture bhv of clock_div is

	constant clk_in_freq : natural := 4;
	constant clk_out_freq: natural := 2;
	constant max : natural := clk_in_freq / clk_out_freq / 2;
	signal count, lastByteCount : integer range 0 to max*2;
	signal clock_signal : std_logic;
	signal byte_count : std_logic_vector (3 downto 0);
	signal bit_count : integer range 0 to 8;
	
	
	
	
	begin
	
		process(clk_in, rst)
		begin
			if(rst = '1' or enable = '0') then
				count <= 0;
				lastByteCount <= 0;
				clk_active <= '0';
				clock_signal <= polarity;
				bit_count <= 0;
				byte_count <= (others => '0');
				byte_flag <= '0';
			
			elsif(clk_in'event and clk_in = '1') then
				if(enable = '1' and byte_count < bytes) then
				
					clk_active <= '1';
					if (count = max-1) then
						count <= 0;
						clock_signal <= not clock_signal;
						
						if((not clock_signal) = polarity) then
							--increment bit count
							--increment byte count after 8 bits and clean bit count
							--clear byte count after numOfBytes and clear active_clk
							
							byte_flag <= '0'; -- clear the byte flag
						
							if(bit_count = 7) then
								byte_count <= std_logic_vector(unsigned(byte_count) + 1);
								bit_count <= 0;
								byte_flag <= '1'; --set byte flag for one sclk cycle
								
								if( byte_count = std_logic_vector(unsigned(bytes) - 1)) then
									--clk_active <= '0';
									--clock_signal <=  clock_signal; --do not toggle clock 
									
								end if;
							
								
							else
								bit_count <= bit_count + 1;
							end if;
							
--							if( byte_count = bytes) then
--								clk_active <= '0';
--							end if;
							
						end if;
					else
						count <= count + 1;
					end if;
				
			
				elsif(enable = '1') then
			
					clk_active <= '1';
						if (lastByteCount = max-1) then
							lastByteCount <= 0;
							clk_active <= '0';
						else
							lastByteCount <= lastByteCount + 1;
						end if;
				end if;
				
				
				
			end if;
		end process;
		
		clk_out <= clock_signal;




end bhv;

// VHDL entity spi_master, as the project stores it:
--spi_master

library ieee;
use ieee.std_logic_1164.all;
use ieee.numeric_std.all;

entity spi_master is
    port (
		clk	: in std_logic;
		rst	: in std_logic;
      mosi	: out std_logic;
		miso 	: in std_logic;
		sclk_out : out std_logic; 
		cs_out	: out std_logic;
		accel_input 	: in std_logic;
		int2 	: in std_logic;
		go		: in std_logic;
		pol	: in std_logic;
		pha   : in std_logic;
		bytes : in std_logic_vector (3 downto 0);
		rxData: out std_logic_vector(7 downto 0);
		txData: in  std_logic_vector(7 downto 0);
		rxDataReady: out std_logic
		);
end spi_master;


architecture FSM_1P of spi_master is


------------------------------------
-- State signals
------------------------------------
type STATE_TYPE is (S_IDLE, S_TXRX);
signal state, next_state : STATE_TYPE;


------------------------------------
-- Clock Div (spi clock) Signals
------------------------------------
signal sclk : std_logic;
signal enable : std_logic := '0';
--signal bytes : std_logic_vector (3 downto 0);
signal polarity : std_logic;
signal last_clk_active : std_logic;
signal clk_active : std_logic;
signal byte_flag : std_logic;

------------------------------------
-- SPI Data Signals
------------------------------------
signal rx_buffer	: std_logic_vector (7 downto 0) := (others => '1');
signal tx_buffer	: std_logic_vector (7 downto 0);
signal cs : std_logic := '1';
constant byte_w : natural := 8;
signal bit : integer range -1 to 8 := 7; --init to msb+1 idx
signal w_r : std_logic := '0'; --write = 0 read = 1
signal phase_Delay : std_logic := '0';
signal last_cs : std_logic := '1';
signal last_sclk : std_logic := '0';

COMPONENT clock_div IS
		port (
		clk_in : in std_logic;
			clk_out : out std_logic;
			rst	: in std_logic;
			enable : in std_logic;
			bytes : in std_logic_vector(3 downto 0);
			polarity : in std_logic;
			clk_active :	out std_logic;
			byte_flag : out std_logic
		);
	END COMPONENT;

begin


	U_CLOCK_DIV : clock_div
		port map(
			clk_in => clk,
			clk_out => sclk,
			rst	=> rst,
			enable => enable,
			bytes	=> bytes,
			polarity => polarity,
			clk_active => clk_active,
			byte_flag => byte_flag);



	--enable <= int1 or int2 or go;
	
	process (clk, rst)
	begin
		
		if(rst = '1') then
			state <= S_IDLE;
			last_clk_active <= '0';
			enable <= '0';
			cs <= '1';
		elsif (clk'event and clk = '1') then
			
	
		--process(state, int1, int2, go, clk_active, byte_flag)--, txData)
		--begin
		
			rxDataReady <= '0'; --only high when data is ready
			polarity <= pol;
			--w_r <= not pha; --first write for phase 1 is pre toggled. 0 is default
		--	next_state <= state;
			enable <= '0';
			
			last_clk_active <= clk_active;
			
			case state is
				when S_IDLE =>
					
					--enable <= '0'; --default 
					cs <= '1';
					if((accel_input = '1' or int2 = '1' or go = '1') and rst = '0') then
						state <= S_TXRX;
	--					polarity <= pol;
	--					w_r <= not pha; --first write for phase 1 is pre toggled. 0 is default
						enable <= '1';
						cs <= '0';
						tx_buffer <= txData; --TEST
						
					end if;
				
				
				when S_TXRX =>
					
					
					enable <= '1';
					
					if(last_clk_active = '1' and clk_active = '0') then  --falling edge of clk_active
						enable <= '0';
						cs <= '1';
						rxDataReady <= '1';
						state <= S_IDLE;
					
					else 
						enable <= '1';
						cs <= '0';
						if(byte_flag = '1') then
							rxDataReady <= '1';
							tx_buffer <= txData;
						end if;
					
					end if;
						
				when others => null;
				
				
			end case;
			
			
		end if;
		
	end process;
	
	cs_out <= cs;
	sclk_out <= sclk;
	
	
	
	
	process (clk, sclk, cs, rst)--, state)
	
	begin
		
		if( rst = '1') then
			bit <= 7;
			mosi <= '1';
		--else
		elsif(clk'event and clk = '1') then
		last_cs <= cs;
		last_sclk <= sclk;  --clk version
			if(cs = '0' and last_cs = '1' ) then
				
				w_r <= not pha;				--pha 1 goes to write and pha 0 goes to read
				
				if(pha = '0') then
					mosi <= tx_buffer(bit); --write	
				end if;
				
			elsif(cs = '0' and (last_sclk /= sclk)) then									-- this point on are only clk events high or low
				
				if(w_r = '0') 	then				-- write
					mosi <= tx_buffer(bit);
					
				elsif (w_r = '1') then		-- read
					rx_buffer <= rx_buffer(6 downto 0) & miso;
					bit <= bit - 1;			-- only decrement after reads
					if(bit = 0) then			-- reset bit to 7 at end of byte instead of decrementing
						bit <= 7;
						--rxData <= rx_buffer;
					end if;
				else 
					null;							-- do nothing
				end if;
				
				w_r <= not w_r;				-- toggle write/read for next clock edge
				
			else 
				--mosi <= 'Z';
				null;
			end if;
			
			if(bit = 7) then
				rxData <= rx_buffer;
			end if;
			
		end if;
	
	
	
	end process;
	

	--rxData <= rx_buffer;
end FSM_1P;

// VHDL entity spi_accelerometer, as the project stores it:
--top_level.vhd
library ieee;
use ieee.std_logic_1164.all;

entity spi_accelerometer is
	port(
		clk50MHz : in std_logic;
		rst 		: in std_logic;
		mosi		: out std_logic;
		miso 		: in std_logic;
		sclk 		: out std_logic;
		cs 		: out std_logic;
		
		accel_input 		: in std_logic;
		enable_accel : in std_logic;

		accel: out std_logic_vector (47 downto 0)
	);
	
end spi_accelerometer;


architecture STR of spi_accelerometer is

	
	signal go : std_logic;
	signal pol : std_logic;
	signal pha : std_logic;
	signal bytes : std_logic_vector (3 downto 0);
	signal rxData : std_logic_vector (7 downto 0);
	signal rxDataReady	: std_logic := '0';
	signal txData 		:		 std_logic_vector (7 downto 0);
	signal accel_data	:		 std_logic_vector (47 downto 0);-- := (others => '0');
	
	signal sclk_out : std_logic;
	
	signal sclk_buffer	:	std_logic;
	signal mosi_buffer	:	std_logic;
	signal cs_buffer	:	std_logic;
	signal int1_buffer : std_logic;
	signal stateID : std_logic_vector(2 downto 0);
	
	COMPONENT spi_master IS
		port (
		clk	: in std_logic;
		rst	: in std_logic;
      	mosi	: out std_logic;
		miso 	: in std_logic;
		sclk_out : out std_logic; 
		cs_out	: out std_logic;
		accel_input 	: in std_logic;
		int2 	: in std_logic;
		go		: in std_logic;
		pol	: in std_logic;
		pha   : in std_logic;
		bytes : in std_logic_vector (3 downto 0);
		rxData: out std_logic_vector(7 downto 0);
		txData: in  std_logic_vector(7 downto 0);
		rxDataReady: out std_logic
		);
	END COMPONENT;

	COMPONENT clock_div IS
		port (
		clk_in : in std_logic;
			clk_out : out std_logic;
			rst	: in std_logic;
			enable : in std_logic;
			bytes : in std_logic_vector(3 downto 0);
			polarity : in std_logic;
			clk_active :	out std_logic;
			byte_flag : out std_logic
		);
	END COMPONENT;

	COMPONENT accel_driver IS
		port (
		rst			:		in std_logic;
		clk			:		in std_logic;
		accel_input			:		in std_logic;
		rxDataReady	:		in	std_logic;
		go				:		out std_logic;
		pol			:		out std_logic;
		pha			:		out std_logic;
		bytes 		:		out std_logic_vector (3 downto 0);
		txData 		:		out std_logic_vector (7 downto 0);
		rxData		: 		in std_logic_vector ( 7 downto 0);
		accel_data	:		out std_logic_vector (47 downto 0);
		
		stateID 		:      out std_logic_vector (2 downto 0);
		c				: out std_logic;
		enable_accel   : in std_logic
        	);
	END COMPONENT;
begin

	------------------------------------
	--SPI MASTER
	------------------------------------
	U_SPI_MASTER	:  spi_master
		port map(
		clk	=> clk50MHz,
		rst	=> rst,
      	mosi	=> mosi_buffer,
		miso 	=> miso,
		sclk_out => sclk_out,
		cs_out	=> cs_buffer,
		accel_input 	=> '0',
		int2 	=> '0',
		go		=> go,
		pol	=> pol,
		pha   => pha,
		bytes => bytes,
		rxData	=> rxData,
		txData	=> txData,
		rxDataReady	=> rxDataReady
	);
	
	mosi <= mosi_buffer;
	cs <= cs_buffer;
	sclk <= sclk_buffer;
	
	U_ACCEL_DRIVER : accel_driver
		port map(
			rst			=> rst,
			clk			=> clk50MHz,
			accel_input			=> int1_buffer,
			rxDataReady	=> rxDataReady,
			go				=> go,
			pol			=> pol,
			pha			=> pha,
			bytes 		=> bytes,
			txData 		=> txData,
			rxData		=> rxData,
			accel_data	=> accel_data,
			stateID => stateID,
			enable_accel => enable_accel
		);

	accel <= accel_data(47 downto 0);
	
	process(clk50MHz, rst)
	begin
	
		if(rst = '1') then
			sclk_buffer <= '1';
			int1_buffer <= '0';
		elsif(clk50MHz'event and clk50MHz = '1') then
			sclk_buffer <= sclk_out;
			int1_buffer <= accel_input;
		end if;
	end process;
	
end STR;

// VHDL entity hex_to_decimal, as the project stores it:
--------------------------------------------------------------------------------
-- Project :
-- File    :
-- Autor   :
-- Date    :
--
--------------------------------------------------------------------------------
-- Description :
--
--------------------------------------------------------------------------------

LIBRARY ieee;
USE ieee.std_logic_1164.all;

ENTITY hex_to_decimal IS
  PORT (
  --Insert input ports below
    val        : IN  std_logic_vector(7 DOWNTO 0); -- input vector example
  ------------------------------------------------------------------------------
  --Insert output ports below
    hundreds        : OUT std_logic_vector(3 DOWNTO 0);  -- output vector example
    tens        	: OUT std_logic_vector(3 DOWNTO 0);
    ones			: OUT std_logic_vector(3 DOWNTO 0)
    );
END hex_to_decimal;

--------------------------------------------------------------------------------
--Complete your VHDL description below
--------------------------------------------------------------------------------

ARCHITECTURE TypeArchitecture OF hex_to_decimal IS
	signal cmpt_2 : std_logic_vector(33 DOWNTO 0);
	signal cmpt_3 : std_logic_vector(33 DOWNTO 0);
	signal cmpt_4 : std_logic_vector(33 DOWNTO 0);
	signal cmpt_5 : std_logic_vector(33 DOWNTO 0);
	signal cmpt_6 : std_logic_vector(33 DOWNTO 0);
	signal no_hundos : std_logic_vector(33 DOWNTO 0);
	
	signal div_one_hundos : std_logic_vector(16 DOWNTO 0);
	signal div_one_hundo : std_logic_vector(15 DOWNTO 0) := X"0148";

	signal times_one_hundos : std_logic_vector(16 DOWNTO 0);
	signal times_one_hundo : std_logic_vector(15 DOWNTO 0) := X"0064";
	
	signal tenners : std_logic_vector(16 DOWNTO 0);
	signal ten : std_logic_vector(15 DOWNTO 0) := X"0CCD";

	signal times_tenner : std_logic_vector(16 DOWNTO 0);
	signal times_ten : std_logic_vector(15 DOWNTO 0) := X"000a";

	signal shift_2 : unsigned(33 DOWNTO 0);
	signal shift_4 : unsigned(33 DOWNTO 0);
	signal shift_5 : unsigned(33 DOWNTO 0);
	signal final_answer_sig : std_logic_vector(7 DOWNTO 0);
	signal hundreds_digit : std_logic_vector(3 DOWNTO 0);
	signal tens_digit : std_logic_vector(3 DOWNTO 0);
BEGIN
	final_answer_sig <= val;
	div_one_hundos <= '0' & div_one_hundo;
	tenners <= '0' & ten;
	times_one_hundos <= '0' & times_one_hundo;
	times_tenner <= '0' & times_ten;

	process (val)
	begin
		cmpt_2 <= std_logic_vector(('0' & X"00" & unsigned(final_answer_sig)) * unsigned(div_one_hundos));
		shift_2 <= shift_right(unsigned(cmpt_2), 15);
		hundreds <= std_logic_vector(shift_2(3 downto 0));
		hundreds_digit <= std_logic_vector(shift_2(3 downto 0));

		cmpt_3 <= std_logic_vector(unsigned('0' & '0' & X"000000" & final_answer_sig) - unsigned('0' & X"000" & hundreds_digit) * unsigned(times_one_hundos));
		no_hundos <= cmpt_3;
		cmpt_4 <= std_logic_vector(unsigned('0' & X"00" & cmpt_3(7 downto 0)) * unsigned(tenners));
		shift_4 <= shift_right(unsigned(cmpt_4), 15);
		tens <= std_logic_vector(shift_4(3 downto 0));
		tens_digit <= std_logic_vector(shift_4(3 downto 0));

		cmpt_5 <= std_logic_vector(unsigned(no_hundos) - unsigned('0' & X"000" & tens_digit) * unsigned(times_tenner));
		ones <= std_logic_vector(cmpt_5(3 downto 0));
		
	end process;

END TypeArchitecture;

// VHDL entity divide_two_num, as the project stores it:
--------------------------------------------------------------------------------
-- Project :
-- File    :
-- Autor   :
-- Date    :
--
--------------------------------------------------------------------------------
-- Description :
--
--------------------------------------------------------------------------------

LIBRARY ieee;
USE ieee.std_logic_1164.all;
use ieee.numeric_std.all;

ENTITY divide_two_num IS
  PORT (
  ------------------------------------------------------------------------------
  --Insert input ports below
    val        : IN  std_logic_vector(15 DOWNTO 0); -- input vector example
    val2        : IN  std_logic_vector(15 DOWNTO 0);
  ------------------------------------------------------------------------------
  --Insert output ports below
    final_answer	: OUT std_logic_vector(7 DOWNTO 0);
    final_answer_sixteen_bits	: OUT std_logic_vector(15 DOWNTO 0)
    );
END divide_two_num;

--------------------------------------------------------------------------------
--Complete your VHDL description below
--------------------------------------------------------------------------------

ARCHITECTURE TypeArchitecture OF divide_two_num IS
	signal cmpt_1 : std_logic_vector(33 DOWNTO 0);
	signal input1_sig : std_logic_vector(16 DOWNTO 0);
	signal input2_sig : std_logic_vector(16 DOWNTO 0);
	signal shift_1 : unsigned(33 DOWNTO 0);
	
BEGIN
	input1_sig <= '0' & val;
	input2_sig <= '0' & val2;
	

	process (val, val2)
	begin

		cmpt_1 <= std_logic_vector(unsigned(input1_sig) * unsigned(input2_sig));
		shift_1 <= shift_right(unsigned(cmpt_1), 15);
		final_answer <= std_logic_vector(shift_1(7 downto 0));
		final_answer_sixteen_bits <= std_logic_vector(shift_1(15 downto 0));
		
	end process;

END TypeArchitecture;

// VHDL entity hex_to_decimal_16_bits, as the project stores it:
--------------------------------------------------------------------------------
-- Project :
-- File    :
-- Autor   :
-- Date    :
--
--------------------------------------------------------------------------------
-- Description :
--
--------------------------------------------------------------------------------

LIBRARY ieee;
USE ieee.std_logic_1164.all;

ENTITY hex_to_decimal_16_bits IS
  PORT (
  --Insert input ports below
    val        : IN  std_logic_vector(15 DOWNTO 0); -- input vector example
  ------------------------------------------------------------------------------
  --Insert output ports below
    hundreds        : OUT std_logic_vector(3 DOWNTO 0);  -- output vector example
    tens        	: OUT std_logic_vector(3 DOWNTO 0);
    ones			: OUT std_logic_vector(3 DOWNTO 0)
    );
END hex_to_decimal_16_bits;

--------------------------------------------------------------------------------
--Complete your VHDL description below
--------------------------------------------------------------------------------

ARCHITECTURE TypeArchitecture OF hex_to_decimal_16_bits IS
	signal cmpt_2 : std_logic_vector(33 DOWNTO 0);
	signal cmpt_3 : std_logic_vector(33 DOWNTO 0);
	signal cmpt_4 : std_logic_vector(33 DOWNTO 0);
	signal cmpt_5 : std_logic_vector(33 DOWNTO 0);
	signal cmpt_6 : std_logic_vector(33 DOWNTO 0);
	signal no_hundos : std_logic_vector(33 DOWNTO 0);
	
	signal div_one_hundos : std_logic_vector(16 DOWNTO 0);
	signal div_one_hundo : std_logic_vector(15 DOWNTO 0) := X"0148";

	signal times_one_hundos : std_logic_vector(16 DOWNTO 0);
	signal times_one_hundo : std_logic_vector(15 DOWNTO 0) := X"0064";
	
	signal tenners : std_logic_vector(16 DOWNTO 0);
	signal ten : std_logic_vector(15 DOWNTO 0) := X"0CCD";

	signal times_tenner : std_logic_vector(16 DOWNTO 0);
	signal times_ten : std_logic_vector(15 DOWNTO 0) := X"000a";

	signal shift_2 : unsigned(33 DOWNTO 0);
	signal shift_4 : unsigned(33 DOWNTO 0);
	signal shift_5 : unsigned(33 DOWNTO 0);
	signal final_answer_sig : std_logic_vector(15 DOWNTO 0);
	signal hundreds_digit : std_logic_vector(3 DOWNTO 0);
	signal tens_digit : std_logic_vector(3 DOWNTO 0);
BEGIN
	final_answer_sig <= val;
	div_one_hundos <= '0' & div_one_hundo;
	tenners <= '0' & ten;
	times_one_hundos <= '0' & times_one_hundo;
	times_tenner <= '0' & times_ten;

	process (val)
	begin
		cmpt_2 <= std_logic_vector(('0' & unsigned(final_answer_sig)) * unsigned(div_one_hundos));
		shift_2 <= shift_right(unsigned(cmpt_2), 15);
		hundreds <= std_logic_vector(shift_2(3 downto 0));
		hundreds_digit <= std_logic_vector(shift_2(3 downto 0));

		cmpt_3 <= std_logic_vector(unsigned('0' & '0' & X"0000" & final_answer_sig) - unsigned('0' & X"000" & hundreds_digit) * unsigned(times_one_hundos));
		no_hundos <= cmpt_3;
		cmpt_4 <= std_logic_vector(unsigned('0' & X"00" & cmpt_3(7 downto 0)) * unsigned(tenners));
		shift_4 <= shift_right(unsigned(cmpt_4), 15);
		tens <= std_logic_vector(shift_4(3 downto 0));
		tens_digit <= std_logic_vector(shift_4(3 downto 0));

		cmpt_5 <= std_logic_vector(unsigned(no_hundos) - unsigned('0' & X"000" & tens_digit) * unsigned(times_tenner));
		ones <= std_logic_vector(cmpt_5(3 downto 0));
		
	end process;

END TypeArchitecture;
