// Logisim project accelerometer_ADXL345_all_circuits.circ as structural Verilog
module show_directions_and_angle (
  input  rst,
  input  miso,
  input  accel_input,
  input  enable_accel,
  output mosi,
  output sclk,
  output cs
);

  wire angle_checker_one_axis_1_l, angle_checker_one_axis_1_m, angle_checker_one_axis_1_s,
       angle_checker_one_axis_2_l, angle_checker_one_axis_2_m, angle_checker_one_axis_2_s, DOWN_within_range,
       LEFT_within_range, or_1_out, or_2_out, RIGHT1_within_range, RIGHT2_within_range, right_force_1_l,
       right_force_1_m, right_force_1_s, UP1_within_range, UP2_within_range;
  wire [15:0] x, y;
  wire [47:32] ADXL345_CHIP_accelerometer;

  accel_main_driver ADXL345_CHIP (
    .rst(rst), .miso(miso), .accel_input(accel_input), .enable_accel(enable_accel), .mosi(mosi), .sclk(sclk),
    .cs(cs), .Accelerometer({ADXL345_CHIP_accelerometer, y, x}));
  in_range LEFT (.Number_to_check(x), .Lower_bound(16'h4d), .Higher_bound(16'hd4), .within_range(LEFT_within_range));
  in_range RIGHT1 (
    .Number_to_check(x), .Lower_bound({16{1'b0}}), .Higher_bound(16'h2d), .within_range(RIGHT1_within_range));
  in_range RIGHT2 (
    .Number_to_check(x), .Lower_bound(16'hffba), .Higher_bound({16{1'b1}}), .within_range(RIGHT2_within_range));
  in_range DOWN (.Number_to_check(y), .Lower_bound(16'h4d), .Higher_bound(16'hd4), .within_range(DOWN_within_range));
  in_range UP1 (.Number_to_check(y), .Lower_bound({16{1'b0}}), .Higher_bound(16'h2d), .within_range(UP1_within_range));
  in_range UP2 (
    .Number_to_check(y), .Lower_bound(16'hffba), .Higher_bound({16{1'b1}}), .within_range(UP2_within_range));
  angle_checker_one_axis angle_checker_one_axis_1 (
    .AXIS(x), .SLB1(16'h4d), .SHB1(16'h7a), .MLB1(16'h7a), .MHB1(16'ha7), .LLB1(16'ha7), .LHB1(16'hd4),
    .SLB2({16{1'b0}}), .SHB2(16'h2d), .MLB2(16'hffd2), .MHB2({16{1'b1}}), .LLB2(16'hffba), .LHB2(16'hffd2),
    .S(angle_checker_one_axis_1_s), .M(angle_checker_one_axis_1_m), .L(angle_checker_one_axis_1_l));
  angle_checker_one_axis angle_checker_one_axis_2 (
    .AXIS(y), .SLB1(16'h4d), .SHB1(16'h7a), .MLB1(16'h7a), .MHB1(16'ha7), .LLB1(16'ha7), .LHB1(16'hd4),
    .SLB2({16{1'b0}}), .SHB2(16'h2d), .MLB2(16'hffd2), .MHB2({16{1'b1}}), .LLB2(16'hffba), .LHB2(16'hffd2),
    .S(angle_checker_one_axis_2_s), .M(angle_checker_one_axis_2_m), .L(angle_checker_one_axis_2_l));
  or or_1 (or_1_out, RIGHT1_within_range, RIGHT2_within_range);
  or or_2 (or_2_out, UP1_within_range, UP2_within_range);
  sevenseg_directions_output sevenseg_directions_output_1 (.L(LEFT_within_range), .R(or_1_out));  // open: U, D, S, M
  sevenseg_directions_output sevenseg_directions_output_2 (.U(or_2_out), .D(DOWN_within_range));  // open: L, R, S, M
  right_force right_force_1 (
    .S1(angle_checker_one_axis_1_s), .S2(angle_checker_one_axis_2_s), .M1(angle_checker_one_axis_1_m),
    .M2(angle_checker_one_axis_2_m), .L1(angle_checker_one_axis_1_l), .L2(angle_checker_one_axis_2_l),
    .S(right_force_1_s), .M(right_force_1_m), .L(right_force_1_l));
  sevenseg_directions_output sevenseg_directions_output_3 (
    .L(right_force_1_l), .S(right_force_1_s), .M(right_force_1_m));  // open: R, U, D

  // Notes on the sheet:
  //   Left/Down angle
  //   Left/Down range
  //   Right/Up range
  //   Right/Up angle
endmodule

module angle_checker_one_axis (
  input  [15:0] AXIS,
  input  [15:0] SLB1,
  input  [15:0] SHB1,
  input  [15:0] MLB1,
  input  [15:0] MHB1,
  input  [15:0] LLB1,
  input  [15:0] LHB1,
  input  [15:0] SLB2,
  input  [15:0] SHB2,
  input  [15:0] MLB2,
  input  [15:0] MHB2,
  input  [15:0] LLB2,
  input  [15:0] LHB2,
  output S,
  output M,
  output L
);

  wire angle_checker_1_l, angle_checker_1_m, angle_checker_1_s, angle_checker_2_l, angle_checker_2_m,
       angle_checker_2_s;

  angle_checker angle_checker_1 (
    .NUMBER_TO_CHECK(AXIS), .SLB(SLB1), .SHB(SHB1), .MLB(MLB1), .MHB(MHB1), .LLB(LLB1), .LHB(LHB1),
    .S(angle_checker_1_s), .M(angle_checker_1_m), .L(angle_checker_1_l));
  angle_checker angle_checker_2 (
    .NUMBER_TO_CHECK(AXIS), .SLB(SLB2), .SHB(SHB2), .MLB(MLB2), .MHB(MHB2), .LLB(LLB2), .LHB(LHB2),
    .S(angle_checker_2_s), .M(angle_checker_2_m), .L(angle_checker_2_l));
  or or_1 (S, angle_checker_1_s, angle_checker_2_s);
  or or_2 (M, angle_checker_1_m, angle_checker_2_m);
  or or_3 (L, angle_checker_1_l, angle_checker_2_l);
endmodule

module angle_checker (
  input  [15:0] NUMBER_TO_CHECK,
  input  [15:0] SLB,
  input  [15:0] SHB,
  input  [15:0] MLB,
  input  [15:0] MHB,
  input  [15:0] LLB,
  input  [15:0] LHB,
  output S,
  output M,
  output L
);

  in_range SMALL_ANGLE (.Number_to_check(NUMBER_TO_CHECK), .Lower_bound(SLB), .Higher_bound(SHB), .within_range(S));
  in_range MEDIUM_ANGLE (.Number_to_check(NUMBER_TO_CHECK), .Lower_bound(MLB), .Higher_bound(MHB), .within_range(M));
  in_range LARGE_ANGLE (.Number_to_check(NUMBER_TO_CHECK), .Lower_bound(LLB), .Higher_bound(LHB), .within_range(L));
endmodule

module right_force (
  input  S1,
  input  S2,
  input  M1,
  input  M2,
  input  L1,
  input  L2,
  output S,
  output M,
  output L
);

  wire and_1_out, and_2_out, and_3_out, and_4_out, and_5_out, and_6_out, and_7_out, not_1_out, not_2_out,
       not_3_out, not_4_out, not_5_out, not_6_out;

  not not_1 (not_1_out, S1);
  not not_2 (not_2_out, S2);
  not not_3 (not_3_out, M1);
  not not_4 (not_4_out, M2);
  not not_5 (not_5_out, L1);
  not not_6 (not_6_out, L2);
  and and_1 (and_1_out, S2, not_3_out, not_4_out, not_5_out, not_6_out);
  and and_2 (and_2_out, S1, not_3_out, not_4_out, not_5_out, not_6_out);
  and and_3 (and_3_out, not_3_out, M2, not_5_out, not_6_out);
  and and_4 (and_4_out, M1, not_4_out, not_5_out, not_6_out);
  and and_5 (and_5_out, S2, M2, not_5_out, not_6_out);
  and and_6 (and_6_out, S1, M1, not_5_out, not_6_out);
  and and_7 (and_7_out, not_1_out, not_2_out, M1, M2);
  or or_1 (S, and_1_out, and_2_out);
  or or_2 (M, and_3_out, and_4_out, and_5_out, and_6_out);
  or or_3 (L, L2, L1, and_7_out);
endmodule

module print_accel_values (
  input  rst,
  input  miso,
  input  accel_input,
  input  enable_accel,
  output mosi,
  output sclk,
  output cs
);

  wire [1:0] SELECTOR;
  wire [3:0] multiplexer_1_out, multiplexer_2_out, multiplexer_3_out, multiplexer_4_out;
  wire [47:0] ADXL345_CHIP_accelerometer;

  DipSwitch #(.number(2)) AXIS_SELECTOR (.sw1(SELECTOR[0]), .sw2(SELECTOR[1]));
  accel_main_driver ADXL345_CHIP (
    .rst(rst), .miso(miso), .accel_input(accel_input), .enable_accel(enable_accel), .mosi(mosi), .sclk(sclk),
    .cs(cs), .Accelerometer(ADXL345_CHIP_accelerometer));
  Multiplexer #(.select(2), .width(4)) multiplexer_1 (
    .in0(ADXL345_CHIP_accelerometer[3:0]), .in1(ADXL345_CHIP_accelerometer[19:16]),
    .in2(ADXL345_CHIP_accelerometer[35:32]), .out(multiplexer_1_out), .sel(SELECTOR));  // open: in3
  sevenseg_accel_output HEX0 (.Input_bus_1(multiplexer_1_out));
  Multiplexer #(.select(2), .width(4)) multiplexer_2 (
    .in0(ADXL345_CHIP_accelerometer[7:4]), .in1(ADXL345_CHIP_accelerometer[23:20]),
    .in2(ADXL345_CHIP_accelerometer[39:36]), .out(multiplexer_2_out), .sel(SELECTOR));  // open: in3
  sevenseg_accel_output HEX1 (.Input_bus_1(multiplexer_2_out));
  Multiplexer #(.select(2), .width(4)) multiplexer_3 (
    .in0(ADXL345_CHIP_accelerometer[11:8]), .in1(ADXL345_CHIP_accelerometer[27:24]),
    .in2(ADXL345_CHIP_accelerometer[43:40]), .out(multiplexer_3_out), .sel(SELECTOR));  // open: in3
  sevenseg_accel_output HEX2 (.Input_bus_1(multiplexer_3_out));
  Multiplexer #(.select(2), .width(4)) multiplexer_4 (
    .in0(ADXL345_CHIP_accelerometer[15:12]), .in1(ADXL345_CHIP_accelerometer[31:28]),
    .in2(ADXL345_CHIP_accelerometer[47:44]), .out(multiplexer_4_out), .sel(SELECTOR));  // open: in3
  sevenseg_accel_output HEX3 (.Input_bus_1(multiplexer_4_out));
endmodule

module accel_main_driver (
  input  rst,
  input  miso,
  input  accel_input,
  input  enable_accel,
  output mosi,
  output sclk,
  output cs,
  output [47:0] Accelerometer
);

  wire clock_1_out;

  Clock clock_1 (.out(clock_1_out));
  spi_accelerometer spi_accelerometer_1 (
    .clk50MHz(clock_1_out), .rst(rst), .miso(miso), .accel_input(accel_input), .enable_accel(enable_accel),
    .mosi(mosi), .sclk(sclk), .cs(cs), .accel(Accelerometer));
  accel_driver accel_driver_1 (
    .rst(1'b0), .clk(1'b0), .accel_input(1'b0), .rxDataReady(1'b0), .rxData({8{1'b0}}), .enable_accel(1'b0));  // open: go, pol, pha, bytes, txData, accel_data, stateID, c
  spi_master spi_master_1 (
    .clk(1'b0), .rst(1'b0), .miso(1'b0), .accel_input(1'b0), .int2(1'b0), .go(1'b0), .pol(1'b0), .pha(1'b0),
    .bytes(4'b0000), .txData({8{1'b0}}));  // open: mosi, sclk_out, cs_out, rxData, rxDataReady
  clock_div clock_div_1 (
    .clk_in(1'b0), .rst(1'b0), .enable(1'b0), .bytes(4'b0000), .polarity(1'b0));  // open: clk_out, clk_active, byte_flag
endmodule

module in_range (
  input  [15:0] Number_to_check,
  input  [15:0] Lower_bound,
  input  [15:0] Higher_bound,
  output within_range
);

  wire or_1_out, or_2_out, sixteen_bits_comparator_1_a_bigger_than_b, sixteen_bits_comparator_1_a_equals_b,
       sixteen_bits_comparator_2_a_equals_b, sixteen_bits_comparator_2_a_less_than_b;

  sixteen_bits_comparator sixteen_bits_comparator_1 (
    .A(Number_to_check), .B(Lower_bound), .A_equals_B(sixteen_bits_comparator_1_a_equals_b),
    .A_bigger_than_B(sixteen_bits_comparator_1_a_bigger_than_b));  // open: A_less_than_B
  sixteen_bits_comparator sixteen_bits_comparator_2 (
    .A(Number_to_check), .B(Higher_bound), .A_less_than_B(sixteen_bits_comparator_2_a_less_than_b),
    .A_equals_B(sixteen_bits_comparator_2_a_equals_b));  // open: A_bigger_than_B
  or or_1 (or_1_out, sixteen_bits_comparator_1_a_equals_b, sixteen_bits_comparator_1_a_bigger_than_b);
  or or_2 (or_2_out, sixteen_bits_comparator_2_a_less_than_b, sixteen_bits_comparator_2_a_equals_b);
  and and_1 (within_range, or_1_out, or_2_out);
endmodule

module sevenseg_accel_logic (
  input  [3:0] accel,
  output [7:0] sevensegment
);

  wire and_1_out, and_2_out, and_3_out, and_4_out, and_5_out, and_6_out, and_7_out, and_8_out, and_9_out,
       and_10_out, and_11_out, and_12_out, and_13_out, and_14_out, and_15_out, and_16_out, and_17_out,
       and_18_out, and_19_out, and_20_out, and_21_out, and_22_out, and_23_out, and_24_out, and_25_out,
       and_26_out, and_27_out, and_28_out, and_29_out, and_30_out, and_31_out, and_32_out, and_33_out,
       and_34_out, and_35_out, and_36_out, not_1_out, not_2_out, not_3_out, not_4_out;

  not not_1 (not_1_out, accel[3]);
  not not_2 (not_2_out, accel[2]);
  not not_3 (not_3_out, accel[1]);
  not not_4 (not_4_out, accel[0]);
  and and_1 (and_1_out, not_2_out, accel[1]);
  and and_2 (and_2_out, accel[1], not_4_out);
  and and_3 (and_3_out, not_1_out, accel[2], not_3_out);
  and and_4 (and_4_out, accel[3], not_2_out);
  and and_5 (and_5_out, accel[3], accel[0]);
  and and_6 (and_6_out, not_3_out, not_4_out);
  and and_7 (and_7_out, not_1_out, accel[2], not_3_out);
  and and_8 (and_8_out, accel[2], not_4_out);
  and and_9 (and_9_out, accel[3], not_2_out);
  and and_10 (and_10_out, accel[3], accel[1]);
  and and_11 (and_11_out, not_2_out, not_4_out);
  and and_12 (and_12_out, accel[1], not_4_out);
  and and_13 (and_13_out, accel[3], accel[1]);
  and and_14 (and_14_out, accel[3], accel[2]);
  and and_15 (and_15_out, not_1_out, not_2_out, not_4_out);
  and and_16 (and_16_out, not_1_out, accel[1], not_4_out);
  and and_17 (and_17_out, not_2_out, accel[1], accel[0]);
  and and_18 (and_18_out, accel[2], not_3_out, accel[0]);
  and and_19 (and_19_out, accel[3], not_3_out);
  and and_20 (and_20_out, accel[3], accel[2], not_4_out);
  and and_21 (and_21_out, not_1_out, not_3_out);
  and and_22 (and_22_out, not_1_out, accel[0]);
  and and_23 (and_23_out, not_3_out, accel[0]);
  and and_24 (and_24_out, not_1_out, accel[2]);
  and and_25 (and_25_out, accel[3], not_2_out);
  and and_26 (and_26_out, not_1_out, not_2_out);
  and and_27 (and_27_out, not_1_out, not_3_out, not_4_out);
  and and_28 (and_28_out, not_2_out, not_4_out);
  and and_29 (and_29_out, not_1_out, accel[1], accel[0]);
  and and_30 (and_30_out, accel[3], not_3_out, accel[0]);
  and and_31 (and_31_out, not_2_out, not_4_out);
  and and_32 (and_32_out, not_1_out, accel[1]);
  and and_33 (and_33_out, not_1_out, accel[2], accel[0]);
  and and_34 (and_34_out, accel[2], accel[1]);
  and and_35 (and_35_out, accel[3], not_2_out, not_3_out);
  and and_36 (and_36_out, accel[3], not_4_out);
  or or_1 (sevensegment[6], and_1_out, and_2_out, and_3_out, and_4_out, and_5_out);
  or or_2 (sevensegment[5], and_6_out, and_7_out, and_8_out, and_9_out, and_10_out);
  or or_3 (sevensegment[4], and_11_out, and_12_out, and_13_out, and_14_out);
  or or_4 (sevensegment[3], and_15_out, and_16_out, and_17_out, and_18_out, and_19_out, and_20_out);
  or or_5 (sevensegment[2], and_21_out, and_22_out, and_23_out, and_24_out, and_25_out);
  or or_6 (sevensegment[1], and_26_out, and_27_out, and_28_out, and_29_out, and_30_out);
  or or_7 (sevensegment[0], and_31_out, and_32_out, and_33_out, and_34_out, and_35_out, and_36_out);

  assign sevensegment[7] = 1'b0;
endmodule

module sevenseg_accel_output (
  input  [3:0] Input_bus_1
);

  wire [7:0] sevenseg_1_sevensegment;

  sevenseg_accel_logic sevenseg_1 (.accel(Input_bus_1), .sevensegment(sevenseg_1_sevensegment));
  _7_Segment_Display L_7_Segment_Display_1 (
    .g(sevenseg_1_sevensegment[6]), .f(sevenseg_1_sevensegment[5]), .a(sevenseg_1_sevensegment[0]),
    .b(sevenseg_1_sevensegment[1]), .e(sevenseg_1_sevensegment[4]), .d(sevenseg_1_sevensegment[3]),
    .c(sevenseg_1_sevensegment[2]), .dp(sevenseg_1_sevensegment[7]));
endmodule

module sevenseg_directions_logic (
  input  L,
  input  R,
  input  U,
  input  D,
  input  S,
  input  M,
  output [7:0] letter_output
);

  wire and_1_out, and_2_out, and_3_out, and_4_out, and_5_out, and_6_out, and_7_out, and_8_out, and_9_out,
       and_10_out, and_11_out, and_12_out, and_13_out, and_14_out, and_15_out, and_16_out, and_17_out,
       and_18_out, and_19_out, and_20_out, and_21_out, and_22_out, and_23_out, and_24_out, and_25_out,
       not_1_out, not_2_out, not_3_out, not_4_out, not_5_out, not_6_out;

  not not_1 (not_1_out, L);
  not not_2 (not_2_out, R);
  not not_3 (not_3_out, U);
  not not_4 (not_4_out, D);
  not not_5 (not_5_out, S);
  not not_6 (not_6_out, M);
  and and_1 (and_1_out, not_1_out, not_2_out, not_3_out, not_4_out, S, not_6_out);
  and and_2 (and_2_out, not_1_out, not_2_out, not_3_out, D, not_5_out, not_6_out);
  and and_3 (and_3_out, not_1_out, R, not_3_out, not_4_out, not_5_out, not_6_out);
  and and_4 (and_4_out, not_1_out, not_2_out, not_3_out, not_4_out, not_5_out, M);
  and and_5 (and_5_out, not_1_out, not_2_out, not_3_out, not_4_out, S, not_6_out);
  and and_6 (and_6_out, not_1_out, not_2_out, U, not_4_out, not_5_out, not_6_out);
  and and_7 (and_7_out, L, not_2_out, not_3_out, not_4_out, not_5_out, not_6_out);
  and and_8 (and_8_out, not_1_out, not_2_out, not_3_out, not_4_out, not_5_out, M);
  and and_9 (and_9_out, not_1_out, not_2_out, not_3_out, D, not_5_out, not_6_out);
  and and_10 (and_10_out, not_1_out, not_2_out, U, not_4_out, not_5_out, not_6_out);
  and and_11 (and_11_out, not_1_out, R, not_3_out, not_4_out, not_5_out, not_6_out);
  and and_12 (and_12_out, L, not_2_out, not_3_out, not_4_out, not_5_out, not_6_out);
  and and_13 (and_13_out, not_1_out, not_2_out, not_3_out, not_4_out, S, not_6_out);
  and and_14 (and_14_out, not_1_out, not_2_out, not_3_out, D, not_5_out, not_6_out);
  and and_15 (and_15_out, not_1_out, not_2_out, U, not_4_out, not_5_out, not_6_out);
  and and_16 (and_16_out, L, not_2_out, not_3_out, not_4_out, not_5_out, not_6_out);
  and and_17 (and_17_out, not_1_out, not_2_out, not_3_out, not_4_out, not_5_out, M);
  and and_18 (and_18_out, not_1_out, not_2_out, not_3_out, not_4_out, S, not_6_out);
  and and_19 (and_19_out, not_1_out, not_2_out, not_3_out, D, not_5_out, not_6_out);
  and and_20 (and_20_out, not_1_out, not_2_out, U, not_4_out, not_5_out, not_6_out);
  and and_21 (and_21_out, not_1_out, not_2_out, not_3_out, not_4_out, not_5_out, M);
  and and_22 (and_22_out, not_1_out, not_2_out, not_3_out, D, not_5_out, not_6_out);
  and and_23 (and_23_out, not_1_out, not_2_out, U, not_4_out, not_5_out, not_6_out);
  and and_24 (and_24_out, not_1_out, not_2_out, not_3_out, not_4_out, not_5_out, M);
  and and_25 (and_25_out, not_1_out, not_2_out, not_3_out, not_4_out, S, not_6_out);
  or or_1 (letter_output[6], and_1_out, and_2_out, and_3_out);
  or or_2 (letter_output[5], and_4_out, and_5_out, and_6_out, and_7_out);
  or or_3 (letter_output[4], and_8_out, and_9_out, and_10_out, and_11_out, and_12_out);
  or or_4 (letter_output[3], and_13_out, and_14_out, and_15_out, and_16_out);
  or or_5 (letter_output[2], and_17_out, and_18_out, and_19_out, and_20_out);
  or or_6 (letter_output[1], and_21_out, and_22_out, and_23_out);
  or or_7 (letter_output[0], and_24_out, and_25_out);

  assign letter_output[7] = 1'b0;
endmodule

module sevenseg_directions_output (
  input  L,
  input  R,
  input  U,
  input  D,
  input  S,
  input  M
);

  wire [7:0] sevenseg_directions_output_letter_output;

  sevenseg_directions_logic sevenseg_directions_output (
    .L(L), .R(R), .U(U), .D(D), .S(S), .M(M), .letter_output(sevenseg_directions_output_letter_output));
  _7_Segment_Display HEX (
    .g(sevenseg_directions_output_letter_output[6]), .f(sevenseg_directions_output_letter_output[5]),
    .a(sevenseg_directions_output_letter_output[0]), .b(sevenseg_directions_output_letter_output[1]),
    .e(sevenseg_directions_output_letter_output[4]), .d(sevenseg_directions_output_letter_output[3]),
    .c(sevenseg_directions_output_letter_output[2]), .dp(sevenseg_directions_output_letter_output[7]));
endmodule

module sixteen_bits_comparator (
  input  [15:0] A,
  input  [15:0] B,
  output A_less_than_B,
  output A_equals_B,
  output A_bigger_than_B
);

  wire Bigger_Row_0, Bigger_Row_1, Bigger_Row_2, Equals_Row_0, Equals_Row_1, Equals_Row_2, Less_Row_0,
       Less_Row_1, Less_Row_2, one_bits_comparator_1_a_bigger_than_b, one_bits_comparator_1_a_equals_b,
       one_bits_comparator_1_a_less_than_b, one_bits_with_inputs_2_a_bigger_than_b_output,
       one_bits_with_inputs_2_a_equals_b_output, one_bits_with_inputs_2_a_less_than_b_output,
       one_bits_with_inputs_3_a_bigger_than_b_output, one_bits_with_inputs_3_a_equals_b_output,
       one_bits_with_inputs_3_a_less_than_b_output, one_bits_with_inputs_5_a_bigger_than_b_output,
       one_bits_with_inputs_5_a_equals_b_output, one_bits_with_inputs_5_a_less_than_b_output,
       one_bits_with_inputs_6_a_bigger_than_b_output, one_bits_with_inputs_6_a_equals_b_output,
       one_bits_with_inputs_6_a_less_than_b_output, one_bits_with_inputs_7_a_bigger_than_b_output,
       one_bits_with_inputs_7_a_equals_b_output, one_bits_with_inputs_7_a_less_than_b_output,
       one_bits_with_inputs_9_a_bigger_than_b_output, one_bits_with_inputs_9_a_equals_b_output,
       one_bits_with_inputs_9_a_less_than_b_output, one_bits_with_inputs_10_a_bigger_than_b_output,
       one_bits_with_inputs_10_a_equals_b_output, one_bits_with_inputs_10_a_less_than_b_output,
       one_bits_with_inputs_11_a_bigger_than_b_output, one_bits_with_inputs_11_a_equals_b_output,
       one_bits_with_inputs_11_a_less_than_b_output, one_bits_with_inputs_13_a_bigger_than_b_output,
       one_bits_with_inputs_13_a_equals_b_output, one_bits_with_inputs_13_a_less_than_b_output,
       one_bits_with_inputs_14_a_bigger_than_b_output, one_bits_with_inputs_14_a_equals_b_output,
       one_bits_with_inputs_14_a_less_than_b_output, one_bits_with_inputs_15_a_bigger_than_b_output,
       one_bits_with_inputs_15_a_equals_b_output, one_bits_with_inputs_15_a_less_than_b_output;

  one_bits_comparator one_bits_comparator_1 (
    .A(A[0]), .B(B[0]), .A_less_than_B(one_bits_comparator_1_a_less_than_b),
    .A_equals_B(one_bits_comparator_1_a_equals_b), .A_bigger_than_B(one_bits_comparator_1_a_bigger_than_b));
  one_bits_with_inputs one_bits_with_inputs_7 (
    .A(A[4]), .B(B[4]), .A_less_B_input(Less_Row_0), .A_equal_B_input(Equals_Row_0),
    .A_bigger_than_B_input(Bigger_Row_0), .A_less_than_B_output(one_bits_with_inputs_7_a_less_than_b_output),
    .A_equals_B_output(one_bits_with_inputs_7_a_equals_b_output),
    .A_bigger_than_B_output(one_bits_with_inputs_7_a_bigger_than_b_output));
  one_bits_with_inputs one_bits_with_inputs_11 (
    .A(A[8]), .B(B[8]), .A_less_B_input(Less_Row_1), .A_equal_B_input(Equals_Row_1),
    .A_bigger_than_B_input(Bigger_Row_1),
    .A_less_than_B_output(one_bits_with_inputs_11_a_less_than_b_output),
    .A_equals_B_output(one_bits_with_inputs_11_a_equals_b_output),
    .A_bigger_than_B_output(one_bits_with_inputs_11_a_bigger_than_b_output));
  one_bits_with_inputs one_bits_with_inputs_15 (
    .A(A[12]), .B(B[12]), .A_less_B_input(Less_Row_2), .A_equal_B_input(Equals_Row_2),
    .A_bigger_than_B_input(Bigger_Row_2),
    .A_less_than_B_output(one_bits_with_inputs_15_a_less_than_b_output),
    .A_equals_B_output(one_bits_with_inputs_15_a_equals_b_output),
    .A_bigger_than_B_output(one_bits_with_inputs_15_a_bigger_than_b_output));
  one_bits_with_inputs one_bits_with_inputs_3 (
    .A(A[1]), .B(B[1]), .A_less_B_input(one_bits_comparator_1_a_less_than_b),
    .A_equal_B_input(one_bits_comparator_1_a_equals_b),
    .A_bigger_than_B_input(one_bits_comparator_1_a_bigger_than_b),
    .A_less_than_B_output(one_bits_with_inputs_3_a_less_than_b_output),
    .A_equals_B_output(one_bits_with_inputs_3_a_equals_b_output),
    .A_bigger_than_B_output(one_bits_with_inputs_3_a_bigger_than_b_output));
  one_bits_with_inputs one_bits_with_inputs_6 (
    .A(A[5]), .B(B[5]), .A_less_B_input(one_bits_with_inputs_7_a_less_than_b_output),
    .A_equal_B_input(one_bits_with_inputs_7_a_equals_b_output),
    .A_bigger_than_B_input(one_bits_with_inputs_7_a_bigger_than_b_output),
    .A_less_than_B_output(one_bits_with_inputs_6_a_less_than_b_output),
    .A_equals_B_output(one_bits_with_inputs_6_a_equals_b_output),
    .A_bigger_than_B_output(one_bits_with_inputs_6_a_bigger_than_b_output));
  one_bits_with_inputs one_bits_with_inputs_10 (
    .A(A[9]), .B(B[9]), .A_less_B_input(one_bits_with_inputs_11_a_less_than_b_output),
    .A_equal_B_input(one_bits_with_inputs_11_a_equals_b_output),
    .A_bigger_than_B_input(one_bits_with_inputs_11_a_bigger_than_b_output),
    .A_less_than_B_output(one_bits_with_inputs_10_a_less_than_b_output),
    .A_equals_B_output(one_bits_with_inputs_10_a_equals_b_output),
    .A_bigger_than_B_output(one_bits_with_inputs_10_a_bigger_than_b_output));
  one_bits_with_inputs one_bits_with_inputs_14 (
    .A(A[13]), .B(B[13]), .A_less_B_input(one_bits_with_inputs_15_a_less_than_b_output),
    .A_equal_B_input(one_bits_with_inputs_15_a_equals_b_output),
    .A_bigger_than_B_input(one_bits_with_inputs_15_a_bigger_than_b_output),
    .A_less_than_B_output(one_bits_with_inputs_14_a_less_than_b_output),
    .A_equals_B_output(one_bits_with_inputs_14_a_equals_b_output),
    .A_bigger_than_B_output(one_bits_with_inputs_14_a_bigger_than_b_output));
  one_bits_with_inputs one_bits_with_inputs_2 (
    .A(A[2]), .B(B[2]), .A_less_B_input(one_bits_with_inputs_3_a_less_than_b_output),
    .A_equal_B_input(one_bits_with_inputs_3_a_equals_b_output),
    .A_bigger_than_B_input(one_bits_with_inputs_3_a_bigger_than_b_output),
    .A_less_than_B_output(one_bits_with_inputs_2_a_less_than_b_output),
    .A_equals_B_output(one_bits_with_inputs_2_a_equals_b_output),
    .A_bigger_than_B_output(one_bits_with_inputs_2_a_bigger_than_b_output));
  one_bits_with_inputs one_bits_with_inputs_5 (
    .A(A[6]), .B(B[6]), .A_less_B_input(one_bits_with_inputs_6_a_less_than_b_output),
    .A_equal_B_input(one_bits_with_inputs_6_a_equals_b_output),
    .A_bigger_than_B_input(one_bits_with_inputs_6_a_bigger_than_b_output),
    .A_less_than_B_output(one_bits_with_inputs_5_a_less_than_b_output),
    .A_equals_B_output(one_bits_with_inputs_5_a_equals_b_output),
    .A_bigger_than_B_output(one_bits_with_inputs_5_a_bigger_than_b_output));
  one_bits_with_inputs one_bits_with_inputs_9 (
    .A(A[10]), .B(B[10]), .A_less_B_input(one_bits_with_inputs_10_a_less_than_b_output),
    .A_equal_B_input(one_bits_with_inputs_10_a_equals_b_output),
    .A_bigger_than_B_input(one_bits_with_inputs_10_a_bigger_than_b_output),
    .A_less_than_B_output(one_bits_with_inputs_9_a_less_than_b_output),
    .A_equals_B_output(one_bits_with_inputs_9_a_equals_b_output),
    .A_bigger_than_B_output(one_bits_with_inputs_9_a_bigger_than_b_output));
  one_bits_with_inputs one_bits_with_inputs_13 (
    .A(A[14]), .B(B[14]), .A_less_B_input(one_bits_with_inputs_14_a_less_than_b_output),
    .A_equal_B_input(one_bits_with_inputs_14_a_equals_b_output),
    .A_bigger_than_B_input(one_bits_with_inputs_14_a_bigger_than_b_output),
    .A_less_than_B_output(one_bits_with_inputs_13_a_less_than_b_output),
    .A_equals_B_output(one_bits_with_inputs_13_a_equals_b_output),
    .A_bigger_than_B_output(one_bits_with_inputs_13_a_bigger_than_b_output));
  one_bits_with_inputs one_bits_with_inputs_1 (
    .A(A[3]), .B(B[3]), .A_less_B_input(one_bits_with_inputs_2_a_less_than_b_output),
    .A_equal_B_input(one_bits_with_inputs_2_a_equals_b_output),
    .A_bigger_than_B_input(one_bits_with_inputs_2_a_bigger_than_b_output), .A_less_than_B_output(Less_Row_0),
    .A_equals_B_output(Equals_Row_0), .A_bigger_than_B_output(Bigger_Row_0));
  one_bits_with_inputs one_bits_with_inputs_4 (
    .A(A[7]), .B(B[7]), .A_less_B_input(one_bits_with_inputs_5_a_less_than_b_output),
    .A_equal_B_input(one_bits_with_inputs_5_a_equals_b_output),
    .A_bigger_than_B_input(one_bits_with_inputs_5_a_bigger_than_b_output), .A_less_than_B_output(Less_Row_1),
    .A_equals_B_output(Equals_Row_1), .A_bigger_than_B_output(Bigger_Row_1));
  one_bits_with_inputs one_bits_with_inputs_8 (
    .A(A[11]), .B(B[11]), .A_less_B_input(one_bits_with_inputs_9_a_less_than_b_output),
    .A_equal_B_input(one_bits_with_inputs_9_a_equals_b_output),
    .A_bigger_than_B_input(one_bits_with_inputs_9_a_bigger_than_b_output), .A_less_than_B_output(Less_Row_2),
    .A_equals_B_output(Equals_Row_2), .A_bigger_than_B_output(Bigger_Row_2));
  one_bits_with_inputs one_bits_with_inputs_12 (
    .A(A[15]), .B(B[15]), .A_less_B_input(one_bits_with_inputs_13_a_less_than_b_output),
    .A_equal_B_input(one_bits_with_inputs_13_a_equals_b_output),
    .A_bigger_than_B_input(one_bits_with_inputs_13_a_bigger_than_b_output),
    .A_less_than_B_output(A_less_than_B), .A_equals_B_output(A_equals_B),
    .A_bigger_than_B_output(A_bigger_than_B));

  // Other names for the same wires on the sheet: A0[3:0] = A[3:0]; A1[3:0] = A[7:4]; A2[3:0] = A[11:8];
  //   A3[3:0] = A[15:12]; B0[3:0] = B[3:0]; B1[3:0] = B[7:4]; B2[3:0] = B[11:8]; B3[3:0] = B[15:12]
endmodule

module one_bits_comparator (
  input  A,
  input  B,
  output A_less_than_B,
  output A_equals_B,
  output A_bigger_than_B
);

  wire and_2_out, and_3_out, not_1_out, not_2_out;

  not not_1 (not_1_out, A);
  not not_2 (not_2_out, B);
  and and_1 (A_less_than_B, not_1_out, B);
  and and_2 (and_2_out, not_1_out, not_2_out);
  and and_3 (and_3_out, A, B);
  and and_4 (A_bigger_than_B, A, not_2_out);
  or or_1 (A_equals_B, and_2_out, and_3_out);
endmodule

module one_bits_with_inputs (
  input  A,
  input  B,
  input  A_less_B_input,
  input  A_equal_B_input,
  input  A_bigger_than_B_input,
  output A_less_than_B_output,
  output A_equals_B_output,
  output A_bigger_than_B_output
);

  wire and_1_out, and_2_out, and_3_out, and_4_out, and_5_out, and_7_out, not_1_out, not_2_out, or_1_out;

  not not_1 (not_1_out, A);
  not not_2 (not_2_out, B);
  and and_1 (and_1_out, not_1_out, B);
  and and_2 (and_2_out, not_1_out, not_2_out);
  and and_3 (and_3_out, A, B);
  and and_4 (and_4_out, A, not_2_out);
  or or_1 (or_1_out, and_2_out, and_3_out);
  and and_5 (and_5_out, or_1_out, A_less_B_input);
  and and_6 (A_equals_B_output, or_1_out, A_equal_B_input);
  and and_7 (and_7_out, or_1_out, A_bigger_than_B_input);
  or or_2 (A_less_than_B_output, and_1_out, and_5_out);
  or or_3 (A_bigger_than_B_output, and_4_out, and_7_out);
endmodule

// VHDL entity spi_accelerometer, as the project stores it:
--top_level.vhd
library ieee;
use ieee.std_logic_1164.all;

entity spi_accelerometer is
	port(
		clk50MHz : in std_logic;
		rst 		: in std_logic;
		mosi		: out std_logic;
		miso 		: in std_logic;
		sclk 		: out std_logic;
		cs 		: out std_logic;
		
		accel_input 		: in std_logic;
		enable_accel : in std_logic;
		
		accel: out std_logic_vector (47 downto 0)
	);
	
end spi_accelerometer;


architecture STR of spi_accelerometer is

	
	signal go : std_logic;
	signal pol : std_logic;
	signal pha : std_logic;
	signal bytes : std_logic_vector (3 downto 0);
	signal rxData : std_logic_vector (7 downto 0);
	signal rxDataReady	: std_logic := '0';
	signal txData 		:		 std_logic_vector (7 downto 0);
	signal accel_data	:		 std_logic_vector (47 downto 0);-- := (others => '0');
	
	signal sclk_out : std_logic;
	
	signal sclk_buffer	:	std_logic;
	signal mosi_buffer	:	std_logic;
	signal cs_buffer	:	std_logic;
	signal int1_buffer : std_logic;
	signal stateID : std_logic_vector(2 downto 0);
	
	COMPONENT spi_master IS
		port (
		clk	: in std_logic;
		rst	: in std_logic;
      	mosi	: out std_logic;
		miso 	: in std_logic;
		sclk_out : out std_logic; 
		cs_out	: out std_logic;
		accel_input 	: in std_logic;
		int2 	: in std_logic;
		go		: in std_logic;
		pol	: in std_logic;
		pha   : in std_logic;
		bytes : in std_logic_vector (3 downto 0);
		rxData: out std_logic_vector(7 downto 0);
		txData: in  std_logic_vector(7 downto 0);
		rxDataReady: out std_logic
		);
	END COMPONENT;

	COMPONENT clock_div IS
		port (
		clk_in : in std_logic;
			clk_out : out std_logic;
			rst	: in std_logic;
			enable : in std_logic;
			bytes : in std_logic_vector(3 downto 0);
			polarity : in std_logic;
			clk_active :	out std_logic;
			byte_flag : out std_logic
		);
	END COMPONENT;

	COMPONENT accel_driver IS
		port (
		rst			:		in std_logic;
		clk			:		in std_logic;
		accel_input			:		in std_logic;
		rxDataReady	:		in	std_logic;
		go				:		out std_logic;
		pol			:		out std_logic;
		pha			:		out std_logic;
		bytes 		:		out std_logic_vector (3 downto 0);
		txData 		:		out std_logic_vector (7 downto 0);
		rxData		: 		in std_logic_vector ( 7 downto 0);
		accel_data	:		out std_logic_vector (47 downto 0);
		
		stateID 		:      out std_logic_vector (2 downto 0);
		c				: out std_logic;
		enable_accel   : in std_logic
        	);
	END COMPONENT;
begin

	------------------------------------
	--SPI MASTER
	------------------------------------
	U_SPI_MASTER	:  spi_master
		port map(
		clk	=> clk50MHz,
		rst	=> rst,
      	mosi	=> mosi_buffer,
		miso 	=> miso,
		sclk_out => sclk_out,
		cs_out	=> cs_buffer,
		accel_input 	=> '0',
		int2 	=> '0',
		go		=> go,
		pol	=> pol,
		pha   => pha,
		bytes => bytes,
		rxData	=> rxData,
		txData	=> txData,
		rxDataReady	=> rxDataReady
	);
	
	mosi <= mosi_buffer;
	cs <= cs_buffer;
	sclk <= sclk_buffer;
	
	U_ACCEL_DRIVER : accel_driver
		port map(
			rst			=> rst,
			clk			=> clk50MHz,
			accel_input			=> int1_buffer,
			rxDataReady	=> rxDataReady,
			go				=> go,
			pol			=> pol,
			pha			=> pha,
			bytes 		=> bytes,
			txData 		=> txData,
			rxData		=> rxData,
			accel_data	=> accel_data,
			stateID => stateID,
			enable_accel => enable_accel
		);

	accel <= accel_data(47 downto 0);
	
	process(clk50MHz, rst)
	begin
	
		if(rst = '1') then
			sclk_buffer <= '1';
			int1_buffer <= '0';
		elsif(clk50MHz'event and clk50MHz = '1') then
			sclk_buffer <= sclk_out;
			int1_buffer <= accel_input;
		end if;
	end process;
	
end STR;

// VHDL entity spi_master, as the project stores it:
--spi_master

library ieee;
use ieee.std_logic_1164.all;
use ieee.numeric_std.all;

entity spi_master is
    port (
		clk	: in std_logic;
		rst	: in std_logic;
      mosi	: out std_logic;
		miso 	: in std_logic;
		sclk_out : out std_logic; 
		cs_out	: out std_logic;
		accel_input 	: in std_logic;
		int2 	: in std_logic;
		go		: in std_logic;
		pol	: in std_logic;
		pha   : in std_logic;
		bytes : in std_logic_vector (3 downto 0);
		rxData: out std_logic_vector(7 downto 0);
		txData: in  std_logic_vector(7 downto 0);
		rxDataReady: out std_logic
		);
end spi_master;


architecture FSM_1P of spi_master is


------------------------------------
-- State signals
------------------------------------
type STATE_TYPE is (S_IDLE, S_TXRX);
signal state, next_state : STATE_TYPE;


------------------------------------
-- Clock Div (spi clock) Signals
------------------------------------
signal sclk : std_logic;
signal enable : std_logic := '0';
--signal bytes : std_logic_vector (3 downto 0);
signal polarity : std_logic;
signal last_clk_active : std_logic;
signal clk_active : std_logic;
signal byte_flag : std_logic;

------------------------------------
-- SPI Data Signals
------------------------------------
signal rx_buffer	: std_logic_vector (7 downto 0) := (others => '1');
signal tx_buffer	: std_logic_vector (7 downto 0);
signal cs : std_logic := '1';
constant byte_w : natural := 8;
signal bit : integer range -1 to 8 := 7; --init to msb+1 idx
signal w_r : std_logic := '0'; --write = 0 read = 1
signal phase_Delay : std_logic := '0';
signal last_cs : std_logic := '1';
signal last_sclk : std_logic := '0';

COMPONENT clock_div IS
		port (
		clk_in : in std_logic;
			clk_out : out std_logic;
			rst	: in std_logic;
			enable : in std_logic;
			bytes : in std_logic_vector(3 downto 0);
			polarity : in std_logic;
			clk_active :	out std_logic;
			byte_flag : out std_logic
		);
	END COMPONENT;

begin


	U_CLOCK_DIV : clock_div
		port map(
			clk_in => clk,
			clk_out => sclk,
			rst	=> rst,
			enable => enable,
			bytes	=> bytes,
			polarity => polarity,
			clk_active => clk_active,
			byte_flag => byte_flag);



	--enable <= int1 or int2 or go;
	
	process (clk, rst)
	begin
		
		if(rst = '1') then
			state <= S_IDLE;
			last_clk_active <= '0';
			enable <= '0';
			cs <= '1';
		elsif (clk'event and clk = '1') then
			
	
		--process(state, int1, int2, go, clk_active, byte_flag)--, txData)
		--begin
		
			rxDataReady <= '0'; --only high when data is ready
			polarity <= pol;
			--w_r <= not pha; --first write for phase 1 is pre toggled. 0 is default
		--	next_state <= state;
			enable <= '0';
			
			last_clk_active <= clk_active;
			
			case state is
				when S_IDLE =>
					
					--enable <= '0'; --default 
					cs <= '1';
					if((accel_input = '1' or int2 = '1' or go = '1') and rst = '0') then
						state <= S_TXRX;
	--					polarity <= pol;
	--					w_r <= not pha; --first write for phase 1 is pre toggled. 0 is default
						enable <= '1';
						cs <= '0';
						tx_buffer <= txData; --TEST
						
					end if;
				
				
				when S_TXRX =>
					
					
					enable <= '1';
					
					if(last_clk_active = '1' and clk_active = '0') then  --falling edge of clk_active
						enable <= '0';
						cs <= '1';
						rxDataReady <= '1';
						state <= S_IDLE;
					
					else 
						enable <= '1';
						cs <= '0';
						if(byte_flag = '1') then
							rxDataReady <= '1';
							tx_buffer <= txData;
						end if;
					
					end if;
						
				when others => null;
				
				
			end case;
			
			
		end if;
		
	end process;
	
	cs_out <= cs;
	sclk_out <= sclk;
	
	
	
	
	process (clk, sclk, cs, rst)--, state)
	
	begin
		
		if( rst = '1') then
			bit <= 7;
			mosi <= '1';
		--else
		elsif(clk'event and clk = '1') then
		last_cs <= cs;
		last_sclk <= sclk;  --clk version
			if(cs = '0' and last_cs = '1' ) then
				
				w_r <= not pha;				--pha 1 goes to write and pha 0 goes to read
				
				if(pha = '0') then
					mosi <= tx_buffer(bit); --write	
				end if;
				
			elsif(cs = '0' and (last_sclk /= sclk)) then									-- this point on are only clk events high or low
				
				if(w_r = '0') 	then				-- write
					mosi <= tx_buffer(bit);
					
				elsif (w_r = '1') then		-- read
					rx_buffer <= rx_buffer(6 downto 0) & miso;
					bit <= bit - 1;			-- only decrement after reads
					if(bit = 0) then			-- reset bit to 7 at end of byte instead of decrementing
						bit <= 7;
						--rxData <= rx_buffer;
					end if;
				else 
					null;							-- do nothing
				end if;
				
				w_r <= not w_r;				-- toggle write/read for next clock edge
				
			else 
				--mosi <= 'Z';
				null;
			end if;
			
			if(bit = 7) then
				rxData <= rx_buffer;
			end if;
			
		end if;
	
	
	
	end process;
	

	--rxData <= rx_buffer;
end FSM_1P;

// VHDL entity clock_div, as the project stores it:
--clock div
library ieee;
use ieee.std_logic_1164.all;
use ieee.numeric_std.all;

entity clock_div is
	port (
			clk_in : in std_logic;
			clk_out : out std_logic;
			rst	: in std_logic;
			enable : in std_logic;
			bytes : in std_logic_vector(3 downto 0);
			polarity : in std_logic;
			clk_active :	out std_logic;
			byte_flag : out std_logic
			);
end clock_div;

architecture bhv of clock_div is

	constant clk_in_freq : natural := 4;
	constant clk_out_freq: natural := 2;
	constant max : natural := clk_in_freq / clk_out_freq / 2;
	signal count, lastByteCount : integer range 0 to max*2;
	signal clock_signal : std_logic;
	signal byte_count : std_logic_vector (3 downto 0);
	signal bit_count : integer range 0 to 8;
	
	
	
	
	begin
	
		process(clk_in, rst)
		begin
			if(rst = '1' or enable = '0') then
				count <= 0;
				lastByteCount <= 0;
				clk_active <= '0';
				clock_signal <= polarity;
				bit_count <= 0;
				byte_count <= (others => '0');
				byte_flag <= '0';
			
			elsif(clk_in'event and clk_in = '1') then
				if(enable = '1' and byte_count < bytes) then
				
					clk_active <= '1';
					if (count = max-1) then
						count <= 0;
						clock_signal <= not clock_signal;
						
						if((not clock_signal) = polarity) then
							--increment bit count
							--increment byte count after 8 bits and clean bit count
							--clear byte count after numOfBytes and clear active_clk
							
							byte_flag <= '0'; -- clear the byte flag
						
							if(bit_count = 7) then
								byte_count <= std_logic_vector(unsigned(byte_count) + 1);
								bit_count <= 0;
								byte_flag <= '1'; --set byte flag for one sclk cycle
								
								if( byte_count = std_logic_vector(unsigned(bytes) - 1)) then
									--clk_active <= '0';
									--clock_signal <=  clock_signal; --do not toggle clock 
									
								end if;
							
								
							else
								bit_count <= bit_count + 1;
							end if;
							
--							if( byte_count = bytes) then
--								clk_active <= '0';
--							end if;
							
						end if;
					else
						count <= count + 1;
					end if;
				
			
				elsif(enable = '1') then
			
					clk_active <= '1';
						if (lastByteCount = max-1) then
							lastByteCount <= 0;
							clk_active <= '0';
						else
							lastByteCount <= lastByteCount + 1;
						end if;
				end if;
				
				
				
			end if;
		
		
--			if(rst = '1' or enable = '0') then
--				count <= 0;
--				lastByteCount <= 0;
--				clk_active <= '0';
--				clock_signal <= polarity;
--				bit_count <= 0;
--				byte_count <= (others => '0');
--				byte_flag <= '0';
--			
--			elsif(rising_edge(clk_in) and enable = '1' and byte_count < bytes) then
--				
--					clk_active <= '1';
--					if (count = max-1) then
--						count <= 0;
--						clock_signal <= not clock_signal;
--						
--						if((not clock_signal) = polarity) then
--							--increment bit count
--							--increment byte count after 8 bits and clean bit count
--							--clear byte count after numOfBytes and clear active_clk
--							
--							byte_flag <= '0'; -- clear the byte flag
--						
--							if(bit_count = 7) then
--								byte_count <= std_logic_vector(unsigned(byte_count) + 1);
--								bit_count <= 0;
--								byte_flag <= '1'; --set byte flag for one cycle
--								
--								if( byte_count = std_logic_vector(unsigned(bytes) - 1)) then
--									--clk_active <= '0';
--									--clock_signal <=  clock_signal; --do not toggle clock 
--									
--								end if;
--							
--								
--							else
--								bit_count <= bit_count + 1;
--							end if;
--							
----							if( byte_count = bytes) then
----								clk_active <= '0';
----							end if;
--							
--						end if;
--					else
--						count <= count + 1;
--					end if;
--				
--			
--			elsif(rising_edge(clk_in) and enable = '1') then
--			
--				clk_active <= '1';
--					if (lastByteCount = max-1) then
--						lastByteCount <= 0;
--						clk_active <= '0';
--					else
--						lastByteCount <= lastByteCount + 1;
--					end if;
--				
--				
--				
--			end if;
		--clk_out <= clock_signal;
		end process;
		
		clk_out <= clock_signal;




end bhv;

// VHDL entity accel_driver, as the project stores it:
--accel_driver
-- TODO:
-- 1) Incorporate data range generic for calibration LSB/g for z axis
library ieee;
use ieee.std_logic_1164.all;
use ieee.numeric_std.all;

entity accel_driver is
	port (
		rst			:		in std_logic;
		clk			:		in std_logic;
		accel_input			:		in std_logic;
		rxDataReady	:		in	std_logic;
		go				:		out std_logic;
		pol			:		out std_logic;
		pha			:		out std_logic;
		bytes 		:		out std_logic_vector (3 downto 0);
		txData 		:		out std_logic_vector (7 downto 0);
		rxData		: 		in std_logic_vector ( 7 downto 0);
		accel_data	:		out std_logic_vector (47 downto 0);
		
		stateID 		:      out std_logic_vector (2 downto 0);
		c				: out std_logic;
		enable_accel   : in std_logic
		
		
	);
end accel_driver;



architecture fsm_1p of accel_driver is
	
	constant max	: natural := 50000000 /  500000 ;
	signal count			:		integer range 0 to max;
	signal countSignal		: std_logic;
	type STATE_TYPE is (S_START, S_IDLE, S_CONFIG, S_WRITE, S_READ, S_READ_WAIT, S_CALIBRATE, S_OUTPUT); --S_CONFIG_TEST, S_WRITE_TEST);
	signal STATE, NEXT_STATE			:		STATE_TYPE;
	--signal accel_x, accel_y, accel_z	:		std_logic_vector(15 downto 0);
	signal accel_data_buff : std_logic_vector( 47 downto 0);
	signal byteCount	: integer range -1 to 16 := 0;
	constant byteCountRead : integer := 7;
	signal mode			: std_logic;
	signal reg	: integer range 0 to 8;
	signal regTest : integer range 0 to 16;
	signal regAddr		: std_logic_vector (5 downto 0);
	signal regData		: std_logic_vector (7 downto 0);
	signal rxDataReadyLast : std_logic := '0';
	
	constant sampleBits : natural := 4;
	constant samples  : natural := 2 ** sampleBits;
	--signal div_padding : std_logic_vector (sampleBits - 1 downto 0);
	signal sample_count : integer range 0 to samples + 1;
	signal calibrate : std_logic;
	--type NIBBLE is array (3 downto 0) of std_ulogic;
	type calibration_array is array (2 downto 0) of std_logic_vector (15 downto 0);  -- (0) X accumulate, (1) Y accumulate, (2) Z accumulate
	signal calibData : calibration_array;
	
begin




	process(clk, rst)
	begin
		if(rst = '1') then
			state <= S_START;
			accel_data <= (others => '0');
			accel_data_buff <= (others => '0');
			regData <= "00000000";
			regAddr <= "000000";
			bytes <= "0000";
			txData <= "00000000";
			mode <= '0';
			count <= 0;
			go <= '0';
			reg <= 0;
			regTest <= 0;
			byteCount <= 0;
			stateID <= "000";
			calibrate <= '0';
			calibData(0) <= (others => '0');
			calibData(1) <= (others => '0');
			calibData(2) <= (others => '0');
			sample_count <= 0;
			--div_padding <= (others => '0');
			
		elsif(clk'event and clk = '1') then
			
			
			
			case state is
			
				when S_START =>
					byteCount <= 0;
					mode <= '0';
					reg <= 0;
					rxDataReadyLast <= '0';
					state <= S_IDLE;
					accel_data <= (others => '0');
					go <= '0';
					
					stateID <= "001";
				
				when S_IDLE =>
					stateID <= "010";
					--if(mode = '1' and int1 = '1') then state <= S_READ;
					--end if;
		
					if(count = max - 1) then							-- delay between each transmission 
						--count <= 0;
						c <= '1';
						
						if(mode = '0') then
							state <= S_CONFIG;		-- mode 0 is config. after config mode goes to 1 for read
							count <= 0; 
						--elsif(int1 = '1')   then
						else
							state <= S_READ_WAIT;	-- mode 1, but only read if interrupt for data_ready is set
							count <= 0;
						--else count <= max - 1;							-- do not set count to 0 to prevent running the delay loop again
						end if;	
			
					else 
						count <= count + 1;
						c <= '0';
					end if;
					
--					if(intBypass = '1') then state <= S_IDLE;
--					end if;
			
				when S_READ_WAIT =>
					stateID <= "111";
					if (calibrate = '1') then state <= S_CALIBRATE;
					elsif(accel_input = '1' or enable_accel = '1') then state <= S_READ;
					end if;
					
				when S_CALIBRATE => 
					case reg is								-- reg should be 0 from config state earlier, represents each offset register
						when 0 =>							-- calculate the negative of x and y offset. subtract 256 (1g) from z and shift 2 (8 bit conversion)
							if(calibData(0)(15) = '0') then  -- x axis negative conversion
								calibData(0) <= std_logic_vector(signed(not calibData(0)) + 1);	-- twos comp conversion from positive to negative
							else
								calibData(0) <= std_logic_vector(not(signed(calibData(0)) - 1));  -- twos comp conversion from negative to positive
							end if;
							
							if(calibData(1)(15) = '0') then -- y axis negative conversion
								calibData(1) <= std_logic_vector(signed(not calibData(1)) + 1);	-- twos comp conversion from positive to negative
							else
								calibData(1) <= std_logic_vector(not(signed(calibData(1)) - 1));  -- twos comp conversion from negative to positive
							end if;
							
							calibData(2) <=std_logic_vector(shift_right(signed(calibData(2)) - 256, 2));	-- find error realtive to gravity in z axis and divide by 4 for 10 to 8 bit conversion			
							reg <= reg + 1;
						
						when 1 =>																					-- calculate Z's negative, store x axis
						
							if(calibData(2)(15) = '0') then 													-- Z axis negative conversion
								calibData(2) <= std_logic_vector(signed(not calibData(2)) + 1);	-- twos comp conversion from positive to negative
							else
								calibData(2) <= std_logic_vector(not(signed(calibData(2)) - 1));  -- twos comp conversion from negative to positive
							end if;
							
							regAddr <= "011110";																	-- Register 0x1E: "X offset" 8 bit 2's comp offset for X axis
							regData <= calibData(0)(7 downto 0);															-- X offset data
							reg <= reg + 1;	
							state  <= S_WRITE;
						when 2 =>
							regAddr <= "011111";																	-- Register 0x1F: "Y offset" 8 bit 2's comp offset for Y axis
							regData <= calibData(1)(7 downto 0);
							reg <= reg + 1;
							state  <= S_WRITE;
						when 3 =>
							regAddr <= "100000";																	-- Register 0x20: "Z offset" 8 bit 2's comp offset for Z axis
							regData <= calibData(2)(7 downto 0);
							reg <= 0;
							state  <= S_WRITE;
							calibrate <= '0';																		-- de-assert calibration flag to continue reading normally
						when others => null;
						
					end case;
				
				when S_CONFIG =>
						stateID <= "011";
					case reg is
						when 0 =>
							regAddr <= "110001"; -- Register 0x31: "Data_Format" sets data range (0b00) to +/- 2g and full resultion (0b1000)
							regData <= "00001000";   
							reg <= reg + 1;
							state <= S_WRITE;
						when 1 => 
							regAddr <= "101100";  -- Register 0x2C: "BW_RATE" sets rate (0b0100) to 1.56 Hz, ideal should be 100hz which is default at power reset, but too fast for 7seg's
							regData <= "00000100";
							reg <= reg + 1;
							state <= S_WRITE;
						when 2 =>
							regAddr <= "011110";					-- Register 0x1E: "X offset" 8 bit 2's comp offset for X axis
							regData <= "00000000";				-- Clear X offset register so calibration will not use data from previous resets
							reg <= reg + 1;
							state  <= S_WRITE;
							
						when 3 =>
							regAddr <= "011111";					-- Register 0x1F: "Y offset" 8 bit 2's comp offset for Y axis
							regData <= "00000000";				-- Clear Y offset register so calibration will not use data from previous resets
							reg <= reg + 1;
							state  <= S_WRITE;
						
						when 4 =>
							regAddr <= "100000";					-- Register 0x20: "Z offset" 8 bit 2's comp offset for Z axis
							regData <= "00000000";				-- Clear Z offset register so calibration will not use data from previous resets
							reg <= reg + 1;
							state  <= S_WRITE;
						
						when 5 => 
							regAddr <= "101101";	 -- Register 0x2D: "Power_CTL" sets measure bit (0b1000) to start sampling. 
							regData <= "00001000";
							reg <= reg + 1;
							state <= S_WRITE;
							--mode <= '1';			-- Switch to Read mode so IDLE turns to S_READ and not S_CONFIG
						when 6 => 
							regAddr <= "101110";	 -- Register 0x2E: "INT_ENABLE" enables Data_Ready interrupt (0b10000000) 
							regData <= "10000000";
							reg <= 0;
							state <= S_WRITE;
							mode <= '1';			-- Switch to Read mode so IDLE turns to S_READ and not S_CONFIG
						when others => null;
					end case;
				
				when S_WRITE =>
					stateID <= "100";
					bytes <= "0010";
					rxDataReadyLast <= rxDataReady;
					if(byteCount = 0) then
						txData <= "00" & regAddr;
						go <= '1';
						byteCount <= 1;
					--elsif(rising_edge(rxDataReady) and byteCount = 1) then
					elsif((rxDataReadyLast = '0' and rxDataReady = '1') and byteCount = 1) then  -- rising edge
						byteCount <= 2;
						go <= '0';
						txData <= regData;
					elsif((rxDataReadyLast = '0' and rxDataReady = '1') and byteCount = 2) then  -- rising edge, nothing is transmitted here
						byteCount <= 3;
							
						
					elsif((rxDataReadyLast = '1' and rxDataReady = '0') and byteCount = 3) then  --falling edge
						state <= S_IDLE;
						byteCount <= 0;
					end if;
				--00111101 00001000
				when S_READ =>
					stateID <= "101";
					
					mode <= '1';
					bytes <= std_logic_vector(to_unsigned(byteCountRead, bytes'length));
					rxDataReadyLast <= rxDataReady;
					if(byteCount = 0) then														-- Send Read Command
						txData <= "11110010";
						go <= '1';
						byteCount <= 1;
					elsif(byteCount = 1) then													--next system clock enters here
						txData <= "00000000";							
						go <= '0';
						if((rxDataReadyLast = '1' and rxDataReady = '0')) then		--wait until 8 bits are sent to update byte count 
							byteCount <= 2;
						end if;
						
					else																				--read bytes 2 3 4 5 6 and 7
						txData <= "00000000";
						go <= '0';
						
						if((rxDataReadyLast = '1' and rxDataReady = '0') and byteCount <= byteCountRead) then
	--						byteCount <= byteCount + 1;
	--						accel_data_buff((byteCount * 8)  - 1 downto (byteCount-1) * 8) <= rxData;
	--						if(byteCount = byteCountRead - 1) then
	--							byteCount <= 0;
	--							next_state <= S_OUTPUT;
	--						end if;
							if(byteCount = byteCountRead) then
								byteCount <= 0;
								state <= S_OUTPUT;
							else
								byteCount <= byteCount + 1;
								accel_data_buff(((byteCount-1) * 8)  - 1 downto (byteCount-2) * 8) <=  rxData;-- std_logic_vector(to_unsigned(byteCount, bytes'length)); -- rxData;
							end if;


						end if;
						
						
					end if;
				when S_OUTPUT =>
					stateID <= "110";
					
					if(sample_count <= samples) then				-- enter for first n samples for calibration
						if(sample_count = samples) then			-- compare sample count to threshold 
							calibrate <= '1';							-- set flag to calibrate with new values
							calibData(0) <= std_logic_vector(shift_right(signed(calibData(0)), 2 + sampleBits)); -- divide by number of samples for average, and convert to 64 LSB/1g (shifting a 10 bit value right arithmetically for an 8 bit value)
							calibData(1) <= std_logic_vector(shift_right(signed(calibData(1)), 2 + sampleBits));
							calibData(2) <= std_logic_vector(shift_right(signed(calibData(2)), sampleBits)); -- get average. Next clock cycle will compare to 1g (2^8), and then convert to 64 LSB/1g
						else 												-- summation of samples
							calibData(0) <= std_logic_vector(signed(calibData(0)) + signed(accel_data_buff(15 downto   0))); -- summation of X data	
							calibData(1) <= std_logic_vector(signed(calibData(1)) + signed(accel_data_buff(31 downto  16))); -- summation of Y data	
							calibData(2) <= std_logic_vector(signed(calibData(2)) + signed(accel_data_buff(47 downto  32))); -- summation of Z data								
						end if;
						sample_count <= sample_count + 1;	-- increment count, if n samples have been collected, one more prevents entering this if statement
					accel_data <= accel_data_buff;
					else
						accel_data <= accel_data_buff;			-- clock collected accelerometer data for ouput
					end if;
						state <= S_IDLE;								-- go back to idle to repeat the cycle
					
				when others => 
					stateID <= "111";
						NULL;
				
			
			
			end case;


			pol <= '1';
			pha <= '1';
		
		end if;
		
	end process;

end fsm_1p;
