// Logisim project directions_and_angles.circ as structural Verilog
module accelerometer_driver_tb (
  input  rst,
  input  miso,
  input  accel_input,
  input  enable_accel,
  input  LSB_selector,
  input  MSB_selector,
  output MOSI,
  output SCLK,
  output CS
);

  wire accelerometer_driver_1_down, accelerometer_driver_1_large_force, accelerometer_driver_1_left,
       accelerometer_driver_1_medium_force, accelerometer_driver_1_negative_value,
       accelerometer_driver_1_right, accelerometer_driver_1_small_force, accelerometer_driver_1_up;
  wire [3:0] hex_to_decimal_2_1_hundreds, hex_to_decimal_2_1_ones, hex_to_decimal_2_1_tens;
  wire [7:0] accelerometer_driver_1_filtered_val;

  accelerometer_driver accelerometer_driver_1 (
    .rst(rst), .miso(miso), .accel_input(accel_input), .enable_accel(enable_accel),
    .LSB_selector(LSB_selector), .MSB_selector(MSB_selector), .mosi(MOSI), .sclk(SCLK), .cs(CS),
    .negative_value(accelerometer_driver_1_negative_value),
    .filtered_val(accelerometer_driver_1_filtered_val), .left(accelerometer_driver_1_left),
    .down(accelerometer_driver_1_down), .right(accelerometer_driver_1_right), .up(accelerometer_driver_1_up),
    .small_force(accelerometer_driver_1_small_force), .medium_force(accelerometer_driver_1_medium_force),
    .large_force(accelerometer_driver_1_large_force));
  sevenseg_directions_output DIRECTIONS (
    .L(accelerometer_driver_1_left), .R(accelerometer_driver_1_right), .U(accelerometer_driver_1_up),
    .D(accelerometer_driver_1_down));  // open: S, M
  sevenseg_directions_output sevenseg_directions_output_1 (
    .L(accelerometer_driver_1_large_force), .S(accelerometer_driver_1_small_force),
    .M(accelerometer_driver_1_medium_force));  // open: R, U, D
  sign_hex_output SIGN (.negative(accelerometer_driver_1_negative_value));
  hex_to_decimal_2 hex_to_decimal_2_1 (
    .val(accelerometer_driver_1_filtered_val), .hundreds(hex_to_decimal_2_1_hundreds),
    .tens(hex_to_decimal_2_1_tens), .ones(hex_to_decimal_2_1_ones));
  sevenseg_accel_output HUNDREDS (.Input_bus_1(hex_to_decimal_2_1_hundreds), .decimal(1'b1));
  sevenseg_accel_output TENS (.Input_bus_1(hex_to_decimal_2_1_tens));  // open: decimal
  sevenseg_accel_output ONES (.Input_bus_1(hex_to_decimal_2_1_ones));  // open: decimal
endmodule

module accelerometer_driver (
  input  rst,
  input  miso,
  input  accel_input,
  input  enable_accel,
  input  LSB_selector,
  input  MSB_selector,
  output mosi,
  output sclk,
  output cs,
  output negative_value,
  output [7:0] filtered_val,
  output left,
  output down,
  output right,
  output up,
  output small_force,
  output medium_force,
  output large_force
);

  wire and_1_out, and_2_out, comparator_1_gt, comparator_2_gt, comparator_3_eq, comparator_3_lt,
       comparator_4_gt, comparator_5_eq, comparator_5_lt, not_1_out, not_2_out, not_3_out, or_1_out, or_2_out;

  Comparator #(.mode("unsigned")) comparator_1 (.a(filtered_val), .b(8'ha), .gt(comparator_1_gt));  // open: eq, lt
  Comparator #(.mode("unsigned")) comparator_2 (.a(filtered_val), .b(8'ha), .gt(comparator_2_gt));  // open: eq, lt
  Comparator #(.mode("unsigned")) comparator_3 (
    .a(filtered_val), .b(8'h28), .eq(comparator_3_eq), .lt(comparator_3_lt));  // open: gt
  Comparator #(.mode("unsigned")) comparator_4 (.a(filtered_val), .b(8'h28), .gt(comparator_4_gt));  // open: eq, lt
  Comparator #(.mode("unsigned")) comparator_5 (
    .a(filtered_val), .b(8'h46), .eq(comparator_5_eq), .lt(comparator_5_lt));  // open: gt
  Comparator #(.mode("unsigned")) comparator_6 (.a(filtered_val), .b(8'h46), .gt(large_force));  // open: eq, lt
  values_fast_filter_driver values_fast_filter_driver_1 (
    .rst(rst), .miso(miso), .accel_input(accel_input), .enable_accel(enable_accel), .LSB(LSB_selector),
    .MSB(MSB_selector), .mosi(mosi), .sclk(sclk), .cs(cs), .negative_val(negative_value),
    .filtered_val(filtered_val));
  not not_1 (not_1_out, negative_value);
  or or_1 (or_1_out, comparator_3_eq, comparator_3_lt);
  or or_2 (or_2_out, comparator_5_eq, comparator_5_lt);
  and and_1 (and_1_out, comparator_1_gt, not_1_out);
  and and_2 (and_2_out, comparator_1_gt, negative_value);
  and and_3 (small_force, comparator_2_gt, or_1_out);
  and and_4 (medium_force, comparator_4_gt, or_2_out);
  not not_2 (not_2_out, LSB_selector);
  and and_5 (left, and_1_out, not_3_out);
  not not_3 (not_3_out, LSB_selector);
  and and_6 (down, and_1_out, LSB_selector);
  and and_7 (right, and_2_out, not_2_out);
  and and_8 (up, and_2_out, LSB_selector);
endmodule

module show_directions_and_angle (
  input  rst,
  input  miso,
  input  accel_input,
  input  enable_accel,
  output mosi,
  output sclk,
  output cs
);

  wire angle_checker_one_axis_1_l, angle_checker_one_axis_1_m, angle_checker_one_axis_1_s,
       angle_checker_one_axis_2_l, angle_checker_one_axis_2_m, angle_checker_one_axis_2_s, DOWN_within_range,
       LEFT_within_range, or_1_out, or_2_out, RIGHT1_within_range, RIGHT2_within_range, right_force_1_l,
       right_force_1_m, right_force_1_s, UP1_within_range, UP2_within_range;
  wire [15:0] x, y;
  wire [47:32] accel_main_driver_1_accelerometer;

  accel_main_driver accel_main_driver_1 (
    .rst(rst), .miso(miso), .accel_input(accel_input), .enable_accel(enable_accel), .mosi(mosi), .sclk(sclk),
    .cs(cs), .Accelerometer({accel_main_driver_1_accelerometer, y, x}));
  in_range LEFT (.Number_to_check(x), .Lower_bound(16'h4d), .Higher_bound(16'hd4), .within_range(LEFT_within_range));
  in_range RIGHT1 (
    .Number_to_check(x), .Lower_bound({16{1'b0}}), .Higher_bound(16'h2d), .within_range(RIGHT1_within_range));
  in_range RIGHT2 (
    .Number_to_check(x), .Lower_bound(16'hffba), .Higher_bound({16{1'b1}}), .within_range(RIGHT2_within_range));
  in_range DOWN (.Number_to_check(y), .Lower_bound(16'h4d), .Higher_bound(16'hd4), .within_range(DOWN_within_range));
  in_range UP1 (.Number_to_check(y), .Lower_bound({16{1'b0}}), .Higher_bound(16'h2d), .within_range(UP1_within_range));
  in_range UP2 (
    .Number_to_check(y), .Lower_bound(16'hffba), .Higher_bound({16{1'b1}}), .within_range(UP2_within_range));
  angle_checker_one_axis angle_checker_one_axis_1 (
    .AXIS(x), .SLB1(16'h4d), .SHB1(16'h7a), .MLB1(16'h7a), .MHB1(16'ha7), .LLB1(16'ha7), .LHB1(16'hd4),
    .SLB2({16{1'b0}}), .SHB2(16'h2d), .MLB2(16'hffd2), .MHB2({16{1'b1}}), .LLB2(16'hffba), .LHB2(16'hffd2),
    .S(angle_checker_one_axis_1_s), .M(angle_checker_one_axis_1_m), .L(angle_checker_one_axis_1_l));
  angle_checker_one_axis angle_checker_one_axis_2 (
    .AXIS(y), .SLB1(16'h4d), .SHB1(16'h7a), .MLB1(16'h7a), .MHB1(16'ha7), .LLB1(16'ha7), .LHB1(16'hd4),
    .SLB2({16{1'b0}}), .SHB2(16'h2d), .MLB2(16'hffd2), .MHB2({16{1'b1}}), .LLB2(16'hffba), .LHB2(16'hffd2),
    .S(angle_checker_one_axis_2_s), .M(angle_checker_one_axis_2_m), .L(angle_checker_one_axis_2_l));
  or or_1 (or_1_out, RIGHT1_within_range, RIGHT2_within_range);
  or or_2 (or_2_out, UP1_within_range, UP2_within_range);
  sevenseg_directions_output sevenseg_directions_output_1 (.L(LEFT_within_range), .R(or_1_out));  // open: U, D, S, M
  sevenseg_directions_output sevenseg_directions_output_2 (.U(or_2_out), .D(DOWN_within_range));  // open: L, R, S, M
  right_force right_force_1 (
    .S1(angle_checker_one_axis_1_s), .S2(angle_checker_one_axis_2_s), .M1(angle_checker_one_axis_1_m),
    .M2(angle_checker_one_axis_2_m), .L1(angle_checker_one_axis_1_l), .L2(angle_checker_one_axis_2_l),
    .S(right_force_1_s), .M(right_force_1_m), .L(right_force_1_l));
  sevenseg_directions_output sevenseg_directions_output_3 (
    .L(right_force_1_l), .S(right_force_1_s), .M(right_force_1_m));  // open: R, U, D

  // Notes on the sheet:
  //   Left/Down angle
  //   Left/Down range
  //   Right/Up range
  //   Right/Up angle
  //   DIRECTIONS_AND_ANGLES
  //   SHOWS ON 1 HEX BY HOW MUCH IT IS TILTED ON 1 HEX (S,M,L) 
  //   SHOWS ON 2 HEXES IN WHICH DIRECTION THE DE10 IS TILTED (L,R,U,D)
  //   THE RANGE OF DETECTION CAN BE TUNED ON THE LEFT (THE TEXTS IN RED)
endmodule

module angle_checker_one_axis (
  input  [15:0] AXIS,
  input  [15:0] SLB1,
  input  [15:0] SHB1,
  input  [15:0] MLB1,
  input  [15:0] MHB1,
  input  [15:0] LLB1,
  input  [15:0] LHB1,
  input  [15:0] SLB2,
  input  [15:0] SHB2,
  input  [15:0] MLB2,
  input  [15:0] MHB2,
  input  [15:0] LLB2,
  input  [15:0] LHB2,
  output S,
  output M,
  output L
);

  wire angle_checker_1_l, angle_checker_1_m, angle_checker_1_s, angle_checker_2_l, angle_checker_2_m,
       angle_checker_2_s;

  angle_checker angle_checker_1 (
    .NUMBER_TO_CHECK(AXIS), .SLB(SLB1), .SHB(SHB1), .MLB(MLB1), .MHB(MHB1), .LLB(LLB1), .LHB(LHB1),
    .S(angle_checker_1_s), .M(angle_checker_1_m), .L(angle_checker_1_l));
  angle_checker angle_checker_2 (
    .NUMBER_TO_CHECK(AXIS), .SLB(SLB2), .SHB(SHB2), .MLB(MLB2), .MHB(MHB2), .LLB(LLB2), .LHB(LHB2),
    .S(angle_checker_2_s), .M(angle_checker_2_m), .L(angle_checker_2_l));
  or or_1 (S, angle_checker_1_s, angle_checker_2_s);
  or or_2 (M, angle_checker_1_m, angle_checker_2_m);
  or or_3 (L, angle_checker_1_l, angle_checker_2_l);
endmodule

module angle_checker (
  input  [15:0] NUMBER_TO_CHECK,
  input  [15:0] SLB,
  input  [15:0] SHB,
  input  [15:0] MLB,
  input  [15:0] MHB,
  input  [15:0] LLB,
  input  [15:0] LHB,
  output S,
  output M,
  output L
);

  in_range SMALL_ANGLE (.Number_to_check(NUMBER_TO_CHECK), .Lower_bound(SLB), .Higher_bound(SHB), .within_range(S));
  in_range MEDIUM_ANGLE (.Number_to_check(NUMBER_TO_CHECK), .Lower_bound(MLB), .Higher_bound(MHB), .within_range(M));
  in_range LARGE_ANGLE (.Number_to_check(NUMBER_TO_CHECK), .Lower_bound(LLB), .Higher_bound(LHB), .within_range(L));
endmodule

module right_force (
  input  S1,
  input  S2,
  input  M1,
  input  M2,
  input  L1,
  input  L2,
  output S,
  output M,
  output L
);

  wire and_1_out, and_2_out, and_3_out, and_4_out, and_5_out, and_6_out, and_7_out, not_1_out, not_2_out,
       not_3_out, not_4_out, not_5_out, not_6_out;

  not not_1 (not_1_out, S1);
  not not_2 (not_2_out, S2);
  not not_3 (not_3_out, M1);
  not not_4 (not_4_out, M2);
  not not_5 (not_5_out, L1);
  not not_6 (not_6_out, L2);
  and and_1 (and_1_out, S2, not_3_out, not_4_out, not_5_out, not_6_out);
  and and_2 (and_2_out, S1, not_3_out, not_4_out, not_5_out, not_6_out);
  and and_3 (and_3_out, not_3_out, M2, not_5_out, not_6_out);
  and and_4 (and_4_out, M1, not_4_out, not_5_out, not_6_out);
  and and_5 (and_5_out, S2, M2, not_5_out, not_6_out);
  and and_6 (and_6_out, S1, M1, not_5_out, not_6_out);
  and and_7 (and_7_out, not_1_out, not_2_out, M1, M2);
  or or_1 (S, and_1_out, and_2_out);
  or or_2 (M, and_3_out, and_4_out, and_5_out, and_6_out);
  or or_3 (L, L2, L1, and_7_out);
endmodule

module in_range (
  input  [15:0] Number_to_check,
  input  [15:0] Lower_bound,
  input  [15:0] Higher_bound,
  output within_range
);

  wire or_1_out, or_2_out, sixteen_bits_comparator_1_a_bigger_than_b, sixteen_bits_comparator_1_a_equals_b,
       sixteen_bits_comparator_2_a_equals_b, sixteen_bits_comparator_2_a_less_than_b;

  sixteen_bits_comparator sixteen_bits_comparator_1 (
    .A(Number_to_check), .B(Lower_bound), .A_equals_B(sixteen_bits_comparator_1_a_equals_b),
    .A_bigger_than_B(sixteen_bits_comparator_1_a_bigger_than_b));  // open: A_less_than_B
  sixteen_bits_comparator sixteen_bits_comparator_2 (
    .A(Number_to_check), .B(Higher_bound), .A_less_than_B(sixteen_bits_comparator_2_a_less_than_b),
    .A_equals_B(sixteen_bits_comparator_2_a_equals_b));  // open: A_bigger_than_B
  or or_1 (or_1_out, sixteen_bits_comparator_1_a_equals_b, sixteen_bits_comparator_1_a_bigger_than_b);
  or or_2 (or_2_out, sixteen_bits_comparator_2_a_less_than_b, sixteen_bits_comparator_2_a_equals_b);
  and and_1 (within_range, or_1_out, or_2_out);
endmodule

module sevenseg_directions_logic (
  input  L,
  input  R,
  input  U,
  input  D,
  input  S,
  input  M,
  output [7:0] letter_output
);

  wire and_1_out, and_2_out, and_3_out, and_4_out, and_5_out, and_6_out, and_7_out, and_8_out, and_9_out,
       and_10_out, and_11_out, and_12_out, and_13_out, and_14_out, and_15_out, and_16_out, and_17_out,
       and_18_out, and_19_out, and_20_out, and_21_out, and_22_out, and_23_out, and_24_out, and_25_out,
       not_1_out, not_2_out, not_3_out, not_4_out, not_5_out, not_6_out;

  not not_1 (not_1_out, L);
  not not_2 (not_2_out, R);
  not not_3 (not_3_out, U);
  not not_4 (not_4_out, D);
  not not_5 (not_5_out, S);
  not not_6 (not_6_out, M);
  and and_1 (and_1_out, not_1_out, not_2_out, not_3_out, not_4_out, S, not_6_out);
  and and_2 (and_2_out, not_1_out, not_2_out, not_3_out, D, not_5_out, not_6_out);
  and and_3 (and_3_out, not_1_out, R, not_3_out, not_4_out, not_5_out, not_6_out);
  and and_4 (and_4_out, not_1_out, not_2_out, not_3_out, not_4_out, not_5_out, M);
  and and_5 (and_5_out, not_1_out, not_2_out, not_3_out, not_4_out, S, not_6_out);
  and and_6 (and_6_out, not_1_out, not_2_out, U, not_4_out, not_5_out, not_6_out);
  and and_7 (and_7_out, L, not_2_out, not_3_out, not_4_out, not_5_out, not_6_out);
  and and_8 (and_8_out, not_1_out, not_2_out, not_3_out, not_4_out, not_5_out, M);
  and and_9 (and_9_out, not_1_out, not_2_out, not_3_out, D, not_5_out, not_6_out);
  and and_10 (and_10_out, not_1_out, not_2_out, U, not_4_out, not_5_out, not_6_out);
  and and_11 (and_11_out, not_1_out, R, not_3_out, not_4_out, not_5_out, not_6_out);
  and and_12 (and_12_out, L, not_2_out, not_3_out, not_4_out, not_5_out, not_6_out);
  and and_13 (and_13_out, not_1_out, not_2_out, not_3_out, not_4_out, S, not_6_out);
  and and_14 (and_14_out, not_1_out, not_2_out, not_3_out, D, not_5_out, not_6_out);
  and and_15 (and_15_out, not_1_out, not_2_out, U, not_4_out, not_5_out, not_6_out);
  and and_16 (and_16_out, L, not_2_out, not_3_out, not_4_out, not_5_out, not_6_out);
  and and_17 (and_17_out, not_1_out, not_2_out, not_3_out, not_4_out, not_5_out, M);
  and and_18 (and_18_out, not_1_out, not_2_out, not_3_out, not_4_out, S, not_6_out);
  and and_19 (and_19_out, not_1_out, not_2_out, not_3_out, D, not_5_out, not_6_out);
  and and_20 (and_20_out, not_1_out, not_2_out, U, not_4_out, not_5_out, not_6_out);
  and and_21 (and_21_out, not_1_out, not_2_out, not_3_out, not_4_out, not_5_out, M);
  and and_22 (and_22_out, not_1_out, not_2_out, not_3_out, D, not_5_out, not_6_out);
  and and_23 (and_23_out, not_1_out, not_2_out, U, not_4_out, not_5_out, not_6_out);
  and and_24 (and_24_out, not_1_out, not_2_out, not_3_out, not_4_out, not_5_out, M);
  and and_25 (and_25_out, not_1_out, not_2_out, not_3_out, not_4_out, S, not_6_out);
  or or_1 (letter_output[6], and_1_out, and_2_out, and_3_out);
  or or_2 (letter_output[5], and_4_out, and_5_out, and_6_out, and_7_out);
  or or_3 (letter_output[4], and_8_out, and_9_out, and_10_out, and_11_out, and_12_out);
  or or_4 (letter_output[3], and_13_out, and_14_out, and_15_out, and_16_out);
  or or_5 (letter_output[2], and_17_out, and_18_out, and_19_out, and_20_out);
  or or_6 (letter_output[1], and_21_out, and_22_out, and_23_out);
  or or_7 (letter_output[0], and_24_out, and_25_out);

  assign letter_output[7] = 1'b0;
endmodule

module sevenseg_directions_output (
  input  L,
  input  R,
  input  U,
  input  D,
  input  S,
  input  M
);

  wire [7:0] sevenseg_directions_output_letter_output;

  sevenseg_directions_logic sevenseg_directions_output (
    .L(L), .R(R), .U(U), .D(D), .S(S), .M(M), .letter_output(sevenseg_directions_output_letter_output));
  _7_Segment_Display HEX (
    .g(sevenseg_directions_output_letter_output[6]), .f(sevenseg_directions_output_letter_output[5]),
    .a(sevenseg_directions_output_letter_output[0]), .b(sevenseg_directions_output_letter_output[1]),
    .e(sevenseg_directions_output_letter_output[4]), .d(sevenseg_directions_output_letter_output[3]),
    .c(sevenseg_directions_output_letter_output[2]), .dp(sevenseg_directions_output_letter_output[7]));
endmodule

module sixteen_bits_comparator (
  input  [15:0] A,
  input  [15:0] B,
  output A_less_than_B,
  output A_equals_B,
  output A_bigger_than_B
);

  wire Bigger_Row_0, Bigger_Row_1, Bigger_Row_2, Equals_Row_0, Equals_Row_1, Equals_Row_2, Less_Row_0,
       Less_Row_1, Less_Row_2, one_bits_comparator_1_a_bigger_than_b, one_bits_comparator_1_a_equals_b,
       one_bits_comparator_1_a_less_than_b, one_bits_with_inputs_2_a_bigger_than_b_output,
       one_bits_with_inputs_2_a_equals_b_output, one_bits_with_inputs_2_a_less_than_b_output,
       one_bits_with_inputs_3_a_bigger_than_b_output, one_bits_with_inputs_3_a_equals_b_output,
       one_bits_with_inputs_3_a_less_than_b_output, one_bits_with_inputs_5_a_bigger_than_b_output,
       one_bits_with_inputs_5_a_equals_b_output, one_bits_with_inputs_5_a_less_than_b_output,
       one_bits_with_inputs_6_a_bigger_than_b_output, one_bits_with_inputs_6_a_equals_b_output,
       one_bits_with_inputs_6_a_less_than_b_output, one_bits_with_inputs_7_a_bigger_than_b_output,
       one_bits_with_inputs_7_a_equals_b_output, one_bits_with_inputs_7_a_less_than_b_output,
       one_bits_with_inputs_9_a_bigger_than_b_output, one_bits_with_inputs_9_a_equals_b_output,
       one_bits_with_inputs_9_a_less_than_b_output, one_bits_with_inputs_10_a_bigger_than_b_output,
       one_bits_with_inputs_10_a_equals_b_output, one_bits_with_inputs_10_a_less_than_b_output,
       one_bits_with_inputs_11_a_bigger_than_b_output, one_bits_with_inputs_11_a_equals_b_output,
       one_bits_with_inputs_11_a_less_than_b_output, one_bits_with_inputs_13_a_bigger_than_b_output,
       one_bits_with_inputs_13_a_equals_b_output, one_bits_with_inputs_13_a_less_than_b_output,
       one_bits_with_inputs_14_a_bigger_than_b_output, one_bits_with_inputs_14_a_equals_b_output,
       one_bits_with_inputs_14_a_less_than_b_output, one_bits_with_inputs_15_a_bigger_than_b_output,
       one_bits_with_inputs_15_a_equals_b_output, one_bits_with_inputs_15_a_less_than_b_output;

  one_bits_comparator one_bits_comparator_1 (
    .A(A[0]), .B(B[0]), .A_less_than_B(one_bits_comparator_1_a_less_than_b),
    .A_equals_B(one_bits_comparator_1_a_equals_b), .A_bigger_than_B(one_bits_comparator_1_a_bigger_than_b));
  one_bits_with_inputs one_bits_with_inputs_7 (
    .A(A[4]), .B(B[4]), .A_less_B_input(Less_Row_0), .A_equal_B_input(Equals_Row_0),
    .A_bigger_than_B_input(Bigger_Row_0), .A_less_than_B_output(one_bits_with_inputs_7_a_less_than_b_output),
    .A_equals_B_output(one_bits_with_inputs_7_a_equals_b_output),
    .A_bigger_than_B_output(one_bits_with_inputs_7_a_bigger_than_b_output));
  one_bits_with_inputs one_bits_with_inputs_11 (
    .A(A[8]), .B(B[8]), .A_less_B_input(Less_Row_1), .A_equal_B_input(Equals_Row_1),
    .A_bigger_than_B_input(Bigger_Row_1),
    .A_less_than_B_output(one_bits_with_inputs_11_a_less_than_b_output),
    .A_equals_B_output(one_bits_with_inputs_11_a_equals_b_output),
    .A_bigger_than_B_output(one_bits_with_inputs_11_a_bigger_than_b_output));
  one_bits_with_inputs one_bits_with_inputs_15 (
    .A(A[12]), .B(B[12]), .A_less_B_input(Less_Row_2), .A_equal_B_input(Equals_Row_2),
    .A_bigger_than_B_input(Bigger_Row_2),
    .A_less_than_B_output(one_bits_with_inputs_15_a_less_than_b_output),
    .A_equals_B_output(one_bits_with_inputs_15_a_equals_b_output),
    .A_bigger_than_B_output(one_bits_with_inputs_15_a_bigger_than_b_output));
  one_bits_with_inputs one_bits_with_inputs_3 (
    .A(A[1]), .B(B[1]), .A_less_B_input(one_bits_comparator_1_a_less_than_b),
    .A_equal_B_input(one_bits_comparator_1_a_equals_b),
    .A_bigger_than_B_input(one_bits_comparator_1_a_bigger_than_b),
    .A_less_than_B_output(one_bits_with_inputs_3_a_less_than_b_output),
    .A_equals_B_output(one_bits_with_inputs_3_a_equals_b_output),
    .A_bigger_than_B_output(one_bits_with_inputs_3_a_bigger_than_b_output));
  one_bits_with_inputs one_bits_with_inputs_6 (
    .A(A[5]), .B(B[5]), .A_less_B_input(one_bits_with_inputs_7_a_less_than_b_output),
    .A_equal_B_input(one_bits_with_inputs_7_a_equals_b_output),
    .A_bigger_than_B_input(one_bits_with_inputs_7_a_bigger_than_b_output),
    .A_less_than_B_output(one_bits_with_inputs_6_a_less_than_b_output),
    .A_equals_B_output(one_bits_with_inputs_6_a_equals_b_output),
    .A_bigger_than_B_output(one_bits_with_inputs_6_a_bigger_than_b_output));
  one_bits_with_inputs one_bits_with_inputs_10 (
    .A(A[9]), .B(B[9]), .A_less_B_input(one_bits_with_inputs_11_a_less_than_b_output),
    .A_equal_B_input(one_bits_with_inputs_11_a_equals_b_output),
    .A_bigger_than_B_input(one_bits_with_inputs_11_a_bigger_than_b_output),
    .A_less_than_B_output(one_bits_with_inputs_10_a_less_than_b_output),
    .A_equals_B_output(one_bits_with_inputs_10_a_equals_b_output),
    .A_bigger_than_B_output(one_bits_with_inputs_10_a_bigger_than_b_output));
  one_bits_with_inputs one_bits_with_inputs_14 (
    .A(A[13]), .B(B[13]), .A_less_B_input(one_bits_with_inputs_15_a_less_than_b_output),
    .A_equal_B_input(one_bits_with_inputs_15_a_equals_b_output),
    .A_bigger_than_B_input(one_bits_with_inputs_15_a_bigger_than_b_output),
    .A_less_than_B_output(one_bits_with_inputs_14_a_less_than_b_output),
    .A_equals_B_output(one_bits_with_inputs_14_a_equals_b_output),
    .A_bigger_than_B_output(one_bits_with_inputs_14_a_bigger_than_b_output));
  one_bits_with_inputs one_bits_with_inputs_2 (
    .A(A[2]), .B(B[2]), .A_less_B_input(one_bits_with_inputs_3_a_less_than_b_output),
    .A_equal_B_input(one_bits_with_inputs_3_a_equals_b_output),
    .A_bigger_than_B_input(one_bits_with_inputs_3_a_bigger_than_b_output),
    .A_less_than_B_output(one_bits_with_inputs_2_a_less_than_b_output),
    .A_equals_B_output(one_bits_with_inputs_2_a_equals_b_output),
    .A_bigger_than_B_output(one_bits_with_inputs_2_a_bigger_than_b_output));
  one_bits_with_inputs one_bits_with_inputs_5 (
    .A(A[6]), .B(B[6]), .A_less_B_input(one_bits_with_inputs_6_a_less_than_b_output),
    .A_equal_B_input(one_bits_with_inputs_6_a_equals_b_output),
    .A_bigger_than_B_input(one_bits_with_inputs_6_a_bigger_than_b_output),
    .A_less_than_B_output(one_bits_with_inputs_5_a_less_than_b_output),
    .A_equals_B_output(one_bits_with_inputs_5_a_equals_b_output),
    .A_bigger_than_B_output(one_bits_with_inputs_5_a_bigger_than_b_output));
  one_bits_with_inputs one_bits_with_inputs_9 (
    .A(A[10]), .B(B[10]), .A_less_B_input(one_bits_with_inputs_10_a_less_than_b_output),
    .A_equal_B_input(one_bits_with_inputs_10_a_equals_b_output),
    .A_bigger_than_B_input(one_bits_with_inputs_10_a_bigger_than_b_output),
    .A_less_than_B_output(one_bits_with_inputs_9_a_less_than_b_output),
    .A_equals_B_output(one_bits_with_inputs_9_a_equals_b_output),
    .A_bigger_than_B_output(one_bits_with_inputs_9_a_bigger_than_b_output));
  one_bits_with_inputs one_bits_with_inputs_13 (
    .A(A[14]), .B(B[14]), .A_less_B_input(one_bits_with_inputs_14_a_less_than_b_output),
    .A_equal_B_input(one_bits_with_inputs_14_a_equals_b_output),
    .A_bigger_than_B_input(one_bits_with_inputs_14_a_bigger_than_b_output),
    .A_less_than_B_output(one_bits_with_inputs_13_a_less_than_b_output),
    .A_equals_B_output(one_bits_with_inputs_13_a_equals_b_output),
    .A_bigger_than_B_output(one_bits_with_inputs_13_a_bigger_than_b_output));
  one_bits_with_inputs one_bits_with_inputs_1 (
    .A(A[3]), .B(B[3]), .A_less_B_input(one_bits_with_inputs_2_a_less_than_b_output),
    .A_equal_B_input(one_bits_with_inputs_2_a_equals_b_output),
    .A_bigger_than_B_input(one_bits_with_inputs_2_a_bigger_than_b_output), .A_less_than_B_output(Less_Row_0),
    .A_equals_B_output(Equals_Row_0), .A_bigger_than_B_output(Bigger_Row_0));
  one_bits_with_inputs one_bits_with_inputs_4 (
    .A(A[7]), .B(B[7]), .A_less_B_input(one_bits_with_inputs_5_a_less_than_b_output),
    .A_equal_B_input(one_bits_with_inputs_5_a_equals_b_output),
    .A_bigger_than_B_input(one_bits_with_inputs_5_a_bigger_than_b_output), .A_less_than_B_output(Less_Row_1),
    .A_equals_B_output(Equals_Row_1), .A_bigger_than_B_output(Bigger_Row_1));
  one_bits_with_inputs one_bits_with_inputs_8 (
    .A(A[11]), .B(B[11]), .A_less_B_input(one_bits_with_inputs_9_a_less_than_b_output),
    .A_equal_B_input(one_bits_with_inputs_9_a_equals_b_output),
    .A_bigger_than_B_input(one_bits_with_inputs_9_a_bigger_than_b_output), .A_less_than_B_output(Less_Row_2),
    .A_equals_B_output(Equals_Row_2), .A_bigger_than_B_output(Bigger_Row_2));
  one_bits_with_inputs one_bits_with_inputs_12 (
    .A(A[15]), .B(B[15]), .A_less_B_input(one_bits_with_inputs_13_a_less_than_b_output),
    .A_equal_B_input(one_bits_with_inputs_13_a_equals_b_output),
    .A_bigger_than_B_input(one_bits_with_inputs_13_a_bigger_than_b_output),
    .A_less_than_B_output(A_less_than_B), .A_equals_B_output(A_equals_B),
    .A_bigger_than_B_output(A_bigger_than_B));

  // Other names for the same wires on the sheet: A0[3:0] = A[3:0]; A1[3:0] = A[7:4]; A2[3:0] = A[11:8];
  //   A3[3:0] = A[15:12]; B0[3:0] = B[3:0]; B1[3:0] = B[7:4]; B2[3:0] = B[11:8]; B3[3:0] = B[15:12]
endmodule

module one_bits_comparator (
  input  A,
  input  B,
  output A_less_than_B,
  output A_equals_B,
  output A_bigger_than_B
);

  wire and_2_out, and_3_out, not_1_out, not_2_out;

  not not_1 (not_1_out, A);
  not not_2 (not_2_out, B);
  and and_1 (A_less_than_B, not_1_out, B);
  and and_2 (and_2_out, not_1_out, not_2_out);
  and and_3 (and_3_out, A, B);
  and and_4 (A_bigger_than_B, A, not_2_out);
  or or_1 (A_equals_B, and_2_out, and_3_out);
endmodule

module one_bits_with_inputs (
  input  A,
  input  B,
  input  A_less_B_input,
  input  A_equal_B_input,
  input  A_bigger_than_B_input,
  output A_less_than_B_output,
  output A_equals_B_output,
  output A_bigger_than_B_output
);

  wire and_1_out, and_2_out, and_3_out, and_4_out, and_5_out, and_7_out, not_1_out, not_2_out, or_1_out;

  not not_1 (not_1_out, A);
  not not_2 (not_2_out, B);
  and and_1 (and_1_out, not_1_out, B);
  and and_2 (and_2_out, not_1_out, not_2_out);
  and and_3 (and_3_out, A, B);
  and and_4 (and_4_out, A, not_2_out);
  or or_1 (or_1_out, and_2_out, and_3_out);
  and and_5 (and_5_out, or_1_out, A_less_B_input);
  and and_6 (A_equals_B_output, or_1_out, A_equal_B_input);
  and and_7 (and_7_out, or_1_out, A_bigger_than_B_input);
  or or_2 (A_less_than_B_output, and_1_out, and_5_out);
  or or_3 (A_bigger_than_B_output, and_4_out, and_7_out);
endmodule

// VHDL entity hex_to_decimal_2, as the project stores it:
--------------------------------------------------------------------------------
-- Project :
-- File    :
-- Autor   :
-- Date    :
--
--------------------------------------------------------------------------------
-- Description :
--
--------------------------------------------------------------------------------

LIBRARY ieee;
USE ieee.std_logic_1164.all;

ENTITY hex_to_decimal_2 IS
  PORT (
  --Insert input ports below
    val        : IN  std_logic_vector(7 DOWNTO 0); -- input vector example
  ------------------------------------------------------------------------------
  --Insert output ports below
    hundreds        : OUT std_logic_vector(3 DOWNTO 0);  -- output vector example
    tens        	: OUT std_logic_vector(3 DOWNTO 0);
    ones			: OUT std_logic_vector(3 DOWNTO 0)
    );
END hex_to_decimal_2;

--------------------------------------------------------------------------------
--Complete your VHDL description below
--------------------------------------------------------------------------------

ARCHITECTURE TypeArchitecture OF hex_to_decimal_2 IS
	signal cmpt_2 : std_logic_vector(33 DOWNTO 0);
	signal cmpt_3 : std_logic_vector(33 DOWNTO 0);
	signal cmpt_4 : std_logic_vector(33 DOWNTO 0);
	signal cmpt_5 : std_logic_vector(33 DOWNTO 0);
	signal cmpt_6 : std_logic_vector(33 DOWNTO 0);
	signal no_hundos : std_logic_vector(33 DOWNTO 0);
	
	signal div_one_hundos : std_logic_vector(16 DOWNTO 0);
	signal div_one_hundo : std_logic_vector(15 DOWNTO 0) := X"0148";

	signal times_one_hundos : std_logic_vector(16 DOWNTO 0);
	signal times_one_hundo : std_logic_vector(15 DOWNTO 0) := X"0064";
	
	signal tenners : std_logic_vector(16 DOWNTO 0);
	signal ten : std_logic_vector(15 DOWNTO 0) := X"0CCD";

	signal times_tenner : std_logic_vector(16 DOWNTO 0);
	signal times_ten : std_logic_vector(15 DOWNTO 0) := X"000a";

	signal shift_2 : unsigned(33 DOWNTO 0);
	signal shift_4 : unsigned(33 DOWNTO 0);
	signal shift_5 : unsigned(33 DOWNTO 0);
	signal final_answer_sig : std_logic_vector(7 DOWNTO 0);
	signal hundreds_digit : std_logic_vector(3 DOWNTO 0);
	signal tens_digit : std_logic_vector(3 DOWNTO 0);
BEGIN
	final_answer_sig <= val;
	div_one_hundos <= '0' & div_one_hundo;
	tenners <= '0' & ten;
	times_one_hundos <= '0' & times_one_hundo;
	times_tenner <= '0' & times_ten;

	process (val)
	begin
		cmpt_2 <= std_logic_vector(('0' & X"00" & unsigned(final_answer_sig)) * unsigned(div_one_hundos));
		shift_2 <= shift_right(unsigned(cmpt_2), 15);
		hundreds <= std_logic_vector(shift_2(3 downto 0));
		hundreds_digit <= std_logic_vector(shift_2(3 downto 0));

		cmpt_3 <= std_logic_vector(unsigned('0' & '0' & X"000000" & final_answer_sig) - unsigned('0' & X"000" & hundreds_digit) * unsigned(times_one_hundos));
		no_hundos <= cmpt_3;
		cmpt_4 <= std_logic_vector(unsigned('0' & X"00" & cmpt_3(7 downto 0)) * unsigned(tenners));
		shift_4 <= shift_right(unsigned(cmpt_4), 15);
		tens <= std_logic_vector(shift_4(3 downto 0));
		tens_digit <= std_logic_vector(shift_4(3 downto 0));

		cmpt_5 <= std_logic_vector(unsigned(no_hundos) - unsigned('0' & X"000" & tens_digit) * unsigned(times_tenner));
		ones <= std_logic_vector(cmpt_5(3 downto 0));
		
	end process;

END TypeArchitecture;
