// Logisim project division.circ as structural Verilog
module twos_complement (
  input  [15:0] negative_number,
  output [15:0] absolute_val
);

  wire [15:0] not_1_out;

  assign not_1_out = ~negative_number;  // NOT_Gate not_1, 16 bits wide
  Adder #(.width(16)) adder_1 (.a(not_1_out), .b(16'h1), .out(absolute_val));  // open: cin, cout
endmodule

module sign_hex (
  input  negative,
  output a,
  output b,
  output c,
  output d,
  output e,
  output f,
  output g
);


  assign a = 1'b0;
  assign b = 1'b0;
  assign c = 1'b0;
  assign d = 1'b0;
  assign e = 1'b0;
  assign f = 1'b0;
  assign g = negative;
endmodule

module sign_hex_out (
  input  negative
);

  wire sign_hex_1_a, sign_hex_1_b, sign_hex_1_c, sign_hex_1_d, sign_hex_1_e, sign_hex_1_f, sign_hex_1_g;

  sign_hex sign_hex_1 (
    .negative(negative), .a(sign_hex_1_a), .b(sign_hex_1_b), .c(sign_hex_1_c), .d(sign_hex_1_d),
    .e(sign_hex_1_e), .f(sign_hex_1_f), .g(sign_hex_1_g));
  _7_Segment_Display L_7_Segment_Display_1 (
    .g(sign_hex_1_g), .f(sign_hex_1_f), .a(sign_hex_1_a), .b(sign_hex_1_b), .e(sign_hex_1_e),
    .d(sign_hex_1_d), .c(sign_hex_1_c), .dp(1'b0));
endmodule

module scale_down (
  input  [15:0] number_input,
  input  [15:0] second_num,
  output negative,
  output [3:0] hundreds,
  output [3:0] tens,
  output [3:0] ones,
  output [15:0] answer
);

  wire [7:0] divide_two_num_1_final_answer;
  wire [15:0] multiplexer_1_out, twos_complement_1_absolute_val;

  twos_complement twos_complement_1 (.negative_number(number_input), .absolute_val(twos_complement_1_absolute_val));
  Multiplexer #(.width(16)) multiplexer_1 (
    .in0(number_input), .in1(twos_complement_1_absolute_val), .out(multiplexer_1_out), .sel(number_input[15]));
  divide_two_num divide_two_num_1 (
    .val(multiplexer_1_out), .val2(second_num), .final_answer(divide_two_num_1_final_answer),
    .final_answer_sixteen_bits(answer));
  hex_to_decimal hex_to_decimal_1 (.val(divide_two_num_1_final_answer), .hundreds(hundreds), .tens(tens), .ones(ones));

  assign negative = number_input[15];
endmodule

module scale_down_sim (
  input  [15:0] number_input,
  input  [31:0] second_num,
  output negative,
  output [3:0] hundreds,
  output [3:0] tens,
  output [3:0] ones,
  output [7:0] answer
);

  wire [15:0] multiplexer_1_out, twos_complement_1_absolute_val;
  wire [31:0] bit_extender_4_out, divide_two_num_sim_1_output_value, hex_to_decimal_sim_1_hundreds,
       hex_to_decimal_sim_1_ones, hex_to_decimal_sim_1_tens;

  twos_complement twos_complement_1 (.negative_number(number_input), .absolute_val(twos_complement_1_absolute_val));
  hex_to_decimal_sim hex_to_decimal_sim_1 (
    .input_num(divide_two_num_sim_1_output_value), .hundreds(hex_to_decimal_sim_1_hundreds),
    .tens(hex_to_decimal_sim_1_tens), .ones(hex_to_decimal_sim_1_ones));
  Multiplexer #(.width(16)) multiplexer_1 (
    .in0(number_input), .in1(twos_complement_1_absolute_val), .out(multiplexer_1_out), .sel(number_input[15]));
  Bit_Extender #(.in_width(32), .out_width(4), .\type ("zero")) bit_extender_1 (
    .in(hex_to_decimal_sim_1_hundreds), .out(hundreds));
  Bit_Extender #(.in_width(32), .out_width(4), .\type ("zero")) bit_extender_2 (
    .in(hex_to_decimal_sim_1_tens), .out(tens));
  Bit_Extender #(.in_width(32), .out_width(4), .\type ("zero")) bit_extender_3 (
    .in(hex_to_decimal_sim_1_ones), .out(ones));
  assign bit_extender_4_out = {{16{1'b0}}, multiplexer_1_out};  // Bit_Extender bit_extender_4
  Bit_Extender #(.in_width(32), .out_width(8)) bit_extender_5 (.in(divide_two_num_sim_1_output_value), .out(answer));
  divide_two_num_sim divide_two_num_sim_1 (
    .value1(bit_extender_4_out), .value2(second_num), .output_value(divide_two_num_sim_1_output_value));

  assign negative = number_input[15];
endmodule

module divide_two_num_sim (
  input  [31:0] value1,
  input  [31:0] value2,
  output [31:0] output_value
);

  wire [31:0] multiplier_1_out;

  Multiplier #(.width(32)) multiplier_1 (.a(value1), .b(value2), .out(multiplier_1_out));  // open: cin, cout
  Shifter #(.shift("lr"), .width(32)) shifter_1 (.in(multiplier_1_out), .\dist (5'b01111), .out(output_value));
endmodule

module hex_to_decimal_sim (
  input  [31:0] input_num,
  output [31:0] hundreds,
  output [31:0] tens,
  output [31:0] ones
);

  wire [31:0] multiplier_1_out, multiplier_2_out, multiplier_3_out, multiplier_4_out, subtractor_1_out;

  Multiplier #(.width(32)) multiplier_1 (.a(input_num), .b(32'h148), .out(multiplier_1_out));  // open: cin, cout
  Multiplier #(.width(32)) multiplier_2 (.a(hundreds), .b(32'h64), .out(multiplier_2_out));  // open: cin, cout
  Multiplier #(.width(32)) multiplier_3 (.a(subtractor_1_out), .b(32'hccd), .out(multiplier_3_out));  // open: cin, cout
  Multiplier #(.width(32)) multiplier_4 (.a(tens), .b(32'ha), .out(multiplier_4_out));  // open: cin, cout
  Shifter #(.shift("lr"), .width(32)) shifter_1 (.in(multiplier_1_out), .\dist (5'b01111), .out(hundreds));
  Subtractor #(.width(32)) subtractor_1 (
    .a(input_num), .b(multiplier_2_out), .out(subtractor_1_out));  // open: bin, bout
  Shifter #(.shift("lr"), .width(32)) shifter_2 (.in(multiplier_3_out), .\dist (5'b01111), .out(tens));
  Subtractor #(.width(32)) subtractor_2 (.a(subtractor_1_out), .b(multiplier_4_out), .out(ones));  // open: bin, bout
  // Probe on subtractor_1_out
endmodule

// VHDL entity divide_two_num, as the project stores it:
--------------------------------------------------------------------------------
-- Project :
-- File    :
-- Autor   :
-- Date    :
--
--------------------------------------------------------------------------------
-- Description :
--
--------------------------------------------------------------------------------

LIBRARY ieee;
USE ieee.std_logic_1164.all;
use ieee.numeric_std.all;

ENTITY divide_two_num IS
  PORT (
  ------------------------------------------------------------------------------
  --Insert input ports below
    val        : IN  std_logic_vector(15 DOWNTO 0); -- input vector example
    val2        : IN  std_logic_vector(15 DOWNTO 0);
  ------------------------------------------------------------------------------
  --Insert output ports below
    final_answer	: OUT std_logic_vector(7 DOWNTO 0);
    final_answer_sixteen_bits	: OUT std_logic_vector(15 DOWNTO 0)
    );
END divide_two_num;

--------------------------------------------------------------------------------
--Complete your VHDL description below
--------------------------------------------------------------------------------

ARCHITECTURE TypeArchitecture OF divide_two_num IS
	signal cmpt_1 : std_logic_vector(33 DOWNTO 0);
	signal input1_sig : std_logic_vector(16 DOWNTO 0);
	signal input2_sig : std_logic_vector(16 DOWNTO 0);
	signal shift_1 : unsigned(33 DOWNTO 0);
	
BEGIN
	input1_sig <= '0' & val;
	input2_sig <= '0' & val2;
	

	process (val, val2)
	begin

		cmpt_1 <= std_logic_vector(unsigned(input1_sig) * unsigned(input2_sig));
		shift_1 <= shift_right(unsigned(cmpt_1), 15);
		final_answer <= std_logic_vector(shift_1(7 downto 0));
		final_answer_sixteen_bits <= std_logic_vector(shift_1(15 downto 0));
		
	end process;

END TypeArchitecture;

// VHDL entity hex_to_decimal, as the project stores it:
--------------------------------------------------------------------------------
-- Project :
-- File    :
-- Autor   :
-- Date    :
--
--------------------------------------------------------------------------------
-- Description :
--
--------------------------------------------------------------------------------

LIBRARY ieee;
USE ieee.std_logic_1164.all;

ENTITY hex_to_decimal IS
  PORT (
  --Insert input ports below
    val        : IN  std_logic_vector(7 DOWNTO 0); -- input vector example
  ------------------------------------------------------------------------------
  --Insert output ports below
    hundreds        : OUT std_logic_vector(3 DOWNTO 0);  -- output vector example
    tens        	: OUT std_logic_vector(3 DOWNTO 0);
    ones			: OUT std_logic_vector(3 DOWNTO 0)
    );
END hex_to_decimal;

--------------------------------------------------------------------------------
--Complete your VHDL description below
--------------------------------------------------------------------------------

ARCHITECTURE TypeArchitecture OF hex_to_decimal IS
	signal cmpt_2 : std_logic_vector(33 DOWNTO 0);
	signal cmpt_3 : std_logic_vector(33 DOWNTO 0);
	signal cmpt_4 : std_logic_vector(33 DOWNTO 0);
	signal cmpt_5 : std_logic_vector(33 DOWNTO 0);
	signal cmpt_6 : std_logic_vector(33 DOWNTO 0);
	signal no_hundos : std_logic_vector(33 DOWNTO 0);
	
	signal div_one_hundos : std_logic_vector(16 DOWNTO 0);
	signal div_one_hundo : std_logic_vector(15 DOWNTO 0) := X"0148";

	signal times_one_hundos : std_logic_vector(16 DOWNTO 0);
	signal times_one_hundo : std_logic_vector(15 DOWNTO 0) := X"0064";
	
	signal tenners : std_logic_vector(16 DOWNTO 0);
	signal ten : std_logic_vector(15 DOWNTO 0) := X"0CCD";

	signal times_tenner : std_logic_vector(16 DOWNTO 0);
	signal times_ten : std_logic_vector(15 DOWNTO 0) := X"000a";

	signal shift_2 : unsigned(33 DOWNTO 0);
	signal shift_4 : unsigned(33 DOWNTO 0);
	signal shift_5 : unsigned(33 DOWNTO 0);
	signal final_answer_sig : std_logic_vector(7 DOWNTO 0);
	signal hundreds_digit : std_logic_vector(3 DOWNTO 0);
	signal tens_digit : std_logic_vector(3 DOWNTO 0);
BEGIN
	final_answer_sig <= val;
	div_one_hundos <= '0' & div_one_hundo;
	tenners <= '0' & ten;
	times_one_hundos <= '0' & times_one_hundo;
	times_tenner <= '0' & times_ten;

	process (val)
	begin
		cmpt_2 <= std_logic_vector(('0' & X"00" & unsigned(final_answer_sig)) * unsigned(div_one_hundos));
		shift_2 <= shift_right(unsigned(cmpt_2), 15);
		hundreds <= std_logic_vector(shift_2(3 downto 0));
		hundreds_digit <= std_logic_vector(shift_2(3 downto 0));

		cmpt_3 <= std_logic_vector(unsigned('0' & '0' & X"000000" & final_answer_sig) - unsigned('0' & X"000" & hundreds_digit) * unsigned(times_one_hundos));
		no_hundos <= cmpt_3;
		cmpt_4 <= std_logic_vector(unsigned('0' & X"00" & cmpt_3(7 downto 0)) * unsigned(tenners));
		shift_4 <= shift_right(unsigned(cmpt_4), 15);
		tens <= std_logic_vector(shift_4(3 downto 0));
		tens_digit <= std_logic_vector(shift_4(3 downto 0));

		cmpt_5 <= std_logic_vector(unsigned(no_hundos) - unsigned('0' & X"000" & tens_digit) * unsigned(times_tenner));
		ones <= std_logic_vector(cmpt_5(3 downto 0));
		
	end process;

END TypeArchitecture;
