// Logisim project johnson.circ as structural Verilog
module main (
  input  rst,
  input  miso,
  input  int1,
  input  intbypass,
  output mosi,
  output sclk,
  output cs,
  output mosi_test,
  output sclck_test,
  output cs_test,
  output miso_test,
  output int1_test,
  output s1_test,
  output s2_test,
  output s3_test,
  output mode_test,
  output dp1,
  output dp2,
  output dp3,
  output dp4,
  output dp5,
  output rst_led
);

  wire clock_1_out, spi_accelerometer_1_led0_dp;
  wire [6:0] spi_accelerometer_1_led0;

  Clock clock_1 (.out(clock_1_out));
  spi_accelerometer spi_accelerometer_1 (
    .clk50MHz(clock_1_out), .rst(rst), .miso(miso), .int1(int1), .intBypass(intbypass), .mosi(mosi),
    .sclk(sclk), .cs(cs), .mosi_test(mosi_test), .sclk_test(sclck_test), .cs_test(cs_test),
    .miso_test(miso_test), .int1_test(int1_test), .s1_test(s1_test), .s2_test(s2_test), .s3_test(s3_test),
    .mode_test(mode_test), .led0(spi_accelerometer_1_led0), .led0_dp(spi_accelerometer_1_led0_dp),
    .led1_dp(dp1), .led2_dp(dp2), .led3_dp(dp3), .led4_dp(dp4), .led5_dp(dp5), .rst_led(rst_led));
  _7_Segment_Display hex (
    .g(spi_accelerometer_1_led0[6]), .f(spi_accelerometer_1_led0[5]), .a(spi_accelerometer_1_led0[0]),
    .b(spi_accelerometer_1_led0[1]), .e(spi_accelerometer_1_led0[4]), .d(spi_accelerometer_1_led0[3]),
    .c(spi_accelerometer_1_led0[2]), .dp(spi_accelerometer_1_led0_dp));
endmodule

// VHDL entity spi_accelerometer, as the project stores it:
--top_level.vhd
library ieee;
use ieee.std_logic_1164.all;

entity spi_accelerometer is
	port(
		clk50MHz : in std_logic;
		rst 		: in std_logic;
		mosi		: out std_logic;
		miso 		: in std_logic;
		sclk 		: out std_logic;
		cs 		: out std_logic;
		
		mosi_test: out std_logic;
		sclk_test: out std_logic;
		cs_test 	: out std_logic;
		miso_test : out std_logic;
		int1_test : out std_logic;
		
		s1_test  : out std_logic;
		s2_test  : out std_logic;
		s3_test  : out std_logic;
		mode_test : out std_logic;
		
		
	
		int1 		: in std_logic;
		intBypass : in std_logic;
--		int2 		: in std_logic;
--		
--		pol		: in std_logic;
--		pha		: in std_logic;
--		bytes		: in std_logic_vector (1 downto 0);
		
		
		led0     : out std_logic_vector(6 downto 0);
      led0_dp  : out std_logic;
      led1_dp  : out std_logic;
      led2_dp  : out std_logic;
      led3_dp  : out std_logic;
      led4_dp  : out std_logic;
      led5_dp  : out std_logic;
		
		rst_led  : out std_logic
	
	);
	
end spi_accelerometer;


architecture STR of spi_accelerometer is

	
	signal go : std_logic;
	signal pol : std_logic;
	signal pha : std_logic;
	signal bytes : std_logic_vector (3 downto 0);
	signal rxData : std_logic_vector (7 downto 0);
	signal rxDataReady	: std_logic := '0';
	signal txData 		:		 std_logic_vector (7 downto 0);
	signal accel_data	:		 std_logic_vector (47 downto 0);-- := (others => '0');
	
	signal sclk_out : std_logic;
	
	signal sclk_buffer	:	std_logic;
	signal mosi_buffer	:	std_logic;
	signal cs_buffer	:	std_logic;
--	signal miso_buffer : std_logic;
	signal int1_buffer : std_logic;
	signal stateID : std_logic_vector(2 downto 0);
	

begin

	------------------------------------
	--SPI MASTER
	------------------------------------
	U_SPI_MASTER	:  spi_master(FSM_1P)
		port map(
		clk	=> clk50MHz,
		rst	=> rst,
      mosi	=> mosi_buffer,
		miso 	=> miso,
		--sclk_out => sclk_buffer,
		sclk_out => sclk_out,
		cs_out	=> cs_buffer,
		int1 	=> '0',
		int2 	=> '0',
		go		=> go,
		pol	=> pol,
		pha   => pha,
		bytes => bytes,
		rxData	=> rxData,
		txData	=> txData,
		rxDataReady	=> rxDataReady
	);
	
	int1_test <= int1_buffer;
	miso_test <= miso;
	mosi <= mosi_buffer;
	cs <= cs_buffer;
	sclk <= sclk_buffer;
	mosi_test <= mosi_buffer;
	sclk_test <= sclk_buffer;
	cs_test 	 <= cs_buffer;
	
	s1_test <= stateID(0);
	s2_test <= stateID(1);
	s3_test <= stateID(2);
	led0_dp <= stateID(0);
	led1_dp <= stateID(1);
	led2_dp <= stateID(2);
	--mode_test <= m;
	
	rst_led <= not rst;
	
	U_ACCEL_DRIVER : accel_driver(FSM_1P)
		port map(
			rst			=> rst,
			clk			=> clk50MHz,
			int1			=> int1_buffer,
			rxDataReady	=> rxDataReady,
			go				=> go,
			pol			=> pol,
			pha			=> pha,
			bytes 		=> bytes,
			txData 		=> txData,
			rxData		=> rxData,
			accel_data	=> accel_data,
			stateID => stateID,
			m => mode_test,
			c => led4_dp,
			intBypass => intBypass
		);
	

	
	------------------------------------
	--LED's
	--      MSB       LSB
	--	XL =  7 downto  0
	--	XH = 15 downto  8
	--	YL = 23 downto 16
	--	YH = 31 downto 24
	--	ZL = 39 downto 32
	--	ZH = 47 downto 40
	------------------------------------
	U_LED0	:	decoder7seg
		port map(
			input => accel_data(7 downto 4),
			output =>led0
		);
	--led0_dp <= '1';
	--led0 <= b"1111111";

	--U_LED1	:	entity work.decoder7seg
		--port map(
			--input => accel_data(7 downto 4),
			--output =>led1
		--);
	--led1_dp <= '0';
	--led1 <= b"1111111";
	
	--U_LED2	:	entity work.decoder7seg
		--port map(
			--input => accel_data(19 downto 16),
			--output =>led2
		--);
--	led2_dp <= '0';
	--led2 <= b"1111111";

	--U_LED3	:	entity work.decoder7seg
		--port map(
			--input => accel_data(23 downto 20),
			--output =>led3
		--);
--	led3_dp <= '0';
	--led3 <= b"1111111";
	
	--U_LED4	:	entity work.decoder7seg
		--port map(
			--input => accel_data(35 downto 32),
			--output =>led4
		--);
--	led4_dp <= '0';
--led4 <= b"1111111";

	--U_LED5	:	entity work.decoder7seg
		--port map(
			--input => accel_data(39 downto 36),
			--output =>led5
		--);
	--led5 <= b"1111111";
	led5_dp <= not int1;


	
	
	
	
	process(clk50MHz, rst)
	begin
	
		if(rst = '1') then
			sclk_buffer <= '1';
			int1_buffer <= '0';
		elsif(clk50MHz'event and clk50MHz = '1') then
			sclk_buffer <= sclk_out;
			int1_buffer <= int1;
		end if;
	end process;
	
	
	

	
	
end STR;

// VHDL entity spi_master, as the project stores it:
--spi_master

library ieee;
use ieee.std_logic_1164.all;
use ieee.numeric_std.all;

entity spi_master is
    port (
		clk	: in std_logic;
		rst	: in std_logic;
      mosi	: out std_logic;
		miso 	: in std_logic;
		sclk_out : out std_logic; 
		cs_out	: out std_logic;
		int1 	: in std_logic;
		int2 	: in std_logic;
		go		: in std_logic;
		pol	: in std_logic;
		pha   : in std_logic;
		bytes : in std_logic_vector (3 downto 0);
		rxData: out std_logic_vector(7 downto 0);
		txData: in  std_logic_vector(7 downto 0);
		rxDataReady: out std_logic
		);
end spi_master;


architecture FSM_1P of spi_master is


------------------------------------
-- State signals
------------------------------------
type STATE_TYPE is (S_IDLE, S_TXRX);
signal state, next_state : STATE_TYPE;


------------------------------------
-- Clock Div (spi clock) Signals
------------------------------------
signal sclk : std_logic;
signal enable : std_logic := '0';
--signal bytes : std_logic_vector (3 downto 0);
signal polarity : std_logic;
signal last_clk_active : std_logic;
signal clk_active : std_logic;
signal byte_flag : std_logic;

------------------------------------
-- SPI Data Signals
------------------------------------
signal rx_buffer	: std_logic_vector (7 downto 0) := (others => '1');
signal tx_buffer	: std_logic_vector (7 downto 0);
signal cs : std_logic := '1';
constant byte_w : natural := 8;
signal bit : integer range -1 to 8 := 7; --init to msb+1 idx
signal w_r : std_logic := '0'; --write = 0 read = 1
signal phase_Delay : std_logic := '0';
signal last_cs : std_logic := '1';
signal last_sclk : std_logic := '0';



begin


	U_CLOCK_DIV : clock_div
		generic map(
			clk_in_freq => 50000000,
			clk_out_freq => 5000000)
		port map(
			clk_in => clk,
			clk_out => sclk,
			rst	=> rst,
			enable => enable,
			bytes	=> bytes,
			polarity => polarity,
			clk_active => clk_active,
			byte_flag => byte_flag);



	--enable <= int1 or int2 or go;
	
	process (clk, rst)
	begin
		
		if(rst = '1') then
			state <= S_IDLE;
			last_clk_active <= '0';
			enable <= '0';
			cs <= '1';
		elsif (clk'event and clk = '1') then
			
	
		--process(state, int1, int2, go, clk_active, byte_flag)--, txData)
		--begin
		
			rxDataReady <= '0'; --only high when data is ready
			polarity <= pol;
			--w_r <= not pha; --first write for phase 1 is pre toggled. 0 is default
		--	next_state <= state;
			enable <= '0';
			
			last_clk_active <= clk_active;
			
			case state is
				when S_IDLE =>
					
					--enable <= '0'; --default 
					cs <= '1';
					if((int1 = '1' or int2 = '1' or go = '1') and rst = '0') then
						state <= S_TXRX;
	--					polarity <= pol;
	--					w_r <= not pha; --first write for phase 1 is pre toggled. 0 is default
						enable <= '1';
						cs <= '0';
						tx_buffer <= txData; --TEST
						
					end if;
				
				
				when S_TXRX =>
					
					
					enable <= '1';
					
					if(last_clk_active = '1' and clk_active = '0') then  --falling edge of clk_active
						enable <= '0';
						cs <= '1';
						rxDataReady <= '1';
						state <= S_IDLE;
					
					else 
						enable <= '1';
						cs <= '0';
						if(byte_flag = '1') then
							rxDataReady <= '1';
							tx_buffer <= txData;
						end if;
					
					end if;
						
				when others => null;
				
				
			end case;
			
			
		end if;
		
	end process;
	
	cs_out <= cs;
	sclk_out <= sclk;
	
	
	
	
	process (clk, sclk, cs, rst)--, state)
	
	begin
		
		if( rst = '1') then
			bit <= 7;
			mosi <= '1';
		--else
		elsif(clk'event and clk = '1') then
		last_cs <= cs;
		last_sclk <= sclk;  --clk version
--		if(state'event and state = S_IDLE) then		-- entering idle init bit and rxbuffer
--			w_r <= pha;
--			bit <= 7;
--			rx_buffer <= (others => '1');
--			--initialize w/r
--			-- this will update whenever pha updates or state changes to re-init
--		
--		elsif ( state'event and state = S_TXRX) then -- state should not trigger any toggling
--			null;
--		else
		
			--pha 0 means write on falling cs
			--pha 1 means write on first clk edge
			-- w/r 0 means write
			--w/r 1 means read
			if(cs = '0' and last_cs = '1' ) then
				
				w_r <= not pha;				--pha 1 goes to write and pha 0 goes to read
				
				if(pha = '0') then
					mosi <= tx_buffer(bit); --write	
				end if;
				
			elsif(cs = '0' and (last_sclk /= sclk)) then									-- this point on are only clk events high or low
				
				if(w_r = '0') 	then				-- write
					mosi <= tx_buffer(bit);
					
				elsif (w_r = '1') then		-- read
					rx_buffer <= rx_buffer(6 downto 0) & miso;
					bit <= bit - 1;			-- only decrement after reads
					if(bit = 0) then			-- reset bit to 7 at end of byte instead of decrementing
						bit <= 7;
						--rxData <= rx_buffer;
					end if;
				else 
					null;							-- do nothing
				end if;
				
				w_r <= not w_r;				-- toggle write/read for next clock edge
				
			else 
				--mosi <= 'Z';
				null;
			end if;
			
			if(bit = 7) then
				rxData <= rx_buffer;
			end if;
			
		end if;
	
	
	
	end process;
	

	--rxData <= rx_buffer;
end FSM_1P;



architecture FSM_2P of spi_master is


------------------------------------
-- State signals
------------------------------------
type STATE_TYPE is (S_IDLE, S_TXRX);
signal state, next_state : STATE_TYPE;


------------------------------------
-- Clock Div (spi clock) Signals
------------------------------------
signal sclk : std_logic;
signal enable : std_logic := '0';
--signal bytes : std_logic_vector (3 downto 0);
signal polarity : std_logic;
signal clk_active : std_logic;
signal byte_flag : std_logic;

------------------------------------
-- SPI Data Signals
------------------------------------
signal rx_buffer	: std_logic_vector (7 downto 0) := (others => '1');
signal tx_buffer	: std_logic_vector (7 downto 0);
signal cs : std_logic := '1';
constant byte_w : natural := 8;
signal bit : integer range -1 to 8 := 7; --init to msb+1 idx
signal w_r : std_logic := '0'; --write = 0 read = 1
signal phase_Delay : std_logic := '0';
signal last_cs : std_logic := '1';
signal last_sclk : std_logic := '0';



begin


	U_CLOCK_DIV : clock_div
		generic map(
			clk_in_freq => 50000000,
			clk_out_freq => 5)
		port map(
			clk_in => clk,
			clk_out => sclk,
			rst	=> rst,
			enable => enable,
			bytes	=> bytes,
			polarity => polarity,
			clk_active => clk_active,
			byte_flag => byte_flag);



	--enable <= int1 or int2 or go;
	
	process (clk, rst)
	begin
		
		if(rst = '1') then
			state <= S_IDLE;
		elsif (clk'event and clk = '1') then
			state <= next_state;
		end if;
	
	
	end process;
	
	
	process(state, int1, int2, go, clk_active, byte_flag)--, txData)
	begin
	
		rxDataReady <= '0'; --only high when data is ready
		polarity <= pol;
		--w_r <= not pha; --first write for phase 1 is pre toggled. 0 is default
		next_state <= state;
		enable <= '0';
		
		
		case state is
			when S_IDLE =>
				
				--enable <= '0'; --default 
				cs <= '1';
				if((int1 = '1' or int2 = '1' or go = '1') and rst = '0') then
					next_state <= S_TXRX;
--					polarity <= pol;
--					w_r <= not pha; --first write for phase 1 is pre toggled. 0 is default
					enable <= '1';
					cs <= '0';
					tx_buffer <= txData; --TEST
					
				end if;
			
			
			when S_TXRX =>
				
				
				enable <= '1';
				
				if(clk_active = '0') then
					enable <= '0';
					cs <= '1';
					rxDataReady <= '1';
					next_state <= S_IDLE;
				
				else 
					enable <= '1';
					cs <= '0';
					if(byte_flag = '1') then
						rxDataReady <= '1';
						tx_buffer <= txData;
					end if;
				
				end if;
					
			when others => null;
			
			
		end case;
		
	end process;
	
	cs_out <= cs;
	sclk_out <= sclk;
	
	
	
	
	process (clk, sclk, cs, rst)--, state)
	
	begin
		
		if( rst = '1') then
			bit <= 7;
			mosi <= '1';
		--else
		elsif(clk'event and clk = '1') then
		last_cs <= cs;
		last_sclk <= sclk;  --clk version
--		if(state'event and state = S_IDLE) then		-- entering idle init bit and rxbuffer
--			w_r <= pha;
--			bit <= 7;
--			rx_buffer <= (others => '1');
--			--initialize w/r
--			-- this will update whenever pha updates or state changes to re-init
--		
--		elsif ( state'event and state = S_TXRX) then -- state should not trigger any toggling
--			null;
--		else
		
			--pha 0 means write on falling cs
			--pha 1 means write on first clk edge
			-- w/r 0 means write
			--w/r 1 means read
			if(cs = '0' and last_cs = '1' ) then
				
				w_r <= not pha;				--pha 1 goes to write and pha 0 goes to read
				
				if(pha = '0') then
					mosi <= tx_buffer(bit); --write	
				end if;
				
			elsif(cs = '0' and (last_sclk /= sclk)) then									-- this point on are only clk events high or low
				
				if(w_r = '0') 	then				-- write
					mosi <= tx_buffer(bit);
					
				elsif (w_r = '1') then		-- read
					rx_buffer <= rx_buffer(6 downto 0) & miso;
					bit <= bit - 1;			-- only decrement after reads
					if(bit = 0) then			-- reset bit to 7 at end of byte instead of decrementing
						bit <= 7;
					end if;
				else 
					null;							-- do nothing
				end if;
				
				w_r <= not w_r;				-- toggle write/read for next clock edge
				
			else 
				--mosi <= 'Z';
				null;
			end if;
		end if;
	
	
	
	end process;
	
--	
--	process (sclk, cs, state, pha)
--		variable clk_cs_event : std_logic;
--	
--	begin
--	
--		if(state = S_IDLE) then
--			w_r <= pha;
--			bit <= 7;
--			rx_buffer <= (others => '1');
--			--initialize w/r
--			-- this will update whenever pha updates or state changes to re-init
--		end if;
--			
--			clk_cs_event := '0';
--			
--		if(falling_edge(cs) or (sclk'event and cs = '0')) then
--			w_r <= not w_r;
--			clk_cs_event := '1';
--		end if;
--		--if sclk event, do w/r and then toggle it
--		-- if cs falls and pha = 1, write
--		
--		--write if w/r = 0 
--			--this works because at init w/r =  pha
--			-- so  pha = 0 is 1. no case will be true and w/r will toggle
--			--next event will be a clok edge
--		-- read if w/r = 1 
--			-- if cs event and pha
--			
--		if(clk_cs_event = '1') then
--			if(w_r = '0') then	--write
--				mosi <= tx_buffer(bit);
--				
--			elsif((falling_edge(cs) and (pha = '0')) or (sclk'event and w_r = '1')) then --read
--				rx_buffer <= rx_buffer(6 downto 0) & miso;
--				bit <= bit - 1;
--				if(bit = 0) then			-- reset bit to 7 at end of byte instead of decrementing
--					bit <= 7;
--				end if;
--				
--			end if;
--			
--
--		end if;
--		
--	
--	end process;
	
	
	
	
--	process(sclk, cs)
--	begin
--		
--		-- phase
--		-- 0 start : write on cs, read on first clock
--		--	0 normal: write on first edge, read on second edge
--		-- 1 start : write on first edge, read on second edge
--		-- 1 normal: write on first edge, read on second edge
--	
--		
--		phase_Delay <= '0'; --set delay to false
--		
--		if( bit = 0) then
--			bit <= 7;
--		end if;
--		
--		bit <= bit - 1;
--		
----	
--		
--		if ( sclk'event ) then
--		--	w_r <= not w_r; 
--		
--		elsif (falling_edge(cs) and pha = '0') then
--			--write
--			--next clock is going to be raising or falling
--			--if pol 0, then rising
--			--if pol 1, then falling
--			phase_Delay <= '1';
--		
--		end if;
--		
--		
--		if ( w_r = '0' and phase_Delay = '0') then --write except if pha = 1 and before first clk event
--			
--			mosi <= tx_buffer(bit);
--			
--		elsif(w_r = '1') then  --read
--			rx_buffer <= miso & rx_buffer(7 downto 1);
--		end if;
--	
--		
--	end process;
	
	--tx_buffer <= txData;
	rxData <= rx_buffer;


end FSM_2P;

// VHDL entity decoder7seg, as the project stores it:
--decoder7seg
library ieee;
use ieee.std_logic_1164.all;

entity decoder7seg is
    port (
        input  : in  std_logic_vector(3 downto 0);
        output : out std_logic_vector(6 downto 0));
end decoder7seg;

architecture BHV of decoder7seg is

begin  -- BHV

	process(input)
		begin
		
			case input is
				when "0000" =>  output <= "1000000";--"0000001";
				when "0001" =>  output <= "1000111";--"0101111";
				when "0010" =>  output <= "1000111";--"0101111";
				when "0011" =>  output <= "1000111";--"0101111";
				when "0100" =>  output <= "1000111";--"0101111";
				when "0101" =>  output <= "1000111";--"0101111";
				when "0110" =>  output <= "1000111";--"0101111";
				when "0111" =>  output <= "1000111";--"0101111";
				when "1000" =>  output <= "1000111";--"0101111";
				when "1001" =>  output <= "0101111";--"1000111";ici
				when "1010" =>  output <= "0101111";--"1000111";
				when "1011" =>  output <= "0101111";--"1000111";
				when "1100" =>  output <= "0101111";--"1000111";
				when "1101" =>  output <= "0101111";--"1000111";
				when "1110" =>  output <= "0101111";--"1000111";
				when "1111" =>  output <= "0101111";--"1000111";
				when others =>  output <= "XXXXXXX";
			end case;
		end process;

end BHV;

// VHDL entity clock_div, as the project stores it:
--clock div
library ieee;
use ieee.std_logic_1164.all;
use ieee.numeric_std.all;

entity clock_div is
	generic(clk_in_freq : natural := 4;
				clk_out_freq : natural := 2);
	port (
			clk_in : in std_logic;
			clk_out : out std_logic;
			rst	: in std_logic;
			enable : in std_logic;
			bytes : in std_logic_vector(3 downto 0);
			polarity : in std_logic;
			clk_active :	out std_logic;
			byte_flag : out std_logic
			);
end clock_div;

architecture bhv of clock_div is

	
	constant max : natural := clk_in_freq / clk_out_freq / 2;
	signal count, lastByteCount : integer range 0 to max*2;
	signal clock_signal : std_logic;
	signal byte_count : std_logic_vector (3 downto 0);
	signal bit_count : integer range 0 to 8;
	
	
	
	
	begin
	
		process(clk_in, rst)
		begin
			if(rst = '1' or enable = '0') then
				count <= 0;
				lastByteCount <= 0;
				clk_active <= '0';
				clock_signal <= polarity;
				bit_count <= 0;
				byte_count <= (others => '0');
				byte_flag <= '0';
			
			elsif(clk_in'event and clk_in = '1') then
				if(enable = '1' and byte_count < bytes) then
				
					clk_active <= '1';
					if (count = max-1) then
						count <= 0;
						clock_signal <= not clock_signal;
						
						if((not clock_signal) = polarity) then
							--increment bit count
							--increment byte count after 8 bits and clean bit count
							--clear byte count after numOfBytes and clear active_clk
							
							byte_flag <= '0'; -- clear the byte flag
						
							if(bit_count = 7) then
								byte_count <= std_logic_vector(unsigned(byte_count) + 1);
								bit_count <= 0;
								byte_flag <= '1'; --set byte flag for one sclk cycle
								
								if( byte_count = std_logic_vector(unsigned(bytes) - 1)) then
									--clk_active <= '0';
									--clock_signal <=  clock_signal; --do not toggle clock 
									
								end if;
							
								
							else
								bit_count <= bit_count + 1;
							end if;
							
--							if( byte_count = bytes) then
--								clk_active <= '0';
--							end if;
							
						end if;
					else
						count <= count + 1;
					end if;
				
			
				elsif(enable = '1') then
			
					clk_active <= '1';
						if (lastByteCount = max-1) then
							lastByteCount <= 0;
							clk_active <= '0';
						else
							lastByteCount <= lastByteCount + 1;
						end if;
				end if;
				
				
				
			end if;
		
		
--			if(rst = '1' or enable = '0') then
--				count <= 0;
--				lastByteCount <= 0;
--				clk_active <= '0';
--				clock_signal <= polarity;
--				bit_count <= 0;
--				byte_count <= (others => '0');
--				byte_flag <= '0';
--			
--			elsif(rising_edge(clk_in) and enable = '1' and byte_count < bytes) then
--				
--					clk_active <= '1';
--					if (count = max-1) then
--						count <= 0;
--						clock_signal <= not clock_signal;
--						
--						if((not clock_signal) = polarity) then
--							--increment bit count
--							--increment byte count after 8 bits and clean bit count
--							--clear byte count after numOfBytes and clear active_clk
--							
--							byte_flag <= '0'; -- clear the byte flag
--						
--							if(bit_count = 7) then
--								byte_count <= std_logic_vector(unsigned(byte_count) + 1);
--								bit_count <= 0;
--								byte_flag <= '1'; --set byte flag for one cycle
--								
--								if( byte_count = std_logic_vector(unsigned(bytes) - 1)) then
--									--clk_active <= '0';
--									--clock_signal <=  clock_signal; --do not toggle clock 
--									
--								end if;
--							
--								
--							else
--								bit_count <= bit_count + 1;
--							end if;
--							
----							if( byte_count = bytes) then
----								clk_active <= '0';
----							end if;
--							
--						end if;
--					else
--						count <= count + 1;
--					end if;
--				
--			
--			elsif(rising_edge(clk_in) and enable = '1') then
--			
--				clk_active <= '1';
--					if (lastByteCount = max-1) then
--						lastByteCount <= 0;
--						clk_active <= '0';
--					else
--						lastByteCount <= lastByteCount + 1;
--					end if;
--				
--				
--				
--			end if;
		--clk_out <= clock_signal;
		end process;
		
		clk_out <= clock_signal;




end bhv;

// VHDL entity accel_driver, as the project stores it:
--accel_driver
-- TODO:
-- 1) Incorporate data range generic for calibration LSB/g for z axis
library ieee;
use ieee.std_logic_1164.all;
use ieee.numeric_std.all;

entity accel_driver is
	port (
		rst			:		in std_logic;
		clk			:		in std_logic;
		int1			:		in std_logic;
		rxDataReady	:		in	std_logic;
		go				:		out std_logic;
		pol			:		out std_logic;
		pha			:		out std_logic;
		bytes 		:		out std_logic_vector (3 downto 0);
		txData 		:		out std_logic_vector (7 downto 0);
		rxData		: 		in std_logic_vector ( 7 downto 0);
		accel_data	:		out std_logic_vector (47 downto 0);
		
		stateID 		:      out std_logic_vector (2 downto 0);
		m				: out std_logic;
		c				: out std_logic;
		intBypass   : in std_logic
		
		
	);
end accel_driver;



architecture fsm_1p of accel_driver is
	
	constant max	: natural := 50000000 /  500000 ;
	signal count			:		integer range 0 to max;
	signal countSignal		: std_logic;
	type STATE_TYPE is (S_START, S_IDLE, S_CONFIG, S_WRITE, S_READ, S_READ_WAIT, S_CALIBRATE, S_OUTPUT); --S_CONFIG_TEST, S_WRITE_TEST);
	signal STATE, NEXT_STATE			:		STATE_TYPE;
	--signal accel_x, accel_y, accel_z	:		std_logic_vector(15 downto 0);
	signal accel_data_buff : std_logic_vector( 47 downto 0);
	signal byteCount	: integer range -1 to 16 := 0;
	constant byteCountRead : integer := 7;
	signal mode			: std_logic;
	signal reg	: integer range 0 to 8;
	signal regTest : integer range 0 to 16;
	signal regAddr		: std_logic_vector (5 downto 0);
	signal regData		: std_logic_vector (7 downto 0);
	signal rxDataReadyLast : std_logic := '0';
	
	constant sampleBits : natural := 4;
	constant samples  : natural := 2 ** sampleBits;
	--signal div_padding : std_logic_vector (sampleBits - 1 downto 0);
	signal sample_count : integer range 0 to samples + 1;
	signal calibrate : std_logic;
	--type NIBBLE is array (3 downto 0) of std_ulogic;
	type calibration_array is array (2 downto 0) of std_logic_vector (15 downto 0);  -- (0) X accumulate, (1) Y accumulate, (2) Z accumulate
	signal calibData : calibration_array;
	
begin




	process(clk, rst)
	begin
		if(rst = '1') then
			state <= S_START;
			accel_data <= (others => '0');
			accel_data_buff <= (others => '0');
			regData <= "00000000";
			regAddr <= "000000";
			bytes <= "0000";
			txData <= "00000000";
			mode <= '0';
			count <= 0;
			go <= '0';
			reg <= 0;
			regTest <= 0;
			byteCount <= 0;
			stateID <= "000";
			calibrate <= '0';
			calibData(0) <= (others => '0');
			calibData(1) <= (others => '0');
			calibData(2) <= (others => '0');
			sample_count <= 0;
			--div_padding <= (others => '0');
			
		elsif(clk'event and clk = '1') then
			
			
			
			case state is
			
				when S_START =>
					byteCount <= 0;
					mode <= '0';
					reg <= 0;
					rxDataReadyLast <= '0';
					state <= S_IDLE;
					accel_data <= (others => '0');
					go <= '0';
					
					stateID <= "001";
				
				when S_IDLE =>
					stateID <= "010";
					--if(mode = '1' and int1 = '1') then state <= S_READ;
					--end if;
		
					if(count = max - 1) then							-- delay between each transmission 
						--count <= 0;
						c <= '1';
						
						if(mode = '0') then
							state <= S_CONFIG;		-- mode 0 is config. after config mode goes to 1 for read
							count <= 0; 
						--elsif(int1 = '1')   then
						else
							state <= S_READ_WAIT;	-- mode 1, but only read if interrupt for data_ready is set
							count <= 0;
						--else count <= max - 1;							-- do not set count to 0 to prevent running the delay loop again
						end if;	
			
					else 
						count <= count + 1;
						c <= '0';
					end if;
					
--					if(intBypass = '1') then state <= S_IDLE;
--					end if;
			
				when S_READ_WAIT =>
					stateID <= "111";
					if (calibrate = '1') then state <= S_CALIBRATE;
					elsif(int1 = '1' or intBypass = '1') then state <= S_READ;
					end if;
					
				when S_CALIBRATE => 
					case reg is								-- reg should be 0 from config state earlier, represents each offset register
						when 0 =>							-- calculate the negative of x and y offset. subtract 256 (1g) from z and shift 2 (8 bit conversion)
							if(calibData(0)(15) = '0') then  -- x axis negative conversion
								calibData(0) <= std_logic_vector(signed(not calibData(0)) + 1);	-- twos comp conversion from positive to negative
							else
								calibData(0) <= std_logic_vector(not(signed(calibData(0)) - 1));  -- twos comp conversion from negative to positive
							end if;
							
							if(calibData(1)(15) = '0') then -- y axis negative conversion
								calibData(1) <= std_logic_vector(signed(not calibData(1)) + 1);	-- twos comp conversion from positive to negative
							else
								calibData(1) <= std_logic_vector(not(signed(calibData(1)) - 1));  -- twos comp conversion from negative to positive
							end if;
							
							calibData(2) <=std_logic_vector(shift_right(signed(calibData(2)) - 256, 2));	-- find error realtive to gravity in z axis and divide by 4 for 10 to 8 bit conversion			
							reg <= reg + 1;
						
						when 1 =>																					-- calculate Z's negative, store x axis
						
							if(calibData(2)(15) = '0') then 													-- Z axis negative conversion
								calibData(2) <= std_logic_vector(signed(not calibData(2)) + 1);	-- twos comp conversion from positive to negative
							else
								calibData(2) <= std_logic_vector(not(signed(calibData(2)) - 1));  -- twos comp conversion from negative to positive
							end if;
							
							regAddr <= "011110";																	-- Register 0x1E: "X offset" 8 bit 2's comp offset for X axis
							regData <= calibData(0)(7 downto 0);															-- X offset data
							reg <= reg + 1;	
							state  <= S_WRITE;
						when 2 =>
							regAddr <= "011111";																	-- Register 0x1F: "Y offset" 8 bit 2's comp offset for Y axis
							regData <= calibData(1)(7 downto 0);
							reg <= reg + 1;
							state  <= S_WRITE;
						when 3 =>
							regAddr <= "100000";																	-- Register 0x20: "Z offset" 8 bit 2's comp offset for Z axis
							regData <= calibData(2)(7 downto 0);
							reg <= 0;
							state  <= S_WRITE;
							calibrate <= '0';																		-- de-assert calibration flag to continue reading normally
						when others => null;
						
					end case;
					
					
--				when S_CONFIG_TEST =>
--						stateID <= "111";
--					case regTest is
--						when 0 =>
--							regAddr <= "110001";			--	Off 		Off   A
--							regData <= "00001010";
--							regTest <= regTest + 1;
--							state <= S_WRITE;
--						when 1 => 
--							regAddr <= "101100";									-- 6
--							regData <= "00000110";
--							regTest <= regTest + 1;
--							state <= S_WRITE;
--						when 2 => 
--							regAddr <= "101101";                          --8
--							regData <= "00001011";
--							regTest <= regTest + 1;
--							state <= S_WRITE;
--						when 3 =>
--							--regAddr <= "000000";    -- A      OFF	ON
--							regAddr <= "110001";
--							regData <= "00001000";
--							regTest <= regTest + 1;
--							--regTest <= 0;
--							
--							state <= S_WRITE_TEST;					
--						when 4 => 						-- E5			ON     ON
--							--regAddr <= "101100";
--							regAddr <= "000000";
--							regData <= "00000000";
--							regTest <= regTest + 1;
--							state <= S_WRITE_TEST;
--							
--						when 5 => 						-- B			ON    OFF
--							regAddr <= "101101";
--							regData <= "00000000";
--							regTest <= 0;
--							state <= S_WRITE_TEST;
--							mode <= '1';
--							
--
--						when others => null;
--					end case;
--					
--				when S_WRITE_TEST =>
--					mode <= '0';
--					bytes <= "0010";
--					rxDataReadyLast <= rxDataReady;
--					if(byteCount = 0) then
--						txData <= "10" & regAddr;
--						go <= '1';
--						byteCount <= 1;
--					else
--						txData <= "00000000";
--						go <= '0';
--						
--						if((rxDataReadyLast = '1' and rxDataReady = '0') and byteCount <= 2) then
--	--						byteCount <= byteCount + 1;
--	--						accel_data_buff((byteCount * 8)  - 1 downto (byteCount-1) * 8) <= rxData;
--	--						if(byteCount = byteCountRead - 1) then
--	--							byteCount <= 0;
--	--							next_state <= S_OUTPUT;
--	--						end if;
--							if(byteCount = 2) then
--								byteCount <= 0;
--								state <= S_OUTPUT;
--							else
--								byteCount <= byteCount + 1;
--								accel_data_buff(23 downto 16) <= rxData;
--							end if;
--
--
--						end if;
--						
--						
--					end if;
--					
--				
				
				
				when S_CONFIG =>
						stateID <= "011";
					case reg is
						when 0 =>
							regAddr <= "110001"; -- Register 0x31: "Data_Format" sets data range (0b00) to +/- 2g and full resultion (0b1000)
							regData <= "00001000";   
							reg <= reg + 1;
							state <= S_WRITE;
						when 1 => 
							regAddr <= "101100";  -- Register 0x2C: "BW_RATE" sets rate (0b0100) to 1.56 Hz, ideal should be 100hz which is default at power reset, but too fast for 7seg's
							regData <= "00000100";
							reg <= reg + 1;
							state <= S_WRITE;
						when 2 =>
							regAddr <= "011110";					-- Register 0x1E: "X offset" 8 bit 2's comp offset for X axis
							regData <= "00000000";				-- Clear X offset register so calibration will not use data from previous resets
							reg <= reg + 1;
							state  <= S_WRITE;
							
						when 3 =>
							regAddr <= "011111";					-- Register 0x1F: "Y offset" 8 bit 2's comp offset for Y axis
							regData <= "00000000";				-- Clear Y offset register so calibration will not use data from previous resets
							reg <= reg + 1;
							state  <= S_WRITE;
						
						when 4 =>
							regAddr <= "100000";					-- Register 0x20: "Z offset" 8 bit 2's comp offset for Z axis
							regData <= "00000000";				-- Clear Z offset register so calibration will not use data from previous resets
							reg <= reg + 1;
							state  <= S_WRITE;
						
						when 5 => 
							regAddr <= "101101";	 -- Register 0x2D: "Power_CTL" sets measure bit (0b1000) to start sampling. 
							regData <= "00001000";
							reg <= reg + 1;
							state <= S_WRITE;
							--mode <= '1';			-- Switch to Read mode so IDLE turns to S_READ and not S_CONFIG
						when 6 => 
							regAddr <= "101110";	 -- Register 0x2E: "INT_ENABLE" enables Data_Ready interrupt (0b10000000) 
							regData <= "10000000";
							reg <= 0;
							state <= S_WRITE;
							mode <= '1';			-- Switch to Read mode so IDLE turns to S_READ and not S_CONFIG
						when others => null;
					end case;
				
				when S_WRITE =>
					stateID <= "100";
					bytes <= "0010";
					rxDataReadyLast <= rxDataReady;
					if(byteCount = 0) then
						txData <= "00" & regAddr;
						go <= '1';
						byteCount <= 1;
					--elsif(rising_edge(rxDataReady) and byteCount = 1) then
					elsif((rxDataReadyLast = '0' and rxDataReady = '1') and byteCount = 1) then  -- rising edge
						byteCount <= 2;
						go <= '0';
						txData <= regData;
					elsif((rxDataReadyLast = '0' and rxDataReady = '1') and byteCount = 2) then  -- rising edge, nothing is transmitted here
						byteCount <= 3;
							
						
					elsif((rxDataReadyLast = '1' and rxDataReady = '0') and byteCount = 3) then  --falling edge
						state <= S_IDLE;
						byteCount <= 0;
					end if;
				--00111101 00001000
				when S_READ =>
					stateID <= "101";
					
					mode <= '1';
					bytes <= std_logic_vector(to_unsigned(byteCountRead, bytes'length));
					rxDataReadyLast <= rxDataReady;
					if(byteCount = 0) then														-- Send Read Command
						txData <= "11110010";
						go <= '1';
						byteCount <= 1;
					elsif(byteCount = 1) then													--next system clock enters here
						txData <= "00000000";							
						go <= '0';
						if((rxDataReadyLast = '1' and rxDataReady = '0')) then		--wait until 8 bits are sent to update byte count 
							byteCount <= 2;
						end if;
						
					else																				--read bytes 2 3 4 5 6 and 7
						txData <= "00000000";
						go <= '0';
						
						if((rxDataReadyLast = '1' and rxDataReady = '0') and byteCount <= byteCountRead) then
	--						byteCount <= byteCount + 1;
	--						accel_data_buff((byteCount * 8)  - 1 downto (byteCount-1) * 8) <= rxData;
	--						if(byteCount = byteCountRead - 1) then
	--							byteCount <= 0;
	--							next_state <= S_OUTPUT;
	--						end if;
							if(byteCount = byteCountRead) then
								byteCount <= 0;
								state <= S_OUTPUT;
							else
								byteCount <= byteCount + 1;
								accel_data_buff(((byteCount-1) * 8)  - 1 downto (byteCount-2) * 8) <=  rxData;-- std_logic_vector(to_unsigned(byteCount, bytes'length)); -- rxData;
							end if;


						end if;
						
						
					end if;
				when S_OUTPUT =>
					stateID <= "110";
					
					if(sample_count <= samples) then				-- enter for first n samples for calibration
						if(sample_count = samples) then			-- compare sample count to threshold 
							calibrate <= '1';							-- set flag to calibrate with new values
							calibData(0) <= std_logic_vector(shift_right(signed(calibData(0)), 2 + sampleBits)); -- divide by number of samples for average, and convert to 64 LSB/1g (shifting a 10 bit value right arithmetically for an 8 bit value)
							calibData(1) <= std_logic_vector(shift_right(signed(calibData(1)), 2 + sampleBits));
							calibData(2) <= std_logic_vector(shift_right(signed(calibData(2)), sampleBits)); -- get average. Next clock cycle will compare to 1g (2^8), and then convert to 64 LSB/1g
						else 												-- summation of samples
							calibData(0) <= std_logic_vector(signed(calibData(0)) + signed(accel_data_buff(15 downto   0))); -- summation of X data	
							calibData(1) <= std_logic_vector(signed(calibData(1)) + signed(accel_data_buff(31 downto  16))); -- summation of Y data	
							calibData(2) <= std_logic_vector(signed(calibData(2)) + signed(accel_data_buff(47 downto  32))); -- summation of Z data								
						end if;
						sample_count <= sample_count + 1;	-- increment count, if n samples have been collected, one more prevents entering this if statement
					accel_data <= accel_data_buff;
					else
						accel_data <= accel_data_buff;			-- clock collected accelerometer data for ouput
					end if;
						state <= S_IDLE;								-- go back to idle to repeat the cycle
					
				when others => 
					stateID <= "111";
						NULL;
				
			
			
			end case;


			pol <= '1';
			pha <= '1';
		
		end if;
		
	end process;

	
		m <= mode;





end fsm_1p;





architecture fsm_2p of accel_driver is
	
	constant max	: natural := 50000000 / 5000000 ;
	signal count			:		integer range 0 to max;
	signal countSignal		: std_logic;
	type STATE_TYPE is (S_START, S_IDLE, S_CONFIG, S_WRITE, S_READ, S_OUTPUT);-- S_TEST_IDLE, S_TEST_OUTPUT);
	signal STATE, NEXT_STATE			:		STATE_TYPE;
	--signal accel_x, accel_y, accel_z	:		std_logic_vector(15 downto 0);
	signal accel_data_buff : std_logic_vector( 47 downto 0);
	signal byteCount	: integer range -1 to 16;
	constant byteCountRead : integer := 7;
	signal mode			: std_logic;
	signal reg	: integer range 0 to 3;
	signal regAddr		: std_logic_vector (5 downto 0);
	signal regData		: std_logic_vector (3 downto 0);
	signal rxDataReadyLast : std_logic := '0';
begin




	process(clk, rst)
	begin
		if(rst = '1') then
			state <= S_START;
			count <= 0;
			
		elsif(clk'event and clk = '1') then
			
			
			if(state = S_IDLE) then
				if(count = max - 1) then
				count <= 0;
				state <= next_state;
			
				else 
				count <= count + 1;
				state <= S_IDLE;
				end if;
			
			else
			
			state <= next_state;
			end if;
				
				
		end if;
		
	end process;

	


	process(state, rxDataReady)
	begin
			next_state <= state;
			go <= '0';
			reg <= 0;
		--	byteCount <= 0;
			accel_data <= (others => '0');
			regData <= "0000";
			regAddr <= "000000";
			bytes <= "0000";
			txData <= "00000000";
			mode <= '0';
		case state is
		
			when S_START =>
				byteCount <= 0;
				mode <= '0';
				reg <= 0;
				rxDataReadyLast <= '0';
				next_state <= S_IDLE;
				--next_state <= S_TEST_IDLE;
				accel_data <= (others => '0');
				--go <= '0';
			
--			when S_TEST_IDLE =>
--				
--				bytes <= "0010";
--				rxDataReadyLast <= rxDataReady;
--				if(byteCount = 0) then
--					txData <= "10000000";
--					go <= '1';
--					byteCount <= 1;
--				--elsif(rising_edge(rxDataReady) and byteCount = 1) then
--				elsif((rxDataReadyLast = '0' and rxDataReady = '1') and byteCount = 1) then  -- rising edge
--					byteCount <= 2;
--					go <= '0';
--					txData <= "10000000";
--				elsif((rxDataReadyLast = '0' and rxDataReady = '1') and byteCount = 2) then  -- rising edge, nothing is transmitted here
--					byteCount <= 3;
--						
--					
--				elsif((rxDataReadyLast = '1' and rxDataReady = '0') and byteCount = 3) then  --falling edge
--					next_state <= S_TEST_OUTPUT;
--					byteCount <= 0;
--					accel_data_buff (7 downto 0) <= rxData;
--				end if;
--				
--			when S_TEST_OUTPUT =>
--				accel_data <= accel_data_buff;
--				--next_state <= S_IDLE;
				
			when S_IDLE =>
				mode <= mode;
				reg <= reg;
				if(mode = '0') then next_state <= S_CONFIG;
				else next_state <= S_READ;
				end if;	
				
					
			
			when S_CONFIG =>
				case reg is
					when 0 =>
						regAddr <= "110001";
						regData <= "1000";
						reg <= reg + 1;
						next_state <= S_WRITE;
					when 1 => 
						regAddr <= "101100";
						regData <= "0100";
						reg <= reg + 1;
						next_state <= S_WRITE;
					when 2 => 
						regAddr <= "101101";
						regData <= "1000";
						reg <= 0;
						next_state <= S_WRITE;
						mode <= '1';
--					when 3 =>
--						regAddr <= "000000";
--						regData <= "0000";
--						reg <= 0;
--						next_state <= S_WRITE;
--						mode <= '1';
					when others => null;
				end case;
			
			when S_WRITE =>
				bytes <= "0010";
				rxDataReadyLast <= rxDataReady;
				regAddr <= regAddr;
				regData <= regData;
				--byteCount <= byteCount;
				reg <= reg;
				mode <= mode;
				--txData <= txData;
				if(byteCount = 0) then
					txData <= "00" & regAddr;
					go <= '1';
					byteCount <= 1;
				--elsif(rising_edge(rxDataReady) and byteCount = 1) then
				elsif((rxDataReadyLast = '0' and rxDataReady = '1') and byteCount = 1) then  -- rising edge
					byteCount <= 2;
					go <= '0';
					txData <= "0000" & regData;
				elsif((rxDataReadyLast = '0' and rxDataReady = '1') and byteCount = 2) then  -- rising edge, nothing is transmitted here
					byteCount <= 3;
						
					
				elsif((rxDataReadyLast = '1' and rxDataReady = '0') and byteCount = 3) then  --falling edge
					next_state <= S_IDLE;
					byteCount <= 0;
				end if;
			--00111101 00001000
			when S_READ =>
				mode <= '1';
				bytes <= std_logic_vector(to_unsigned(byteCountRead, bytes'length));
				rxDataReadyLast <= rxDataReady;
				if(byteCount = 0) then
					txData <= "11110010";
					go <= '1';
					byteCount <= 1;
				else
					txData <= "00000000";
					go <= '0';
					--if(falling_edge(rxDataReady) and byteCount < byteCountRead) then		-- falling edge
					if((rxDataReadyLast = '1' and rxDataReady = '0') and byteCount <= byteCountRead) then
--						byteCount <= byteCount + 1;
--						accel_data_buff((byteCount * 8)  - 1 downto (byteCount-1) * 8) <= rxData;
--						if(byteCount = byteCountRead - 1) then
--							byteCount <= 0;
--							next_state <= S_OUTPUT;
--						end if;
						if(byteCount = byteCountRead) then
							byteCount <= 0;
							next_state <= S_OUTPUT;
						else
							byteCount <= byteCount + 1;
							accel_data_buff((byteCount * 8)  - 1 downto (byteCount-1) * 8) <= rxData;
						end if;


					end if;
					
					
				end if;
			when S_OUTPUT =>
				mode <= '1';
				accel_data <= accel_data_buff;
				next_state <= S_IDLE;
			when others => 
				NULL;
			
		
		
		end case;


		pol <= '1';
		pha <= '1';
		
		
		
	end process;







end fsm_2p;
