// Logisim project Lights_and_switches.circ as structural Verilog
module main (
  output [9:0] Output_bus_1
);

  wire [9:0] DipSwitch_1_sw10;

  DipSwitch #(.number(10)) DipSwitch_1 (
    .sw1(DipSwitch_1_sw10[9]), .sw2(DipSwitch_1_sw10[8]), .sw3(DipSwitch_1_sw10[7]),
    .sw4(DipSwitch_1_sw10[6]), .sw5(DipSwitch_1_sw10[5]), .sw6(DipSwitch_1_sw10[4]),
    .sw7(DipSwitch_1_sw10[3]), .sw8(DipSwitch_1_sw10[2]), .sw9(DipSwitch_1_sw10[1]),
    .sw10(DipSwitch_1_sw10[0]));
  lab1_1 lab1_1_1 (.SW(DipSwitch_1_sw10), .LEDR(Output_bus_1));
endmodule

// VHDL entity lab1_1, as the project stores it:
LIBRARY ieee;
USE ieee.std_logic_1164.all;-- Simple entity that connects the SW switches to the LEDR lights

ENTITY lab1_1 IS
PORT ( 	SW : IN STD_LOGIC_VECTOR(9 DOWNTO 0);
		LEDR : OUT STD_LOGIC_VECTOR(9 DOWNTO 0));
END lab1_1;

ARCHITECTURE Behavior OF lab1_1 IS
BEGIN
	LEDR<=SW;
END Behavior;
