// Logisim project Main_Proj.circ as structural Verilog
module main (
  input  run_tx,
  input  input_rx,
  input  reset,
  output tx_out,
  output rx_done,
  output [7:0] seg0,
  output [7:0] seg1,
  output [7:0] seg2,
  output [7:0] seg3,
  output [7:0] seg4,
  output [7:0] seg5,
  output j_first,
  output lf_first
);

  wire clock_1_out, not_1_out, uart_rx_1_o_rx_dv, uart_tx_1_busy, uart_tx_tester_1_trigger;
  wire [7:0] uart_rx_1_o_rx_byte, uart_tx_tester_1_data_out;

  Clock clock_1 (.out(clock_1_out));
  uart_tx_tester uart_tx_tester_1 (
    .clk_50M(clock_1_out), .run_test_raw(run_tx), .tx_busy(uart_tx_1_busy),
    .data_out(uart_tx_tester_1_data_out), .trigger(uart_tx_tester_1_trigger));
  uart_rx uart_rx_1 (
    .i_Clock(clock_1_out), .i_RX_Serial(tx_out), .o_RX_DV(uart_rx_1_o_rx_dv), .o_RX_Byte(uart_rx_1_o_rx_byte));  // open: o_Start_Done, o_FSM_Mode, o_Bit_Index
  uart_tx uart_tx_1 (
    .clk_50M(clock_1_out), .data_raw(uart_tx_tester_1_data_out), .trigger_raw(uart_tx_tester_1_trigger),
    .busy(uart_tx_1_busy), .serial_out(tx_out));  // open: tx_index_out
  not not_1 (not_1_out, rx_done);
  D_Flip_Flop d_ff_1 (.D(not_1_out), .clk(uart_rx_1_o_rx_dv), .Q(rx_done));  // open: Qn, preset, reset
  rx_display rx_display_1 (
    .rx_ready(uart_rx_1_o_rx_dv), .new_letter(uart_rx_1_o_rx_byte), .reset(reset), .clk(clock_1_out),
    .seg0(seg0), .seg1(seg1), .seg2(seg2), .seg3(seg3), .seg4(seg4), .seg5(seg5), .j_first(j_first),
    .lf_first(lf_first));
endmodule

module demux8 (
  input  in_bit,
  input  [2:0] decision,
  output choice0,
  output choice1,
  output choice2,
  output choice3,
  output choice4,
  output choice5,
  output choice6,
  output choice7
);

  wire not_1_out, not_2_out, not_3_out;

  not not_1 (not_1_out, decision[2]);
  not not_2 (not_2_out, decision[1]);
  not not_3 (not_3_out, decision[0]);
  and and_1 (choice0, in_bit, not_1_out, not_2_out, not_3_out);
  and and_2 (choice1, in_bit, not_1_out, not_2_out, decision[0]);
  and and_3 (choice2, in_bit, not_1_out, decision[1], not_3_out);
  and and_4 (choice3, in_bit, not_1_out, decision[1], decision[0]);
  and and_5 (choice4, in_bit, decision[2], not_2_out, not_3_out);
  and and_6 (choice5, in_bit, decision[2], not_2_out, decision[0]);
  and and_7 (choice6, in_bit, decision[2], decision[1], not_3_out);
  and and_8 (choice7, in_bit, decision[2], decision[1], decision[0]);
endmodule

module demux6 (
  input  [2:0] decision,
  output seg0,
  output seg1,
  output seg2,
  output seg3,
  output seg4,
  output seg5
);

  wire not_1_out, not_2_out, not_3_out;

  not not_1 (not_1_out, decision[2]);
  not not_2 (not_2_out, decision[1]);
  not not_3 (not_3_out, decision[0]);
  and and_1 (seg0, not_1_out, not_2_out, not_3_out);
  and and_2 (seg1, not_1_out, not_2_out, decision[0]);
  and and_3 (seg2, not_1_out, decision[1], not_3_out);
  and and_4 (seg3, not_1_out, decision[1], decision[0]);
  and and_5 (seg4, decision[2], not_2_out, not_3_out);
  and and_6 (seg5, decision[2], not_2_out, decision[0]);
endmodule

module bin_to_seg (
  input  [7:0] ascii_in,
  output [7:0] seg_out
);

  wire and_1_out, and_2_out, and_3_out, and_4_out, and_5_out, and_6_out, and_7_out, and_8_out, and_9_out,
       and_10_out, and_11_out, and_12_out, and_13_out, and_14_out, and_15_out, and_16_out, and_17_out,
       and_18_out, and_19_out, and_20_out, and_21_out, and_22_out, and_23_out, and_24_out, and_25_out,
       and_26_out, and_27_out, and_28_out, and_29_out, and_30_out, and_31_out, and_32_out, and_33_out,
       and_34_out, and_35_out, and_36_out, and_37_out, and_38_out, and_39_out, and_40_out, and_41_out,
       and_42_out, and_43_out, and_44_out, and_45_out, and_46_out, and_47_out, and_48_out, and_49_out,
       and_50_out, and_51_out, and_52_out, and_53_out, and_54_out, and_55_out, and_56_out, and_57_out,
       and_58_out, and_59_out, and_60_out, and_61_out, and_62_out, and_63_out, and_64_out, and_65_out,
       and_66_out, and_67_out, and_68_out, and_69_out, and_70_out, and_71_out, and_72_out, and_73_out,
       and_74_out, and_75_out, and_76_out, and_77_out, and_78_out, and_79_out, and_80_out, not_1_out,
       not_2_out, not_3_out, not_4_out, not_5_out, not_6_out, not_7_out, not_8_out;

  not not_1 (not_1_out, ascii_in[7]);
  not not_2 (not_2_out, ascii_in[6]);
  not not_3 (not_3_out, ascii_in[5]);
  not not_4 (not_4_out, ascii_in[4]);
  not not_5 (not_5_out, ascii_in[3]);
  not not_6 (not_6_out, ascii_in[2]);
  not not_7 (not_7_out, ascii_in[1]);
  not not_8 (not_8_out, ascii_in[0]);
  and and_1 (and_1_out, not_1_out, not_2_out, not_3_out, not_4_out, not_5_out, not_6_out, not_7_out, not_8_out);
  and and_2 (and_2_out, not_1_out, not_2_out, ascii_in[5], not_4_out, not_5_out, not_6_out, not_7_out, ascii_in[0]);
  and and_3 (and_3_out, not_1_out, not_2_out, ascii_in[5], not_4_out, ascii_in[3], ascii_in[2], ascii_in[1], not_8_out);
  and and_4 (and_4_out, not_1_out, ascii_in[6], not_4_out, ascii_in[3], not_6_out, ascii_in[1], ascii_in[0]);
  and and_5 (and_5_out, ascii_in[7], ascii_in[6], ascii_in[5], ascii_in[4], ascii_in[3], ascii_in[2], ascii_in[1], ascii_in[0]);
  and and_6 (and_6_out, not_1_out, ascii_in[6], not_4_out, not_5_out, not_7_out, ascii_in[0]);
  and and_7 (and_7_out, not_1_out, ascii_in[6], not_4_out, not_5_out, ascii_in[1], not_8_out);
  and and_8 (and_8_out, not_1_out, ascii_in[6], not_5_out, ascii_in[2], not_7_out, not_8_out);
  and and_9 (and_9_out, not_1_out, ascii_in[6], not_4_out, ascii_in[2], ascii_in[1], not_8_out);
  and and_10 (and_10_out, not_1_out, ascii_in[6], not_4_out, ascii_in[3], not_6_out, not_7_out, not_8_out);
  and and_11 (and_11_out, not_1_out, ascii_in[6], not_4_out, ascii_in[3], not_6_out, ascii_in[1], ascii_in[0]);
  and and_12 (and_12_out, not_1_out, ascii_in[6], ascii_in[4], not_5_out, not_6_out);
  and and_13 (and_13_out, not_1_out, ascii_in[6], ascii_in[4], not_6_out, not_7_out, ascii_in[0]);
  and and_14 (and_14_out, not_1_out, ascii_in[6], ascii_in[4], not_6_out, ascii_in[1], not_8_out);
  and and_15 (and_15_out, not_1_out, ascii_in[6], ascii_in[5], not_5_out, not_6_out, ascii_in[0]);
  and and_16 (and_16_out, not_1_out, ascii_in[6], ascii_in[5], not_4_out, ascii_in[1], ascii_in[0]);
  and and_17 (and_17_out, ascii_in[7], ascii_in[6], ascii_in[5], ascii_in[4], ascii_in[3], ascii_in[2], ascii_in[1], ascii_in[0]);
  and and_18 (and_18_out, not_1_out, ascii_in[6], not_5_out, not_7_out, ascii_in[0]);
  and and_19 (and_19_out, not_1_out, ascii_in[6], not_3_out, not_4_out, not_5_out, ascii_in[1]);
  and and_20 (and_20_out, not_1_out, ascii_in[6], not_4_out, not_5_out, ascii_in[1], not_8_out);
  and and_21 (and_21_out, not_1_out, ascii_in[6], not_3_out, not_4_out, ascii_in[2], ascii_in[0]);
  and and_22 (and_22_out, not_1_out, ascii_in[6], not_4_out, not_5_out, ascii_in[2], ascii_in[1]);
  and and_23 (and_23_out, not_1_out, ascii_in[6], not_4_out, ascii_in[3], not_7_out, not_8_out);
  and and_24 (and_24_out, not_1_out, ascii_in[6], not_4_out, ascii_in[3], not_6_out, ascii_in[1], ascii_in[0]);
  and and_25 (and_25_out, not_1_out, ascii_in[6], not_4_out, ascii_in[3], ascii_in[2], not_7_out);
  and and_26 (and_26_out, not_1_out, ascii_in[6], ascii_in[4], not_5_out, not_7_out);
  and and_27 (and_27_out, not_1_out, ascii_in[6], ascii_in[4], not_6_out, not_7_out);
  and and_28 (and_28_out, not_1_out, ascii_in[6], ascii_in[4], not_5_out, not_6_out, ascii_in[0]);
  and and_29 (and_29_out, ascii_in[7], ascii_in[6], ascii_in[5], ascii_in[4], ascii_in[3], ascii_in[2], ascii_in[1], ascii_in[0]);
  and and_30 (and_30_out, not_1_out, ascii_in[6], not_3_out, not_4_out, ascii_in[0]);
  and and_31 (and_31_out, not_1_out, ascii_in[6], not_4_out, not_6_out, ascii_in[0]);
  and and_32 (and_32_out, not_1_out, ascii_in[6], not_5_out, ascii_in[1], not_8_out);
  and and_33 (and_33_out, not_1_out, ascii_in[6], not_5_out, ascii_in[2], not_7_out);
  and and_34 (and_34_out, not_1_out, ascii_in[6], not_4_out, ascii_in[3], not_7_out);
  and and_35 (and_35_out, not_1_out, ascii_in[6], not_4_out, ascii_in[3], ascii_in[2]);
  and and_36 (and_36_out, not_1_out, ascii_in[6], ascii_in[4], not_6_out, not_8_out);
  and and_37 (and_37_out, not_1_out, ascii_in[6], ascii_in[4], not_5_out, ascii_in[2]);
  and and_38 (and_38_out, ascii_in[7], ascii_in[6], ascii_in[5], ascii_in[4], ascii_in[3], ascii_in[2], ascii_in[1], ascii_in[0]);
  and and_39 (and_39_out, not_1_out, not_3_out, not_4_out, ascii_in[3], not_6_out, ascii_in[1], not_8_out);
  and and_40 (and_40_out, not_1_out, ascii_in[6], not_4_out, not_5_out, not_6_out, ascii_in[1]);
  and and_41 (and_41_out, not_1_out, ascii_in[6], not_5_out, ascii_in[1], ascii_in[0]);
  and and_42 (and_42_out, not_1_out, ascii_in[6], not_3_out, not_4_out, ascii_in[2], not_7_out, not_8_out);
  and and_43 (and_43_out, not_1_out, ascii_in[6], not_4_out, not_5_out, ascii_in[2], not_7_out);
  and and_44 (and_44_out, not_1_out, ascii_in[6], not_5_out, ascii_in[2], ascii_in[0]);
  and and_45 (and_45_out, not_1_out, ascii_in[6], not_4_out, ascii_in[2], ascii_in[1], ascii_in[0]);
  and and_46 (and_46_out, not_1_out, ascii_in[6], ascii_in[3], not_6_out, ascii_in[1], not_8_out);
  and and_47 (and_47_out, ascii_in[7], ascii_in[6], ascii_in[5], ascii_in[4], ascii_in[3], ascii_in[2], ascii_in[1], ascii_in[0]);
  and and_48 (and_48_out, not_1_out, ascii_in[6], not_5_out, not_6_out, not_7_out, ascii_in[0]);
  and and_49 (and_49_out, not_1_out, ascii_in[6], not_4_out, not_6_out, ascii_in[1], not_8_out);
  and and_50 (and_50_out, not_1_out, ascii_in[6], not_4_out, not_5_out, ascii_in[2], not_7_out, not_8_out);
  and and_51 (and_51_out, not_1_out, ascii_in[6], not_4_out, ascii_in[2], ascii_in[1], ascii_in[0]);
  and and_52 (and_52_out, not_1_out, ascii_in[6], ascii_in[3], not_6_out, not_7_out, not_8_out);
  and and_53 (and_53_out, not_1_out, ascii_in[6], not_4_out, ascii_in[3], ascii_in[1], not_8_out);
  and and_54 (and_54_out, not_1_out, ascii_in[6], not_4_out, ascii_in[3], ascii_in[2], ascii_in[0]);
  and and_55 (and_55_out, not_1_out, ascii_in[6], ascii_in[4], not_5_out, ascii_in[0]);
  and and_56 (and_56_out, not_1_out, ascii_in[6], ascii_in[4], not_5_out, ascii_in[2], ascii_in[1]);
  and and_57 (and_57_out, not_1_out, ascii_in[6], ascii_in[4], ascii_in[3], not_6_out, not_7_out);
  and and_58 (and_58_out, ascii_in[7], ascii_in[6], ascii_in[5], ascii_in[4], ascii_in[3], ascii_in[2], ascii_in[1], ascii_in[0]);
  and and_59 (and_59_out, not_1_out, not_3_out, not_4_out, ascii_in[3], not_6_out, ascii_in[1], not_8_out);
  and and_60 (and_60_out, not_1_out, ascii_in[5], not_4_out, not_5_out, not_6_out, not_7_out, ascii_in[0]);
  and and_61 (and_61_out, not_1_out, ascii_in[6], not_5_out, not_6_out, not_7_out, ascii_in[0]);
  and and_62 (and_62_out, not_1_out, ascii_in[6], not_4_out, not_5_out, ascii_in[2], not_7_out, not_8_out);
  and and_63 (and_63_out, not_1_out, ascii_in[6], not_3_out, ascii_in[3], not_6_out, not_8_out);
  and and_64 (and_64_out, not_1_out, ascii_in[6], not_4_out, ascii_in[3], not_6_out, ascii_in[1]);
  and and_65 (and_65_out, not_1_out, ascii_in[6], not_3_out, not_4_out, ascii_in[3], ascii_in[2], ascii_in[0]);
  and and_66 (and_66_out, not_1_out, ascii_in[6], not_4_out, ascii_in[3], ascii_in[2], not_7_out, ascii_in[0]);
  and and_67 (and_67_out, not_1_out, ascii_in[6], ascii_in[4], not_6_out, not_7_out);
  and and_68 (and_68_out, not_1_out, ascii_in[6], ascii_in[4], not_5_out, not_7_out, ascii_in[0]);
  and and_69 (and_69_out, not_1_out, ascii_in[6], ascii_in[4], ascii_in[3], not_6_out, not_8_out);
  and and_70 (and_70_out, not_1_out, ascii_in[6], ascii_in[5], not_4_out, not_5_out, ascii_in[2], ascii_in[1], ascii_in[0]);
  and and_71 (and_71_out, ascii_in[7], ascii_in[6], ascii_in[5], ascii_in[4], ascii_in[3], ascii_in[2], ascii_in[1], ascii_in[0]);
  and and_72 (and_72_out, not_1_out, ascii_in[6], not_3_out, not_5_out, not_6_out, ascii_in[0]);
  and and_73 (and_73_out, not_1_out, ascii_in[6], not_5_out, not_6_out, not_7_out, ascii_in[0]);
  and and_74 (and_74_out, not_1_out, ascii_in[6], not_3_out, not_4_out, ascii_in[2], ascii_in[0]);
  and and_75 (and_75_out, not_1_out, ascii_in[6], not_4_out, ascii_in[2], not_7_out, ascii_in[0]);
  and and_76 (and_76_out, not_1_out, ascii_in[6], not_4_out, not_5_out, ascii_in[2], ascii_in[1]);
  and and_77 (and_77_out, not_1_out, ascii_in[6], ascii_in[4], not_5_out, not_6_out, not_7_out);
  and and_78 (and_78_out, not_1_out, ascii_in[6], ascii_in[4], not_5_out, not_6_out, ascii_in[0]);
  and and_79 (and_79_out, not_1_out, ascii_in[6], ascii_in[4], ascii_in[3], not_6_out, ascii_in[1], not_8_out);
  and and_80 (and_80_out, ascii_in[7], ascii_in[6], ascii_in[5], ascii_in[4], ascii_in[3], ascii_in[2], ascii_in[1], ascii_in[0]);
  or or_1 (seg_out[7], and_1_out, and_2_out, and_3_out, and_4_out, and_5_out);
  or or_2 (seg_out[6], and_6_out, and_7_out, and_8_out, and_9_out, and_10_out, and_11_out, and_12_out, and_13_out, and_14_out, and_15_out, and_16_out, and_17_out);
  or or_3 (seg_out[5], and_18_out, and_19_out, and_20_out, and_21_out, and_22_out, and_23_out, and_24_out, and_25_out, and_26_out, and_27_out, and_28_out, and_29_out);
  or or_4 (seg_out[4], and_30_out, and_31_out, and_32_out, and_33_out, and_34_out, and_35_out, and_36_out, and_37_out, and_38_out);
  or or_5 (seg_out[3], and_39_out, and_40_out, and_41_out, and_42_out, and_43_out, and_44_out, and_45_out, and_46_out, and_47_out);
  or or_6 (seg_out[2], and_48_out, and_49_out, and_50_out, and_51_out, and_52_out, and_53_out, and_54_out, and_55_out, and_56_out, and_57_out, and_58_out);
  or or_7 (seg_out[1], and_59_out, and_60_out, and_61_out, and_62_out, and_63_out, and_64_out, and_65_out, and_66_out, and_67_out, and_68_out, and_69_out, and_70_out, and_71_out);
  or or_8 (seg_out[0], and_72_out, and_73_out, and_74_out, and_75_out, and_76_out, and_77_out, and_78_out, and_79_out, and_80_out);
endmodule

module letter8_writer (
  input  [7:0] new_letter,
  input  clk,
  input  reset,
  input  update,
  output [7:0] newline,
  output write_done,
  output [63:0] stored_message,
  output j_first,
  output lf_first,
  output [7:0] J_found
);

  wire and_1_out, comparator_1_eq, comparator_2_eq, comparator_3_eq, comparator_4_eq, comparator_5_eq,
       comparator_6_eq, comparator_7_eq, comparator_8_eq, comparator_9_eq, comparator_10_eq, d_ff_1_q,
       demux_1_choice0, demux_1_choice1, demux_1_choice2, demux_1_choice3, demux_1_choice4, demux_1_choice5,
       demux_1_choice6, demux_1_choice7, not_1_out, or_1_out, or_2_out, s_r_ff_1_qn;
  wire [2:0] counter_1_q;
  wire [7:0] multiplexer_2_out, multiplexer_3_out, multiplexer_4_out, multiplexer_5_out, multiplexer_6_out,
       multiplexer_7_out, multiplexer_8_out, multiplexer_9_out, multiplexer_10_out, multiplexer_11_out,
       multiplexer_12_out, multiplexer_13_out, multiplexer_14_out, multiplexer_15_out, multiplexer_16_out,
       multiplexer_17_out, multiplexer_18_out;

  Comparator #(.mode("unsigned"), .width(3)) comparator_1 (
    .a(3'b111), .b(counter_1_q), .eq(comparator_1_eq));  // open: gt, lt
  D_Flip_Flop d_ff_1 (.D(comparator_1_eq), .clk(clk), .Q(d_ff_1_q), .preset(1'b0), .reset(1'b0));  // open: Qn
  Counter #(.max('h7), .width(3)) counter_1 (
    .clr(reset), .load(1'b0), .up(1'b1), .count(1'b1), .clk(update), .D(3'b001), .Q(counter_1_q));  // open: carry
  not not_1 (not_1_out, comparator_1_eq);
  Comparator #(.mode("unsigned")) comparator_2 (.a(new_letter), .b(8'ha), .eq(comparator_2_eq));  // open: gt, lt
  and and_1 (and_1_out, not_1_out, d_ff_1_q);
  Multiplexer #(.width(8)) multiplexer_1 (.in0({8{1'b0}}), .in1(new_letter), .out(newline), .sel(comparator_2_eq));
  Multiplexer #(.width(8)) multiplexer_2 (
    .in0(new_letter), .in1({8{1'b0}}), .out(multiplexer_2_out), .sel(comparator_2_eq));
  or or_1 (or_1_out, comparator_2_eq, and_1_out);
  S_R_Flip_Flop s_r_ff_1 (
    .S(1'b0), .R(1'b0), .clk(clk), .Q(write_done), .reset(reset), .Qn(s_r_ff_1_qn), .preset(or_1_out));
  demux8 demux_1 (
    .in_bit(s_r_ff_1_qn), .decision(counter_1_q), .choice0(demux_1_choice0), .choice1(demux_1_choice1),
    .choice2(demux_1_choice2), .choice3(demux_1_choice3), .choice4(demux_1_choice4),
    .choice5(demux_1_choice5), .choice6(demux_1_choice6), .choice7(demux_1_choice7));
  Multiplexer #(.width(8)) multiplexer_3 (
    .in0(stored_message[7:0]), .in1(multiplexer_2_out), .out(multiplexer_3_out), .sel(demux_1_choice0));
  Multiplexer #(.width(8)) multiplexer_4 (
    .in0(stored_message[15:8]), .in1(multiplexer_2_out), .out(multiplexer_4_out), .sel(demux_1_choice1));
  Multiplexer #(.width(8)) multiplexer_5 (
    .in0(stored_message[23:16]), .in1(multiplexer_2_out), .out(multiplexer_5_out), .sel(demux_1_choice2));
  Multiplexer #(.width(8)) multiplexer_6 (
    .in0(stored_message[31:24]), .in1(multiplexer_2_out), .out(multiplexer_6_out), .sel(demux_1_choice3));
  Multiplexer #(.width(8)) multiplexer_7 (
    .in0(stored_message[39:32]), .in1(multiplexer_2_out), .out(multiplexer_7_out), .sel(demux_1_choice4));
  Multiplexer #(.width(8)) multiplexer_8 (
    .in0(stored_message[47:40]), .in1(multiplexer_2_out), .out(multiplexer_8_out), .sel(demux_1_choice5));
  Multiplexer #(.width(8)) multiplexer_9 (
    .in0(stored_message[55:48]), .in1(multiplexer_2_out), .out(multiplexer_9_out), .sel(demux_1_choice6));
  Multiplexer #(.width(8)) multiplexer_10 (
    .in0(stored_message[63:56]), .in1(multiplexer_2_out), .out(multiplexer_10_out), .sel(demux_1_choice7));
  Register register_1 (.D(multiplexer_3_out), .en(1'b1), .clk(clk), .Q(stored_message[7:0]), .clr(reset));
  Register register_2 (.D(multiplexer_4_out), .en(1'b1), .clk(clk), .Q(stored_message[15:8]), .clr(reset));
  Register register_3 (.D(multiplexer_5_out), .en(1'b1), .clk(clk), .Q(stored_message[23:16]), .clr(reset));
  Register register_4 (.D(multiplexer_6_out), .en(1'b1), .clk(clk), .Q(stored_message[31:24]), .clr(reset));
  Register register_5 (.D(multiplexer_7_out), .en(1'b1), .clk(clk), .Q(stored_message[39:32]), .clr(reset));
  Register register_6 (.D(multiplexer_8_out), .en(1'b1), .clk(clk), .Q(stored_message[47:40]), .clr(reset));
  Register register_7 (.D(multiplexer_9_out), .en(1'b1), .clk(clk), .Q(stored_message[55:48]), .clr(reset));
  Register register_8 (.D(multiplexer_10_out), .en(1'b1), .clk(clk), .Q(stored_message[63:56]), .clr(reset));
  Comparator #(.mode("unsigned")) comparator_3 (
    .a(stored_message[7:0]), .b(8'he), .eq(comparator_3_eq));  // open: gt, lt
  Comparator #(.mode("unsigned")) comparator_4 (
    .a(stored_message[15:8]), .b(8'he), .eq(comparator_4_eq));  // open: gt, lt
  Comparator #(.mode("unsigned")) comparator_5 (
    .a(stored_message[23:16]), .b(8'he), .eq(comparator_5_eq));  // open: gt, lt
  Comparator #(.mode("unsigned")) comparator_6 (
    .a(stored_message[31:24]), .b(8'he), .eq(comparator_6_eq));  // open: gt, lt
  Comparator #(.mode("unsigned")) comparator_7 (
    .a(stored_message[39:32]), .b(8'he), .eq(comparator_7_eq));  // open: gt, lt
  Comparator #(.mode("unsigned")) comparator_8 (
    .a(stored_message[47:40]), .b(8'he), .eq(comparator_8_eq));  // open: gt, lt
  Comparator #(.mode("unsigned")) comparator_9 (
    .a(stored_message[55:48]), .b(8'he), .eq(comparator_9_eq));  // open: gt, lt
  Comparator #(.mode("unsigned")) comparator_10 (
    .a(stored_message[63:56]), .b(8'he), .eq(comparator_10_eq));  // open: gt, lt
  Multiplexer #(.width(8)) multiplexer_11 (
    .in0(stored_message[7:0]), .in1({8{1'b0}}), .out(multiplexer_11_out), .sel(comparator_3_eq));
  Multiplexer #(.width(8)) multiplexer_12 (
    .in0(stored_message[15:8]), .in1({8{1'b0}}), .out(multiplexer_12_out), .sel(comparator_4_eq));
  Multiplexer #(.width(8)) multiplexer_13 (
    .in0(stored_message[23:16]), .in1({8{1'b0}}), .out(multiplexer_13_out), .sel(comparator_5_eq));
  Multiplexer #(.width(8)) multiplexer_14 (
    .in0(stored_message[31:24]), .in1({8{1'b0}}), .out(multiplexer_14_out), .sel(comparator_6_eq));
  Multiplexer #(.width(8)) multiplexer_15 (
    .in0(stored_message[39:32]), .in1({8{1'b0}}), .out(multiplexer_15_out), .sel(comparator_7_eq));
  Multiplexer #(.width(8)) multiplexer_16 (
    .in0(stored_message[47:40]), .in1({8{1'b0}}), .out(multiplexer_16_out), .sel(comparator_8_eq));
  Multiplexer #(.width(8)) multiplexer_17 (
    .in0(stored_message[55:48]), .in1({8{1'b0}}), .out(multiplexer_17_out), .sel(comparator_9_eq));
  Multiplexer #(.width(8)) multiplexer_18 (
    .in0(stored_message[63:56]), .in1({8{1'b0}}), .out(multiplexer_18_out), .sel(comparator_10_eq));
  Multiplexer #(.select(3), .width(8)) multiplexer_19 (
    .in0(multiplexer_11_out), .in1(multiplexer_12_out), .in2(multiplexer_13_out), .in3(multiplexer_14_out),
    .in4(multiplexer_15_out), .in5(multiplexer_16_out), .in6(multiplexer_17_out), .in7(multiplexer_18_out),
    .out(J_found), .sel(counter_1_q));
  or or_2 (or_2_out, comparator_3_eq, comparator_4_eq, comparator_5_eq, comparator_6_eq, comparator_7_eq, comparator_8_eq, comparator_9_eq, comparator_10_eq);
  order_checker order_checker_1 (.lf(comparator_2_eq), .j(or_2_out), .j_first(j_first), .lf_first(lf_first));

  // Notes on the sheet:
  //   if count =7 and next count not 7, stop
  //   count to 7 for 8 bytes
  //   if lstop
  //   asynchronously
  //   8 bytes, saved or passed on
endmodule

module letter8_reader (
  input  write_done,
  input  [63:0] saved_message,
  input  reset,
  input  clk,
  output [7:0] output_letter,
  output update_disp
);

  wire comparator_1_eq, not_1_out, or_1_out;
  wire [3:0] letter_count_q;
  wire [21:0] slow_clock_q;

  not not_1 (not_1_out, write_done);
  or or_1 (or_1_out, not_1_out, reset);
  Counter #(.max('h2faf08), .width(22)) slow_clock (
    .clr(or_1_out), .load(1'b0), .up(1'b1), .count(1'b1), .clk(clk), .D(22'h2faf08), .Q(slow_clock_q));  // open: carry
  Comparator #(.mode("unsigned"), .width(22)) comparator_1 (
    .a(slow_clock_q), .b(22'h2faf08), .eq(comparator_1_eq));  // open: gt, lt
  and and_1 (update_disp, write_done, comparator_1_eq);
  Counter #(.max('h8), .width(4)) letter_count (
    .clr(reset), .load(1'b0), .up(1'b1), .count(1'b1), .clk(update_disp), .D(4'b1000), .Q(letter_count_q));  // open: carry
  Multiplexer #(.select(4), .width(8)) multiplexer_1 (
    .in0({8{1'b0}}), .in1(saved_message[7:0]), .in2(saved_message[15:8]), .in3(saved_message[23:16]),
    .in4(saved_message[31:24]), .in5(saved_message[39:32]), .in6(saved_message[47:40]),
    .in7(saved_message[55:48]), .in8(saved_message[63:56]), .in9({8{1'b0}}), .in10({8{1'b0}}),
    .in11({8{1'b0}}), .in12({8{1'b0}}), .in13({8{1'b0}}), .in14({8{1'b0}}), .in15({8{1'b0}}),
    .out(output_letter), .sel(letter_count_q));
endmodule

module sentence_disp (
  input  [7:0] newletter,
  input  enable,
  input  reset,
  input  clk,
  output [7:0] letter0,
  output [7:0] letter1,
  output [7:0] letter2,
  output [7:0] letter3,
  output [7:0] letter4,
  output [7:0] letter5
);

  Register register_1 (.D(newletter), .en(enable), .clk(clk), .Q(letter0), .clr(reset));
  Register register_2 (.D(letter0), .en(enable), .clk(clk), .Q(letter1), .clr(reset));
  Register register_3 (.D(letter1), .en(enable), .clk(clk), .Q(letter2), .clr(reset));
  Register register_4 (.D(letter2), .en(enable), .clk(clk), .Q(letter3), .clr(reset));
  Register register_5 (.D(letter3), .en(enable), .clk(clk), .Q(letter4), .clr(reset));
  Register register_6 (.D(letter4), .en(enable), .clk(clk), .Q(letter5), .clr(reset));
endmodule

module rx_display (
  input  rx_ready,
  input  [7:0] new_letter,
  input  reset,
  input  clk,
  output [7:0] seg0,
  output [7:0] seg1,
  output [7:0] seg2,
  output [7:0] seg3,
  output [7:0] seg4,
  output [7:0] seg5,
  output j_first,
  output lf_first
);

  wire letter8_reader_1_update_disp, letter8_writer_1_j_first, letter8_writer_1_lf_first,
       letter8_writer_1_write_done;
  wire [7:0] bin_to_seg_1_seg_out, letter8_reader_1_output_letter;
  wire [63:0] letter8_writer_1_stored_message;

  bin_to_seg bin_to_seg_1 (.ascii_in(new_letter), .seg_out(bin_to_seg_1_seg_out));
  letter8_writer letter8_writer_1 (
    .new_letter(bin_to_seg_1_seg_out), .clk(clk), .reset(reset), .update(rx_ready),
    .write_done(letter8_writer_1_write_done), .stored_message(letter8_writer_1_stored_message),
    .j_first(letter8_writer_1_j_first), .lf_first(letter8_writer_1_lf_first));  // open: newline, J_found
  S_R_Flip_Flop s_r_ff_1 (
    .S(1'b0), .R(1'b0), .clk(clk), .Q(j_first), .reset(reset), .preset(letter8_writer_1_j_first));  // open: Qn
  S_R_Flip_Flop s_r_ff_2 (
    .S(1'b0), .R(1'b0), .clk(clk), .Q(lf_first), .reset(reset), .preset(letter8_writer_1_lf_first));  // open: Qn
  letter8_reader letter8_reader_1 (
    .write_done(letter8_writer_1_write_done), .saved_message(letter8_writer_1_stored_message), .reset(reset),
    .clk(clk), .output_letter(letter8_reader_1_output_letter), .update_disp(letter8_reader_1_update_disp));
  sentence_disp sentence_disp_1 (
    .newletter(letter8_reader_1_output_letter), .enable(letter8_reader_1_update_disp), .reset(reset),
    .clk(clk), .letter0(seg0), .letter1(seg1), .letter2(seg2), .letter3(seg3), .letter4(seg4), .letter5(seg5));
endmodule

module order_checker (
  input  lf,
  input  j,
  output j_first,
  output lf_first
);

  wire not_1_out, not_2_out;

  not not_1 (not_1_out, j);
  not not_2 (not_2_out, lf);
  and and_1 (j_first, j, not_2_out);
  and and_2 (lf_first, not_1_out, lf);
endmodule

// VHDL entity uart_rx, as the project stores it:
--------------------------------------------------------------------------------
-- Project :
-- File    : uart_rx.vhd
-- Author  :
-- Date    :
--
--------------------------------------------------------------------------------
-- Description :
-- UART receiver module for asynchronous serial communication. This version
-- includes improvements for bit timing, stop bit verification, and output signal
-- handling.
--------------------------------------------------------------------------------

LIBRARY ieee;
USE ieee.std_logic_1164.all;
USE ieee.numeric_std.all;

ENTITY uart_rx IS
    PORT (
        i_Clock      : IN  std_logic;                    -- System clock input
        i_RX_Serial  : IN  std_logic;                    -- Serial data input
        o_RX_DV      : OUT std_logic;                    -- Data valid signal
        o_RX_Byte    : OUT std_logic_vector(7 downto 0); -- Output byte
        o_Start_Done : OUT std_logic;                    -- Start bit detected signal
        o_FSM_Mode   : OUT std_logic_vector(2 downto 0);  -- FSM state output for debugging
        o_Bit_Index	 : OUT std_logic_vector(2 downto 0)
    );
END uart_rx;

ARCHITECTURE Behavioral OF uart_rx IS
    type state_type IS (IDLE, RX_START_BIT, RX_DATA_BITS, RX_STOP_BIT, CLEANUP);
    signal r_SM_Main : state_type := IDLE;
    signal r_Start_Done : std_logic := '0';
    signal r_Clock_Count : unsigned(23 downto 0) := (others => '0');
    signal r_Bit_Index : unsigned(2 downto 0) := (others => '0');
    signal r_RX_Byte : std_logic_vector(7 downto 0) := (others => '0');
    signal r_RX_DV : std_logic := '0';
    signal r_FSM_Mode : std_logic_vector(2 downto 0) := (others => '0'); 
    constant N : integer := 3;  -- Number of cycles to confirm bit
    signal bit_counter : integer range 0 to N := 0;  -- N is the number of clock cycles for confirmation
    
    constant CLKS_PER_BIT : integer := 27;  -- Clock cycles per bit, 3 for 1khz (8k/8) and 300 br
    
begin
    process(i_Clock)
    begin
        if rising_edge(i_Clock) then            
            case r_SM_Main is
                when IDLE =>
                    r_FSM_Mode <= "001";
                    r_RX_DV <= '0';
                    r_Clock_Count <= (others => '0');
                    r_Bit_Index <= (others => '0');
                    r_Start_Done <= '0';

                    if i_RX_Serial = '0' then
                        bit_counter <= bit_counter + 1;
                        if bit_counter >= N then  -- Confirmed low for N clock cycles
                            r_SM_Main <= RX_START_BIT;
                            bit_counter <= 0;  -- Reset counter
                        end if;
                    else
                        bit_counter <= 0;  -- Reset counter if high is detected
                    end if;

                when RX_START_BIT =>
                    r_FSM_Mode <= "010";
                    r_Clock_Count <= r_Clock_Count + 1;
                    if r_Clock_Count = CLKS_PER_BIT/2 then
                        if i_RX_Serial = '0' then
                            r_Start_Done <= '1';  -- Midpoint confirmation of the start bit
                        else
                            r_Start_Done <= '0';
                        end if;
                    end if;
                    if r_Clock_Count = CLKS_PER_BIT - 1 then
                        r_Clock_Count <= (others => '0');  -- Reset the counter for use in the next state
                        if r_Start_Done = '1' then
                            r_SM_Main <= RX_DATA_BITS;  -- Transition to data bits after confirming start bit
                        else
                            r_SM_Main <= IDLE;  -- Reset if the start bit is not sustained
                        end if;
                    end if;

                when RX_DATA_BITS =>
                    r_FSM_Mode <= "011";
                    r_Clock_Count <= r_Clock_Count + 1;
                    if r_Clock_Count = CLKS_PER_BIT/2 then
                        r_RX_Byte(to_integer(r_Bit_Index)) <= i_RX_Serial;  -- Sample at mid-point
                    end if;
                    if r_Clock_Count = CLKS_PER_BIT - 1 then
                        r_Clock_Count <= (others => '0');    -- Reset for next bit
                        if r_Bit_Index < 7 then
                            r_Bit_Index <= r_Bit_Index + 1;
                        else
                            r_Bit_Index <= (others => '0');
                            r_SM_Main <= RX_STOP_BIT;  -- Proceed to stop bit verification
                        end if;
                    end if;

                when RX_STOP_BIT =>
                    r_FSM_Mode <= "100";
                    r_Clock_Count <= r_Clock_Count + 1;
                    if r_Clock_Count = CLKS_PER_BIT/2 then
                        if i_RX_Serial = '1' then
                            r_RX_DV <= '1';  -- Midpoint confirmation of the stop bit
                        end if;
                    end if;
                    if r_Clock_Count = CLKS_PER_BIT - 1 then
                        r_Clock_Count <= (others => '0');
                        r_SM_Main <= CLEANUP;  -- Cleanup and prepare to return to IDLE
                    end if;

                    -- bit parity

                when CLEANUP =>
                    r_FSM_Mode <= "101";
                    r_SM_Main <= IDLE;
                    r_RX_DV <= '0';

                when others =>
                    r_SM_Main <= IDLE;

            end case;
            o_Bit_Index <= std_logic_vector(r_Bit_Index);
        end if;
    end process;

    o_RX_DV <= r_RX_DV;
    o_RX_Byte <= r_RX_Byte;
    o_Start_Done <= r_Start_Done;
    o_FSM_Mode <= r_FSM_Mode;

END ARCHITECTURE Behavioral;

// VHDL entity uart_tx, as the project stores it:
--------------------------------------------------------------------------------
-- Project : Main_Proj
-- File    : UART_TX
-- Author   : Selma Benhassine
-- Date    :
--
--------------------------------------------------------------------------------
-- Description :
-- The transmitter file for the UART_transmission portion of the project
--
--------------------------------------------------------------------------------

library IEEE;
use IEEE.STD_LOGIC_1164.ALL;
use IEEE.NUMERIC_STD.ALL;

entity uart_tx is
    Port (
        clk_50M : in STD_LOGIC;               -- Input clock, assumed 50 MHz
        data_raw : in STD_LOGIC_VECTOR (7 downto 0);  -- Data byte (8 bits) to transmit
        trigger_raw : in STD_LOGIC;           -- Tells module to begin transmission of data_raw byte
        busy : out STD_LOGIC;                 -- Flag to indicate a transmission is in progress
        serial_out : out STD_LOGIC;            -- UART output serial datastream
        tx_index_out : out STD_LOGIC_VECTOR(3 downto 0) 
    );
end uart_tx;

--------------------------------------------------------------------------------
--Complete your VHDL description below
--------------------------------------------------------------------------------

architecture Behavioral of uart_tx is
	 
	 constant CLKS_PER_BIT: integer := 54;
--  The calculation is as follows:
--  
--                                                  1
--     CLKS_PER_BIT =  F_clk [cycles/sec] * --------------------
--                                           baud_rate[bit/sec]
--  so 5208 gives k baud rate for clk at 50MHz
--  f = 50MHz / 8 when going through logisim
-- last done 217
	 
    type state_type is (STATE_IDLE, STATE_TRANSMITTING, STATE_CLEANUP);
    signal tx_state : state_type := STATE_IDLE;  -- State variable for main finite state machine
    signal data_aug : std_logic_vector(9 downto 0) := (others => '0');  -- Augmented data word to transmit that includes START bit, data byte, and STOP BIT
    signal tx_index : unsigned(3 downto 0) := (others => '0');  -- Index of bit currently transmitting
    signal bit_delay : unsigned(31 downto 0) := (others => '0'); -- Timer to regulate baud rate
   

    signal trigger_0 : std_logic := '0';  -- Synchronizer on trigger input signal
    signal trigger : std_logic := '0';    -- Synchronizer on trigger input signal

    -- Localparam CLKS_PER_BIT is not needed in VHDL since it's used as a constant value in the code directly

begin

    process (clk_50M) begin
        if rising_edge(clk_50M) then
            case tx_state is
                -- Wait for trigger condition indicating it's time to transmit a byte.
                when STATE_IDLE =>
                    busy <= '0';                 -- Indicate that transmitter is idle.
                    serial_out <= '1';           -- Idle output HIGH, per standard UART behavior.
                    if trigger = '1' then        -- Check if received trigger to TX a byte
                        data_aug <= '1' & data_raw & '0';   -- Create augmented byte with start and stop bits
                        busy <= '1';                        -- Indicate that transmitter is busy.
                        bit_delay <= (others => '0');       -- Clear timer used to track duration of each bit
                        tx_index <= (others => '0');        -- Point to first bit of data_aug to TX, namely the start bit
                        tx_state <= STATE_TRANSMITTING;     -- Move on to next state
                    end if;
                    
                -- Transmit all 10 bits with proper the proper duration per bit based on the selected baud rate.
                when STATE_TRANSMITTING =>
                    serial_out <= data_aug(to_integer(tx_index));  -- Set output based on current bit to transmit
                    bit_delay <= bit_delay + 1;                     -- Keep track of duration to hold this bit
                    if bit_delay > to_unsigned(CLKS_PER_BIT, 32) then  -- Check if bit duration has expired
                        if tx_index = "1001" then                  -- Check if just transmitted the final bit, i.e. the STOP bit
                            tx_state <= STATE_CLEANUP;            -- Move on to next state
                        else
                            tx_index <= tx_index + 1;             -- Still more bits to send so, point to next bit
                            bit_delay <= (others => '0');         -- Clear counter used to regulate baud rate
                        end if;
                    end if;
                    
                -- Pause for a few bit durations after full byte transmitted.
                when STATE_CLEANUP =>
                    bit_delay <= bit_delay + 1;                    -- Keep track of how long been in cleanup state
                    if bit_delay > to_unsigned(5 * CLKS_PER_BIT, 32) then  -- If paused HIGH long enough, then return to idle state
                        tx_state <= STATE_IDLE;
                    end if;
                    
                -- Should never get here, but if do, return to IDLE
                when others =>
                    tx_state <= STATE_IDLE;
            end case;
            tx_index_out <= std_logic_vector(tx_index);
        end if;
    end process;

    -- Synchronizer for trigger input
    process (clk_50M) begin
        if rising_edge(clk_50M) then
            trigger_0 <= trigger_raw;
            trigger <= trigger_0;
        end if;
    end process;

end Behavioral;

// VHDL entity uart_tx_tester, as the project stores it:
--------------------------------------------------------------------------------
-- Project : UART_Module
-- File    : UART_Transmitter_Tester
-- Autor   : Selma Benhassine
-- Date    :
--
--------------------------------------------------------------------------------
-- Description : Testbench file for the UART transmitter
--
--------------------------------------------------------------------------------

library IEEE;
use IEEE.STD_LOGIC_1164.ALL;
use IEEE.NUMERIC_STD.ALL;

entity uart_tx_tester is
    Port (
        clk_50M : in STD_LOGIC;               -- Input clock, assumed 50 MHz
        run_test_raw : in STD_LOGIC;          -- HIGH indicates to continuously run test
        tx_busy : in STD_LOGIC;               -- HIGH indicates transmitter is busy 
        data_out : out STD_LOGIC_VECTOR (7 downto 0);  -- Data byte (8 bits) to transmit
        trigger : out STD_LOGIC                -- Trigger to tell UART module to begin transmission
    );
end uart_tx_tester;

architecture Behavioral of uart_tx_tester is

    signal run_test_0 : std_logic := '0';          -- Synchronizer for 'start test' switch input
    signal run_test : std_logic := '0';            -- Synchronizer for 'start test' switch input
    signal tester_state : unsigned(5 downto 0) := (others => '0');  -- FSM state variable
    -- signal byte_index : unsigned(31 downto 0) := unsigned(8*16)-unsigned(1);          -- Pointer to beginning of next byte to transmit in 16 byte message
    constant BYTE_INDEX_INIT: natural := (8*16)-1; -- Calculate the initial value for byte_index
    signal byte_index : unsigned(31 downto 0) := to_unsigned(BYTE_INDEX_INIT, 32); -- Initialize byte_index with the calculated value
	 signal pause_delay : unsigned(31 downto 0) := (others => '0');  -- Counter for delay between re-transmissions of message
    signal trigger_ctr : unsigned(5 downto 0) := (others => '0');    -- Delay to hold trigger high, in clock cycles

    constant STATE_IDLE : unsigned(5 downto 0) := "000000";          -- Legal values for tester_state
    constant STATE_LOAD : unsigned(5 downto 0) := "000010";          -- Legal values for tester_state
    constant STATE_TRIGGER : unsigned(5 downto 0) := "000100";       -- Legal values for tester_state
    constant STATE_POLL_BUSY : unsigned(5 downto 0) := "001000";     -- Legal values for tester_state
    constant STATE_PAUSE : unsigned(5 downto 0) := "010000";         -- Legal values for tester_state

    constant MSG_DELAY : unsigned(31 downto 0) := to_unsigned(100_000, 32);  -- Delay between messages re-transmissions, in clk cycles
	 
	 -- Message to transmit
    signal byte_str : std_logic_vector((8*16)-1 downto 0) := "01001000" & "01100101" & "01101100" & "01101100" & "01101111" & "00100000" & "01010111" & "01101111" &
                                                             "01110010" & "01101100" & "01100100" & "00100001" & "00100000" & "00100000" & "00100000" & "00100000";

-- hello world! is "01001000" & "01100101" & "01101100" & "01101100" & "01101111" & "00100000" & "01010111" & "01101111" &
                                                            -- "01110010" & "01101100" & "01100100" & "00100001" & "00100000" & "00100000" & "00100000" & "00100000";


begin

    -- Synchronizer for "run_test" input since, as tested, this comes from a 
    -- slide switch on the DE10-Lite board, which is not synchronous with the
    -- clock.
    process (clk_50M) begin
        if rising_edge(clk_50M) then
            run_test_0 <= run_test_raw;
            run_test <= run_test_0;
        end if;
    end process;

    -- Main Finite State Machine that sequences the test
    process (clk_50M) begin
        if rising_edge(clk_50M) then
            case tester_state is
                -- Wait for request to begin test.
                when STATE_IDLE =>
                    trigger <= '0';
                    if run_test = '1' then
                        byte_index <= to_unsigned(BYTE_INDEX_INIT, 32);
                        tester_state <= STATE_LOAD;
                    end if;
                    
                -- Output next byte to transmitter module, with trigger still low
                -- so it won't transmit yet.
                when STATE_LOAD =>
                    trigger <= '0';
                    data_out <= byte_str(to_integer(byte_index) downto to_integer(byte_index)-7);
                    trigger_ctr <= to_unsigned(5, 6);
                    tester_state <= STATE_TRIGGER;
                    
                -- Now that previous state output'd the next byte to transmit,
                -- assert the trigger signal to begin the transmission.
                when STATE_TRIGGER =>
                    trigger <= '1';
                    trigger_ctr <= trigger_ctr - 1;
                    if trigger_ctr = 0 then
                        tester_state <= STATE_POLL_BUSY;
                    end if;
                    
                -- Clear trigger signal, and wait until all bits shifted out
                -- for the current byte.
                when STATE_POLL_BUSY =>
                    trigger <= '0';
                    if tx_busy = '0' then
                        if byte_index <= 7 then
                            pause_delay <= (others => '0');
                            tester_state <= STATE_PAUSE;
                        else
                            byte_index <= byte_index - 8;
                            tester_state <= STATE_LOAD;
                        end if;
                    end if;
                    
                -- Once transmitted full message, pause before 
                -- transmitting message again for testing convenience.
                when STATE_PAUSE =>
                    pause_delay <= pause_delay + 1;
                    if pause_delay > to_integer(MSG_DELAY) then
                        tester_state <= STATE_IDLE;
                    end if;
                    
                -- Should never get here, but if do, return to IDLE
                when others =>
                    tester_state <= STATE_IDLE;
            end case;
        end if;
    end process;

end Behavioral;
