// Logisim project uart_rx_log.circ as structural Verilog
module main (
  input  run_tx,
  input  input_rx,
  input  reset,
  output tx_out,
  output [7:0] seg0,
  output write_done
);

  wire clock_1_out, uart_rx_1_o_rx_dv, uart_tx_1_busy, uart_tx_tester_1_trigger;
  wire [7:0] uart_rx_1_o_rx_byte, uart_tx_tester_1_data_out;

  Clock clock_1 (.out(clock_1_out));
  uart_tx_tester uart_tx_tester_1 (
    .clk_50M(clock_1_out), .run_test_raw(run_tx), .tx_busy(uart_tx_1_busy),
    .data_out(uart_tx_tester_1_data_out), .trigger(uart_tx_tester_1_trigger));
  uart_rx uart_rx_1 (
    .i_Clock(clock_1_out), .i_RX_Serial(input_rx), .o_RX_DV(uart_rx_1_o_rx_dv),
    .o_RX_Byte(uart_rx_1_o_rx_byte));  // open: o_Start_Done, o_FSM_Mode, o_Bit_Index
  uart_tx uart_tx_1 (
    .clk_50M(clock_1_out), .data_raw(uart_tx_tester_1_data_out), .trigger_raw(uart_tx_tester_1_trigger),
    .busy(uart_tx_1_busy), .serial_out(tx_out));  // open: tx_index_out
  save_display save_display_1 (
    .rx_ready(uart_rx_1_o_rx_dv), .Input_bus_1(uart_rx_1_o_rx_byte), .clk(clock_1_out), .reset(reset),
    .Output_bus_1(seg0), .write_done(write_done));
endmodule

module bin_to_letter (
  input  [7:0] Input_bus_1,
  output [7:0] Output_bus_1
);

  wire and_1_out, and_2_out, and_3_out, and_4_out, and_5_out, and_6_out, and_7_out, and_8_out, and_9_out,
       and_10_out, and_11_out, and_12_out, and_13_out, and_14_out, and_15_out, and_16_out, and_17_out,
       and_18_out, and_19_out, and_20_out, and_21_out, and_22_out, and_23_out, and_24_out, and_25_out,
       and_26_out, and_27_out, and_28_out, and_29_out, and_30_out, and_31_out, and_32_out, and_33_out,
       and_34_out, and_35_out, and_36_out, and_37_out, and_38_out, and_39_out, and_40_out, and_41_out,
       and_42_out, and_43_out, and_44_out, and_45_out, and_46_out, and_47_out, and_48_out, and_49_out,
       and_50_out, and_51_out, and_52_out, and_53_out, and_54_out, and_55_out, and_56_out, and_57_out,
       and_58_out, and_59_out, and_60_out, and_61_out, and_62_out, and_63_out, and_64_out, and_65_out,
       and_66_out, and_67_out, and_68_out, and_69_out, and_70_out, and_71_out, and_72_out, and_73_out,
       and_74_out, and_75_out, and_76_out, and_77_out, and_78_out, and_79_out, and_80_out, not_1_out,
       not_2_out, not_3_out, not_4_out, not_5_out, not_6_out, not_7_out, not_8_out;

  not not_1 (not_1_out, Input_bus_1[7]);
  not not_2 (not_2_out, Input_bus_1[6]);
  not not_3 (not_3_out, Input_bus_1[5]);
  not not_4 (not_4_out, Input_bus_1[4]);
  not not_5 (not_5_out, Input_bus_1[3]);
  not not_6 (not_6_out, Input_bus_1[2]);
  not not_7 (not_7_out, Input_bus_1[1]);
  not not_8 (not_8_out, Input_bus_1[0]);
  and and_1 (and_1_out, not_1_out, not_2_out, not_3_out, not_4_out, not_5_out, not_6_out, not_7_out, not_8_out);
  and and_2 (and_2_out, not_1_out, not_2_out, Input_bus_1[5], not_4_out, not_5_out, not_6_out, not_7_out, Input_bus_1[0]);
  and and_3 (and_3_out, not_1_out, not_2_out, Input_bus_1[5], not_4_out, Input_bus_1[3], Input_bus_1[2], Input_bus_1[1], not_8_out);
  and and_4 (and_4_out, not_1_out, Input_bus_1[6], not_4_out, Input_bus_1[3], not_6_out, Input_bus_1[1], Input_bus_1[0]);
  and and_5 (and_5_out, Input_bus_1[7], Input_bus_1[6], Input_bus_1[5], Input_bus_1[4], Input_bus_1[3], Input_bus_1[2], Input_bus_1[1], Input_bus_1[0]);
  and and_6 (and_6_out, not_1_out, Input_bus_1[6], not_4_out, not_5_out, not_7_out, Input_bus_1[0]);
  and and_7 (and_7_out, not_1_out, Input_bus_1[6], not_4_out, not_5_out, Input_bus_1[1], not_8_out);
  and and_8 (and_8_out, not_1_out, Input_bus_1[6], not_5_out, Input_bus_1[2], not_7_out, not_8_out);
  and and_9 (and_9_out, not_1_out, Input_bus_1[6], not_4_out, Input_bus_1[2], Input_bus_1[1], not_8_out);
  and and_10 (and_10_out, not_1_out, Input_bus_1[6], not_4_out, Input_bus_1[3], not_6_out, not_7_out, not_8_out);
  and and_11 (and_11_out, not_1_out, Input_bus_1[6], not_4_out, Input_bus_1[3], not_6_out, Input_bus_1[1], Input_bus_1[0]);
  and and_12 (and_12_out, not_1_out, Input_bus_1[6], Input_bus_1[4], not_5_out, not_6_out);
  and and_13 (and_13_out, not_1_out, Input_bus_1[6], Input_bus_1[4], not_6_out, not_7_out, Input_bus_1[0]);
  and and_14 (and_14_out, not_1_out, Input_bus_1[6], Input_bus_1[4], not_6_out, Input_bus_1[1], not_8_out);
  and and_15 (and_15_out, not_1_out, Input_bus_1[6], Input_bus_1[5], not_5_out, not_6_out, Input_bus_1[0]);
  and and_16 (and_16_out, not_1_out, Input_bus_1[6], Input_bus_1[5], not_4_out, Input_bus_1[1], Input_bus_1[0]);
  and and_17 (and_17_out, Input_bus_1[7], Input_bus_1[6], Input_bus_1[5], Input_bus_1[4], Input_bus_1[3], Input_bus_1[2], Input_bus_1[1], Input_bus_1[0]);
  and and_18 (and_18_out, not_1_out, Input_bus_1[6], not_5_out, not_7_out, Input_bus_1[0]);
  and and_19 (and_19_out, not_1_out, Input_bus_1[6], not_3_out, not_4_out, not_5_out, Input_bus_1[1]);
  and and_20 (and_20_out, not_1_out, Input_bus_1[6], not_4_out, not_5_out, Input_bus_1[1], not_8_out);
  and and_21 (and_21_out, not_1_out, Input_bus_1[6], not_3_out, not_4_out, Input_bus_1[2], Input_bus_1[0]);
  and and_22 (and_22_out, not_1_out, Input_bus_1[6], not_4_out, not_5_out, Input_bus_1[2], Input_bus_1[1]);
  and and_23 (and_23_out, not_1_out, Input_bus_1[6], not_4_out, Input_bus_1[3], not_7_out, not_8_out);
  and and_24 (and_24_out, not_1_out, Input_bus_1[6], not_4_out, Input_bus_1[3], not_6_out, Input_bus_1[1], Input_bus_1[0]);
  and and_25 (and_25_out, not_1_out, Input_bus_1[6], not_4_out, Input_bus_1[3], Input_bus_1[2], not_7_out);
  and and_26 (and_26_out, not_1_out, Input_bus_1[6], Input_bus_1[4], not_5_out, not_7_out);
  and and_27 (and_27_out, not_1_out, Input_bus_1[6], Input_bus_1[4], not_6_out, not_7_out);
  and and_28 (and_28_out, not_1_out, Input_bus_1[6], Input_bus_1[4], not_5_out, not_6_out, Input_bus_1[0]);
  and and_29 (and_29_out, Input_bus_1[7], Input_bus_1[6], Input_bus_1[5], Input_bus_1[4], Input_bus_1[3], Input_bus_1[2], Input_bus_1[1], Input_bus_1[0]);
  and and_30 (and_30_out, not_1_out, Input_bus_1[6], not_3_out, not_4_out, Input_bus_1[0]);
  and and_31 (and_31_out, not_1_out, Input_bus_1[6], not_4_out, not_6_out, Input_bus_1[0]);
  and and_32 (and_32_out, not_1_out, Input_bus_1[6], not_5_out, Input_bus_1[1], not_8_out);
  and and_33 (and_33_out, not_1_out, Input_bus_1[6], not_5_out, Input_bus_1[2], not_7_out);
  and and_34 (and_34_out, not_1_out, Input_bus_1[6], not_4_out, Input_bus_1[3], not_7_out);
  and and_35 (and_35_out, not_1_out, Input_bus_1[6], not_4_out, Input_bus_1[3], Input_bus_1[2]);
  and and_36 (and_36_out, not_1_out, Input_bus_1[6], Input_bus_1[4], not_6_out, not_8_out);
  and and_37 (and_37_out, not_1_out, Input_bus_1[6], Input_bus_1[4], not_5_out, Input_bus_1[2]);
  and and_38 (and_38_out, Input_bus_1[7], Input_bus_1[6], Input_bus_1[5], Input_bus_1[4], Input_bus_1[3], Input_bus_1[2], Input_bus_1[1], Input_bus_1[0]);
  and and_39 (and_39_out, not_1_out, not_3_out, not_4_out, Input_bus_1[3], not_6_out, Input_bus_1[1], not_8_out);
  and and_40 (and_40_out, not_1_out, Input_bus_1[6], not_4_out, not_5_out, not_6_out, Input_bus_1[1]);
  and and_41 (and_41_out, not_1_out, Input_bus_1[6], not_5_out, Input_bus_1[1], Input_bus_1[0]);
  and and_42 (and_42_out, not_1_out, Input_bus_1[6], not_3_out, not_4_out, Input_bus_1[2], not_7_out, not_8_out);
  and and_43 (and_43_out, not_1_out, Input_bus_1[6], not_4_out, not_5_out, Input_bus_1[2], not_7_out);
  and and_44 (and_44_out, not_1_out, Input_bus_1[6], not_5_out, Input_bus_1[2], Input_bus_1[0]);
  and and_45 (and_45_out, not_1_out, Input_bus_1[6], not_4_out, Input_bus_1[2], Input_bus_1[1], Input_bus_1[0]);
  and and_46 (and_46_out, not_1_out, Input_bus_1[6], Input_bus_1[3], not_6_out, Input_bus_1[1], not_8_out);
  and and_47 (and_47_out, Input_bus_1[7], Input_bus_1[6], Input_bus_1[5], Input_bus_1[4], Input_bus_1[3], Input_bus_1[2], Input_bus_1[1], Input_bus_1[0]);
  and and_48 (and_48_out, not_1_out, Input_bus_1[6], not_5_out, not_6_out, not_7_out, Input_bus_1[0]);
  and and_49 (and_49_out, not_1_out, Input_bus_1[6], not_4_out, not_6_out, Input_bus_1[1], not_8_out);
  and and_50 (and_50_out, not_1_out, Input_bus_1[6], not_4_out, not_5_out, Input_bus_1[2], not_7_out, not_8_out);
  and and_51 (and_51_out, not_1_out, Input_bus_1[6], not_4_out, Input_bus_1[2], Input_bus_1[1], Input_bus_1[0]);
  and and_52 (and_52_out, not_1_out, Input_bus_1[6], Input_bus_1[3], not_6_out, not_7_out, not_8_out);
  and and_53 (and_53_out, not_1_out, Input_bus_1[6], not_4_out, Input_bus_1[3], Input_bus_1[1], not_8_out);
  and and_54 (and_54_out, not_1_out, Input_bus_1[6], not_4_out, Input_bus_1[3], Input_bus_1[2], Input_bus_1[0]);
  and and_55 (and_55_out, not_1_out, Input_bus_1[6], Input_bus_1[4], not_5_out, Input_bus_1[0]);
  and and_56 (and_56_out, not_1_out, Input_bus_1[6], Input_bus_1[4], not_5_out, Input_bus_1[2], Input_bus_1[1]);
  and and_57 (and_57_out, not_1_out, Input_bus_1[6], Input_bus_1[4], Input_bus_1[3], not_6_out, not_7_out);
  and and_58 (and_58_out, Input_bus_1[7], Input_bus_1[6], Input_bus_1[5], Input_bus_1[4], Input_bus_1[3], Input_bus_1[2], Input_bus_1[1], Input_bus_1[0]);
  and and_59 (and_59_out, not_1_out, not_3_out, not_4_out, Input_bus_1[3], not_6_out, Input_bus_1[1], not_8_out);
  and and_60 (and_60_out, not_1_out, Input_bus_1[5], not_4_out, not_5_out, not_6_out, not_7_out, Input_bus_1[0]);
  and and_61 (and_61_out, not_1_out, Input_bus_1[6], not_5_out, not_6_out, not_7_out, Input_bus_1[0]);
  and and_62 (and_62_out, not_1_out, Input_bus_1[6], not_4_out, not_5_out, Input_bus_1[2], not_7_out, not_8_out);
  and and_63 (and_63_out, not_1_out, Input_bus_1[6], not_3_out, Input_bus_1[3], not_6_out, not_8_out);
  and and_64 (and_64_out, not_1_out, Input_bus_1[6], not_4_out, Input_bus_1[3], not_6_out, Input_bus_1[1]);
  and and_65 (and_65_out, not_1_out, Input_bus_1[6], not_3_out, not_4_out, Input_bus_1[3], Input_bus_1[2], Input_bus_1[0]);
  and and_66 (and_66_out, not_1_out, Input_bus_1[6], not_4_out, Input_bus_1[3], Input_bus_1[2], not_7_out, Input_bus_1[0]);
  and and_67 (and_67_out, not_1_out, Input_bus_1[6], Input_bus_1[4], not_6_out, not_7_out);
  and and_68 (and_68_out, not_1_out, Input_bus_1[6], Input_bus_1[4], not_5_out, not_7_out, Input_bus_1[0]);
  and and_69 (and_69_out, not_1_out, Input_bus_1[6], Input_bus_1[4], Input_bus_1[3], not_6_out, not_8_out);
  and and_70 (and_70_out, not_1_out, Input_bus_1[6], Input_bus_1[5], not_4_out, not_5_out, Input_bus_1[2], Input_bus_1[1], Input_bus_1[0]);
  and and_71 (and_71_out, Input_bus_1[7], Input_bus_1[6], Input_bus_1[5], Input_bus_1[4], Input_bus_1[3], Input_bus_1[2], Input_bus_1[1], Input_bus_1[0]);
  and and_72 (and_72_out, not_1_out, Input_bus_1[6], not_3_out, not_5_out, not_6_out, Input_bus_1[0]);
  and and_73 (and_73_out, not_1_out, Input_bus_1[6], not_5_out, not_6_out, not_7_out, Input_bus_1[0]);
  and and_74 (and_74_out, not_1_out, Input_bus_1[6], not_3_out, not_4_out, Input_bus_1[2], Input_bus_1[0]);
  and and_75 (and_75_out, not_1_out, Input_bus_1[6], not_4_out, Input_bus_1[2], not_7_out, Input_bus_1[0]);
  and and_76 (and_76_out, not_1_out, Input_bus_1[6], not_4_out, not_5_out, Input_bus_1[2], Input_bus_1[1]);
  and and_77 (and_77_out, not_1_out, Input_bus_1[6], Input_bus_1[4], not_5_out, not_6_out, not_7_out);
  and and_78 (and_78_out, not_1_out, Input_bus_1[6], Input_bus_1[4], not_5_out, not_6_out, Input_bus_1[0]);
  and and_79 (and_79_out, not_1_out, Input_bus_1[6], Input_bus_1[4], Input_bus_1[3], not_6_out, Input_bus_1[1], not_8_out);
  and and_80 (and_80_out, Input_bus_1[7], Input_bus_1[6], Input_bus_1[5], Input_bus_1[4], Input_bus_1[3], Input_bus_1[2], Input_bus_1[1], Input_bus_1[0]);
  or or_1 (Output_bus_1[7], and_1_out, and_2_out, and_3_out, and_4_out, and_5_out);
  or or_2 (Output_bus_1[6], and_6_out, and_7_out, and_8_out, and_9_out, and_10_out, and_11_out, and_12_out, and_13_out, and_14_out, and_15_out, and_16_out, and_17_out);
  or or_3 (Output_bus_1[5], and_18_out, and_19_out, and_20_out, and_21_out, and_22_out, and_23_out, and_24_out, and_25_out, and_26_out, and_27_out, and_28_out, and_29_out);
  or or_4 (Output_bus_1[4], and_30_out, and_31_out, and_32_out, and_33_out, and_34_out, and_35_out, and_36_out, and_37_out, and_38_out);
  or or_5 (Output_bus_1[3], and_39_out, and_40_out, and_41_out, and_42_out, and_43_out, and_44_out, and_45_out, and_46_out, and_47_out);
  or or_6 (Output_bus_1[2], and_48_out, and_49_out, and_50_out, and_51_out, and_52_out, and_53_out, and_54_out, and_55_out, and_56_out, and_57_out, and_58_out);
  or or_7 (Output_bus_1[1], and_59_out, and_60_out, and_61_out, and_62_out, and_63_out, and_64_out, and_65_out, and_66_out, and_67_out, and_68_out, and_69_out, and_70_out, and_71_out);
  or or_8 (Output_bus_1[0], and_72_out, and_73_out, and_74_out, and_75_out, and_76_out, and_77_out, and_78_out, and_79_out, and_80_out);
endmodule

module sentence_disp (
  input  [7:0] newletter,
  input  enable,
  input  clk,
  input  reset,
  output [7:0] letter0,
  output [7:0] letter1,
  output [7:0] letter2,
  output [7:0] letter3,
  output [7:0] letter4,
  output [7:0] letter5
);

  Register register_1 (.D(newletter), .en(enable), .clk(clk), .Q(letter0), .clr(reset));
  Register register_2 (.D(letter0), .en(enable), .clk(clk), .Q(letter1), .clr(reset));
  Register register_3 (.D(letter1), .en(enable), .clk(clk), .Q(letter2), .clr(reset));
  Register register_4 (.D(letter2), .en(enable), .clk(clk), .Q(letter3), .clr(reset));
  Register register_5 (.D(letter3), .en(enable), .clk(clk), .Q(letter4), .clr(reset));
  Register register_6 (.D(letter4), .en(enable), .clk(clk), .Q(letter5), .clr(reset));
endmodule

module letter8_reader (
  input  enable_read,
  input  [63:0] saved_message,
  input  clk,
  input  reset,
  output [7:0] letter0,
  output [7:0] letter1,
  output [7:0] letter2,
  output [7:0] letter3,
  output [7:0] letter4,
  output [7:0] letter5,
  output countffff
);

  wire and_1_out, comparator_1_gt, not_1_out, or_1_out;
  wire [2:0] counter_2_q;
  wire [7:0] multiplexer_1_out;
  wire [15:0] counter_1_q;

  not not_1 (not_1_out, enable_read);
  or or_1 (or_1_out, not_1_out, reset);
  Counter #(.max('hffff), .width(16)) counter_1 (
    .clr(or_1_out), .load(1'b0), .up(1'b1), .count(1'b1), .clk(clk), .D({16{1'b1}}), .Q(counter_1_q));  // open: carry
  Comparator #(.mode("unsigned"), .width(16)) comparator_1 (
    .a(counter_1_q), .b(16'hfff0), .gt(comparator_1_gt));  // open: eq, lt
  and and_1 (and_1_out, enable_read, comparator_1_gt);
  Counter #(.max('h7), .width(3)) counter_2 (
    .clr(reset), .load(1'b0), .up(1'b1), .count(1'b1), .clk(and_1_out), .D(3'b111), .Q(counter_2_q));  // open: carry
  S_R_Flip_Flop s_r_ff_1 (.S(comparator_1_gt), .clk(clk), .Q(countffff), .reset(reset));  // open: R, Qn, preset
  Multiplexer #(.select(3), .width(8)) multiplexer_1 (
    .in0(saved_message[7:0]), .in1(saved_message[15:8]), .in2(saved_message[23:16]),
    .in3(saved_message[31:24]), .in4(saved_message[39:32]), .in5(saved_message[47:40]),
    .in6(saved_message[55:48]), .in7(saved_message[63:56]), .out(multiplexer_1_out), .sel(counter_2_q));
  sentence_disp sentence_disp_1 (
    .newletter(multiplexer_1_out), .enable(and_1_out), .clk(clk), .reset(reset), .letter0(letter0),
    .letter1(letter1), .letter2(letter2), .letter3(letter3), .letter4(letter4), .letter5(letter5));
endmodule

module save_display (
  input  rx_ready,
  input  [7:0] Input_bus_1,
  input  clk,
  input  reset,
  output [7:0] Output_bus_1,
  output write_done
);

  wire [7:0] bin_to_letter_1_output_bus_1;
  wire [63:0] letter8_writer_1_saved_message;

  bin_to_letter bin_to_letter_1 (.Input_bus_1(Input_bus_1), .Output_bus_1(bin_to_letter_1_output_bus_1));
  letter8_writer letter8_writer_1 (
    .new_letter(bin_to_letter_1_output_bus_1), .update(rx_ready), .clk(clk), .reset(reset),
    .Output_1(write_done), .saved_message(letter8_writer_1_saved_message));
  letter8_reader_slow letter8_reader_slow_1 (
    .write_done(write_done), .saved_message(letter8_writer_1_saved_message), .clk(clk), .reset(reset),
    .Output_bus_1(Output_bus_1));
endmodule

module debug (
  input  [7:0] in_1,
  output [7:0] letter_0,
  output [7:0] letter_1,
  output [7:0] letter_2,
  output [7:0] letter_3,
  output [7:0] letter_4,
  output [7:0] letter_5
);

  wire undriven, undriven_3, undriven_4;
  wire [7:0] bin_to_letter_1_output_bus_1;
  wire [47:0] undriven_2;

  bin_to_letter bin_to_letter_1 (.Input_bus_1(in_1), .Output_bus_1(bin_to_letter_1_output_bus_1));
  _7_Segment_Display u_7_segment_display_1 (
    .g(bin_to_letter_1_output_bus_1[6]), .f(bin_to_letter_1_output_bus_1[5]),
    .a(bin_to_letter_1_output_bus_1[0]), .b(bin_to_letter_1_output_bus_1[1]),
    .e(bin_to_letter_1_output_bus_1[4]), .d(bin_to_letter_1_output_bus_1[3]),
    .c(bin_to_letter_1_output_bus_1[2]), .dp(bin_to_letter_1_output_bus_1[7]));
  Register register_1 (.D(undriven_2[7:0]), .en(undriven), .clk(undriven_3), .Q(letter_0), .clr(undriven_4));
  Register register_2 (.D(undriven_2[15:8]), .en(undriven), .clk(undriven_3), .Q(letter_1), .clr(undriven_4));
  Register register_3 (.D(undriven_2[23:16]), .en(undriven), .clk(undriven_3), .Q(letter_2), .clr(undriven_4));
  Register register_4 (.D(undriven_2[31:24]), .en(undriven), .clk(undriven_3), .Q(letter_3), .clr(undriven_4));
  Register register_5 (.D(undriven_2[39:32]), .en(undriven), .clk(undriven_3), .Q(letter_4), .clr(undriven_4));
  Register register_6 (.D(undriven_2[47:40]), .en(undriven), .clk(undriven_3), .Q(letter_5), .clr(undriven_4));
endmodule

module letter8_writer (
  input  [7:0] new_letter,
  input  update,
  input  clk,
  input  reset,
  output Output_1,
  output [63:0] saved_message
);

  wire and_1_out, and_2_out, clock_1_out, comparator_1_eq, comparator_2_eq, d_ff_1_q, d_ff_2_q,
       demux8_1_output_1, demux8_1_output_2, demux8_1_output_3, demux8_1_output_4, demux8_1_output_5,
       demux8_1_output_6, demux8_1_output_7, demux8_1_output_8, not_1_out, not_2_out, or_1_out, s_r_ff_1_qn;
  wire [2:0] counter_1_q;
  wire [7:0] multiplexer_1_out, multiplexer_2_out, multiplexer_3_out, multiplexer_4_out, multiplexer_5_out,
       multiplexer_6_out, multiplexer_7_out, multiplexer_8_out;

  Clock clock_1 (.out(clock_1_out));
  D_Flip_Flop d_ff_1 (.D(update), .clk(clock_1_out), .Q(d_ff_1_q), .preset(1'b0), .reset(reset));  // open: Qn
  Comparator #(.mode("unsigned"), .width(3)) comparator_1 (
    .a(3'b111), .b(counter_1_q), .eq(comparator_1_eq));  // open: gt, lt
  not not_1 (not_1_out, update);
  D_Flip_Flop d_ff_2 (.D(comparator_1_eq), .clk(clock_1_out), .Q(d_ff_2_q), .preset(1'b0), .reset(1'b0));  // open: Qn
  Counter #(.max('h7), .width(3)) counter_1 (
    .clr(reset), .load(1'b0), .up(1'b1), .count(1'b1), .clk(and_1_out), .D(3'b001), .Q(counter_1_q));  // open: carry
  and and_1 (and_1_out, d_ff_1_q, not_1_out);
  not not_2 (not_2_out, comparator_1_eq);
  and and_2 (and_2_out, not_2_out, d_ff_2_q);
  Comparator #(.mode("unsigned")) comparator_2 (.a(new_letter), .b(8'ha), .eq(comparator_2_eq));  // open: gt, lt
  or or_1 (or_1_out, comparator_2_eq, and_2_out);
  S_R_Flip_Flop s_r_ff_1 (
    .S(1'b0), .R(1'b0), .clk(clock_1_out), .Q(Output_1), .reset(reset), .Qn(s_r_ff_1_qn), .preset(or_1_out));
  demux8 demux8_1 (
    .Input_1(s_r_ff_1_qn), .Input_bus_1(counter_1_q), .Output_1(demux8_1_output_1),
    .Output_2(demux8_1_output_2), .Output_3(demux8_1_output_3), .Output_4(demux8_1_output_4),
    .Output_5(demux8_1_output_5), .Output_6(demux8_1_output_6), .Output_7(demux8_1_output_7),
    .Output_8(demux8_1_output_8));
  Multiplexer #(.width(8)) multiplexer_1 (
    .in0(saved_message[7:0]), .in1(new_letter), .out(multiplexer_1_out), .sel(demux8_1_output_1));
  Multiplexer #(.width(8)) multiplexer_2 (
    .in0(saved_message[15:8]), .in1(new_letter), .out(multiplexer_2_out), .sel(demux8_1_output_2));
  Multiplexer #(.width(8)) multiplexer_3 (
    .in0(saved_message[23:16]), .in1(new_letter), .out(multiplexer_3_out), .sel(demux8_1_output_3));
  Multiplexer #(.width(8)) multiplexer_4 (
    .in0(saved_message[31:24]), .in1(new_letter), .out(multiplexer_4_out), .sel(demux8_1_output_4));
  Multiplexer #(.width(8)) multiplexer_5 (
    .in0(saved_message[39:32]), .in1(new_letter), .out(multiplexer_5_out), .sel(demux8_1_output_5));
  Multiplexer #(.width(8)) multiplexer_6 (
    .in0(saved_message[47:40]), .in1(new_letter), .out(multiplexer_6_out), .sel(demux8_1_output_6));
  Multiplexer #(.width(8)) multiplexer_7 (
    .in0(saved_message[55:48]), .in1(new_letter), .out(multiplexer_7_out), .sel(demux8_1_output_7));
  Multiplexer #(.width(8)) multiplexer_8 (
    .in0(saved_message[63:56]), .in1(new_letter), .out(multiplexer_8_out), .sel(demux8_1_output_8));
  Register register_1 (.D(multiplexer_1_out), .en(update), .clk(clock_1_out), .Q(saved_message[7:0]), .clr(reset));
  Register register_2 (.D(multiplexer_2_out), .en(update), .clk(clock_1_out), .Q(saved_message[15:8]), .clr(reset));
  Register register_3 (.D(multiplexer_3_out), .en(update), .clk(clock_1_out), .Q(saved_message[23:16]), .clr(reset));
  Register register_4 (.D(multiplexer_4_out), .en(update), .clk(clock_1_out), .Q(saved_message[31:24]), .clr(reset));
  Register register_5 (.D(multiplexer_5_out), .en(update), .clk(clock_1_out), .Q(saved_message[39:32]), .clr(reset));
  Register register_6 (.D(multiplexer_6_out), .en(update), .clk(clock_1_out), .Q(saved_message[47:40]), .clr(reset));
  Register register_7 (.D(multiplexer_7_out), .en(update), .clk(clock_1_out), .Q(saved_message[55:48]), .clr(reset));
  Register register_8 (.D(multiplexer_8_out), .en(update), .clk(clock_1_out), .Q(saved_message[63:56]), .clr(reset));

  // Notes on the sheet:
  //   if count =7 and next count not 7, stop
  //   if lstop
  //   only count after new_b turns on AND off
  //   count to 7 for 8 bytes
  //   asynchronously
  //   8 bytes, saved or passed on
endmodule

module demux8 (
  input  Input_1,
  input  [2:0] Input_bus_1,
  output Output_1,
  output Output_2,
  output Output_3,
  output Output_4,
  output Output_5,
  output Output_6,
  output Output_7,
  output Output_8
);

  wire not_1_out, not_2_out, not_3_out;

  not not_1 (not_1_out, Input_bus_1[2]);
  not not_2 (not_2_out, Input_bus_1[1]);
  not not_3 (not_3_out, Input_bus_1[0]);
  and and_1 (Output_1, Input_1, not_1_out, not_2_out, not_3_out);
  and and_2 (Output_2, Input_1, not_1_out, not_2_out, Input_bus_1[0]);
  and and_3 (Output_3, Input_1, not_1_out, Input_bus_1[1], not_3_out);
  and and_4 (Output_4, Input_1, not_1_out, Input_bus_1[1], Input_bus_1[0]);
  and and_5 (Output_5, Input_1, Input_bus_1[2], not_2_out, not_3_out);
  and and_6 (Output_6, Input_1, Input_bus_1[2], not_2_out, Input_bus_1[0]);
  and and_7 (Output_7, Input_1, Input_bus_1[2], Input_bus_1[1], not_3_out);
  and and_8 (Output_8, Input_1, Input_bus_1[2], Input_bus_1[1], Input_bus_1[0]);
endmodule

module letter8_reader_slow (
  input  write_done,
  input  [63:0] saved_message,
  input  clk,
  input  reset,
  output [7:0] Output_bus_1
);

  wire and_1_out, comparator_1_eq, not_1_out, or_1_out;
  wire [2:0] counter_2_q;
  wire [8:0] counter_1_q;

  not not_1 (not_1_out, write_done);
  or or_1 (or_1_out, not_1_out, reset);
  Counter #(.max('h1c7), .width(9)) counter_1 (
    .clr(or_1_out), .load(1'b0), .up(1'b1), .count(1'b1), .clk(clk), .D(9'h1c7), .Q(counter_1_q));  // open: carry
  Comparator #(.mode("unsigned"), .width(9)) comparator_1 (
    .a(counter_1_q), .b(9'h1c7), .eq(comparator_1_eq));  // open: gt, lt
  and and_1 (and_1_out, write_done, comparator_1_eq);
  Counter #(.max('h7), .width(3)) counter_2 (
    .clr(reset), .load(1'b0), .up(1'b1), .count(1'b1), .clk(and_1_out), .D(3'b111), .Q(counter_2_q));  // open: carry
  Multiplexer #(.select(3), .width(8)) multiplexer_1 (
    .in0(saved_message[7:0]), .in1(saved_message[15:8]), .in2(saved_message[23:16]),
    .in3(saved_message[31:24]), .in4(saved_message[39:32]), .in5(saved_message[47:40]),
    .in6(saved_message[55:48]), .in7(saved_message[63:56]), .out(Output_bus_1), .sel(counter_2_q));
endmodule

// VHDL entity uart_rx, as the project stores it:
--------------------------------------------------------------------------------
-- Project :
-- File    : uart_rx.vhd
-- Author  :
-- Date    :
--
--------------------------------------------------------------------------------
-- Description :
-- UART receiver module for asynchronous serial communication. This version
-- includes improvements for bit timing, stop bit verification, and output signal
-- handling.
--------------------------------------------------------------------------------

LIBRARY ieee;
USE ieee.std_logic_1164.all;
USE ieee.numeric_std.all;

ENTITY uart_rx IS
    PORT (
        i_Clock      : IN  std_logic;                    -- System clock input
        i_RX_Serial  : IN  std_logic;                    -- Serial data input
        o_RX_DV      : OUT std_logic;                    -- Data valid signal
        o_RX_Byte    : OUT std_logic_vector(7 downto 0); -- Output byte
        o_Start_Done : OUT std_logic;                    -- Start bit detected signal
        o_FSM_Mode   : OUT std_logic_vector(2 downto 0);  -- FSM state output for debugging
        o_Bit_Index	 : OUT std_logic_vector(2 downto 0)
    );
END uart_rx;

ARCHITECTURE Behavioral OF uart_rx IS
    type state_type IS (IDLE, RX_START_BIT, RX_DATA_BITS, RX_STOP_BIT, CLEANUP);
    signal r_SM_Main : state_type := IDLE;
    signal r_Start_Done : std_logic := '0';
    signal r_Clock_Count : unsigned(23 downto 0) := (others => '0');
    signal r_Bit_Index : unsigned(2 downto 0) := (others => '0');
    signal r_RX_Byte : std_logic_vector(7 downto 0) := (others => '0');
    signal r_RX_DV : std_logic := '0';
    signal r_FSM_Mode : std_logic_vector(2 downto 0) := (others => '0'); 
    constant N : integer := 3;  -- Number of cycles to confirm bit
    signal bit_counter : integer range 0 to N := 0;  -- N is the number of clock cycles for confirmation
    
    constant CLKS_PER_BIT : integer := 3;  -- Clock cycles per bit, 3 for 1khz (8k/8) and 300 br
    
begin
    process(i_Clock)
    begin
        if rising_edge(i_Clock) then            
            case r_SM_Main is
                when IDLE =>
                    r_FSM_Mode <= "001";
                    r_RX_DV <= '0';
                    r_Clock_Count <= (others => '0');
                    r_Bit_Index <= (others => '0');
                    r_Start_Done <= '0';

                    if i_RX_Serial = '0' then
                        bit_counter <= bit_counter + 1;
                        if bit_counter >= N then  -- Confirmed low for N clock cycles
                            r_SM_Main <= RX_START_BIT;
                            bit_counter <= 0;  -- Reset counter
                        end if;
                    else
                        bit_counter <= 0;  -- Reset counter if high is detected
                    end if;

                when RX_START_BIT =>
                    r_FSM_Mode <= "010";
                    r_Clock_Count <= r_Clock_Count + 1;
                    if r_Clock_Count = CLKS_PER_BIT/2 then
                        if i_RX_Serial = '0' then
                            r_Start_Done <= '1';  -- Midpoint confirmation of the start bit
                        else
                            r_Start_Done <= '0';
                        end if;
                    end if;
                    if r_Clock_Count = CLKS_PER_BIT - 1 then
                        r_Clock_Count <= (others => '0');  -- Reset the counter for use in the next state
                        if r_Start_Done = '1' then
                            r_SM_Main <= RX_DATA_BITS;  -- Transition to data bits after confirming start bit
                        else
                            r_SM_Main <= IDLE;  -- Reset if the start bit is not sustained
                        end if;
                    end if;

                when RX_DATA_BITS =>
                    r_FSM_Mode <= "011";
                    r_Clock_Count <= r_Clock_Count + 1;
                    if r_Clock_Count = CLKS_PER_BIT/2 then
                        r_RX_Byte(to_integer(r_Bit_Index)) <= i_RX_Serial;  -- Sample at mid-point
                    end if;
                    if r_Clock_Count = CLKS_PER_BIT - 1 then
                        r_Clock_Count <= (others => '0');    -- Reset for next bit
                        if r_Bit_Index < 7 then
                            r_Bit_Index <= r_Bit_Index + 1;
                        else
                            r_Bit_Index <= (others => '0');
                            r_SM_Main <= RX_STOP_BIT;  -- Proceed to stop bit verification
                        end if;
                    end if;

                when RX_STOP_BIT =>
                    r_FSM_Mode <= "100";
                    r_Clock_Count <= r_Clock_Count + 1;
                    if r_Clock_Count = CLKS_PER_BIT/2 then
                        if i_RX_Serial = '1' then
                            r_RX_DV <= '1';  -- Midpoint confirmation of the stop bit
                        end if;
                    end if;
                    if r_Clock_Count = CLKS_PER_BIT - 1 then
                        r_Clock_Count <= (others => '0');
                        r_SM_Main <= CLEANUP;  -- Cleanup and prepare to return to IDLE
                    end if;

                    -- bit parity

                when CLEANUP =>
                    r_FSM_Mode <= "101";
                    r_SM_Main <= IDLE;
                    r_RX_DV <= '0';

                when others =>
                    r_SM_Main <= IDLE;

            end case;
            o_Bit_Index <= std_logic_vector(r_Bit_Index);
        end if;
    end process;

    o_RX_DV <= r_RX_DV;
    o_RX_Byte <= r_RX_Byte;
    o_Start_Done <= r_Start_Done;
    o_FSM_Mode <= r_FSM_Mode;

END ARCHITECTURE Behavioral;

// VHDL entity uart_tx, as the project stores it:
--------------------------------------------------------------------------------
-- Project :
-- uart_rx_log
-- File    :
-- UART_TX
-- Autor   :
-- Selma Benhassine
-- Date    :
 
--
--------------------------------------------------------------------------------
-- Description :
-- The transmitter file for the UART_transmission portion of the project
--
--------------------------------------------------------------------------------

library IEEE;
use IEEE.STD_LOGIC_1164.ALL;
use IEEE.NUMERIC_STD.ALL;

entity uart_tx is
    Port (
        clk_50M : in STD_LOGIC;               -- Input clock, assumed 50 MHz
        data_raw : in STD_LOGIC_VECTOR (7 downto 0);  -- Data byte (8 bits) to transmit
        trigger_raw : in STD_LOGIC;           -- Tells module to begin transmission of data_raw byte
        busy : out STD_LOGIC;                 -- Flag to indicate a transmission is in progress
        serial_out : out STD_LOGIC;            -- UART output serial datastream
        tx_index_out : out STD_LOGIC_VECTOR(3 downto 0) 
    );
end uart_tx;

--------------------------------------------------------------------------------
--Complete your VHDL description below
--------------------------------------------------------------------------------

architecture Behavioral of uart_tx is
	 
	 constant CLKS_PER_BIT: integer := 5208;
--  The calculation is as follows:
--  
--                                                  1
--     CLKS_PER_BIT =  F_clk [cycles/sec] * --------------------
--                                           baud_rate[bit/sec]
--  so 5208 gives 9.6k baud rate for clk at 50MHz
--  f = 50MHz / 8 when going through logisim
-- last done 217
	 
    type state_type is (STATE_IDLE, STATE_TRANSMITTING, STATE_CLEANUP);
    signal tx_state : state_type := STATE_IDLE;  -- State variable for main finite state machine
    signal data_aug : std_logic_vector(9 downto 0) := (others => '0');  -- Augmented data word to transmit that includes START bit, data byte, and STOP BIT
    signal tx_index : unsigned(3 downto 0) := (others => '0');  -- Index of bit currently transmitting
    signal bit_delay : unsigned(31 downto 0) := (others => '0'); -- Timer to regulate baud rate
   

    signal trigger_0 : std_logic := '0';  -- Synchronizer on trigger input signal
    signal trigger : std_logic := '0';    -- Synchronizer on trigger input signal

    -- Localparam CLKS_PER_BIT is not needed in VHDL since it's used as a constant value in the code directly

begin

    process (clk_50M) begin
        if rising_edge(clk_50M) then
            case tx_state is
                -- Wait for trigger condition indicating it's time to transmit a byte.
                when STATE_IDLE =>
                    busy <= '0';                 -- Indicate that transmitter is idle.
                    serial_out <= '1';           -- Idle output HIGH, per standard UART behavior.
                    if trigger = '1' then        -- Check if received trigger to TX a byte
                        data_aug <= '1' & data_raw & '0';   -- Create augmented byte with start and stop bits
                        busy <= '1';                        -- Indicate that transmitter is busy.
                        bit_delay <= (others => '0');       -- Clear timer used to track duration of each bit
                        tx_index <= (others => '0');        -- Point to first bit of data_aug to TX, namely the start bit
                        tx_state <= STATE_TRANSMITTING;     -- Move on to next state
                    end if;
                    
                -- Transmit all 10 bits with proper the proper duration per bit based on the selected baud rate.
                when STATE_TRANSMITTING =>
                    serial_out <= data_aug(to_integer(tx_index));  -- Set output based on current bit to transmit
                    bit_delay <= bit_delay + 1;                     -- Keep track of duration to hold this bit
                    if bit_delay > to_unsigned(CLKS_PER_BIT, 32) then  -- Check if bit duration has expired
                        if tx_index = "1001" then                  -- Check if just transmitted the final bit, i.e. the STOP bit
                            tx_state <= STATE_CLEANUP;            -- Move on to next state
                        else
                            tx_index <= tx_index + 1;             -- Still more bits to send so, point to next bit
                            bit_delay <= (others => '0');         -- Clear counter used to regulate baud rate
                        end if;
                    end if;
                    
                -- Pause for a few bit durations after full byte transmitted.
                when STATE_CLEANUP =>
                    bit_delay <= bit_delay + 1;                    -- Keep track of how long been in cleanup state
                    if bit_delay > to_unsigned(5 * CLKS_PER_BIT, 32) then  -- If paused HIGH long enough, then return to idle state
                        tx_state <= STATE_IDLE;
                    end if;
                    
                -- Should never get here, but if do, return to IDLE
                when others =>
                    tx_state <= STATE_IDLE;
            end case;
            tx_index_out <= std_logic_vector(tx_index);
        end if;
    end process;

    -- Synchronizer for trigger input
    process (clk_50M) begin
        if rising_edge(clk_50M) then
            trigger_0 <= trigger_raw;
            trigger <= trigger_0;
        end if;
    end process;

end Behavioral;

// VHDL entity uart_tx_tester, as the project stores it:
--------------------------------------------------------------------------------
-- Project : UART_Module
-- File    : UART_Transmitter_Tester
-- Autor   : Selma Benhassine
-- Date    :
--
--------------------------------------------------------------------------------
-- Description : Testbench file for the UART transmitter
--
--------------------------------------------------------------------------------

library IEEE;
use IEEE.STD_LOGIC_1164.ALL;
use IEEE.NUMERIC_STD.ALL;

entity uart_tx_tester is
    Port (
        clk_50M : in STD_LOGIC;               -- Input clock, assumed 50 MHz
        run_test_raw : in STD_LOGIC;          -- HIGH indicates to continuously run test
        tx_busy : in STD_LOGIC;               -- HIGH indicates transmitter is busy 
        data_out : out STD_LOGIC_VECTOR (7 downto 0);  -- Data byte (8 bits) to transmit
        trigger : out STD_LOGIC                -- Trigger to tell UART module to begin transmission
    );
end uart_tx_tester;

architecture Behavioral of uart_tx_tester is

    signal run_test_0 : std_logic := '0';          -- Synchronizer for 'start test' switch input
    signal run_test : std_logic := '0';            -- Synchronizer for 'start test' switch input
    signal tester_state : unsigned(5 downto 0) := (others => '0');  -- FSM state variable
    -- signal byte_index : unsigned(31 downto 0) := unsigned(8*16)-unsigned(1);          -- Pointer to beginning of next byte to transmit in 16 byte message
    constant BYTE_INDEX_INIT: natural := (8*16)-1; -- Calculate the initial value for byte_index
    signal byte_index : unsigned(31 downto 0) := to_unsigned(BYTE_INDEX_INIT, 32); -- Initialize byte_index with the calculated value
	 signal pause_delay : unsigned(31 downto 0) := (others => '0');  -- Counter for delay between re-transmissions of message
    signal trigger_ctr : unsigned(5 downto 0) := (others => '0');    -- Delay to hold trigger high, in clock cycles

    constant STATE_IDLE : unsigned(5 downto 0) := "000000";          -- Legal values for tester_state
    constant STATE_LOAD : unsigned(5 downto 0) := "000010";          -- Legal values for tester_state
    constant STATE_TRIGGER : unsigned(5 downto 0) := "000100";       -- Legal values for tester_state
    constant STATE_POLL_BUSY : unsigned(5 downto 0) := "001000";     -- Legal values for tester_state
    constant STATE_PAUSE : unsigned(5 downto 0) := "010000";         -- Legal values for tester_state

    constant MSG_DELAY : unsigned(31 downto 0) := to_unsigned(100_000, 32);  -- Delay between messages re-transmissions, in clk cycles
	 
	 -- Message to transmit
    signal byte_str : std_logic_vector((8*16)-1 downto 0) := "01001000" & "01100101" & "01101100" & "01101100" & "01101111" & "00100000" & "01010111" & "01101111" &
                                                             "01110010" & "01101100" & "01100100" & "00100001" & "00100000" & "00100000" & "00100000" & "00100000";

-- hello world! is "01001000" & "01100101" & "01101100" & "01101100" & "01101111" & "00100000" & "01010111" & "01101111" &
                                                            -- "01110010" & "01101100" & "01100100" & "00100001" & "00100000" & "00100000" & "00100000" & "00100000";


begin

    -- Synchronizer for "run_test" input since, as tested, this comes from a 
    -- slide switch on the DE10-Lite board, which is not synchronous with the
    -- clock.
    process (clk_50M) begin
        if rising_edge(clk_50M) then
            run_test_0 <= run_test_raw;
            run_test <= run_test_0;
        end if;
    end process;

    -- Main Finite State Machine that sequences the test
    process (clk_50M) begin
        if rising_edge(clk_50M) then
            case tester_state is
                -- Wait for request to begin test.
                when STATE_IDLE =>
                    trigger <= '0';
                    if run_test = '1' then
                        byte_index <= to_unsigned(BYTE_INDEX_INIT, 32);
                        tester_state <= STATE_LOAD;
                    end if;
                    
                -- Output next byte to transmitter module, with trigger still low
                -- so it won't transmit yet.
                when STATE_LOAD =>
                    trigger <= '0';
                    data_out <= byte_str(to_integer(byte_index) downto to_integer(byte_index)-7);
                    trigger_ctr <= to_unsigned(5, 6);
                    tester_state <= STATE_TRIGGER;
                    
                -- Now that previous state output'd the next byte to transmit,
                -- assert the trigger signal to begin the transmission.
                when STATE_TRIGGER =>
                    trigger <= '1';
                    trigger_ctr <= trigger_ctr - 1;
                    if trigger_ctr = 0 then
                        tester_state <= STATE_POLL_BUSY;
                    end if;
                    
                -- Clear trigger signal, and wait until all bits shifted out
                -- for the current byte.
                when STATE_POLL_BUSY =>
                    trigger <= '0';
                    if tx_busy = '0' then
                        if byte_index <= 7 then
                            pause_delay <= (others => '0');
                            tester_state <= STATE_PAUSE;
                        else
                            byte_index <= byte_index - 8;
                            tester_state <= STATE_LOAD;
                        end if;
                    end if;
                    
                -- Once transmitted full message, pause before 
                -- transmitting message again for testing convenience.
                when STATE_PAUSE =>
                    pause_delay <= pause_delay + 1;
                    if pause_delay > to_integer(MSG_DELAY) then
                        tester_state <= STATE_IDLE;
                    end if;
                    
                -- Should never get here, but if do, return to IDLE
                when others =>
                    tester_state <= STATE_IDLE;
            end case;
        end if;
    end process;

end Behavioral;
