// Logisim project TestBench_WaveForms.circ as structural Verilog: 1 circuit, main circuit main
module main (
  output Test
);

  wire Anything_sw1, Anything_sw2, Anything_sw3, Anything_sw4, Anything_sw5, Anything_sw6, Anything_sw7,
       Anything_sw8;

  DipSwitch Anything (
    .sw1(Anything_sw1), .sw2(Anything_sw2), .sw3(Anything_sw3), .sw4(Anything_sw4), .sw5(Anything_sw5),
    .sw6(Anything_sw6), .sw7(Anything_sw7), .sw8(Anything_sw8));
  or or_1 (Test, Anything_sw1, Anything_sw2, Anything_sw3, Anything_sw4, Anything_sw5, Anything_sw6, Anything_sw7, Anything_sw8);
endmodule
