// Logisim project Testing_Signals.circ as structural Verilog: 9 circuits, main circuit main
module main (
  input  rx_received,
  input  cycle_button,
  input  select_button,
  output tx_serial,
  output stored,
  output [2:0] tx_mode,
  output [4:0] rx_mode,
  output [7:0] Output_bus_1,
  output [7:0] Output_bus_2,
  output [7:0] Output_bus_3,
  output [7:0] Output_bus_4,
  output [7:0] Output_bus_5,
  output [7:0] Output_bus_6,
  output clockk
);

  wire button_press_1_cycle, button_press_1_reset, button_press_1_selector, button_press_1_tx_go, or_1_out;
  wire [63:0] driver_1_stored_message, fsm_1_tx_message;

  Clock clock_1 (.out(clockk));
  button_press button_press_1 (
    .cycle_button(cycle_button), .select_button(select_button), .clk(clockk), .cycle(button_press_1_cycle),
    .selector(button_press_1_selector), .tx_go(button_press_1_tx_go), .reset(button_press_1_reset));
  or or_1 (or_1_out, button_press_1_reset, button_press_1_cycle);
  driver driver_1 (
    .run_tx(button_press_1_tx_go), .message_tx(fsm_1_tx_message), .input_rx(rx_received), .clk(clockk),
    .reset(or_1_out), .tx_out(tx_serial), .stored_message(driver_1_stored_message), .message_stored(stored),
    .tx_Mode(tx_mode), .rx_Mode(rx_mode));
  fsm fsm_1 (
    .rx_message(driver_1_stored_message), .cycle(button_press_1_cycle),
    .select_mode(button_press_1_selector), .clk(clockk), .reset(button_press_1_reset),
    .tx_message(fsm_1_tx_message),
    .display({Output_bus_6, Output_bus_5, Output_bus_4, Output_bus_3, Output_bus_2, Output_bus_1}));  // open: checknum
endmodule

module letter8_reader (
  input  [63:0] saved_message,
  input  write_done,
  input  clk,
  input  reset,
  output [7:0] output_letter,
  output update_disp
);

  wire comparator_1_eq, not_1_out, or_1_out;
  wire [3:0] letter_count_q;
  wire [21:0] slow_clock_q;

  not not_1 (not_1_out, write_done);
  or or_1 (or_1_out, not_1_out, reset);
  Counter #(.max('h7a120), .width(22)) slow_clock (
    .clr(or_1_out), .load(1'b0), .up(1'b1), .count(1'b1), .clk(clk), .D(22'h7a120), .Q(slow_clock_q));  // open: carry
  Comparator #(.mode("unsigned"), .width(22)) comparator_1 (
    .a(slow_clock_q), .b(22'h7a120), .eq(comparator_1_eq));  // open: gt, lt
  and and_1 (update_disp, write_done, comparator_1_eq);
  Counter #(.max('h8), .width(4)) letter_count (
    .clr(reset), .load(1'b0), .up(1'b1), .count(1'b1), .clk(update_disp), .D(4'b1000), .Q(letter_count_q));  // open: carry
  Multiplexer #(.select(4), .width(8)) multiplexer_1 (
    .in0({8{1'b0}}), .in1(saved_message[7:0]), .in2(saved_message[15:8]), .in3(saved_message[23:16]),
    .in4(saved_message[31:24]), .in5(saved_message[39:32]), .in6(saved_message[47:40]),
    .in7(saved_message[55:48]), .in8(saved_message[63:56]), .in9({8{1'b0}}), .in10({8{1'b0}}),
    .in11({8{1'b0}}), .in12({8{1'b0}}), .in13({8{1'b0}}), .in14({8{1'b0}}), .in15({8{1'b0}}),
    .out(output_letter), .sel(letter_count_q));
endmodule

module sentence_disp (
  input  [7:0] newletter,
  input  enable,
  input  clk,
  input  reset,
  output [47:0] disp_rx
);

  Register register_1 (.D(newletter), .en(enable), .clk(clk), .Q(disp_rx[7:0]), .clr(reset));
  Register register_2 (.D(disp_rx[7:0]), .en(enable), .clk(clk), .Q(disp_rx[15:8]), .clr(reset));
  Register register_3 (.D(disp_rx[15:8]), .en(enable), .clk(clk), .Q(disp_rx[23:16]), .clr(reset));
  Register register_4 (.D(disp_rx[23:16]), .en(enable), .clk(clk), .Q(disp_rx[31:24]), .clr(reset));
  Register register_5 (.D(disp_rx[31:24]), .en(enable), .clk(clk), .Q(disp_rx[39:32]), .clr(reset));
  Register register_6 (.D(disp_rx[39:32]), .en(enable), .clk(clk), .Q(disp_rx[47:40]), .clr(reset));
endmodule

module bin_to_seg (
  input  [7:0] ascii_in,
  output [7:0] seg_out
);

  wire and_1_out, and_2_out, and_3_out, and_4_out, and_5_out, and_6_out, and_7_out, and_8_out, and_9_out,
       and_10_out, and_11_out, and_12_out, and_13_out, and_14_out, and_15_out, and_16_out, and_17_out,
       and_18_out, and_19_out, and_20_out, and_21_out, and_22_out, and_23_out, and_24_out, and_25_out,
       and_26_out, and_27_out, and_28_out, and_29_out, and_30_out, and_31_out, and_32_out, and_33_out,
       and_34_out, and_35_out, and_36_out, and_37_out, and_38_out, and_39_out, and_40_out, and_41_out,
       and_42_out, and_43_out, and_44_out, and_45_out, and_46_out, and_47_out, and_48_out, and_49_out,
       and_50_out, and_51_out, and_52_out, and_53_out, and_54_out, and_55_out, and_56_out, and_57_out,
       and_58_out, and_59_out, and_60_out, and_61_out, and_62_out, and_63_out, and_64_out, and_65_out,
       and_66_out, and_67_out, and_68_out, and_69_out, and_70_out, and_71_out, and_72_out, and_73_out,
       and_74_out, and_75_out, and_76_out, and_77_out, and_78_out, and_79_out, and_80_out, and_81_out,
       and_82_out, and_83_out, and_84_out, and_85_out, and_86_out, and_87_out, and_88_out, and_89_out,
       and_90_out, and_91_out, and_92_out, and_93_out, and_94_out, and_95_out, and_96_out, and_97_out,
       and_98_out, and_99_out, and_100_out, and_101_out, and_102_out, and_103_out, and_104_out, and_105_out,
       and_106_out, and_107_out, and_108_out, and_109_out, and_110_out, and_111_out, and_112_out,
       and_113_out, and_114_out, and_115_out, and_116_out, and_117_out, and_118_out, and_119_out,
       and_120_out, and_121_out, and_122_out, and_123_out, and_124_out, and_125_out, and_126_out,
       and_127_out, and_128_out, and_129_out, and_130_out, and_131_out, not_1_out, not_2_out, not_3_out,
       not_4_out, not_5_out, not_6_out, not_7_out, not_8_out;

  not not_1 (not_1_out, ascii_in[7]);
  not not_2 (not_2_out, ascii_in[6]);
  not not_3 (not_3_out, ascii_in[5]);
  not not_4 (not_4_out, ascii_in[4]);
  not not_5 (not_5_out, ascii_in[3]);
  not not_6 (not_6_out, ascii_in[2]);
  not not_7 (not_7_out, ascii_in[1]);
  not not_8 (not_8_out, ascii_in[0]);
  and and_1 (and_1_out, not_1_out, not_2_out, ascii_in[5], not_4_out, not_5_out, not_6_out, not_7_out, ascii_in[0]);
  and and_2 (and_2_out, not_1_out, not_2_out, ascii_in[5], not_4_out, ascii_in[3], ascii_in[2], ascii_in[1], not_8_out);
  and and_3 (and_3_out, not_1_out, not_2_out, ascii_in[5], ascii_in[4], ascii_in[3], ascii_in[2], ascii_in[1], ascii_in[0]);
  and and_4 (and_4_out, not_1_out, ascii_in[6], not_4_out, ascii_in[3], not_6_out, ascii_in[1], ascii_in[0]);
  and and_5 (and_5_out, ascii_in[7], ascii_in[6], ascii_in[5], ascii_in[4], ascii_in[3], ascii_in[2], ascii_in[1], ascii_in[0]);
  and and_6 (and_6_out, not_1_out, not_2_out, not_3_out, not_4_out, not_5_out, not_6_out, ascii_in[1]);
  and and_7 (and_7_out, not_1_out, not_3_out, not_4_out, not_5_out, ascii_in[2], not_7_out);
  and and_8 (and_8_out, not_1_out, not_2_out, not_3_out, not_4_out, not_5_out, ascii_in[2], ascii_in[0]);
  and and_9 (and_9_out, not_1_out, not_2_out, not_3_out, not_4_out, ascii_in[3], not_6_out, not_7_out);
  and and_10 (and_10_out, not_1_out, not_2_out, ascii_in[5], ascii_in[3], ascii_in[2], not_7_out, ascii_in[0]);
  and and_11 (and_11_out, not_1_out, ascii_in[5], ascii_in[4], not_5_out, not_6_out, ascii_in[1]);
  and and_12 (and_12_out, not_1_out, ascii_in[5], ascii_in[4], not_5_out, ascii_in[2], not_7_out, not_8_out);
  and and_13 (and_13_out, not_1_out, not_2_out, ascii_in[5], ascii_in[4], ascii_in[2], ascii_in[0]);
  and and_14 (and_14_out, not_1_out, not_2_out, ascii_in[5], ascii_in[4], ascii_in[3], not_6_out, not_7_out);
  and and_15 (and_15_out, not_1_out, ascii_in[6], not_4_out, not_5_out, not_7_out, ascii_in[0]);
  and and_16 (and_16_out, not_1_out, ascii_in[6], not_5_out, not_6_out, ascii_in[1], not_8_out);
  and and_17 (and_17_out, not_1_out, ascii_in[6], not_5_out, ascii_in[2], not_7_out, not_8_out);
  and and_18 (and_18_out, not_1_out, ascii_in[6], not_4_out, ascii_in[2], ascii_in[1], not_8_out);
  and and_19 (and_19_out, not_1_out, ascii_in[6], not_4_out, ascii_in[3], not_6_out, not_7_out, not_8_out);
  and and_20 (and_20_out, not_1_out, ascii_in[6], not_4_out, ascii_in[3], not_6_out, ascii_in[1], ascii_in[0]);
  and and_21 (and_21_out, not_1_out, ascii_in[6], ascii_in[4], not_5_out, not_6_out);
  and and_22 (and_22_out, not_1_out, ascii_in[6], ascii_in[4], not_6_out, not_7_out, ascii_in[0]);
  and and_23 (and_23_out, not_1_out, ascii_in[6], ascii_in[4], not_6_out, ascii_in[1], not_8_out);
  and and_24 (and_24_out, not_1_out, ascii_in[6], ascii_in[5], not_5_out, not_6_out, ascii_in[0]);
  and and_25 (and_25_out, not_1_out, ascii_in[6], ascii_in[5], not_4_out, ascii_in[1], ascii_in[0]);
  and and_26 (and_26_out, ascii_in[7], ascii_in[6], ascii_in[5], ascii_in[4], ascii_in[3], ascii_in[2], ascii_in[1], ascii_in[0]);
  and and_27 (and_27_out, not_1_out, not_2_out, not_3_out, not_4_out, not_5_out, ascii_in[2], not_7_out);
  and and_28 (and_28_out, not_1_out, not_3_out, not_4_out, not_5_out, ascii_in[2], ascii_in[0]);
  and and_29 (and_29_out, not_1_out, not_2_out, not_3_out, not_4_out, ascii_in[3], not_6_out, not_7_out);
  and and_30 (and_30_out, not_1_out, ascii_in[5], ascii_in[4], not_5_out, ascii_in[2], not_7_out);
  and and_31 (and_31_out, not_1_out, not_2_out, ascii_in[5], ascii_in[4], not_5_out, ascii_in[2], ascii_in[0]);
  and and_32 (and_32_out, not_1_out, ascii_in[5], ascii_in[4], ascii_in[3], not_6_out, not_7_out);
  and and_33 (and_33_out, not_1_out, ascii_in[6], not_5_out, not_7_out, ascii_in[0]);
  and and_34 (and_34_out, not_1_out, ascii_in[6], not_4_out, not_5_out, ascii_in[1], not_8_out);
  and and_35 (and_35_out, not_1_out, ascii_in[6], not_3_out, not_4_out, ascii_in[1], ascii_in[0]);
  and and_36 (and_36_out, not_1_out, ascii_in[6], not_4_out, ascii_in[2], not_7_out, ascii_in[0]);
  and and_37 (and_37_out, not_1_out, ascii_in[6], not_4_out, not_5_out, ascii_in[2], ascii_in[1]);
  and and_38 (and_38_out, not_1_out, ascii_in[6], not_4_out, ascii_in[3], not_7_out, not_8_out);
  and and_39 (and_39_out, not_1_out, ascii_in[6], ascii_in[3], not_6_out, not_7_out, not_8_out);
  and and_40 (and_40_out, not_1_out, ascii_in[6], not_4_out, ascii_in[3], not_6_out, ascii_in[1], ascii_in[0]);
  and and_41 (and_41_out, not_1_out, ascii_in[6], ascii_in[4], not_5_out, not_7_out);
  and and_42 (and_42_out, not_1_out, ascii_in[6], ascii_in[4], not_6_out, not_7_out);
  and and_43 (and_43_out, not_1_out, ascii_in[6], ascii_in[4], not_5_out, not_6_out, ascii_in[0]);
  and and_44 (and_44_out, ascii_in[7], ascii_in[6], ascii_in[5], ascii_in[4], ascii_in[3], ascii_in[2], ascii_in[1], ascii_in[0]);
  and and_45 (and_45_out, not_1_out, not_3_out, not_4_out, not_5_out, not_6_out, ascii_in[1], not_8_out);
  and and_46 (and_46_out, not_1_out, not_3_out, not_4_out, not_5_out, ascii_in[2], ascii_in[0]);
  and and_47 (and_47_out, not_1_out, ascii_in[5], ascii_in[4], not_5_out, not_6_out, ascii_in[1], not_8_out);
  and and_48 (and_48_out, not_1_out, ascii_in[5], ascii_in[4], not_5_out, ascii_in[2], ascii_in[0]);
  and and_49 (and_49_out, not_1_out, not_2_out, ascii_in[5], ascii_in[4], ascii_in[2], ascii_in[1], ascii_in[0]);
  and and_50 (and_50_out, not_1_out, ascii_in[6], not_4_out, not_6_out, ascii_in[0]);
  and and_51 (and_51_out, not_1_out, ascii_in[6], not_4_out, not_7_out, ascii_in[0]);
  and and_52 (and_52_out, not_1_out, ascii_in[6], not_5_out, ascii_in[1], not_8_out);
  and and_53 (and_53_out, not_1_out, ascii_in[6], not_4_out, ascii_in[2], not_7_out);
  and and_54 (and_54_out, not_1_out, ascii_in[6], not_4_out, ascii_in[3], not_7_out);
  and and_55 (and_55_out, not_1_out, ascii_in[6], not_4_out, ascii_in[3], ascii_in[0]);
  and and_56 (and_56_out, not_1_out, ascii_in[6], not_4_out, ascii_in[3], ascii_in[2]);
  and and_57 (and_57_out, not_1_out, ascii_in[6], ascii_in[4], not_6_out, not_8_out);
  and and_58 (and_58_out, not_1_out, ascii_in[6], ascii_in[4], not_5_out, ascii_in[2]);
  and and_59 (and_59_out, ascii_in[7], ascii_in[6], ascii_in[5], ascii_in[4], ascii_in[3], ascii_in[2], ascii_in[1], ascii_in[0]);
  and and_60 (and_60_out, not_1_out, not_3_out, not_4_out, not_5_out, not_6_out, ascii_in[1]);
  and and_61 (and_61_out, not_1_out, not_3_out, not_4_out, not_6_out, ascii_in[1], not_8_out);
  and and_62 (and_62_out, not_1_out, not_3_out, not_4_out, not_5_out, ascii_in[2], ascii_in[0]);
  and and_63 (and_63_out, not_1_out, not_2_out, not_3_out, not_4_out, ascii_in[3], not_6_out, not_7_out);
  and and_64 (and_64_out, not_1_out, not_2_out, not_3_out, not_4_out, ascii_in[3], not_7_out, ascii_in[0]);
  and and_65 (and_65_out, not_1_out, not_2_out, ascii_in[5], ascii_in[4], not_5_out, not_6_out, ascii_in[1]);
  and and_66 (and_66_out, not_1_out, ascii_in[5], ascii_in[4], not_5_out, ascii_in[2], ascii_in[0]);
  and and_67 (and_67_out, not_1_out, not_2_out, ascii_in[5], ascii_in[4], ascii_in[3], not_6_out, not_7_out);
  and and_68 (and_68_out, not_1_out, not_2_out, ascii_in[5], ascii_in[4], ascii_in[3], not_7_out, ascii_in[0]);
  and and_69 (and_69_out, not_1_out, ascii_in[6], not_4_out, not_5_out, not_6_out, ascii_in[1]);
  and and_70 (and_70_out, not_1_out, ascii_in[6], not_5_out, ascii_in[1], ascii_in[0]);
  and and_71 (and_71_out, not_1_out, ascii_in[6], not_3_out, not_4_out, ascii_in[2], not_7_out, not_8_out);
  and and_72 (and_72_out, not_1_out, ascii_in[6], not_4_out, not_5_out, ascii_in[2], not_7_out);
  and and_73 (and_73_out, not_1_out, ascii_in[6], not_5_out, ascii_in[2], ascii_in[0]);
  and and_74 (and_74_out, not_1_out, ascii_in[6], not_3_out, ascii_in[2], ascii_in[1], ascii_in[0]);
  and and_75 (and_75_out, not_1_out, ascii_in[6], not_4_out, ascii_in[2], ascii_in[1], ascii_in[0]);
  and and_76 (and_76_out, not_1_out, ascii_in[6], ascii_in[3], not_6_out, ascii_in[1], not_8_out);
  and and_77 (and_77_out, ascii_in[7], ascii_in[6], ascii_in[5], ascii_in[4], ascii_in[3], ascii_in[2], ascii_in[1], ascii_in[0]);
  and and_78 (and_78_out, not_1_out, not_2_out, not_3_out, not_4_out, not_5_out, ascii_in[0]);
  and and_79 (and_79_out, not_1_out, not_2_out, not_3_out, not_4_out, not_7_out, ascii_in[0]);
  and and_80 (and_80_out, not_1_out, not_2_out, not_3_out, not_4_out, not_5_out, ascii_in[2]);
  and and_81 (and_81_out, not_1_out, not_3_out, not_4_out, ascii_in[3], not_6_out, not_7_out, not_8_out);
  and and_82 (and_82_out, not_1_out, ascii_in[5], ascii_in[4], not_5_out, ascii_in[0]);
  and and_83 (and_83_out, not_1_out, not_2_out, ascii_in[5], ascii_in[4], not_5_out, ascii_in[2]);
  and and_84 (and_84_out, not_1_out, ascii_in[5], ascii_in[4], ascii_in[3], not_6_out, not_7_out);
  and and_85 (and_85_out, not_1_out, ascii_in[6], not_5_out, not_6_out, not_7_out, ascii_in[0]);
  and and_86 (and_86_out, not_1_out, ascii_in[6], not_4_out, not_6_out, ascii_in[1], not_8_out);
  and and_87 (and_87_out, not_1_out, ascii_in[6], not_4_out, not_5_out, ascii_in[2], not_7_out, not_8_out);
  and and_88 (and_88_out, not_1_out, ascii_in[6], not_4_out, ascii_in[2], ascii_in[1], ascii_in[0]);
  and and_89 (and_89_out, not_1_out, ascii_in[6], not_5_out, ascii_in[2], ascii_in[1], ascii_in[0]);
  and and_90 (and_90_out, not_1_out, ascii_in[6], ascii_in[3], not_6_out, not_7_out, not_8_out);
  and and_91 (and_91_out, not_1_out, ascii_in[6], not_4_out, ascii_in[3], ascii_in[1], not_8_out);
  and and_92 (and_92_out, not_1_out, ascii_in[6], not_4_out, ascii_in[3], ascii_in[2], ascii_in[0]);
  and and_93 (and_93_out, not_1_out, ascii_in[6], ascii_in[4], not_5_out, ascii_in[0]);
  and and_94 (and_94_out, not_1_out, ascii_in[6], ascii_in[4], not_6_out, not_7_out, ascii_in[0]);
  and and_95 (and_95_out, not_1_out, ascii_in[6], ascii_in[4], not_5_out, ascii_in[2], ascii_in[1]);
  and and_96 (and_96_out, ascii_in[7], ascii_in[6], ascii_in[5], ascii_in[4], ascii_in[3], ascii_in[2], ascii_in[1], ascii_in[0]);
  and and_97 (and_97_out, not_1_out, not_4_out, not_5_out, not_6_out, not_7_out, ascii_in[0]);
  and and_98 (and_98_out, not_1_out, not_2_out, not_3_out, not_4_out, not_5_out, ascii_in[1]);
  and and_99 (and_99_out, not_1_out, not_3_out, not_4_out, not_5_out, ascii_in[2], not_7_out, not_8_out);
  and and_100 (and_100_out, not_1_out, not_2_out, not_3_out, not_4_out, ascii_in[3], not_6_out, not_7_out);
  and and_101 (and_101_out, not_1_out, not_3_out, not_4_out, ascii_in[3], not_6_out, not_8_out);
  and and_102 (and_102_out, not_1_out, ascii_in[5], ascii_in[4], not_6_out, not_7_out, ascii_in[0]);
  and and_103 (and_103_out, not_1_out, not_2_out, ascii_in[5], ascii_in[4], not_5_out, ascii_in[1]);
  and and_104 (and_104_out, not_1_out, not_2_out, ascii_in[5], ascii_in[4], not_5_out, ascii_in[2], not_8_out);
  and and_105 (and_105_out, not_1_out, not_2_out, ascii_in[5], ascii_in[4], ascii_in[2], ascii_in[1], ascii_in[0]);
  and and_106 (and_106_out, not_1_out, ascii_in[5], ascii_in[4], ascii_in[3], not_6_out, not_7_out);
  and and_107 (and_107_out, not_1_out, ascii_in[6], not_4_out, not_5_out, ascii_in[2], not_7_out, not_8_out);
  and and_108 (and_108_out, not_1_out, ascii_in[6], not_4_out, ascii_in[3], not_6_out, ascii_in[1]);
  and and_109 (and_109_out, not_1_out, ascii_in[6], ascii_in[3], not_6_out, ascii_in[1], not_8_out);
  and and_110 (and_110_out, not_1_out, ascii_in[6], not_3_out, not_4_out, ascii_in[3], ascii_in[2], ascii_in[0]);
  and and_111 (and_111_out, not_1_out, ascii_in[6], not_4_out, ascii_in[3], ascii_in[2], not_7_out, ascii_in[0]);
  and and_112 (and_112_out, not_1_out, ascii_in[6], ascii_in[4], not_6_out, not_7_out);
  and and_113 (and_113_out, not_1_out, ascii_in[6], ascii_in[4], not_5_out, not_7_out, ascii_in[0]);
  and and_114 (and_114_out, not_1_out, ascii_in[6], ascii_in[5], not_4_out, not_5_out, ascii_in[2], ascii_in[1], ascii_in[0]);
  and and_115 (and_115_out, ascii_in[7], ascii_in[6], ascii_in[5], ascii_in[4], ascii_in[3], ascii_in[2], ascii_in[1], ascii_in[0]);
  and and_116 (and_116_out, not_1_out, not_2_out, not_3_out, not_4_out, not_5_out, ascii_in[1]);
  and and_117 (and_117_out, not_1_out, not_3_out, not_4_out, ascii_in[2], not_7_out, ascii_in[0]);
  and and_118 (and_118_out, not_1_out, not_2_out, not_3_out, not_4_out, ascii_in[3], not_6_out, not_7_out);
  and and_119 (and_119_out, not_1_out, not_2_out, ascii_in[5], ascii_in[4], not_5_out, ascii_in[1]);
  and and_120 (and_120_out, not_1_out, not_2_out, ascii_in[5], ascii_in[4], not_5_out, ascii_in[2], ascii_in[0]);
  and and_121 (and_121_out, not_1_out, not_2_out, ascii_in[5], ascii_in[4], ascii_in[2], ascii_in[1], ascii_in[0]);
  and and_122 (and_122_out, not_1_out, not_2_out, ascii_in[5], ascii_in[4], ascii_in[3], not_6_out, not_7_out);
  and and_123 (and_123_out, not_1_out, ascii_in[6], not_3_out, not_5_out, not_6_out, ascii_in[0]);
  and and_124 (and_124_out, not_1_out, ascii_in[6], not_4_out, not_5_out, not_7_out, ascii_in[0]);
  and and_125 (and_125_out, not_1_out, ascii_in[6], not_3_out, not_4_out, ascii_in[2], ascii_in[0]);
  and and_126 (and_126_out, not_1_out, ascii_in[6], not_4_out, ascii_in[2], not_7_out, ascii_in[0]);
  and and_127 (and_127_out, not_1_out, ascii_in[6], not_4_out, not_5_out, ascii_in[2], ascii_in[1]);
  and and_128 (and_128_out, not_1_out, ascii_in[6], ascii_in[4], not_5_out, not_6_out, not_7_out);
  and and_129 (and_129_out, not_1_out, ascii_in[6], ascii_in[4], not_5_out, not_6_out, ascii_in[0]);
  and and_130 (and_130_out, not_1_out, ascii_in[6], ascii_in[4], ascii_in[3], not_6_out, ascii_in[1], not_8_out);
  and and_131 (and_131_out, ascii_in[7], ascii_in[6], ascii_in[5], ascii_in[4], ascii_in[3], ascii_in[2], ascii_in[1], ascii_in[0]);
  or or_1 (seg_out[7], and_1_out, and_2_out, and_3_out, and_4_out, and_5_out);
  or or_2 (seg_out[6], and_6_out, and_7_out, and_8_out, and_9_out, and_10_out, and_11_out, and_12_out, and_13_out, and_14_out, and_15_out, and_16_out, and_17_out, and_18_out, and_19_out, and_20_out, and_21_out, and_22_out, and_23_out, and_24_out, and_25_out, and_26_out);
  or or_3 (seg_out[5], and_27_out, and_28_out, and_29_out, and_30_out, and_31_out, and_32_out, and_33_out, and_34_out, and_35_out, and_36_out, and_37_out, and_38_out, and_39_out, and_40_out, and_41_out, and_42_out, and_43_out, and_44_out);
  or or_4 (seg_out[4], and_45_out, and_46_out, and_47_out, and_48_out, and_49_out, and_50_out, and_51_out, and_52_out, and_53_out, and_54_out, and_55_out, and_56_out, and_57_out, and_58_out, and_59_out);
  or or_5 (seg_out[3], and_60_out, and_61_out, and_62_out, and_63_out, and_64_out, and_65_out, and_66_out, and_67_out, and_68_out, and_69_out, and_70_out, and_71_out, and_72_out, and_73_out, and_74_out, and_75_out, and_76_out, and_77_out);
  or or_6 (seg_out[2], and_78_out, and_79_out, and_80_out, and_81_out, and_82_out, and_83_out, and_84_out, and_85_out, and_86_out, and_87_out, and_88_out, and_89_out, and_90_out, and_91_out, and_92_out, and_93_out, and_94_out, and_95_out, and_96_out);
  or or_7 (seg_out[1], and_97_out, and_98_out, and_99_out, and_100_out, and_101_out, and_102_out, and_103_out, and_104_out, and_105_out, and_106_out, and_107_out, and_108_out, and_109_out, and_110_out, and_111_out, and_112_out, and_113_out, and_114_out, and_115_out);
  or or_8 (seg_out[0], and_116_out, and_117_out, and_118_out, and_119_out, and_120_out, and_121_out, and_122_out, and_123_out, and_124_out, and_125_out, and_126_out, and_127_out, and_128_out, and_129_out, and_130_out, and_131_out);
endmodule

module message_display (
  input  [63:0] message,
  input  disp_ready,
  input  clk,
  input  reset,
  output [7:0] checknum,
  output [47:0] seg0
);

  wire letter8_reader_1_update_disp;
  wire [7:0] conversion_seg_out;

  letter8_reader letter8_reader_1 (
    .saved_message(message), .write_done(disp_ready), .clk(clk), .reset(reset), .output_letter(checknum),
    .update_disp(letter8_reader_1_update_disp));
  bin_to_seg conversion (.ascii_in(checknum), .seg_out(conversion_seg_out));
  sentence_disp sentence_disp_1 (
    .newletter(conversion_seg_out), .enable(letter8_reader_1_update_disp), .clk(clk), .reset(reset),
    .disp_rx(seg0));
endmodule

module fsm (
  input  [63:0] rx_message,
  input  cycle,
  input  select_mode,
  input  clk,
  input  reset,
  output [7:0] checknum,
  output [63:0] tx_message,
  output [47:0] display
);

  wire and_1_out, and_2_out, and_3_out, and_4_out, comparator_1_eq, comparator_2_eq, comparator_3_eq,
       comparator_4_eq, d_ff_1_q, not_1_out, or_1_out, or_2_out, register_1_q;
  wire [1:0] main_options_cycle_q, new_state_1_state, record_main_choice_q, tx_options_cycle_q,
       wait_button_release_q;
  wire [47:0] multiplexer_2_out, rx_disp, tx_disp;
  wire [63:0] multiplexer_1_out;

  D_Flip_Flop d_ff_1 (.D(cycle), .clk(clk), .Q(d_ff_1_q));  // open: Qn, preset, reset
  // Probe on wait_button_release_q
  Comparator #(.mode("unsigned"), .width(2)) comparator_1 (
    .a(2'b00), .b(wait_button_release_q), .eq(comparator_1_eq));  // open: gt, lt
  Comparator #(.mode("unsigned"), .width(2)) comparator_2 (
    .a(2'b01), .b(wait_button_release_q), .eq(comparator_2_eq));  // open: gt, lt
  and and_1 (and_1_out, d_ff_1_q, comparator_1_eq);
  Counter #(.max('h3), .width(2)) tx_options_cycle (
    .clr(reset), .load(1'b0), .up(1'b1), .count(1'b1), .clk(and_2_out), .Q(tx_options_cycle_q));  // open: D, carry
  and and_2 (and_2_out, d_ff_1_q, comparator_2_eq);
  or or_1 (or_1_out, reset, select_mode);
  Counter #(.max('h1), .width(2)) main_options_cycle (
    .clr(reset), .load(1'b0), .up(1'b1), .count(1'b1), .clk(and_1_out), .Q(main_options_cycle_q));  // open: D, carry
  // Probe on tx_options_cycle_q
  message_display updated_message_disp (
    .message(rx_message), .disp_ready(1'b1), .clk(clk), .reset(or_1_out), .checknum(checknum), .seg0(rx_disp));
  Multiplexer #(.select(2), .width(64)) multiplexer_1 (
    .in0(64'h656e696874206f54), .in1(64'h666c6573206e774f), .in2(64'h2065757274206542),
    .in3(64'h202e532e57202d20), .out(multiplexer_1_out), .sel(tx_options_cycle_q));
  // Probe on rx_disp
  Multiplexer #(.width(48)) multiplexer_2 (
    .in0(48'h7036), .in1(48'h5036), .out(multiplexer_2_out), .sel(main_options_cycle_q[0]));
  Counter #(.max('h1), .width(2)) record_main_choice (
    .clr(reset), .load(1'b0), .up(1'b1), .count(1'b1), .clk(and_3_out), .Q(record_main_choice_q));  // open: D, carry
  and and_3 (and_3_out, select_mode, comparator_3_eq);
  Comparator #(.mode("unsigned"), .width(2)) comparator_3 (
    .a(2'b00), .b(wait_button_release_q), .eq(comparator_3_eq));  // open: gt, lt
  Comparator #(.mode("unsigned"), .width(2)) comparator_4 (
    .a(2'b01), .b(wait_button_release_q), .eq(comparator_4_eq));  // open: gt, lt
  or or_2 (or_2_out, reset, select_mode);
  Register #(.width(1)) register_1 (
    .D(main_options_cycle_q[0]), .en(select_mode), .clk(clk), .Q(register_1_q), .clr(reset));
  Register #(.width(64)) record_tx_mess_chosen (
    .D(multiplexer_1_out), .en(and_4_out), .clk(clk), .Q(tx_message), .clr(reset));
  and and_4 (and_4_out, select_mode, comparator_4_eq);
  message_display update_mess_disp (
    .message(tx_message), .disp_ready(1'b1), .clk(clk), .reset(or_2_out), .seg0(tx_disp));  // open: checknum
  // Probe on wait_button_release_q
  Multiplexer #(.select(2), .width(48)) multiplexer_3 (
    .in0(multiplexer_2_out), .in1(tx_disp), .in2(rx_disp), .out(display), .sel(wait_button_release_q));  // open: in3
  new_state new_state_1 (.main_choice(register_1_q), .main_chosen(record_main_choice_q[0]), .state(new_state_1_state));
  Register #(.width(2)) wait_button_release (
    .D(new_state_1_state), .en(not_1_out), .clk(clk), .Q(wait_button_release_q), .clr(reset));
  not not_1 (not_1_out, select_mode);

  // Other names for the same wires on the sheet: tx[63:0] = tx_message

  // Notes on the sheet:
  //   tx disp
  //   rx disp
  //   main menu
  //   main option selector
endmodule

module new_state (
  input  main_choice,
  input  main_chosen,
  output [1:0] state
);

  wire not_1_out;

  not not_1 (not_1_out, main_choice);
  and and_1 (state[1], main_chosen, main_choice);
  and and_2 (state[0], main_chosen, not_1_out);
endmodule

module button_press (
  input  cycle_button,
  input  select_button,
  input  clk,
  output cycle,
  output selector,
  output tx_go,
  output reset
);

  wire and_1_out, comparator_1_eq, d_ff_1_q, d_ff_2_q, d_ff_3_q, d_ff_4_q, d_ff_5_q, d_ff_6_q, d_ff_7_q,
       d_ff_8_q, d_ff_9_q, d_ff_10_q, not_1_out, register_1_q;
  wire [21:0] slow_clock_q;

  D_Flip_Flop d_ff_1 (.D(cycle_button), .clk(clk), .Q(d_ff_1_q));  // open: Qn, preset, reset
  D_Flip_Flop d_ff_2 (.D(select_button), .clk(clk), .Q(d_ff_2_q));  // open: Qn, preset, reset
  D_Flip_Flop d_ff_3 (.D(d_ff_1_q), .clk(clk), .Q(d_ff_3_q));  // open: Qn, preset, reset
  D_Flip_Flop d_ff_4 (.D(d_ff_2_q), .clk(clk), .Q(d_ff_4_q));  // open: Qn, preset, reset
  D_Flip_Flop d_ff_5 (.D(d_ff_3_q), .clk(clk), .Q(d_ff_5_q));  // open: Qn, preset, reset
  D_Flip_Flop d_ff_6 (.D(d_ff_4_q), .clk(clk), .Q(d_ff_6_q));  // open: Qn, preset, reset
  D_Flip_Flop d_ff_7 (.D(d_ff_5_q), .clk(clk), .Q(d_ff_7_q));  // open: Qn, preset, reset
  D_Flip_Flop d_ff_8 (.D(d_ff_6_q), .clk(clk), .Q(d_ff_8_q));  // open: Qn, preset, reset
  D_Flip_Flop d_ff_9 (.D(d_ff_7_q), .clk(clk), .Q(d_ff_9_q));  // open: Qn, preset, reset
  D_Flip_Flop d_ff_10 (.D(d_ff_8_q), .clk(clk), .Q(d_ff_10_q));  // open: Qn, preset, reset
  Register #(.width(1)) register_1 (.D(d_ff_10_q), .en(d_ff_10_q), .clk(clk), .Q(register_1_q), .clr(not_1_out));
  not not_1 (not_1_out, d_ff_10_q);
  and and_1 (and_1_out, register_1_q, comparator_1_eq);
  Counter #(.max('h1e8480), .width(22)) slow_clock (
    .clr(not_1_out), .load(1'b0), .up(1'b1), .count(1'b1), .clk(clk), .D(22'h1e8480), .Q(slow_clock_q));  // open: carry
  longpress longpress_1 (
    .cycle_5dff(d_ff_9_q), .select_5dff(d_ff_10_q), .select_1s(and_1_out), .cycle(cycle),
    .selector(selector), .tx_go(tx_go), .reset(reset));
  Comparator #(.mode("unsigned"), .width(22)) comparator_1 (
    .a(slow_clock_q), .b(22'h1e8480), .eq(comparator_1_eq));  // open: gt, lt
endmodule

module longpress (
  input  cycle_5dff,
  input  select_5dff,
  input  select_1s,
  output cycle,
  output selector,
  output tx_go,
  output reset
);

  wire not_1_out, not_2_out, not_3_out;

  not not_1 (not_1_out, cycle_5dff);
  not not_2 (not_2_out, select_5dff);
  not not_3 (not_3_out, select_1s);
  and and_1 (cycle, cycle_5dff, not_2_out);
  and and_2 (selector, not_1_out, select_5dff, not_3_out);
  and and_3 (tx_go, not_1_out, select_5dff, select_1s);
  and and_4 (reset, cycle_5dff, select_5dff);
endmodule
