// Logisim project uart_tx.circ as structural Verilog
module main (
  input  Run_test,
  output letter_busy,
  output Serial_n_out,
  output display_n_out,
  output [7:0] letter
);

  wire clock_1_out, uart_tx_tester_1_trigger;

  Clock clock_1 (.out(clock_1_out));
  uart_tx_tester uart_tx_tester_1 (
    .clk_50M(clock_1_out), .run_test_raw(Run_test), .tx_busy(letter_busy), .data_out(letter),
    .trigger(uart_tx_tester_1_trigger));
  uart_tx uart_tx_1 (
    .clk_50M(clock_1_out), .data_raw(letter), .trigger_raw(uart_tx_tester_1_trigger), .busy(letter_busy),
    .serial_out(display_n_out));

  assign Serial_n_out = display_n_out;
endmodule

// VHDL entity uart_tx, as the project stores it:
--------------------------------------------------------------------------------
-- Project : UART_Module
-- File    : UART_TX
-- Autor   : Selma Benhassine
-- Date    : 
--
--------------------------------------------------------------------------------
-- Description : The transmitter file for the UART_transmission portion of the project
--
--------------------------------------------------------------------------------

library IEEE;
use IEEE.STD_LOGIC_1164.ALL;
use IEEE.NUMERIC_STD.ALL;

entity uart_tx is
    Port (
        clk_50M : in STD_LOGIC;               -- Input clock, assumed 50 MHz
        data_raw : in STD_LOGIC_VECTOR (7 downto 0);  -- Data byte (8 bits) to transmit
        trigger_raw : in STD_LOGIC;           -- Tells module to begin transmission of data_raw byte
        busy : out STD_LOGIC;                 -- Flag to indicate a transmission is in progress
        serial_out : out STD_LOGIC            -- UART output serial datastream
    );
end uart_tx;

--------------------------------------------------------------------------------
--Complete your VHDL description below
--------------------------------------------------------------------------------

architecture Behavioral of uart_tx is
	 
	 constant CLKS_PER_BIT: integer := 217;
--  The calculation is as follows:
--
--                                                  1
--     CLKS_PER_BIT =  F_clk [cycles/sec] * --------------------
--                                           baud_rate[bit/sec]
--  so 5208 gives 9.6k baud rate for clk at 50MHz
--  f = 50MHz / 8 when going through logisim
	 
    type state_type is (STATE_IDLE, STATE_TRANSMITTING, STATE_CLEANUP);
    signal tx_state : state_type := STATE_IDLE;  -- State variable for main finite state machine
    signal data_aug : std_logic_vector(9 downto 0) := (others => '0');  -- Augmented data word to transmit that includes START bit, data byte, and STOP BIT
    signal tx_index : unsigned(3 downto 0) := (others => '0');  -- Index of bit currently transmitting
    signal bit_delay : unsigned(31 downto 0) := (others => '0'); -- Timer to regulate baud rate

    signal trigger_0 : std_logic := '0';  -- Synchronizer on trigger input signal
    signal trigger : std_logic := '0';    -- Synchronizer on trigger input signal

    -- Localparam CLKS_PER_BIT is not needed in VHDL since it's used as a constant value in the code directly

begin

    process (clk_50M) begin
        if rising_edge(clk_50M) then
            case tx_state is
                -- Wait for trigger condition indicating it's time to transmit a byte.
                when STATE_IDLE =>
                    busy <= '0';                 -- Indicate that transmitter is idle.
                    serial_out <= '1';           -- Idle output HIGH, per standard UART behavior.
                    if trigger = '1' then        -- Check if received trigger to TX a byte
                        data_aug <= '1' & data_raw & '0';   -- Create augmented byte with start and stop bits
                        busy <= '1';                        -- Indicate that transmitter is busy.
                        bit_delay <= (others => '0');       -- Clear timer used to track duration of each bit
                        tx_index <= (others => '0');        -- Point to first bit of data_aug to TX, namely the start bit
                        tx_state <= STATE_TRANSMITTING;     -- Move on to next state
                    end if;
                    
                -- Transmit all 10 bits with proper the proper duration per bit based on the selected baud rate.
                when STATE_TRANSMITTING =>
                    serial_out <= data_aug(to_integer(tx_index));  -- Set output based on current bit to transmit
                    bit_delay <= bit_delay + 1;                     -- Keep track of duration to hold this bit
                    if bit_delay > to_unsigned(CLKS_PER_BIT, 32) then  -- Check if bit duration has expired
                        if tx_index = "1001" then                  -- Check if just transmitted the final bit, i.e. the STOP bit
                            tx_state <= STATE_CLEANUP;            -- Move on to next state
                        else
                            tx_index <= tx_index + 1;             -- Still more bits to send so, point to next bit
                            bit_delay <= (others => '0');         -- Clear counter used to regulate baud rate
                        end if;
                    end if;
                    
                -- Pause for a few bit durations after full byte transmitted.
                when STATE_CLEANUP =>
                    bit_delay <= bit_delay + 1;                    -- Keep track of how long been in cleanup state
                    if bit_delay > to_unsigned(5 * CLKS_PER_BIT, 32) then  -- If paused HIGH long enough, then return to idle state
                        tx_state <= STATE_IDLE;
                    end if;
                    
                -- Should never get here, but if do, return to IDLE
                when others =>
                    tx_state <= STATE_IDLE;
            end case;
        end if;
    end process;

    -- Synchronizer for trigger input
    process (clk_50M) begin
        if rising_edge(clk_50M) then
            trigger_0 <= trigger_raw;
            trigger <= trigger_0;
        end if;
    end process;

end Behavioral;

// VHDL entity uart_tx_tester, as the project stores it:
--------------------------------------------------------------------------------
-- Project : UART_Module
-- File    : UART_Transmitter_Tester
-- Autor   : Selma Benhassine
-- Date    :
--
--------------------------------------------------------------------------------
-- Description : Testbench file for the UART transmitter
--
--------------------------------------------------------------------------------

library IEEE;
use IEEE.STD_LOGIC_1164.ALL;
use IEEE.NUMERIC_STD.ALL;

entity uart_tx_tester is
    Port (
        clk_50M : in STD_LOGIC;               -- Input clock, assumed 50 MHz
        run_test_raw : in STD_LOGIC;          -- HIGH indicates to continuously run test
        tx_busy : in STD_LOGIC;               -- HIGH indicates transmitter is busy 
        data_out : out STD_LOGIC_VECTOR (7 downto 0);  -- Data byte (8 bits) to transmit
        trigger : out STD_LOGIC                -- Trigger to tell UART module to begin transmission
    );
end uart_tx_tester;

architecture Behavioral of uart_tx_tester is

    signal run_test_0 : std_logic := '0';          -- Synchronizer for 'start test' switch input
    signal run_test : std_logic := '0';            -- Synchronizer for 'start test' switch input
    signal tester_state : unsigned(5 downto 0) := (others => '0');  -- FSM state variable
    -- signal byte_index : unsigned(31 downto 0) := unsigned(8*16)-unsigned(1);          -- Pointer to beginning of next byte to transmit in 16 byte message
    constant BYTE_INDEX_INIT: natural := (8*16)-1; -- Calculate the initial value for byte_index
    signal byte_index : unsigned(31 downto 0) := to_unsigned(BYTE_INDEX_INIT, 32); -- Initialize byte_index with the calculated value
	 signal pause_delay : unsigned(31 downto 0) := (others => '0');  -- Counter for delay between re-transmissions of message
    signal trigger_ctr : unsigned(5 downto 0) := (others => '0');    -- Delay to hold trigger high, in clock cycles

    constant STATE_IDLE : unsigned(5 downto 0) := "000000";          -- Legal values for tester_state
    constant STATE_LOAD : unsigned(5 downto 0) := "000010";          -- Legal values for tester_state
    constant STATE_TRIGGER : unsigned(5 downto 0) := "000100";       -- Legal values for tester_state
    constant STATE_POLL_BUSY : unsigned(5 downto 0) := "001000";     -- Legal values for tester_state
    constant STATE_PAUSE : unsigned(5 downto 0) := "010000";         -- Legal values for tester_state

    constant MSG_DELAY : unsigned(31 downto 0) := to_unsigned(100_000, 32);  -- Delay between messages re-transmissions, in clk cycles
	 
	 -- Message to transmit
    signal byte_str : std_logic_vector((8*16)-1 downto 0) := "01001000" & "01100101" & "01101100" & "01101100" & "01101111" & "00100000" & "01010111" & "01101111" &
                                                             "01110010" & "01101100" & "01100100" & "00100001" & "00100000" & "00100000" & "00100000" & "00100000";

-- hello world! is "01001000" & "01100101" & "01101100" & "01101100" & "01101111" & "00100000" & "01010111" & "01101111" &
                                                            -- "01110010" & "01101100" & "01100100" & "00100001" & "00100000" & "00100000" & "00100000" & "00100000";


begin

    -- Synchronizer for "run_test" input since, as tested, this comes from a 
    -- slide switch on the DE10-Lite board, which is not synchronous with the
    -- clock.
    process (clk_50M) begin
        if rising_edge(clk_50M) then
            run_test_0 <= run_test_raw;
            run_test <= run_test_0;
        end if;
    end process;

    -- Main Finite State Machine that sequences the test
    process (clk_50M) begin
        if rising_edge(clk_50M) then
            case tester_state is
                -- Wait for request to begin test.
                when STATE_IDLE =>
                    trigger <= '0';
                    if run_test = '1' then
                        byte_index <= to_unsigned(BYTE_INDEX_INIT, 32);
                        tester_state <= STATE_LOAD;
                    end if;
                    
                -- Output next byte to transmitter module, with trigger still low
                -- so it won't transmit yet.
                when STATE_LOAD =>
                    trigger <= '0';
                    data_out <= byte_str(to_integer(byte_index) downto to_integer(byte_index)-7);
                    trigger_ctr <= to_unsigned(5, 6);
                    tester_state <= STATE_TRIGGER;
                    
                -- Now that previous state output'd the next byte to transmit,
                -- assert the trigger signal to begin the transmission.
                when STATE_TRIGGER =>
                    trigger <= '1';
                    trigger_ctr <= trigger_ctr - 1;
                    if trigger_ctr = 0 then
                        tester_state <= STATE_POLL_BUSY;
                    end if;
                    
                -- Clear trigger signal, and wait until all bits shifted out
                -- for the current byte.
                when STATE_POLL_BUSY =>
                    trigger <= '0';
                    if tx_busy = '0' then
                        if byte_index <= 7 then
                            pause_delay <= (others => '0');
                            tester_state <= STATE_PAUSE;
                        else
                            byte_index <= byte_index - 8;
                            tester_state <= STATE_LOAD;
                        end if;
                    end if;
                    
                -- Once transmitted full message, pause before 
                -- transmitting message again for testing convenience.
                when STATE_PAUSE =>
                    pause_delay <= pause_delay + 1;
                    if pause_delay > to_integer(MSG_DELAY) then
                        tester_state <= STATE_IDLE;
                    end if;
                    
                -- Should never get here, but if do, return to IDLE
                when others =>
                    tester_state <= STATE_IDLE;
            end case;
        end if;
    end process;

end Behavioral;
