// Logisim project uart_tx_test.circ as structural Verilog: 1 circuit, main circuit main
module main (
  input  [7:0] in_1,
  input  in_2,
  output out_3,
  output out_4
);

  wire clock_1_out;

  Clock clock_1 (.out(clock_1_out));
  // VHDL_Entity #(.content("library IEEE;\nuse IEEE.STD_LOGIC_1164.ALL;\nuse IEEE.NUMERIC_STD.ALL;\n\nentity uart_tx is\n    Port (\n        clk_50M : in STD_LOGIC;               -- Input clock, assumed 50 MHz\n        data_raw : in STD_LOGIC_VECTOR (7 downto 0);  -- Data byte (8 bits) to transmit\n        trigger_raw : in STD_LOGIC;           -- Tells module to begin transmission of data_raw byte\n        busy : out STD_LOGIC;                 -- Flag to indicate a transmission is in progress\n        serial_out : out STD_LOGIC            -- UART output serial datastream\n    );\nend uart_tx;\n\narchitecture Behavioral of uart_tx is\n	 \n	 constant CLKS_PER_BIT: integer := 124; -- normally 868, but let's try lower\n	 \n    type state_type is (STATE_IDLE, STATE_TRANSMITTING, STATE_CLEANUP);\n    signal tx_state : state_type := STATE_IDLE;  -- State variable for main finite state machine\n    signal data_aug : std_logic_vector(9 downto 0) := (others => '0');  -- Augmented data word to transmit that includes START bit, data byte, and STOP BIT\n    signal tx_index : unsigned(3 downto 0) := (others => '0');  -- Index of bit currently transmitting\n    signal bit_delay : unsigned(31 downto 0) := (others => '0'); -- Timer to regulate baud rate\n\n    signal trigger_0 : std_logic := '0';  -- Synchronizer on trigger input signal\n    signal trigger : std_logic := '0';    -- Synchronizer on trigger input signal\n\n    -- Localparam CLKS_PER_BIT is not needed in VHDL since it's used as a constant value in the code directly\n\nbegin\n\n    process (clk_50M) begin\n        if rising_edge(clk_50M) then\n            case tx_state is\n                -- Wait for trigger condition indicating it's time to transmit a byte.\n                when STATE_IDLE =>\n                    busy <= '0';                 -- Indicate that transmitter is idle.\n                    serial_out <= '1';           -- Idle output HIGH, per standard UART behavior.\n                    if trigger = '1' then        -- Check if received trigger to TX a byte\n                        data_aug <= '1' & data_raw & '0';   -- Create augmented byte with start and stop bits\n                        busy <= '1';                        -- Indicate that transmitter is busy.\n                        bit_delay <= (others => '0');       -- Clear timer used to track duration of each bit\n                        tx_index <= (others => '0');        -- Point to first bit of data_aug to TX, namely the start bit\n                        tx_state <= STATE_TRANSMITTING;     -- Move on to next state\n                    end if;\n                    \n                -- Transmit all 10 bits with proper the proper duration per bit based on the selected baud rate.\n                when STATE_TRANSMITTING =>\n                    serial_out <= data_aug(to_integer(tx_index));  -- Set output based on current bit to transmit\n                    bit_delay <= bit_delay + 1;                     -- Keep track of duration to hold this bit\n                    if bit_delay > to_unsigned(CLKS_PER_BIT, 32) then  -- Check if bit duration has expired\n                        if tx_index = \"1001\" then                  -- Check if just transmitted the final bit, i.e. the STOP bit\n                            tx_state <= STATE_CLEANUP;            -- Move on to next state\n                        else\n                            tx_index <= tx_index + 1;             -- Still more bits to send so, point to next bit\n                            bit_delay <= (others => '0');         -- Clear counter used to regulate baud rate\n                        end if;\n                    end if;\n                    \n                -- Pause for a few bit durations after full byte transmitted.\n                when STATE_CLEANUP =>\n                    bit_delay <= bit_delay + 1;                    -- Keep track of how long been in cleanup state\n                    if bit_delay > to_unsigned(5 * CLKS_PER_BIT, 32) then  -- If paused HIGH long enough, then return to idle state\n                        tx_state <= STATE_IDLE;\n                    end if;\n                    \n                -- Should never get here, but if do, return to IDLE\n                when others =>\n                    tx_state <= STATE_IDLE;\n            end case;\n        end if;\n    end process;\n\n    -- Synchronizer for trigger input\n    process (clk_50M) begin\n        if rising_edge(clk_50M) then\n            trigger_0 <= trigger_raw;\n            trigger <= trigger_0;\n        end if;\n    end process;\n\nend Behavioral;")) vhdl_entity_1: pin names not known; wires that end beside it: clock_1_out, in_1, in_2, out_3, out_4
endmodule
