// Logisim project uart_tx_tester_test.circ as structural Verilog: 1 circuit, main circuit main
module main (
  input  in_1,
  input  in_2,
  output [7:0] out_3,
  output out_4
);

  wire vhdl_entity_1_p1;

  // VHDL_Entity #(.content("library IEEE;\nuse IEEE.STD_LOGIC_1164.ALL;\nuse IEEE.NUMERIC_STD.ALL;\n\nentity uart_tx_tester is\n    Port (\n        clk_50M : in STD_LOGIC;               -- Input clock, assumed 50 MHz\n        run_test_raw : in STD_LOGIC;          -- HIGH indicates to continuously run test\n        tx_busy : in STD_LOGIC;               -- HIGH indicates transmitter is busy \n        data_out : out STD_LOGIC_VECTOR (7 downto 0);  -- Data byte (8 bits) to transmit\n        trigger : out STD_LOGIC                -- Trigger to tell UART module to begin transmission\n    );\nend uart_tx_tester;\n\narchitecture Behavioral of uart_tx_tester is\n\n    signal run_test_0 : std_logic := '0';          -- Synchronizer for 'start test' switch input\n    signal run_test : std_logic := '0';            -- Synchronizer for 'start test' switch input\n    signal tester_state : unsigned(5 downto 0) := (others => '0');  -- FSM state variable\n    -- signal byte_index : unsigned(31 downto 0) := unsigned(8*16)-unsigned(1);          -- Pointer to beginning of next byte to transmit in 16 byte message\n    constant BYTE_INDEX_INIT: natural := (8*16)-1; -- Calculate the initial value for byte_index\n    signal byte_index : unsigned(31 downto 0) := to_unsigned(BYTE_INDEX_INIT, 32); -- Initialize byte_index with the calculated value\n	 signal pause_delay : unsigned(31 downto 0) := (others => '0');  -- Counter for delay between re-transmissions of message\n    signal trigger_ctr : unsigned(5 downto 0) := (others => '0');    -- Delay to hold trigger high, in clock cycles\n\n    constant STATE_IDLE : unsigned(5 downto 0) := \"000000\";          -- Legal values for tester_state\n    constant STATE_LOAD : unsigned(5 downto 0) := \"000010\";          -- Legal values for tester_state\n    constant STATE_TRIGGER : unsigned(5 downto 0) := \"000100\";       -- Legal values for tester_state\n    constant STATE_POLL_BUSY : unsigned(5 downto 0) := \"001000\";     -- Legal values for tester_state\n    constant STATE_PAUSE : unsigned(5 downto 0) := \"010000\";         -- Legal values for tester_state\n\n    constant MSG_DELAY : unsigned(31 downto 0) := to_unsigned(100_000_000, 32);  -- Delay between messages re-transmissions, in clk cycles\n	 \n	 -- Message to transmit\n    signal byte_str : std_logic_vector((8*16)-1 downto 0) := \"01001000\" & \"01100101\" & \"01101100\" & \"01101100\" & \"01101111\" & \"00100000\" & \"01010111\" & \"01101111\" &\n                                                            \"01110010\" & \"01101100\" & \"01100100\" & \"00100001\" & \"00100000\" & \"00100000\" & \"00100000\" & \"00100000\";\n\n\nbegin\n\n    -- Synchronizer for \"run_test\" input since, as tested, this comes from a \n    -- slide switch on the DE10-Lite board, which is not synchronous with the\n    -- clock.\n    process (clk_50M) begin\n        if rising_edge(clk_50M) then\n            run_test_0 <= run_test_raw;\n            run_test <= run_test_0;\n        end if;\n    end process;\n\n    -- Main Finite State Machine that sequences the test\n    process (clk_50M) begin\n        if rising_edge(clk_50M) then\n            case tester_state is\n                -- Wait for request to begin test.\n                when STATE_IDLE =>\n                    trigger <= '0';\n                    if run_test = '1' then\n                        byte_index <= to_unsigned(BYTE_INDEX_INIT, 32);\n                        tester_state <= STATE_LOAD;\n                    end if;\n                    \n                -- Output next byte to transmitter module, with trigger still low\n                -- so it won't transmit yet.\n                when STATE_LOAD =>\n                    trigger <= '0';\n                    data_out <= byte_str(to_integer(byte_index) downto to_integer(byte_index)-7);\n                    trigger_ctr <= to_unsigned(5, 6);\n                    tester_state <= STATE_TRIGGER;\n                    \n                -- Now that previous state output'd the next byte to transmit,\n                -- assert the trigger signal to begin the transmission.\n                when STATE_TRIGGER =>\n                    trigger <= '1';\n                    trigger_ctr <= trigger_ctr - 1;\n                    if trigger_ctr = 0 then\n                        tester_state <= STATE_POLL_BUSY;\n                    end if;\n                    \n                -- Clear trigger signal, and wait until all bits shifted out\n                -- for the current byte.\n                when STATE_POLL_BUSY =>\n                    trigger <= '0';\n                    if tx_busy = '0' then\n                        if byte_index <= 7 then\n                            pause_delay <= (others => '0');\n                            tester_state <= STATE_PAUSE;\n                        else\n                            byte_index <= byte_index - 8;\n                            tester_state <= STATE_LOAD;\n                        end if;\n                    end if;\n                    \n                -- Once transmitted full message, pause before \n                -- transmitting message again for testing convenience.\n                when STATE_PAUSE =>\n                    pause_delay <= pause_delay + 1;\n                    if pause_delay > to_integer(MSG_DELAY) then\n                        tester_state <= STATE_IDLE;\n                    end if;\n                    \n                -- Should never get here, but if do, return to IDLE\n                when others =>\n                    tester_state <= STATE_IDLE;\n            end case;\n        end if;\n    end process;\n\nend Behavioral;")) vhdl_entity_1: pin names not known; wires that end beside it: vhdl_entity_1_p1, in_1, in_2, out_3, out_4
  Clock clock_1 (.out(vhdl_entity_1_p1));
endmodule
