// Logisim project Uart_Driver.circ as structural Verilog
module driver (
  input  run_tx,
  input  [63:0] message_tx,
  input  input_rx,
  input  clk,
  input  reset,
  output tx_out,
  output [63:0] stored_message,
  output message_stored
);

  wire uart_rx_1_o_rx_dv, uart_tx_1_busy, uart_tx_tester_1_trigger;
  wire [7:0] uart_rx_1_o_rx_byte, uart_tx_tester_1_data_out;

  uart_tx_tester uart_tx_tester_1 (
    .clk_50M(clk), .run_test_raw(run_tx), .tx_busy(uart_tx_1_busy), .byte_str(message_tx),
    .data_out(uart_tx_tester_1_data_out), .trigger(uart_tx_tester_1_trigger));
  uart_rx uart_rx_1 (
    .i_Clock(clk), .i_RX_Serial(input_rx), .o_RX_Byte(uart_rx_1_o_rx_byte), .o_RX_DV(uart_rx_1_o_rx_dv));
  uart_tx uart_tx_1 (
    .clk_50M(clk), .data_raw(uart_tx_tester_1_data_out), .trigger_raw(uart_tx_tester_1_trigger),
    .busy(uart_tx_1_busy), .serial_out(tx_out));
  letter8_writer1 letter8_writer_1 (
    .new_letter(uart_rx_1_o_rx_byte), .update(uart_rx_1_o_rx_dv), .clk(clk), .reset(reset),
    .stored_message(stored_message), .write_done(message_stored));
endmodule

module demux8 (
  input  in_bit,
  input  [3:0] decision,
  output choice0,
  output choice1,
  output choice2,
  output choice3,
  output choice4,
  output choice5,
  output choice6,
  output choice7
);

  wire not_1_out, not_2_out, not_3_out, not_4_out;

  not not_1 (not_1_out, decision[3]);
  not not_2 (not_2_out, decision[2]);
  not not_3 (not_3_out, decision[1]);
  not not_4 (not_4_out, decision[0]);
  and and_1 (choice0, in_bit, not_1_out, not_2_out, not_3_out, not_4_out);
  and and_2 (choice1, in_bit, not_1_out, not_2_out, not_3_out, decision[0]);
  and and_3 (choice2, in_bit, not_1_out, not_2_out, decision[1], not_4_out);
  and and_4 (choice3, in_bit, not_1_out, not_2_out, decision[1], decision[0]);
  and and_5 (choice4, in_bit, not_1_out, decision[2], not_3_out, not_4_out);
  and and_6 (choice5, in_bit, not_1_out, decision[2], not_3_out, decision[0]);
  and and_7 (choice6, in_bit, not_1_out, decision[2], decision[1], not_4_out);
  and and_8 (choice7, in_bit, not_1_out, decision[2], decision[1], decision[0]);
endmodule

module letter8_writer1 (
  input  [7:0] new_letter,
  input  update,
  input  clk,
  input  reset,
  output [63:0] stored_message,
  output write_done
);

  wire and_1_out, and_2_out, comparator_1_eq, comparator_2_eq, demux_1_choice0, demux_1_choice1,
       demux_1_choice2, demux_1_choice3, demux_1_choice4, demux_1_choice5, demux_1_choice6, demux_1_choice7,
       not_1_out, not_2_out, not_3_out, or_1_out, or_2_out;
  wire [3:0] counter_1_q;
  wire [7:0] multiplexer_1_out, multiplexer_2_out, multiplexer_3_out, multiplexer_4_out, multiplexer_5_out,
       multiplexer_6_out, multiplexer_7_out, multiplexer_8_out, multiplexer_9_out, register_2_q,
       register_3_q, register_4_q, register_5_q, register_6_q, register_7_q, register_8_q, register_9_q;

  Comparator #(.mode("unsigned"), .width(4)) comparator_1 (
    .a(4'b1000), .b(counter_1_q), .eq(comparator_1_eq));  // open: gt, lt
  not not_1 (not_1_out, not_2_out);
  Counter #(.max('h8), .width(4)) counter_1 (
    .clr(or_1_out), .load(1'b0), .up(1'b1), .count(1'b1), .clk(and_1_out), .D(4'b1000), .Q(counter_1_q));  // open: carry
  or or_1 (or_1_out, not_1_out, reset);
  and and_1 (and_1_out, not_2_out, update);
  Comparator #(.mode("unsigned")) comparator_2 (.a(new_letter), .b(8'ha), .eq(comparator_2_eq));  // open: gt, lt
  Multiplexer #(.width(8)) multiplexer_1 (
    .in0(new_letter), .in1({8{1'b0}}), .out(multiplexer_1_out), .sel(comparator_2_eq));
  or or_2 (or_2_out, comparator_2_eq, comparator_1_eq);
  Register #(.width(1)) register_1 (.D(or_2_out), .en(and_2_out), .clk(clk), .Q(write_done), .clr(reset));
  and and_2 (and_2_out, update, not_2_out);
  not not_2 (not_2_out, write_done);
  demux8 demux_1 (
    .in_bit(not_2_out), .decision(counter_1_q), .choice0(demux_1_choice0), .choice1(demux_1_choice1),
    .choice2(demux_1_choice2), .choice3(demux_1_choice3), .choice4(demux_1_choice4),
    .choice5(demux_1_choice5), .choice6(demux_1_choice6), .choice7(demux_1_choice7));
  Multiplexer #(.width(8)) multiplexer_2 (
    .in0(register_2_q), .in1(multiplexer_1_out), .out(multiplexer_2_out), .sel(demux_1_choice0));
  Multiplexer #(.width(8)) multiplexer_3 (
    .in0(register_3_q), .in1(multiplexer_1_out), .out(multiplexer_3_out), .sel(demux_1_choice1));
  Multiplexer #(.width(8)) multiplexer_4 (
    .in0(register_4_q), .in1(multiplexer_1_out), .out(multiplexer_4_out), .sel(demux_1_choice2));
  Multiplexer #(.width(8)) multiplexer_5 (
    .in0(register_5_q), .in1(multiplexer_1_out), .out(multiplexer_5_out), .sel(demux_1_choice3));
  Multiplexer #(.width(8)) multiplexer_6 (
    .in0(register_6_q), .in1(multiplexer_1_out), .out(multiplexer_6_out), .sel(demux_1_choice4));
  Multiplexer #(.width(8)) multiplexer_7 (
    .in0(register_7_q), .in1(multiplexer_1_out), .out(multiplexer_7_out), .sel(demux_1_choice5));
  Multiplexer #(.width(8)) multiplexer_8 (
    .in0(register_8_q), .in1(multiplexer_1_out), .out(multiplexer_8_out), .sel(demux_1_choice6));
  Multiplexer #(.width(8)) multiplexer_9 (
    .in0(register_9_q), .in1(multiplexer_1_out), .out(multiplexer_9_out), .sel(demux_1_choice7));
  not not_3 (not_3_out, reset);
  Register register_2 (.D(multiplexer_2_out), .en(not_3_out), .clk(clk), .Q(register_2_q), .clr(reset));
  Register register_3 (.D(multiplexer_3_out), .en(not_3_out), .clk(clk), .Q(register_3_q), .clr(reset));
  Register register_4 (.D(multiplexer_4_out), .en(not_3_out), .clk(clk), .Q(register_4_q), .clr(reset));
  Register register_5 (.D(multiplexer_5_out), .en(not_3_out), .clk(clk), .Q(register_5_q), .clr(reset));
  Register register_6 (.D(multiplexer_6_out), .en(not_3_out), .clk(clk), .Q(register_6_q), .clr(reset));
  Register register_7 (.D(multiplexer_7_out), .en(not_3_out), .clk(clk), .Q(register_7_q), .clr(reset));
  Register register_8 (.D(multiplexer_8_out), .en(not_3_out), .clk(clk), .Q(register_8_q), .clr(reset));
  Register register_9 (.D(multiplexer_9_out), .en(not_3_out), .clk(clk), .Q(register_9_q), .clr(reset));
  Multiplexer #(.width(8)) multiplexer_10 (.in0(register_2_q), .in1({8{1'b0}}), .out(stored_message[7:0]), .sel(reset));
  Multiplexer #(.width(8)) multiplexer_11 (
    .in0(register_3_q), .in1({8{1'b0}}), .out(stored_message[15:8]), .sel(reset));
  Multiplexer #(.width(8)) multiplexer_12 (
    .in0(register_4_q), .in1({8{1'b0}}), .out(stored_message[23:16]), .sel(reset));
  Multiplexer #(.width(8)) multiplexer_13 (
    .in0(register_5_q), .in1({8{1'b0}}), .out(stored_message[31:24]), .sel(reset));
  Multiplexer #(.width(8)) multiplexer_14 (
    .in0(register_6_q), .in1({8{1'b0}}), .out(stored_message[39:32]), .sel(reset));
  Multiplexer #(.width(8)) multiplexer_15 (
    .in0(register_7_q), .in1({8{1'b0}}), .out(stored_message[47:40]), .sel(reset));
  Multiplexer #(.width(8)) multiplexer_16 (
    .in0(register_8_q), .in1({8{1'b0}}), .out(stored_message[55:48]), .sel(reset));
  Multiplexer #(.width(8)) multiplexer_17 (
    .in0(register_9_q), .in1({8{1'b0}}), .out(stored_message[63:56]), .sel(reset));

  // Notes on the sheet:
  //   if count =7 wait one more and stop
  //   count to 7 for 8 bytes
  //   if lstop
  //   asynchronously
  //   8 bytes, saved or passed on
endmodule

// VHDL entity uart_rx, as the project stores it:
--------------------------------------------------------------------------------
-- Project : Semester Project - UART on FPGA
-- File    : uart_rx.vhd
-- Author  : Selma Benhassine
-- Date    :
--
--------------------------------------------------------------------------------
-- Description :
-- UART receiver module for asynchronous serial communication. 
--------------------------------------------------------------------------------

LIBRARY ieee;
USE ieee.std_logic_1164.all;
USE ieee.numeric_std.all;

ENTITY uart_rx IS
    PORT (
        i_Clock      : IN  std_logic;                    -- System clock input
        i_RX_Serial  : IN  std_logic;                    -- Serial data input
        o_RX_Byte    : OUT std_logic_vector(7 downto 0); -- Output byte
        o_RX_DV      : OUT std_logic                    -- Data valid signal
    );
END uart_rx;

ARCHITECTURE Behavioral OF uart_rx IS
    type state_type IS (IDLE, RX_START_BIT, RX_DATA_BITS, RX_STOP_BIT, CLEANUP);
    signal r_SM_Main : state_type := IDLE;
    signal r_Start_Done : std_logic := '0';
    signal r_Clock_Count : unsigned(23 downto 0) := (others => '0');
    signal r_Bit_Index : unsigned(2 downto 0) := (others => '0');
    signal r_RX_Byte : std_logic_vector(7 downto 0) := (others => '0');
    signal r_RX_DV : std_logic := '0';
    signal r_FSM_Mode : std_logic_vector(2 downto 0) := (others => '0'); 
    constant N : integer := 3;  -- Number of cycles to confirm bit
    signal bit_counter : integer range 0 to N := 0;  -- N is the number of clock cycles for confirmation
    
    constant CLKS_PER_BIT : integer := 15;  -- Clock cycles per bit, baud rate for 1.25MHz clock works from 77100-80900
    
begin
    process(i_Clock)
    begin
        if rising_edge(i_Clock) then            
            case r_SM_Main is
                when IDLE =>
                    r_FSM_Mode <= "001";
                    r_RX_DV <= '0';
                    r_Clock_Count <= (others => '0');
                    r_Bit_Index <= (others => '0');
                    r_Start_Done <= '0';

                    if i_RX_Serial = '0' then
                        bit_counter <= bit_counter + 1;
                        if bit_counter >= N then  -- Confirmed low for N clock cycles
                            r_SM_Main <= RX_START_BIT;
                            bit_counter <= 0;  -- Reset counter
                        end if;
                    else
                        bit_counter <= 0;  -- Reset counter if high is detected
                    end if;

                when RX_START_BIT =>
                    r_FSM_Mode <= "010";
                    r_Clock_Count <= r_Clock_Count + 1;
                    if r_Clock_Count = CLKS_PER_BIT/2 then
                        if i_RX_Serial = '0' then
                            r_Start_Done <= '1';  -- Midpoint confirmation of the start bit
                        else
                            r_Start_Done <= '0';
                        end if;
                    end if;
                    if r_Clock_Count = CLKS_PER_BIT - 1 then
                        r_Clock_Count <= (others => '0');  -- Reset the counter for use in the next state
                        if r_Start_Done = '1' then
                            r_SM_Main <= RX_DATA_BITS;  -- Transition to data bits after confirming start bit
                        else
                            r_SM_Main <= IDLE;  -- Reset if the start bit is not sustained
                        end if;
                    end if;

                when RX_DATA_BITS =>
                    r_FSM_Mode <= "011";
                    r_Clock_Count <= r_Clock_Count + 1;
                    if r_Clock_Count = CLKS_PER_BIT/2 then
                        r_RX_Byte(to_integer(r_Bit_Index)) <= i_RX_Serial;  -- Sample at mid-point
                    end if;
                    if r_Clock_Count = CLKS_PER_BIT - 1 then
                        r_Clock_Count <= (others => '0');    -- Reset for next bit
                        if r_Bit_Index < 7 then
                            r_Bit_Index <= r_Bit_Index + 1;
                        else
                            r_Bit_Index <= (others => '0');
                            r_SM_Main <= RX_STOP_BIT;  -- Proceed to stop bit verification
                        end if;
                    end if;

                -- eventually check for parity bit

                when RX_STOP_BIT =>
                    r_FSM_Mode <= "100";
                    r_Clock_Count <= r_Clock_Count + 1;
                    if r_Clock_Count = CLKS_PER_BIT/2 then
                        if i_RX_Serial = '1' then
                            r_RX_DV <= '1';  -- Midpoint confirmation of the stop bit
                        end if;
                    end if;
                    if r_Clock_Count = CLKS_PER_BIT - 1 then
                        r_Clock_Count <= (others => '0');
                        r_SM_Main <= CLEANUP;  -- Cleanup and prepare to return to IDLE
                    end if;

                when CLEANUP =>
                    r_FSM_Mode <= "101";
                    r_SM_Main <= IDLE;
                    r_RX_DV <= '0';

                when others =>
                    r_SM_Main <= IDLE;

            end case;
        end if;
    end process;

    
    o_RX_Byte <= r_RX_Byte;
    o_RX_DV <= r_RX_DV;

END ARCHITECTURE Behavioral;

// VHDL entity uart_tx, as the project stores it:
--------------------------------------------------------------------------------
-- Project : Semester Project - UART on FPGA
-- File    : UART_TX
-- Author   : Selma Benhassine
-- Date    :
--
--------------------------------------------------------------------------------
-- Description :
-- The transmitter file for the UART_transmission portion of the project
--
--------------------------------------------------------------------------------

library IEEE;
use IEEE.STD_LOGIC_1164.ALL;
use IEEE.NUMERIC_STD.ALL;

entity uart_tx is
    Port (
        clk_50M : in STD_LOGIC;               -- Input clock, assumed 50 MHz
        data_raw : in STD_LOGIC_VECTOR (7 downto 0);  -- Data byte (8 bits) to transmit
        trigger_raw : in STD_LOGIC;           -- Tells module to begin transmission of data_raw byte
        busy : out STD_LOGIC;                 -- Flag to indicate a transmission is in progress
        serial_out : out STD_LOGIC            -- UART output serial datastream
    );
end uart_tx;


architecture Behavioral of uart_tx is
	 
	constant CLKS_PER_BIT: integer := 15; -- Clock cycles per bit, baud rate for 1.25MHz clock works from 69500-77400
--                                                  1
--     CLKS_PER_BIT =  F_clk [cycles/sec] * --------------------
--                                           baud_rate[bit/sec]
	 
    type state_type is (STATE_IDLE, STATE_TRANSMITTING, STATE_CLEANUP);
    signal tx_state : state_type := STATE_IDLE;  -- State variable for main finite state machine
    signal data_aug : std_logic_vector(9 downto 0) := (others => '0');  -- Augmented data word to transmit that includes START bit, data byte, and STOP BIT
    signal tx_index : unsigned(3 downto 0) := (others => '0');  -- Index of bit currently transmitting
    signal bit_delay : unsigned(31 downto 0) := (others => '0'); -- Timer to regulate baud rate
   

    signal trigger_0 : std_logic := '0';  -- Synchronizer on trigger input signal
    signal trigger : std_logic := '0';    -- Synchronizer on trigger input signal

begin

    process (clk_50M) begin
        if rising_edge(clk_50M) then
            case tx_state is
                -- Wait for trigger condition indicating it's time to transmit a byte.
                when STATE_IDLE =>
                    busy <= '0';                 -- Indicate that transmitter is idle.
                    serial_out <= '1';           -- Idle output HIGH, per standard UART behavior.
                    if trigger = '1' then        -- Check if received trigger to TX a byte
                        data_aug <= '1' & data_raw & '0';   -- Create augmented byte with start and stop bits, eventually add parity bit
                        busy <= '1';                        -- Indicate that transmitter is busy.
                        bit_delay <= (others => '0');       -- Clear timer used to track duration of each bit
                        tx_index <= (others => '0');        -- Point to first bit of data_aug to TX, namely the start bit
                        tx_state <= STATE_TRANSMITTING;     -- Move on to next state
                    end if;
                    
                -- Transmit all 10 bits with proper the proper duration per bit based on the selected baud rate.
                when STATE_TRANSMITTING =>
                    serial_out <= data_aug(to_integer(tx_index));  -- Set output based on current bit to transmit
                    bit_delay <= bit_delay + 1;                     -- Keep track of duration to hold this bit
                    if bit_delay > to_unsigned(CLKS_PER_BIT, 32) then  -- Check if bit duration has expired
                        if tx_index = "1001" then                  -- Check if just transmitted the final bit, i.e. the STOP bit
                            tx_state <= STATE_CLEANUP;            -- Move on to next state
                        else
                            tx_index <= tx_index + 1;             -- Still more bits to send so, point to next bit
                            bit_delay <= (others => '0');         -- Clear counter used to regulate baud rate
                        end if;
                    end if;
                    
                -- Pause for a few bit durations after full byte transmitted.
                when STATE_CLEANUP =>
                    bit_delay <= bit_delay + 1;                    -- Keep track of how long been in cleanup state
                    if bit_delay > to_unsigned(5 * CLKS_PER_BIT, 32) then  -- If paused HIGH long enough, then return to idle state
                        tx_state <= STATE_IDLE;
                    end if;
                    
                -- Should never get here, but if do, return to IDLE
                when others =>
                    tx_state <= STATE_IDLE;
            end case;
        end if;
    end process;

    -- Synchronizer for trigger input
    process (clk_50M) begin
        if rising_edge(clk_50M) then
            trigger_0 <= trigger_raw;
            trigger <= trigger_0;
        end if;
    end process;

end Behavioral;

// VHDL entity uart_tx_tester, as the project stores it:
library IEEE;
use IEEE.STD_LOGIC_1164.ALL;
use IEEE.NUMERIC_STD.ALL;

entity uart_tx_tester is
    Port (
        clk_50M : in STD_LOGIC;               -- Input clock, assumed 50 MHz
        run_test_raw : in STD_LOGIC;          -- HIGH indicates to continuously run test
        tx_busy : in STD_LOGIC;               -- HIGH indicates transmitter is busy 
        byte_str : in STD_LOGIC_VECTOR(63 downto 0); -- Test to output (8 bytes)
        data_out : out STD_LOGIC_VECTOR (7 downto 0);  -- Data byte (8 bits) to transmit
        trigger : out STD_LOGIC               -- Trigger to tell UART module to begin transmission
    );
end uart_tx_tester;

architecture Behavioral of uart_tx_tester is

    signal run_test_0 : std_logic := '0';          -- Synchronizer for 'start test' switch input
    signal run_test : std_logic := '0';            -- Synchronizer for 'start test' switch input
    signal run_test_prev : std_logic := '0';       -- Previous state of run_test
    signal tester_state : unsigned(5 downto 0) := (others => '0');  -- FSM state variable
    signal byte_index : unsigned(5 downto 0) := (others => '0');     -- Pointer to the current byte to transmit in the message
    signal pause_delay : unsigned(31 downto 0) := (others => '0');  -- Counter for delay between re-transmissions of message
    signal trigger_ctr : unsigned(5 downto 0) := (others => '0');    -- Delay to hold trigger high, in clock cycles

    signal extended_byte_str : std_logic_vector(71 downto 0);        -- Extended byte string (9 bytes)

    constant STATE_IDLE : unsigned(5 downto 0) := "000000";          -- Legal values for tester_state
    constant STATE_LOAD : unsigned(5 downto 0) := "000010";          -- Legal values for tester_state
    constant STATE_TRIGGER : unsigned(5 downto 0) := "000100";       -- Legal values for tester_state
    constant STATE_POLL_BUSY : unsigned(5 downto 0) := "001000";     -- Legal values for tester_state
    constant STATE_PAUSE : unsigned(5 downto 0) := "010000";         -- Legal values for tester_state

    constant MSG_DELAY : unsigned(31 downto 0) := to_unsigned(100, 32);  -- Delay between messages re-transmissions, in clk cycles
    constant BYTE_STR_LENGTH : unsigned(5 downto 0) := to_unsigned(8, 6);    -- Length of the byte string (number of bytes - 1, now 8+1=9)

begin

    -- Synchronizer for "run_test" input since, as tested, this comes from a 
    -- slide switch on the DE10-Lite board, which is not synchronous with the
    -- clock.
    process (clk_50M) begin
        if rising_edge(clk_50M) then
            run_test_0 <= run_test_raw;
            run_test <= run_test_0;
        end if;
    end process;

    -- Process to detect the rising edge of run_test
    process (clk_50M) begin
        if rising_edge(clk_50M) then
            run_test_prev <= run_test;
        end if;
    end process;

    -- Extend the byte string with '00001010' at the end
    extended_byte_str <= byte_str & "00001010";

    -- Main Finite State Machine that sequences the test
    process (clk_50M) begin
        if rising_edge(clk_50M) then
            case tester_state is
                -- Wait for request to begin test.
                when STATE_IDLE =>
                    trigger <= '0';
                    if run_test = '1' and run_test_prev = '0' then
                        byte_index <= (others => '0');  -- Initialize byte_index to zero
                        tester_state <= STATE_LOAD;
                    end if;
                    
                -- Output next byte to transmitter module, with trigger still low
                -- so it won't transmit yet.
                when STATE_LOAD =>
                    trigger <= '0';
                    data_out <= extended_byte_str(to_integer(byte_index) * 8 + 7 downto to_integer(byte_index) * 8);
                    trigger_ctr <= to_unsigned(5, 6);
                    tester_state <= STATE_TRIGGER;
                    
                -- Now that previous state output'd the next byte to transmit,
                -- assert the trigger signal to begin the transmission.
                when STATE_TRIGGER =>
                    trigger <= '1';
                    trigger_ctr <= trigger_ctr - 1;
                    if trigger_ctr = 0 then
                        tester_state <= STATE_POLL_BUSY;
                    end if;
                    
                -- Clear trigger signal, and wait until all bits shifted out
                -- for the current byte.
                when STATE_POLL_BUSY =>
                    trigger <= '0';
                    if tx_busy = '0' then
                        if byte_index = BYTE_STR_LENGTH then
                            pause_delay <= (others => '0');
                            tester_state <= STATE_PAUSE;
                        else
                            byte_index <= byte_index + 1;
                            tester_state <= STATE_LOAD;
                        end if;
                    end if;
                    
                -- Once transmitted full message, pause before 
                -- transmitting message again for testing convenience.
                when STATE_PAUSE =>
                    pause_delay <= pause_delay + 1;
                    if pause_delay > to_integer(MSG_DELAY) then
                        tester_state <= STATE_IDLE;
                    end if;
                    
                -- Should never get here, but if do, return to IDLE
                when others =>
                    tester_state <= STATE_IDLE;
            end case;
        end if;
    end process;

end Behavioral;
