// Logisim project basic_selmikins_fsm.circ as structural Verilog: 2 circuits, main circuit main
module main (
  input  reset,
  input  cycle,
  input  select_mode
);

  wire and_1_out, and_2_out, clock_1_out, comparator_1_eq, comparator_2_eq, cycle_t, main_selector,
       select_pressed;
  wire [1:0] main_menu, messages, rx, state;

  Comparator #(.mode("unsigned"), .width(2)) comparator_1 (.a(2'b10), .b(state), .eq(comparator_1_eq));  // open: gt, lt
  Comparator #(.mode("unsigned"), .width(2)) comparator_2 (.a(2'b01), .b(state), .eq(comparator_2_eq));  // open: gt, lt
  and and_1 (and_1_out, cycle_t, comparator_1_eq);
  // Probe on and_1_out
  and and_2 (and_2_out, cycle_t, comparator_2_eq);
  // Probe on and_2_out
  Multiplexer #(.width(2)) multiplexer_1 (.in0(2'b10), .in1(2'b01), .out(rx), .sel(and_1_out));
  Counter #(.max('h1), .width(1)) counter_1 (.clr(reset), .clk(cycle), .carry(cycle_t));  // open: load, up, count, D, Q
  // Probe on cycle_t
  Clock clock_1 (.out(clock_1_out));
  Multiplexer #(.width(2)) multiplexer_2 (.in0(2'b11), .in1(2'b01), .out(messages), .sel(and_2_out));
  Multiplexer #(.width(2)) multiplexer_3 (.in0(2'b11), .in1(2'b01), .out(main_menu), .sel(cycle_t));
  Register #(.width(1)) register_1 (.D(cycle_t), .en(select_mode), .clk(clock_1_out), .Q(main_selector), .clr(reset));
  Counter #(.max('h1), .width(1)) counter_2 (
    .clr(reset), .clk(select_mode), .Q(select_pressed));  // open: load, up, count, D, carry
  Multiplexer #(.select(2)) multiplexer_4 (
    .in0(main_menu[0]), .in1(messages[0]), .in2(rx[0]), .sel(state));  // open: in3, out
  Multiplexer #(.select(2)) multiplexer_5 (.in0(main_menu[1]), .in1(messages[1]), .in2(rx[1]));  // open: in3, out, sel
  Multiplexer #(.select(2)) multiplexer_6 (.sel(state));  // open: in0, in1, in2, in3, out
  Multiplexer #(.select(2)) multiplexer_7 (.sel(state));  // open: in0, in1, in2, in3, out
  Multiplexer #(.select(2)) multiplexer_8 (.sel(state));  // open: in0, in1, in2, in3, out
  Multiplexer #(.select(2)) multiplexer_9 (.sel(state));  // open: in0, in1, in2, in3, out
  // Probe on state
  selmikinsFSM selmikinsfsm_1 (.select_pressed(select_pressed), .main_selector(main_selector), .state(state));
endmodule

module selmikinsFSM (
  input  select_pressed,
  input  main_selector,
  output [1:0] state
);

  wire not_1_out;

  not not_1 (not_1_out, main_selector);
  and and_1 (state[1], select_pressed, main_selector);
  and and_2 (state[0], select_pressed, not_1_out);
endmodule
