// Logisim project test_Sr.circ as structural Verilog: 2 circuits, main circuit main
module main (
  input  reset,
  output [7:0] seg0,
  output [7:0] seg1,
  output [7:0] seg2,
  output [7:0] seg3,
  output [7:0] seg4,
  output [7:0] seg5
);

  wire clock_1_out, d_ff_1_q;
  wire [2:0] counter_1_q;
  wire [7:0] multiplexer_1_out;

  Clock clock_1 (.out(clock_1_out));
  Counter #(.max('h7), .width(3)) counter_1 (
    .clr(reset), .load(1'b0), .up(1'b1), .count(1'b1), .clk(clock_1_out), .D(3'b111), .Q(counter_1_q));  // open: carry
  D_Flip_Flop d_ff_1 (.clk(clock_1_out), .Q(d_ff_1_q));  // open: D, Qn, preset, reset
  Multiplexer #(.select(3), .width(8)) multiplexer_1 (
    .in0(8'h41), .in1(8'h42), .in2(8'h43), .in3(8'h44), .in4(8'h45), .in5(8'h46), .in6(8'h47), .in7(8'h48),
    .out(multiplexer_1_out), .sel(counter_1_q));
  Register register_1 (.D(multiplexer_1_out), .en(d_ff_1_q), .clk(clock_1_out), .Q(seg0), .clr(reset));
  Register register_2 (.D(seg0), .en(d_ff_1_q), .clk(clock_1_out), .Q(seg1), .clr(reset));
  Register register_3 (.D(seg1), .en(d_ff_1_q), .clk(clock_1_out), .Q(seg2), .clr(reset));
  Register register_4 (.D(seg2), .en(d_ff_1_q), .clk(clock_1_out), .Q(seg3), .clr(reset));
  Register register_5 (.D(seg3), .en(d_ff_1_q), .clk(clock_1_out), .Q(seg4), .clr(reset));
  Register register_6 (.D(seg4), .en(d_ff_1_q), .clk(clock_1_out), .Q(seg5), .clr(reset));
endmodule

module demux (
  input  in_bit,
  input  [2:0] decision,
  output choice0,
  output choice1,
  output choice2,
  output choice3,
  output choice4,
  output choice5,
  output choice6,
  output choice7
);

  wire not_1_out, not_2_out, not_3_out;

  not not_1 (not_1_out, decision[2]);
  not not_2 (not_2_out, decision[1]);
  not not_3 (not_3_out, decision[0]);
  and and_1 (choice0, in_bit, not_1_out, not_2_out, not_3_out);
  and and_2 (choice1, in_bit, not_1_out, not_2_out, decision[0]);
  and and_3 (choice2, in_bit, not_1_out, decision[1], not_3_out);
  and and_4 (choice3, in_bit, not_1_out, decision[1], decision[0]);
  and and_5 (choice4, in_bit, decision[2], not_2_out, not_3_out);
  and and_6 (choice5, in_bit, decision[2], not_2_out, decision[0]);
  and and_7 (choice6, in_bit, decision[2], decision[1], not_3_out);
  and and_8 (choice7, in_bit, decision[2], decision[1], decision[0]);
endmodule
